// Logisim project vrc6_cells.circ as structural Verilog: 6 circuits, main circuit vrc6_31aoi
module vrc6_31aoi (
  input  a0,
  input  a1,
  input  b0,
  input  b1,
  output x
);

  wire transistor_1_out, transistor_5_out, transistor_7_out;

  Transistor transistor_1 (.in(1'b1), .out(transistor_1_out), .gate(a0));
  Transistor transistor_2 (.in(1'b1), .out(transistor_1_out), .gate(a1));
  Transistor transistor_3 (.in(transistor_1_out), .out(x), .gate(b0));
  Transistor transistor_4 (.in(transistor_1_out), .out(x), .gate(b1));
  Transistor #(.\type ("n")) transistor_5 (.in(1'b0), .out(transistor_5_out), .gate(a0));
  Transistor #(.\type ("n")) transistor_6 (.in(transistor_5_out), .out(x), .gate(a1));
  Transistor #(.\type ("n")) transistor_7 (.in(1'b0), .out(transistor_7_out), .gate(b0));
  Transistor #(.\type ("n")) transistor_8 (.in(transistor_7_out), .out(x), .gate(b1));
endmodule

module mux2 (
  input  s0,
  input  s1,
  input  a0,
  input  a1,
  input  a2,
  input  a3,
  output x
);

  wire nand_1_out, nand_2_out, nand_3_out, nand_4_out, not_1_out, not_2_out, not_3_out, not_4_out;

  not not_1 (not_1_out, s0);
  not not_2 (not_2_out, s1);
  not not_3 (not_3_out, not_1_out);
  not not_4 (not_4_out, not_2_out);
  nand nand_1 (nand_1_out, a0, not_1_out, not_2_out);
  nand nand_2 (nand_2_out, a1, not_3_out, not_2_out);
  nand nand_3 (nand_3_out, a2, not_1_out, not_4_out);
  nand nand_4 (nand_4_out, a3, not_3_out, not_4_out);
  nand nand_5 (x, nand_1_out, nand_2_out, nand_3_out, nand_4_out);

  // Notes on the sheet:
  //   k1
  //   k2
  //   k3
  //   k4
  //   t1
  //   t2
  //   t3
  //   t4
endmodule

module vrc6_xor (
  input  a,
  input  b,
  output x
);

  wire nand_1_out, nand_2_out, or_1_out;

  nand nand_1 (nand_1_out, a, b);
  or or_1 (or_1_out, a, b);
  nand nand_2 (nand_2_out, or_1_out, nand_1_out);
  not not_1 (x, nand_2_out);
endmodule

module dec2 (
  input  n_ena,
  input  a1,
  input  a0,
  output nx0,
  output nx1,
  output nx2,
  output nx3
);

  wire not_1_out, not_2_out, not_3_out, not_4_out, not_5_out;

  not not_1 (not_1_out, n_ena);
  not not_2 (not_2_out, a1);
  not not_3 (not_3_out, a0);
  not not_4 (not_4_out, not_2_out);
  not not_5 (not_5_out, not_3_out);
  nand nand_1 (nx0, not_1_out, not_3_out, not_2_out);
  nand nand_2 (nx1, not_1_out, not_5_out, not_2_out);
  nand nand_3 (nx2, not_1_out, not_3_out, not_4_out);
  nand nand_4 (nx3, not_1_out, not_5_out, not_4_out);

  // Notes on the sheet:
  //   k1
  //   k4
  //   k5
  //   k2
  //   k3
endmodule

module dec4 (
  input  a4,
  input  a3,
  input  a2,
  input  a1,
  input  bin,
  output x4,
  output x3,
  output x2,
  output x1,
  output bout
);

  wire and_1_out, and_2_out, and_3_out, nand_1_out, nand_2_out, nand_3_out, nor_1_out, nor_2_out, nor_3_out,
       nor_4_out, nor_5_out, nor_6_out, nor_7_out, or_1_out;

  nand nand_1 (nand_1_out, nand_3_out, a4);
  or or_1 (or_1_out, nand_3_out, a4);
  and and_1 (and_1_out, a3, nor_2_out);
  nor nor_1 (nor_1_out, a3, nor_2_out);
  nor nor_2 (nor_2_out, nand_3_out, a4);
  nor nor_3 (nor_3_out, a4, a3, nand_3_out);
  and and_2 (and_2_out, nor_3_out, a2);
  nor nor_4 (nor_4_out, nor_3_out, a2);
  nor nor_5 (nor_5_out, a2, a3, a4, nand_3_out);
  nor nor_6 (nor_6_out, a1, a2, a3, a4);
  nor nor_7 (nor_7_out, a1, nor_5_out);
  and and_3 (and_3_out, a1, nor_5_out);
  not not_1 (bout, nand_2_out);
  nand nand_2 (nand_2_out, nor_6_out, bin);
  nand nand_3 (nand_3_out, bin, bin);
  nand nand_4 (x4, or_1_out, nand_1_out);
  nor nor_8 (x3, and_1_out, nor_1_out);
  nor nor_9 (x2, and_2_out, nor_4_out);
  nor nor_10 (x1, and_3_out, nor_7_out);

  // Notes on the sheet:
  //   lsb
  //   msb
  //   k1
  //   k1
  //   k4
  //   k3
  //   k3
  //   k2
  //   k1
  //   k1
  //   k1
  //   k4
  //   k3
  //   k2
  //   k1
  //   lsb
  //   msb
endmodule

module dec4_opt (
  input  in_1,
  input  in_2,
  input  a4,
  input  a3,
  input  a2,
  input  a1,
  input  in_7,
  input  in_8,
  input  bin,
  output x4,
  output out_11,
  output x3,
  output x2,
  output out_14,
  output x1,
  output bout
);

  wire and_2_out, nand_1_out, nor_1_out, nor_2_out, nor_3_out, nor_4_out, nor_6_out, not_1_out, or_1_out,
       xnor_2_out, xor_4_out;

  not not_1 (not_1_out, bin);
  nor nor_1 (nor_1_out, not_1_out, a4);
  nor nor_2 (nor_2_out, a4, a3, not_1_out);
  nor nor_3 (nor_3_out, a2, a3, a4, not_1_out);
  nor nor_4 (nor_4_out, a1, a2, a3, a4);
  xnor xnor_1 (x4, not_1_out, a4);
  and and_1 (bout, nor_4_out, bin);
  xor xor_1 (x3, a3, nor_1_out);
  xor xor_2 (x2, nor_2_out, a2);
  xor xor_3 (x1, a1, nor_3_out);
  or or_1 (or_1_out, in_1, in_2);
  and and_2 (and_2_out, in_7, in_8);
  nor nor_5 (out_14, and_2_out, nor_6_out);
  nor nor_6 (nor_6_out, in_7, in_8);
  nand nand_1 (nand_1_out, in_1, in_2);
  nand nand_2 (out_11, or_1_out, nand_1_out);
  xor xor_4 (xor_4_out, in_7, in_8);
  xnor xnor_2 (xnor_2_out, in_1, in_2);

  // Notes on the sheet:
  //   k1
  //   k1
  //   k1
  //   k1
  //   k1
  //   k1
  //   k1
  //   = 
  //   =
endmodule
