// Logisim project vrc7.circ as structural Verilog: 51 circuits, main circuit ds1001
module sr_bit (
  input  value,
  input  clk1,
  input  clk2,
  output valout
);

  wire d_ff_1_qn;

  D_Flip_Flop #(.trigger("high")) d_ff_1 (.D(value), .clk(clk1), .Qn(d_ff_1_qn));  // open: Q, preset, reset
  D_Flip_Flop #(.trigger("high")) d_ff_2 (.D(d_ff_1_qn), .clk(clk2), .Qn(valout));  // open: Q, preset, reset
endmodule

module noise_lfsr (
  input  test,
  input  clk1,
  input  clk2,
  output out_4
);

  wire nor_1_out, or_1_out, sr_bit_1_valout, sr_bit_2_valout, sr_bit_3_valout, sr_bit_4_valout,
       sr_bit_5_valout, sr_bit_6_valout, sr_bit_7_valout, sr_bit_8_valout, sr_bit_9_valout, sr_bit_10_valout,
       sr_bit_11_valout, sr_bit_12_valout, sr_bit_13_valout, sr_bit_14_valout, sr_bit_15_valout,
       sr_bit_16_valout, sr_bit_17_valout, sr_bit_18_valout, sr_bit_19_valout, sr_bit_20_valout,
       sr_bit_21_valout, sr_bit_22_valout, xor_1_out;

  sr_bit sr_bit_1 (.value(or_1_out), .clk1(clk1), .clk2(clk2), .valout(sr_bit_1_valout));
  sr_bit sr_bit_2 (.value(sr_bit_1_valout), .clk1(clk1), .clk2(clk2), .valout(sr_bit_2_valout));
  sr_bit sr_bit_3 (.value(sr_bit_2_valout), .clk1(clk1), .clk2(clk2), .valout(sr_bit_3_valout));
  sr_bit sr_bit_4 (.value(sr_bit_3_valout), .clk1(clk1), .clk2(clk2), .valout(sr_bit_4_valout));
  sr_bit sr_bit_5 (.value(sr_bit_4_valout), .clk1(clk1), .clk2(clk2), .valout(sr_bit_5_valout));
  sr_bit sr_bit_6 (.value(sr_bit_5_valout), .clk1(clk1), .clk2(clk2), .valout(sr_bit_6_valout));
  sr_bit sr_bit_7 (.value(sr_bit_6_valout), .clk1(clk1), .clk2(clk2), .valout(sr_bit_7_valout));
  sr_bit sr_bit_8 (.value(sr_bit_7_valout), .clk1(clk1), .clk2(clk2), .valout(sr_bit_8_valout));
  sr_bit sr_bit_9 (.value(sr_bit_8_valout), .clk1(clk1), .clk2(clk2), .valout(sr_bit_9_valout));
  sr_bit sr_bit_10 (.value(sr_bit_9_valout), .clk1(clk1), .clk2(clk2), .valout(sr_bit_10_valout));
  sr_bit sr_bit_11 (.value(sr_bit_10_valout), .clk1(clk1), .clk2(clk2), .valout(sr_bit_11_valout));
  sr_bit sr_bit_12 (.value(sr_bit_11_valout), .clk1(clk1), .clk2(clk2), .valout(sr_bit_12_valout));
  sr_bit sr_bit_13 (.value(sr_bit_12_valout), .clk1(clk1), .clk2(clk2), .valout(sr_bit_13_valout));
  sr_bit sr_bit_14 (.value(sr_bit_13_valout), .clk1(clk1), .clk2(clk2), .valout(sr_bit_14_valout));
  sr_bit sr_bit_15 (.value(sr_bit_14_valout), .clk1(clk1), .clk2(clk2), .valout(sr_bit_15_valout));
  sr_bit sr_bit_16 (.value(sr_bit_15_valout), .clk1(clk1), .clk2(clk2), .valout(sr_bit_16_valout));
  sr_bit sr_bit_17 (.value(sr_bit_16_valout), .clk1(clk1), .clk2(clk2), .valout(sr_bit_17_valout));
  sr_bit sr_bit_18 (.value(sr_bit_17_valout), .clk1(clk1), .clk2(clk2), .valout(sr_bit_18_valout));
  sr_bit sr_bit_19 (.value(sr_bit_18_valout), .clk1(clk1), .clk2(clk2), .valout(sr_bit_19_valout));
  sr_bit sr_bit_20 (.value(sr_bit_19_valout), .clk1(clk1), .clk2(clk2), .valout(sr_bit_20_valout));
  sr_bit sr_bit_21 (.value(sr_bit_20_valout), .clk1(clk1), .clk2(clk2), .valout(sr_bit_21_valout));
  sr_bit sr_bit_22 (.value(sr_bit_21_valout), .clk1(clk1), .clk2(clk2), .valout(sr_bit_22_valout));
  sr_bit sr_bit_23 (.value(sr_bit_22_valout), .clk1(clk1), .clk2(clk2), .valout(out_4));
  nor nor_1 (nor_1_out, sr_bit_1_valout, sr_bit_2_valout, sr_bit_3_valout, sr_bit_4_valout, sr_bit_5_valout, sr_bit_6_valout, sr_bit_7_valout, sr_bit_8_valout, sr_bit_9_valout, sr_bit_10_valout, sr_bit_11_valout, sr_bit_12_valout, sr_bit_13_valout, sr_bit_14_valout, sr_bit_15_valout, sr_bit_16_valout, sr_bit_17_valout, sr_bit_18_valout, sr_bit_19_valout, sr_bit_20_valout, sr_bit_21_valout, sr_bit_22_valout, out_4);
  xor xor_1 (xor_1_out, sr_bit_9_valout, out_4);
  or or_1 (or_1_out, test, nor_1_out, xor_1_out);
endmodule

module reg_bit (
  input  value,
  input  write,
  input  n_write,
  input  reset,
  output valout
);

  wire controlled_buffer_1_out, d_ff_1_qn, nor_1_out;

  assign controlled_buffer_1_out = write ? value : 1'bz;  // Controlled_Buffer controlled_buffer_1
  D_Flip_Flop #(.trigger("high")) d_ff_1 (
    .D(controlled_buffer_1_out), .clk(1'b1), .Qn(d_ff_1_qn));  // open: Q, preset, reset
  assign controlled_buffer_1_out = n_write ? nor_1_out : 1'bz;  // Controlled_Buffer controlled_buffer_2
  not not_1 (valout, d_ff_1_qn);
  nor nor_1 (nor_1_out, d_ff_1_qn, reset);
endmodule

module ds1001 (
  input  debug_pin,
  input  in_2,
  input  in_3,
  input  in_4,
  input  in_5,
  input  [7:0] data_in,
  input  in_7,
  input  in_8,
  input  in_9,
  input  in_10,
  input  in_11,
  input  in_12,
  output [3:0] out_13,
  output out_14,
  output out_15,
  output out_16,
  output out_17,
  output [4:0] out_18,
  output out_19,
  output out_20,
  output out_21,
  output out_22,
  output out_23,
  output out_24,
  output out_25,
  output out_26,
  output out_27,
  output out_28,
  output out_29,
  output out_30,
  output out_31,
  output out_32,
  output out_33,
  output [7:0] out_34,
  output [8:0] out_35,
  output [2:0] out_36
);

  wire chan_registers_1_key_on, chan_registers_1_sus_on, chan_registers_ctrl_1_write10,
       chan_registers_ctrl_1_write20, chan_registers_ctrl_1_write30, clock_1_out, clock_handler_1_clk1,
       clock_handler_1_clk2, clock_handler_1_mclk1, clock_handler_1_mclk2, instrument_ctrl_1_car_sel,
       instrument_ctrl_1_car_sel_custom, instrument_ctrl_1_ch_sel_custom, instrument_ctrl_1_clk2_inv,
       instrument_ctrl_1_force_zerorate, instrument_ctrl_1_mod_sel, instrument_ctrl_1_mod_sel_custom,
       instrument_ctrl_1_out_sel1, instrument_ctrl_1_out_sel2, not_1_out, not_2_out, not_4_out, not_8_out,
       not_9_out, or_1_out, registers_1_bass_drum, registers_1_high_hat, registers_1_ksr, registers_1_rhythm,
       registers_1_snare_drum, registers_1_sustain, registers_1_tom_tom, registers_1_top_cymbal,
       registers_1_tremolo, registers_1_vibrato, registers_1_wf_car, registers_1_wf_mod, rhythm_ctrl1_1_bd0,
       rhythm_ctrl1_1_bd1, rhythm_ctrl1_1_hh, rhythm_ctrl1_1_sd, rhythm_ctrl1_1_tc, rhythm_ctrl1_1_tom;
  wire [1:0] registers_1_ksl;
  wire [2:0] registers_1_feedback;
  wire [3:0] chan_registers_1_instrument, registers_1_attack, registers_1_decay, registers_1_release_rate,
       registers_1_sustain_level;
  wire [5:0] registers_1_tl;
  wire [7:0] chan_registers_ctrl_1_data_out, not_3_out, not_5_out, not_6_out, not_7_out,
       transparent_latch8_1_out_2, transparent_latch8_2_out_2;
  wire [20:0] instrument_ctrl_1_inst_sel;

  Clock clock_1 (.out(clock_1_out));
  not not_1 (not_1_out, debug_pin);
  not not_2 (not_2_out, not_1_out);
  assign not_3_out = ~data_in;  // NOT_Gate not_3, 8 bits wide
  not not_4 (not_4_out, not_2_out);
  assign not_5_out = ~not_3_out;  // NOT_Gate not_5, 8 bits wide
  clock_handler clock_handler_1 (
    .MCLK(clock_1_out), .reset(in_2), .MCLK1(clock_handler_1_mclk1), .MCLK2(clock_handler_1_mclk2),
    .clk1(clock_handler_1_clk1), .clk2(clock_handler_1_clk2));  // open: dac_clk
  io_handler io_handler_1 (
    .CS(in_3), .WR(in_4), .A0(in_5), .reset(in_2), .mclk1(clock_handler_1_mclk1),
    .mclk2(clock_handler_1_mclk2), .clk1(clock_handler_1_clk1), .clk2(clock_handler_1_clk2), .write(out_19),
    .write0(out_20), .write1(out_21));
  transparent_latch8 transparent_latch8_1 (.in_1(not_5_out), .out_2(transparent_latch8_1_out_2));
  transparent_latch8 transparent_latch8_2 (.in_1(transparent_latch8_1_out_2), .out_2(transparent_latch8_2_out_2));
  chan_registers_ctrl chan_registers_ctrl_1 (
    .data(out_34), .write_addr(out_20), .write_data(out_21), .reset(in_2), .sync(out_32),
    .clk1(clock_handler_1_clk1), .clk2(clock_handler_1_clk2), .data_out(chan_registers_ctrl_1_data_out),
    .write20(chan_registers_ctrl_1_write20), .write30(chan_registers_ctrl_1_write30),
    .write10(chan_registers_ctrl_1_write10));
  rhythm_ctrl1 rhythm_ctrl1_1 (
    .rhythm(or_1_out), .sync(out_28), .clk1(clock_handler_1_clk1), .clk2(clock_handler_1_clk2),
    .bd0(rhythm_ctrl1_1_bd0), .hh(rhythm_ctrl1_1_hh), .tom(rhythm_ctrl1_1_tom), .bd1(rhythm_ctrl1_1_bd1),
    .sd(rhythm_ctrl1_1_sd), .tc(rhythm_ctrl1_1_tc));
  assign not_6_out = ~transparent_latch8_2_out_2;  // NOT_Gate not_6, 8 bits wide
  registers registers_1 (
    .clk1(clock_handler_1_clk1), .clk2(clock_handler_1_clk2), .sel_mod(instrument_ctrl_1_mod_sel_custom),
    .sel_car(instrument_ctrl_1_car_sel_custom), .sel_chn(instrument_ctrl_1_ch_sel_custom), .reset(in_2),
    .write_signal1(out_21), .write_signal2(out_20), .databus(out_34), .multi(out_13), .ksr(registers_1_ksr),
    .sustain(registers_1_sustain), .vibrato(registers_1_vibrato), .tremolo(registers_1_tremolo),
    .tl(registers_1_tl), .ksl(registers_1_ksl), .feedback(registers_1_feedback), .wf_mod(registers_1_wf_mod),
    .wf_car(registers_1_wf_car), .decay(registers_1_decay), .attack(registers_1_attack),
    .release_rate(registers_1_release_rate), .sustain_level(registers_1_sustain_level),
    .rhythm(registers_1_rhythm), .bass_drum(registers_1_bass_drum), .snare_drum(registers_1_snare_drum),
    .tom_tom(registers_1_tom_tom), .top_cymbal(registers_1_top_cymbal), .high_hat(registers_1_high_hat),
    .test0(out_14), .test1(out_15), .test2(out_16), .test3(out_17));
  assign not_7_out = ~not_6_out;  // NOT_Gate not_7, 8 bits wide
  fsm_counters fsm_counters_1 (
    .reset(in_2), .clk1(clock_handler_1_clk1), .clk2(clock_handler_1_clk2), .fsm_cnt(out_18));
  fsm_table_ds1001 fsm_table_ds1001_1 (
    .counter(out_18), .rhythm(or_1_out), .clk1(clock_handler_1_clk1), .clk2(clock_handler_1_clk2),
    .out_5(out_22), .out_6(out_23), .out_7(out_24), .out_8(out_25), .out_9(out_26), .out_10(out_27),
    .out_11(out_28), .out_12(out_29), .out_13(out_30), .out_14(out_31), .out_15(out_32), .out_16(out_33));
  chan_registers chan_registers_1 (
    .data(chan_registers_ctrl_1_data_out), .write20(chan_registers_ctrl_1_write20),
    .write10(chan_registers_ctrl_1_write10), .write30(chan_registers_ctrl_1_write30), .sel1(in_7),
    .sel2(in_8), .sel3(in_9), .volsel1(in_10), .volsel2(in_11), .clk1(clock_handler_1_clk1),
    .clk2(clock_handler_1_clk2), .fnum(out_35), .block_num(out_36), .key_on(chan_registers_1_key_on),
    .sus_on(chan_registers_1_sus_on), .instrument(chan_registers_1_instrument));  // open: volume
  instrument_ctrl instrument_ctrl_1 (
    .instr(chan_registers_1_instrument), .bd0(rhythm_ctrl1_1_bd0), .hh(rhythm_ctrl1_1_hh),
    .tom(rhythm_ctrl1_1_tom), .bd1(rhythm_ctrl1_1_bd1), .sd(rhythm_ctrl1_1_sd), .tc(rhythm_ctrl1_1_tc),
    .kon(in_12), .modcar_sel(out_25), .clk1(clock_handler_1_clk1), .clk2(clock_handler_1_clk2),
    .clk2_inv(instrument_ctrl_1_clk2_inv), .force_zerorate(instrument_ctrl_1_force_zerorate),
    .mod_sel_custom(instrument_ctrl_1_mod_sel_custom), .ch_sel_custom(instrument_ctrl_1_ch_sel_custom),
    .car_sel_custom(instrument_ctrl_1_car_sel_custom), .out_sel1(instrument_ctrl_1_out_sel1),
    .out_sel2(instrument_ctrl_1_out_sel2), .car_sel(instrument_ctrl_1_car_sel),
    .mod_sel(instrument_ctrl_1_mod_sel), .inst_sel(instrument_ctrl_1_inst_sel));  // open: out_13, modcar_sel_clk1
  not not_8 (not_8_out, not_4_out);
  or or_1 (or_1_out, not_8_out, registers_1_rhythm);
  data_register data_register_1 (.data(not_7_out), .write(out_19), .data_reg(out_34));
  kon_ctrl kon_ctrl_1 (
    .keyon(chan_registers_1_key_on), .hh(rhythm_ctrl1_1_hh), .tc(rhythm_ctrl1_1_tc),
    .tomtom(rhythm_ctrl1_1_tom), .sd(rhythm_ctrl1_1_sd), .bd0(rhythm_ctrl1_1_bd0), .bd1(rhythm_ctrl1_1_bd1),
    .hh_kon(registers_1_high_hat), .tc_kon(registers_1_top_cymbal), .tom_kon(registers_1_tom_tom),
    .sd_kon(registers_1_snare_drum), .bd_kon(registers_1_bass_drum));  // open: keyon_comb
  instrument_ds1001 instrument_ds1001_1 (
    .instr_sel(instrument_ctrl_1_inst_sel), .mod_sel(instrument_ctrl_1_mod_sel),
    .car_sel(instrument_ctrl_1_car_sel), .out_sel1(instrument_ctrl_1_out_sel1),
    .out_sel2(instrument_ctrl_1_out_sel2), .clk1(clock_handler_1_clk1), .clk2(clock_handler_1_clk2),
    .clk2_inv(instrument_ctrl_1_clk2_inv), .tl(registers_1_tl), .dc(registers_1_wf_car),
    .dm(registers_1_wf_mod), .fb(registers_1_feedback), .am(registers_1_tremolo), .vib(registers_1_vibrato),
    .et(registers_1_sustain), .ksr(registers_1_ksr), .multi(out_13), .ksl(registers_1_ksl),
    .ar(registers_1_attack), .dr(registers_1_decay), .sl(registers_1_sustain_level),
    .rr(registers_1_release_rate));
  not not_9 (not_9_out, registers_1_ksr);
  rate_calc rate_calc_1 (
    .ar(registers_1_attack), .dr(registers_1_decay), .rr(registers_1_release_rate), .egtype(not_9_out),
    .sustain(chan_registers_1_sus_on), .zero_rate(instrument_ctrl_1_force_zerorate),
    .clk1(clock_handler_1_clk1));  // open: eg_state, rate
  operator operator_1 ();  // open: phase, env, env_mute, feedback, fb_enable, mod_enable, modcar_sel, wf_mod, wf_car, clk1, clk2, chan_out

  // Notes on the sheet:
  //   Yamaha DS1001 (VRC7)
endmodule

module reg_bit2 (
  input  value,
  input  write,
  input  n_write,
  input  reset,
  input  oe,
  output valout
);

  wire controlled_buffer_1_out, controlled_buffer_3_out, d_ff_1_qn, nor_1_out;

  assign controlled_buffer_1_out = write ? value : 1'bz;  // Controlled_Buffer controlled_buffer_1
  assign controlled_buffer_1_out = n_write ? nor_1_out : 1'bz;  // Controlled_Buffer controlled_buffer_2
  D_Flip_Flop #(.trigger("high")) d_ff_1 (
    .D(controlled_buffer_1_out), .clk(1'b1), .Qn(d_ff_1_qn));  // open: Q, preset, reset
  nor nor_1 (nor_1_out, d_ff_1_qn, reset);
  assign controlled_buffer_3_out = nor_1_out ? 1'b1 : 1'bz;  // Controlled_Buffer controlled_buffer_3
  assign controlled_buffer_3_out = d_ff_1_qn ? 1'b0 : 1'bz;  // Controlled_Buffer controlled_buffer_4
  assign valout = oe ? controlled_buffer_3_out : 1'bz;  // Controlled_Buffer controlled_buffer_5
endmodule

module reg_handler (
  input  value,
  input  write,
  input  n_write,
  input  and_val,
  input  clk1,
  input  clk2,
  output valout,
  output n_valout
);

  wire and_1_out, controlled_buffer_1_out, sr_bit_1_valout;

  assign controlled_buffer_1_out = write ? value : 1'bz;  // Controlled_Buffer controlled_buffer_1
  assign controlled_buffer_1_out = n_write ? sr_bit_1_valout : 1'bz;  // Controlled_Buffer controlled_buffer_2
  sr_bit sr_bit_1 (.value(controlled_buffer_1_out), .clk1(clk1), .clk2(clk2), .valout(sr_bit_1_valout));
  and and_1 (and_1_out, sr_bit_1_valout, and_val);
  buf buffer_1 (valout, and_1_out);
  not not_1 (n_valout, and_1_out);
endmodule

module registers (
  input  clk1,
  input  clk2,
  input  sel_mod,
  input  sel_car,
  input  sel_chn,
  input  reset,
  input  write_signal1,
  input  write_signal2,
  input  [7:0] databus,
  output [3:0] multi,
  output ksr,
  output sustain,
  output vibrato,
  output tremolo,
  output [5:0] tl,
  output [1:0] ksl,
  output [2:0] feedback,
  output wf_mod,
  output wf_car,
  output [3:0] decay,
  output [3:0] attack,
  output [3:0] release_rate,
  output [3:0] sustain_level,
  output rhythm,
  output bass_drum,
  output snare_drum,
  output tom_tom,
  output top_cymbal,
  output high_hat,
  output test0,
  output test1,
  output test2,
  output test3
);

  wire not_1_out, not_2_out, reg_addr_decoder_1_addr_0, reg_addr_decoder_1_addr_1, reg_addr_decoder_1_addr_2,
       reg_addr_decoder_1_addr_3, reg_addr_decoder_1_addr_4, reg_addr_decoder_1_addr_5,
       reg_addr_decoder_1_addr_6, reg_addr_decoder_1_addr_7, reg_addr_decoder_1_addr_e,
       reg_addr_decoder_1_addr_f, reg_handler_1_n_valout, reg_handler_1_valout, reg_handler_2_n_valout,
       reg_handler_2_valout, reg_handler_3_n_valout, reg_handler_3_valout, reg_handler_4_n_valout,
       reg_handler_4_valout, reg_handler_5_n_valout, reg_handler_5_valout, reg_handler_6_n_valout,
       reg_handler_6_valout, reg_handler_7_n_valout, reg_handler_7_valout, reg_handler_8_n_valout,
       reg_handler_8_valout, reg_handler_9_n_valout, reg_handler_9_valout, reg_handler_10_n_valout,
       reg_handler_10_valout;

  not not_1 (not_1_out, write_signal2);
  not not_2 (not_2_out, not_1_out);
  reg_addr_decoder reg_addr_decoder_1 (
    .in_1(databus), .addr_f(reg_addr_decoder_1_addr_f), .addr_e(reg_addr_decoder_1_addr_e),
    .addr_0(reg_addr_decoder_1_addr_0), .addr_1(reg_addr_decoder_1_addr_1),
    .addr_2(reg_addr_decoder_1_addr_2), .addr_3(reg_addr_decoder_1_addr_3),
    .addr_4(reg_addr_decoder_1_addr_4), .addr_5(reg_addr_decoder_1_addr_5),
    .addr_6(reg_addr_decoder_1_addr_6), .addr_7(reg_addr_decoder_1_addr_7));
  reg_bit2 reg_bit2_1 (
    .value(databus[7]), .write(reg_handler_5_valout), .n_write(reg_handler_5_n_valout), .reset(reset),
    .oe(sel_car), .valout(sustain_level[3]));
  reg_bit2 reg_bit2_2 (
    .value(databus[6]), .write(reg_handler_5_valout), .n_write(reg_handler_5_n_valout), .reset(reset),
    .oe(sel_car), .valout(sustain_level[2]));
  reg_bit2 reg_bit2_3 (
    .value(databus[5]), .write(reg_handler_5_valout), .n_write(reg_handler_5_n_valout), .reset(reset),
    .oe(sel_car), .valout(sustain_level[1]));
  reg_bit2 reg_bit2_4 (
    .value(databus[4]), .write(reg_handler_5_valout), .n_write(reg_handler_5_n_valout), .reset(reset),
    .oe(sel_car), .valout(sustain_level[0]));
  reg_bit2 reg_bit2_5 (
    .value(databus[3]), .write(reg_handler_5_valout), .n_write(reg_handler_5_n_valout), .reset(reset),
    .oe(sel_car), .valout(release_rate[3]));
  reg_bit2 reg_bit2_6 (
    .value(databus[2]), .write(reg_handler_5_valout), .n_write(reg_handler_5_n_valout), .reset(reset),
    .oe(sel_car), .valout(release_rate[2]));
  reg_bit2 reg_bit2_7 (
    .value(databus[1]), .write(reg_handler_5_valout), .n_write(reg_handler_5_n_valout), .reset(reset),
    .oe(sel_car), .valout(release_rate[1]));
  reg_bit2 reg_bit2_8 (
    .value(databus[0]), .write(reg_handler_5_valout), .n_write(reg_handler_5_n_valout), .reset(reset),
    .oe(sel_car), .valout(release_rate[0]));
  reg_handler reg_handler_1 (
    .value(reg_addr_decoder_1_addr_3), .write(not_1_out), .n_write(not_2_out), .and_val(write_signal1),
    .clk1(clk1), .clk2(clk2), .valout(reg_handler_1_valout), .n_valout(reg_handler_1_n_valout));
  reg_handler reg_handler_2 (
    .value(reg_addr_decoder_1_addr_4), .write(not_1_out), .n_write(not_2_out), .and_val(write_signal1),
    .clk1(clk1), .clk2(clk2), .valout(reg_handler_2_valout), .n_valout(reg_handler_2_n_valout));
  reg_handler reg_handler_3 (
    .value(reg_addr_decoder_1_addr_5), .write(not_1_out), .n_write(not_2_out), .and_val(write_signal1),
    .clk1(clk1), .clk2(clk2), .valout(reg_handler_3_valout), .n_valout(reg_handler_3_n_valout));
  reg_handler reg_handler_4 (
    .value(reg_addr_decoder_1_addr_6), .write(not_1_out), .n_write(not_2_out), .and_val(write_signal1),
    .clk1(clk1), .clk2(clk2), .valout(reg_handler_4_valout), .n_valout(reg_handler_4_n_valout));
  reg_handler reg_handler_5 (
    .value(reg_addr_decoder_1_addr_7), .write(not_1_out), .n_write(not_2_out), .and_val(write_signal1),
    .clk1(clk1), .clk2(clk2), .valout(reg_handler_5_valout), .n_valout(reg_handler_5_n_valout));
  reg_bit2 reg_bit2_9 (
    .value(databus[7]), .write(reg_handler_4_valout), .n_write(reg_handler_4_n_valout), .reset(reset),
    .oe(sel_mod), .valout(sustain_level[3]));
  reg_bit2 reg_bit2_10 (
    .value(databus[6]), .write(reg_handler_4_valout), .n_write(reg_handler_4_n_valout), .reset(reset),
    .oe(sel_mod), .valout(sustain_level[2]));
  reg_bit2 reg_bit2_11 (
    .value(databus[5]), .write(reg_handler_4_valout), .n_write(reg_handler_4_n_valout), .reset(reset),
    .oe(sel_mod), .valout(sustain_level[1]));
  reg_bit2 reg_bit2_12 (
    .value(databus[4]), .write(reg_handler_4_valout), .n_write(reg_handler_4_n_valout), .reset(reset),
    .oe(sel_mod), .valout(sustain_level[0]));
  reg_bit2 reg_bit2_13 (
    .value(databus[3]), .write(reg_handler_4_valout), .n_write(reg_handler_4_n_valout), .reset(reset),
    .oe(sel_mod), .valout(release_rate[3]));
  reg_bit2 reg_bit2_14 (
    .value(databus[2]), .write(reg_handler_4_valout), .n_write(reg_handler_4_n_valout), .reset(reset),
    .oe(sel_mod), .valout(release_rate[2]));
  reg_bit2 reg_bit2_15 (
    .value(databus[1]), .write(reg_handler_4_valout), .n_write(reg_handler_4_n_valout), .reset(reset),
    .oe(sel_mod), .valout(release_rate[1]));
  reg_bit2 reg_bit2_16 (
    .value(databus[0]), .write(reg_handler_4_valout), .n_write(reg_handler_4_n_valout), .reset(reset),
    .oe(sel_mod), .valout(release_rate[0]));
  reg_handler reg_handler_6 (
    .value(reg_addr_decoder_1_addr_f), .write(not_1_out), .n_write(not_2_out), .and_val(write_signal1),
    .clk1(clk1), .clk2(clk2), .valout(reg_handler_6_valout), .n_valout(reg_handler_6_n_valout));
  reg_handler reg_handler_7 (
    .value(reg_addr_decoder_1_addr_e), .write(not_1_out), .n_write(not_2_out), .and_val(write_signal1),
    .clk1(clk1), .clk2(clk2), .valout(reg_handler_7_valout), .n_valout(reg_handler_7_n_valout));
  reg_handler reg_handler_8 (
    .value(reg_addr_decoder_1_addr_0), .write(not_1_out), .n_write(not_2_out), .and_val(write_signal1),
    .clk1(clk1), .clk2(clk2), .valout(reg_handler_8_valout), .n_valout(reg_handler_8_n_valout));
  reg_handler reg_handler_9 (
    .value(reg_addr_decoder_1_addr_1), .write(not_1_out), .n_write(not_2_out), .and_val(write_signal1),
    .clk1(clk1), .clk2(clk2), .valout(reg_handler_9_valout), .n_valout(reg_handler_9_n_valout));
  reg_handler reg_handler_10 (
    .value(reg_addr_decoder_1_addr_2), .write(not_1_out), .n_write(not_2_out), .and_val(write_signal1),
    .clk1(clk1), .clk2(clk2), .valout(reg_handler_10_valout), .n_valout(reg_handler_10_n_valout));
  reg_bit2 reg_bit2_17 (
    .value(databus[7]), .write(reg_handler_3_valout), .n_write(reg_handler_3_n_valout), .reset(reset),
    .oe(sel_car), .valout(attack[3]));
  reg_bit2 reg_bit2_18 (
    .value(databus[6]), .write(reg_handler_3_valout), .n_write(reg_handler_3_n_valout), .reset(reset),
    .oe(sel_car), .valout(attack[2]));
  reg_bit2 reg_bit2_19 (
    .value(databus[5]), .write(reg_handler_3_valout), .n_write(reg_handler_3_n_valout), .reset(reset),
    .oe(sel_car), .valout(attack[1]));
  reg_bit2 reg_bit2_20 (
    .value(databus[4]), .write(reg_handler_3_valout), .n_write(reg_handler_3_n_valout), .reset(reset),
    .oe(sel_car), .valout(attack[0]));
  reg_bit2 reg_bit2_21 (
    .value(databus[3]), .write(reg_handler_3_valout), .n_write(reg_handler_3_n_valout), .reset(reset),
    .oe(sel_car), .valout(decay[3]));
  reg_bit2 reg_bit2_22 (
    .value(databus[2]), .write(reg_handler_3_valout), .n_write(reg_handler_3_n_valout), .reset(reset),
    .oe(sel_car), .valout(decay[2]));
  reg_bit2 reg_bit2_23 (
    .value(databus[1]), .write(reg_handler_3_valout), .n_write(reg_handler_3_n_valout), .reset(reset),
    .oe(sel_car), .valout(decay[1]));
  reg_bit2 reg_bit2_24 (
    .value(databus[0]), .write(reg_handler_3_valout), .n_write(reg_handler_3_n_valout), .reset(reset),
    .oe(sel_car), .valout(decay[0]));
  reg_bit2 reg_bit2_25 (
    .value(databus[7]), .write(reg_handler_2_valout), .n_write(reg_handler_2_n_valout), .reset(reset),
    .oe(sel_mod), .valout(attack[3]));
  reg_bit2 reg_bit2_26 (
    .value(databus[6]), .write(reg_handler_2_valout), .n_write(reg_handler_2_n_valout), .reset(reset),
    .oe(sel_mod), .valout(attack[2]));
  reg_bit2 reg_bit2_27 (
    .value(databus[5]), .write(reg_handler_2_valout), .n_write(reg_handler_2_n_valout), .reset(reset),
    .oe(sel_mod), .valout(attack[1]));
  reg_bit2 reg_bit2_28 (
    .value(databus[4]), .write(reg_handler_2_valout), .n_write(reg_handler_2_n_valout), .reset(reset),
    .oe(sel_mod), .valout(attack[0]));
  reg_bit2 reg_bit2_29 (
    .value(databus[3]), .write(reg_handler_2_valout), .n_write(reg_handler_2_n_valout), .reset(reset),
    .oe(sel_mod), .valout(decay[3]));
  reg_bit2 reg_bit2_30 (
    .value(databus[2]), .write(reg_handler_2_valout), .n_write(reg_handler_2_n_valout), .reset(reset),
    .oe(sel_mod), .valout(decay[2]));
  reg_bit2 reg_bit2_31 (
    .value(databus[1]), .write(reg_handler_2_valout), .n_write(reg_handler_2_n_valout), .reset(reset),
    .oe(sel_mod), .valout(decay[1]));
  reg_bit2 reg_bit2_32 (
    .value(databus[0]), .write(reg_handler_2_valout), .n_write(reg_handler_2_n_valout), .reset(reset),
    .oe(sel_mod), .valout(decay[0]));
  reg_bit2 reg_bit2_33 (
    .value(databus[7]), .write(reg_handler_1_valout), .n_write(reg_handler_1_n_valout), .reset(reset),
    .oe(sel_car), .valout(ksl[1]));
  reg_bit2 reg_bit2_34 (
    .value(databus[6]), .write(reg_handler_1_valout), .n_write(reg_handler_1_n_valout), .reset(reset),
    .oe(sel_car), .valout(ksl[0]));
  reg_bit2 reg_bit2_35 (
    .value(databus[4]), .write(reg_handler_1_valout), .n_write(reg_handler_1_n_valout), .reset(reset),
    .oe(sel_chn), .valout(wf_car));
  reg_bit2 reg_bit2_36 (
    .value(databus[3]), .write(reg_handler_1_valout), .n_write(reg_handler_1_n_valout), .reset(reset),
    .oe(sel_chn), .valout(wf_mod));
  reg_bit2 reg_bit2_37 (
    .value(databus[2]), .write(reg_handler_1_valout), .n_write(reg_handler_1_n_valout), .reset(reset),
    .oe(sel_chn), .valout(feedback[2]));
  reg_bit2 reg_bit2_38 (
    .value(databus[1]), .write(reg_handler_1_valout), .n_write(reg_handler_1_n_valout), .reset(reset),
    .oe(sel_chn), .valout(feedback[1]));
  reg_bit2 reg_bit2_39 (
    .value(databus[0]), .write(reg_handler_1_valout), .n_write(reg_handler_1_n_valout), .reset(reset),
    .oe(sel_chn), .valout(feedback[0]));
  reg_bit2 reg_bit2_40 (
    .value(databus[7]), .write(reg_handler_10_valout), .n_write(reg_handler_10_n_valout), .reset(reset),
    .oe(sel_mod), .valout(ksl[1]));
  reg_bit2 reg_bit2_41 (
    .value(databus[6]), .write(reg_handler_10_valout), .n_write(reg_handler_10_n_valout), .reset(reset),
    .oe(sel_mod), .valout(ksl[0]));
  reg_bit2 reg_bit2_42 (
    .value(databus[5]), .write(reg_handler_10_valout), .n_write(reg_handler_10_n_valout), .reset(reset),
    .oe(sel_mod), .valout(tl[5]));
  reg_bit2 reg_bit2_43 (
    .value(databus[4]), .write(reg_handler_10_valout), .n_write(reg_handler_10_n_valout), .reset(reset),
    .oe(sel_mod), .valout(tl[4]));
  reg_bit2 reg_bit2_44 (
    .value(databus[3]), .write(reg_handler_10_valout), .n_write(reg_handler_10_n_valout), .reset(reset),
    .oe(sel_mod), .valout(tl[3]));
  reg_bit2 reg_bit2_45 (
    .value(databus[2]), .write(reg_handler_10_valout), .n_write(reg_handler_10_n_valout), .reset(reset),
    .oe(sel_mod), .valout(tl[2]));
  reg_bit2 reg_bit2_46 (
    .value(databus[1]), .write(reg_handler_10_valout), .n_write(reg_handler_10_n_valout), .reset(reset),
    .oe(sel_mod), .valout(tl[1]));
  reg_bit2 reg_bit2_47 (
    .value(databus[0]), .write(reg_handler_10_valout), .n_write(reg_handler_10_n_valout), .reset(reset),
    .oe(sel_mod), .valout(tl[0]));
  reg_bit2 reg_bit2_48 (
    .value(databus[7]), .write(reg_handler_9_valout), .n_write(reg_handler_9_n_valout), .reset(reset),
    .oe(sel_car), .valout(tremolo));
  reg_bit2 reg_bit2_49 (
    .value(databus[6]), .write(reg_handler_9_valout), .n_write(reg_handler_9_n_valout), .reset(reset),
    .oe(sel_car), .valout(vibrato));
  reg_bit2 reg_bit2_50 (
    .value(databus[5]), .write(reg_handler_9_valout), .n_write(reg_handler_9_n_valout), .reset(reset),
    .oe(sel_car), .valout(sustain));
  reg_bit2 reg_bit2_51 (
    .value(databus[4]), .write(reg_handler_9_valout), .n_write(reg_handler_9_n_valout), .reset(reset),
    .oe(sel_car), .valout(ksr));
  reg_bit2 reg_bit2_52 (
    .value(databus[3]), .write(reg_handler_9_valout), .n_write(reg_handler_9_n_valout), .reset(reset),
    .oe(sel_car), .valout(multi[3]));
  reg_bit2 reg_bit2_53 (
    .value(databus[2]), .write(reg_handler_9_valout), .n_write(reg_handler_9_n_valout), .reset(reset),
    .oe(sel_car), .valout(multi[2]));
  reg_bit2 reg_bit2_54 (
    .value(databus[1]), .write(reg_handler_9_valout), .n_write(reg_handler_9_n_valout), .reset(reset),
    .oe(sel_car), .valout(multi[1]));
  reg_bit2 reg_bit2_55 (
    .value(databus[0]), .write(reg_handler_9_valout), .n_write(reg_handler_9_n_valout), .reset(reset),
    .oe(sel_car), .valout(multi[0]));
  reg_bit2 reg_bit2_56 (
    .value(databus[7]), .write(reg_handler_8_valout), .n_write(reg_handler_8_n_valout), .reset(reset),
    .oe(sel_mod), .valout(tremolo));
  reg_bit2 reg_bit2_57 (
    .value(databus[6]), .write(reg_handler_8_valout), .n_write(reg_handler_8_n_valout), .reset(reset),
    .oe(sel_mod), .valout(vibrato));
  reg_bit2 reg_bit2_58 (
    .value(databus[5]), .write(reg_handler_8_valout), .n_write(reg_handler_8_n_valout), .reset(reset),
    .oe(sel_mod), .valout(sustain));
  reg_bit2 reg_bit2_59 (
    .value(databus[4]), .write(reg_handler_8_valout), .n_write(reg_handler_8_n_valout), .reset(reset),
    .oe(sel_mod), .valout(ksr));
  reg_bit2 reg_bit2_60 (
    .value(databus[3]), .write(reg_handler_8_valout), .n_write(reg_handler_8_n_valout), .reset(reset),
    .oe(sel_mod), .valout(multi[3]));
  reg_bit2 reg_bit2_61 (
    .value(databus[2]), .write(reg_handler_8_valout), .n_write(reg_handler_8_n_valout), .reset(reset),
    .oe(sel_mod), .valout(multi[2]));
  reg_bit2 reg_bit2_62 (
    .value(databus[1]), .write(reg_handler_8_valout), .n_write(reg_handler_8_n_valout), .reset(reset),
    .oe(sel_mod), .valout(multi[1]));
  reg_bit2 reg_bit2_63 (
    .value(databus[0]), .write(reg_handler_8_valout), .n_write(reg_handler_8_n_valout), .reset(reset),
    .oe(sel_mod), .valout(multi[0]));
  reg_bit reg_bit_1 (
    .value(databus[5]), .write(reg_handler_7_valout), .n_write(reg_handler_7_n_valout), .reset(reset),
    .valout(rhythm));
  reg_bit reg_bit_2 (
    .value(databus[4]), .write(reg_handler_7_valout), .n_write(reg_handler_7_n_valout), .reset(reset),
    .valout(bass_drum));
  reg_bit reg_bit_3 (
    .value(databus[3]), .write(reg_handler_7_valout), .n_write(reg_handler_7_n_valout), .reset(reset),
    .valout(snare_drum));
  reg_bit reg_bit_4 (
    .value(databus[2]), .write(reg_handler_7_valout), .n_write(reg_handler_7_n_valout), .reset(reset),
    .valout(tom_tom));
  reg_bit reg_bit_5 (
    .value(databus[1]), .write(reg_handler_7_valout), .n_write(reg_handler_7_n_valout), .reset(reset),
    .valout(top_cymbal));
  reg_bit reg_bit_6 (
    .value(databus[0]), .write(reg_handler_7_valout), .n_write(reg_handler_7_n_valout), .reset(reset),
    .valout(high_hat));
  reg_bit reg_bit_7 (
    .value(databus[3]), .write(reg_handler_6_valout), .n_write(reg_handler_6_n_valout), .reset(reset),
    .valout(test3));
  reg_bit reg_bit_8 (
    .value(databus[2]), .write(reg_handler_6_valout), .n_write(reg_handler_6_n_valout), .reset(reset),
    .valout(test2));
  reg_bit reg_bit_9 (
    .value(databus[1]), .write(reg_handler_6_valout), .n_write(reg_handler_6_n_valout), .reset(reset),
    .valout(test1));
  reg_bit reg_bit_10 (
    .value(databus[0]), .write(reg_handler_6_valout), .n_write(reg_handler_6_n_valout), .reset(reset),
    .valout(test0));
endmodule

module reg_addr_decoder (
  input  [7:0] in_1,
  output addr_f,
  output addr_e,
  output addr_0,
  output addr_1,
  output addr_2,
  output addr_3,
  output addr_4,
  output addr_5,
  output addr_6,
  output addr_7
);

  wire [7:0] not_1_out;

  assign not_1_out = ~in_1;  // NOT_Gate not_1, 8 bits wide
  nor nor_1 (addr_f, not_1_out[0], not_1_out[1], not_1_out[2], not_1_out[3], in_1[4], in_1[5], in_1[6], in_1[7]);
  nor nor_2 (addr_e, in_1[0], not_1_out[1], not_1_out[2], not_1_out[3], in_1[4], in_1[5], in_1[6], in_1[7]);
  nor nor_3 (addr_0, in_1[0], in_1[1], in_1[2], in_1[3], in_1[4], in_1[5], in_1[6], in_1[7]);
  nor nor_4 (addr_1, not_1_out[0], in_1[1], in_1[2], in_1[3], in_1[4], in_1[5], in_1[6], in_1[7]);
  nor nor_5 (addr_2, in_1[0], not_1_out[1], in_1[2], in_1[3], in_1[4], in_1[5], in_1[6], in_1[7]);
  nor nor_6 (addr_3, not_1_out[0], not_1_out[1], in_1[2], in_1[3], in_1[4], in_1[5], in_1[6], in_1[7]);
  nor nor_7 (addr_4, in_1[0], in_1[1], not_1_out[2], in_1[3], in_1[4], in_1[5], in_1[6], in_1[7]);
  nor nor_8 (addr_5, not_1_out[0], in_1[1], not_1_out[2], in_1[3], in_1[4], in_1[5], in_1[6], in_1[7]);
  nor nor_9 (addr_6, in_1[0], not_1_out[1], not_1_out[2], in_1[3], in_1[4], in_1[5], in_1[6], in_1[7]);
  nor nor_10 (addr_7, not_1_out[0], not_1_out[1], not_1_out[2], in_1[3], in_1[4], in_1[5], in_1[6], in_1[7]);
endmodule

module logsin (
  input  [6:0] index,
  output [18:0] logsin_out
);

  wire [45:0] multiplexer_1_out;

  Multiplexer #(.select(5), .width(46)) multiplexer_1 (
    .in0(46'h60b88666285), .in1(46'h1293089e33e5), .in2(46'h16829dd0eaf5), .in3(46'h17a8036a3b6c),
    .in4(46'h17b92686e356), .in5(46'h22a9366ef2cd), .in6(46'h22b9b3963bd6), .in7(46'h23aaab5cfb6e),
    .in8(46'h23bed0222b44), .in9(46'h23bfd0eaaa86), .in10(46'h2c8cc920ea0f), .in11(46'h2c8dcd0d5ce8),
    .in12(46'h2c9cec9412e7), .in13(46'h2c9df45f5104), .in14(46'h2d8cf49f69e4), .in15(46'h2d8eef472d01),
    .in16(46'h2d8fef8b9468), .in17(46'h2ddad640969b), .in18(46'h2ddadec3e05d), .in19(46'h2ddbde8df184),
    .in20(46'h38e8c705cd88), .in21(46'h38e8cf91bd58), .in22(46'h38e9d719a995), .in23(46'h38e9fe351c88),
    .in24(46'h38f8f6b17430), .in25(46'h38fae67b4c5a), .in26(46'h38faee7f7458), .in27(46'h38fbe7f15c69),
    .in28(46'h38fbff336cd8), .in29(46'h39eaf73d4cf9), .in30(46'h39eaf7fb6ceb), .in31(46'h39eedef555da),
    .out(multiplexer_1_out), .sel(index[4:0]));
  Multiplexer #(.select(2), .width(19)) multiplexer_2 (
    .in0({multiplexer_1_out[45:44], multiplexer_1_out[42], multiplexer_1_out[40:39], multiplexer_1_out[36:35], multiplexer_1_out[32:31], multiplexer_1_out[27:26], multiplexer_1_out[22:21], multiplexer_1_out[17], multiplexer_1_out[15], multiplexer_1_out[11], multiplexer_1_out[8], multiplexer_1_out[4], multiplexer_1_out[0]}),
    .in1({2'b11, multiplexer_1_out[43], multiplexer_1_out[41], 1'b1, multiplexer_1_out[37], 1'b1, multiplexer_1_out[33], 1'b1, multiplexer_1_out[28], 1'b1, multiplexer_1_out[23], 1'b1, multiplexer_1_out[18], multiplexer_1_out[16], multiplexer_1_out[12], multiplexer_1_out[9], multiplexer_1_out[5], multiplexer_1_out[1]}),
    .in2({{5{1'b1}}, multiplexer_1_out[38], 1'b1, multiplexer_1_out[34], 1'b1, multiplexer_1_out[29], 1'b1, multiplexer_1_out[24], 1'b1, multiplexer_1_out[19], 1'b1, multiplexer_1_out[13], multiplexer_1_out[10], multiplexer_1_out[6], multiplexer_1_out[2]}),
    .in3({{9{1'b1}}, multiplexer_1_out[30], 1'b1, multiplexer_1_out[25], 1'b1, multiplexer_1_out[20], 1'b1, multiplexer_1_out[14], 1'b1, multiplexer_1_out[7], multiplexer_1_out[3]}),
    .out(logsin_out), .sel(index[6:5]));
endmodule

module operator_logsin (
  input  [7:0] phase,
  input  clk1,
  input  clk2,
  output [11:0] logsin_out
);

  wire adder_1_cout, adder_1_out, adder_2_cout, adder_2_out, adder_3_cout, adder_3_out, adder_4_cout,
       adder_4_out, adder_5_cout, adder_5_out, adder_6_cout, adder_6_out, adder_7_cout, adder_7_out,
       adder_8_cout, adder_8_out, adder_9_cout, adder_9_out, adder_10_cout, adder_10_out, adder_11_cout,
       adder_11_out, and_1_out, and_2_out, and_3_out, and_4_out, and_5_out, and_6_out, and_7_out, and_8_out,
       d_ff_1_qn, d_ff_2_qn, d_ff_3_qn, d_ff_4_qn, d_ff_5_qn, d_ff_6_qn, d_ff_7_qn, d_ff_8_qn, d_ff_9_qn,
       d_ff_10_qn, d_ff_11_qn, d_ff_12_qn, d_ff_13_qn, d_ff_14_qn, d_ff_15_qn, d_ff_16_qn, d_ff_17_qn,
       d_ff_18_qn, d_ff_19_qn, d_ff_20_qn;
  wire [18:0] logsin_1_logsin_out;

  logsin logsin_1 (.index(phase[7:1]), .logsin_out(logsin_1_logsin_out));
  D_Flip_Flop #(.trigger("high")) d_ff_1 (.D(phase[0]), .clk(clk1), .Qn(d_ff_1_qn));  // open: Q, preset, reset
  D_Flip_Flop #(.trigger("high")) d_ff_2 (
    .D(logsin_1_logsin_out[0]), .clk(clk1), .Qn(d_ff_2_qn));  // open: Q, preset, reset
  D_Flip_Flop #(.trigger("high")) d_ff_3 (
    .D(logsin_1_logsin_out[1]), .clk(clk1), .Qn(d_ff_3_qn));  // open: Q, preset, reset
  D_Flip_Flop #(.trigger("high")) d_ff_4 (
    .D(logsin_1_logsin_out[2]), .clk(clk1), .Qn(d_ff_4_qn));  // open: Q, preset, reset
  D_Flip_Flop #(.trigger("high")) d_ff_5 (
    .D(logsin_1_logsin_out[3]), .clk(clk1), .Qn(d_ff_5_qn));  // open: Q, preset, reset
  D_Flip_Flop #(.trigger("high")) d_ff_6 (
    .D(logsin_1_logsin_out[4]), .clk(clk1), .Qn(d_ff_6_qn));  // open: Q, preset, reset
  D_Flip_Flop #(.trigger("high")) d_ff_7 (
    .D(logsin_1_logsin_out[5]), .clk(clk1), .Qn(d_ff_7_qn));  // open: Q, preset, reset
  D_Flip_Flop #(.trigger("high")) d_ff_8 (
    .D(logsin_1_logsin_out[6]), .clk(clk1), .Qn(d_ff_8_qn));  // open: Q, preset, reset
  D_Flip_Flop #(.trigger("high")) d_ff_9 (
    .D(logsin_1_logsin_out[7]), .clk(clk1), .Qn(d_ff_9_qn));  // open: Q, preset, reset
  D_Flip_Flop #(.trigger("high")) d_ff_10 (
    .D(logsin_1_logsin_out[8]), .clk(clk1), .Qn(d_ff_10_qn));  // open: Q, preset, reset
  D_Flip_Flop #(.trigger("high")) d_ff_11 (
    .D(logsin_1_logsin_out[9]), .clk(clk1), .Qn(d_ff_11_qn));  // open: Q, preset, reset
  D_Flip_Flop #(.trigger("high")) d_ff_12 (
    .D(logsin_1_logsin_out[10]), .clk(clk1), .Qn(d_ff_12_qn));  // open: Q, preset, reset
  D_Flip_Flop #(.trigger("high")) d_ff_13 (
    .D(logsin_1_logsin_out[11]), .clk(clk1), .Qn(d_ff_13_qn));  // open: Q, preset, reset
  D_Flip_Flop #(.trigger("high")) d_ff_14 (
    .D(logsin_1_logsin_out[12]), .clk(clk1), .Qn(d_ff_14_qn));  // open: Q, preset, reset
  D_Flip_Flop #(.trigger("high")) d_ff_15 (
    .D(logsin_1_logsin_out[13]), .clk(clk1), .Qn(d_ff_15_qn));  // open: Q, preset, reset
  D_Flip_Flop #(.trigger("high")) d_ff_16 (
    .D(logsin_1_logsin_out[14]), .clk(clk1), .Qn(d_ff_16_qn));  // open: Q, preset, reset
  D_Flip_Flop #(.trigger("high")) d_ff_17 (
    .D(logsin_1_logsin_out[15]), .clk(clk1), .Qn(d_ff_17_qn));  // open: Q, preset, reset
  D_Flip_Flop #(.trigger("high")) d_ff_18 (
    .D(logsin_1_logsin_out[16]), .clk(clk1), .Qn(d_ff_18_qn));  // open: Q, preset, reset
  D_Flip_Flop #(.trigger("high")) d_ff_19 (
    .D(logsin_1_logsin_out[17]), .clk(clk1), .Qn(d_ff_19_qn));  // open: Q, preset, reset
  D_Flip_Flop #(.trigger("high")) d_ff_20 (
    .D(logsin_1_logsin_out[18]), .clk(clk1), .Qn(d_ff_20_qn));  // open: Q, preset, reset
  and and_1 (and_1_out, d_ff_1_qn, d_ff_2_qn);
  and and_2 (and_2_out, d_ff_1_qn, d_ff_4_qn);
  and and_3 (and_3_out, d_ff_1_qn, d_ff_6_qn);
  and and_4 (and_4_out, d_ff_1_qn, d_ff_8_qn);
  and and_5 (and_5_out, d_ff_1_qn, d_ff_10_qn);
  and and_6 (and_6_out, d_ff_1_qn, d_ff_12_qn);
  and and_7 (and_7_out, d_ff_1_qn, d_ff_14_qn);
  and and_8 (and_8_out, d_ff_1_qn, d_ff_16_qn);
  Adder #(.width(1)) adder_1 (.a(and_1_out), .b(d_ff_3_qn), .out(adder_1_out), .cin(1'b0), .cout(adder_1_cout));
  Adder #(.width(1)) adder_2 (.a(and_2_out), .b(d_ff_5_qn), .out(adder_2_out), .cin(adder_1_cout), .cout(adder_2_cout));
  Adder #(.width(1)) adder_3 (.a(and_3_out), .b(d_ff_7_qn), .out(adder_3_out), .cin(adder_2_cout), .cout(adder_3_cout));
  Adder #(.width(1)) adder_4 (.a(and_4_out), .b(d_ff_9_qn), .out(adder_4_out), .cin(adder_3_cout), .cout(adder_4_cout));
  Adder #(.width(1)) adder_5 (
    .a(and_5_out), .b(d_ff_11_qn), .out(adder_5_out), .cin(adder_4_cout), .cout(adder_5_cout));
  Adder #(.width(1)) adder_6 (
    .a(and_6_out), .b(d_ff_13_qn), .out(adder_6_out), .cin(adder_5_cout), .cout(adder_6_cout));
  Adder #(.width(1)) adder_7 (
    .a(and_7_out), .b(d_ff_15_qn), .out(adder_7_out), .cin(adder_6_cout), .cout(adder_7_cout));
  Adder #(.width(1)) adder_8 (
    .a(and_8_out), .b(d_ff_17_qn), .out(adder_8_out), .cin(adder_7_cout), .cout(adder_8_cout));
  Adder #(.width(1)) adder_9 (
    .a(and_8_out), .b(d_ff_18_qn), .out(adder_9_out), .cin(adder_8_cout), .cout(adder_9_cout));
  Adder #(.width(1)) adder_10 (.a(1'b0), .b(d_ff_19_qn), .out(adder_10_out), .cin(adder_9_cout), .cout(adder_10_cout));
  Adder #(.width(1)) adder_11 (.a(1'b0), .b(d_ff_20_qn), .out(adder_11_out), .cin(adder_10_cout), .cout(adder_11_cout));
  D_Flip_Flop #(.trigger("high")) d_ff_21 (.D(adder_1_out), .clk(clk2), .Q(logsin_out[0]));  // open: Qn, preset, reset
  D_Flip_Flop #(.trigger("high")) d_ff_22 (.D(adder_2_out), .clk(clk2), .Q(logsin_out[1]));  // open: Qn, preset, reset
  D_Flip_Flop #(.trigger("high")) d_ff_23 (.D(adder_3_out), .clk(clk2), .Q(logsin_out[2]));  // open: Qn, preset, reset
  D_Flip_Flop #(.trigger("high")) d_ff_24 (.D(adder_4_out), .clk(clk2), .Q(logsin_out[3]));  // open: Qn, preset, reset
  D_Flip_Flop #(.trigger("high")) d_ff_25 (.D(adder_5_out), .clk(clk2), .Q(logsin_out[4]));  // open: Qn, preset, reset
  D_Flip_Flop #(.trigger("high")) d_ff_26 (.D(adder_6_out), .clk(clk2), .Q(logsin_out[5]));  // open: Qn, preset, reset
  D_Flip_Flop #(.trigger("high")) d_ff_27 (.D(adder_7_out), .clk(clk2), .Q(logsin_out[6]));  // open: Qn, preset, reset
  D_Flip_Flop #(.trigger("high")) d_ff_28 (.D(adder_8_out), .clk(clk2), .Q(logsin_out[7]));  // open: Qn, preset, reset
  D_Flip_Flop #(.trigger("high")) d_ff_29 (.D(adder_9_out), .clk(clk2), .Q(logsin_out[8]));  // open: Qn, preset, reset
  D_Flip_Flop #(.trigger("high")) d_ff_30 (.D(adder_10_out), .clk(clk2), .Q(logsin_out[9]));  // open: Qn, preset, reset
  D_Flip_Flop #(.trigger("high")) d_ff_31 (
    .D(adder_11_out), .clk(clk2), .Q(logsin_out[10]));  // open: Qn, preset, reset
  D_Flip_Flop #(.trigger("high")) d_ff_32 (
    .D(adder_11_cout), .clk(clk2), .Q(logsin_out[11]));  // open: Qn, preset, reset
endmodule

module operator_add_env (
  input  [11:0] logsin,
  input  [6:0] envelope,
  output [7:0] attenuation,
  output [3:0] shift
);

  wire adder_1_cout, adder_1_out, adder_2_cout, adder_2_out, adder_3_cout, adder_3_out, adder_4_cout,
       adder_4_out, adder_5_cout, adder_5_out, adder_6_cout, adder_6_out, adder_7_cout, adder_7_out,
       adder_8_cout, adder_8_out;

  Adder #(.width(1)) adder_1 (.a(logsin[4]), .b(envelope[0]), .out(adder_1_out), .cin(1'b0), .cout(adder_1_cout));
  Adder #(.width(1)) adder_2 (
    .a(logsin[5]), .b(envelope[1]), .out(adder_2_out), .cin(adder_1_cout), .cout(adder_2_cout));
  Adder #(.width(1)) adder_3 (
    .a(logsin[6]), .b(envelope[2]), .out(adder_3_out), .cin(adder_2_cout), .cout(adder_3_cout));
  Adder #(.width(1)) adder_4 (
    .a(logsin[7]), .b(envelope[3]), .out(adder_4_out), .cin(adder_3_cout), .cout(adder_4_cout));
  Adder #(.width(1)) adder_5 (
    .a(logsin[8]), .b(envelope[4]), .out(adder_5_out), .cin(adder_4_cout), .cout(adder_5_cout));
  Adder #(.width(1)) adder_6 (
    .a(logsin[9]), .b(envelope[5]), .out(adder_6_out), .cin(adder_5_cout), .cout(adder_6_cout));
  Adder #(.width(1)) adder_7 (
    .a(logsin[10]), .b(envelope[6]), .out(adder_7_out), .cin(adder_6_cout), .cout(adder_7_cout));
  Adder #(.width(1)) adder_8 (.a(logsin[11]), .b(1'b0), .out(adder_8_out), .cin(adder_7_cout), .cout(adder_8_cout));
  nor nor_1 (attenuation[0], adder_8_cout, logsin[0]);
  nor nor_2 (attenuation[1], adder_8_cout, logsin[1]);
  nor nor_3 (attenuation[2], adder_8_cout, logsin[2]);
  nor nor_4 (attenuation[3], adder_8_cout, logsin[3]);
  nor nor_5 (attenuation[4], adder_8_cout, adder_1_out);
  nor nor_6 (attenuation[5], adder_8_cout, adder_2_out);
  nor nor_7 (attenuation[6], adder_8_cout, adder_3_out);
  nor nor_8 (attenuation[7], adder_8_cout, adder_4_out);
  nor nor_9 (shift[0], adder_8_cout, adder_5_out);
  nor nor_10 (shift[1], adder_8_cout, adder_6_out);
  nor nor_11 (shift[2], adder_8_cout, adder_7_out);
  nor nor_12 (shift[3], adder_8_cout, adder_8_out);
endmodule

module exponent (
  input  [6:0] index,
  output [12:0] exp_out
);

  wire [47:0] multiplexer_1_out;

  Multiplexer #(.select(5), .width(48)) multiplexer_1 (
    .in0(48'h68e9b99fc54f), .in1(48'h68adde8b6eff), .in2(48'h68add81acc44), .in3(48'h688fa79ac54e),
    .in4(48'h688be48e6e6f), .in5(48'h688ad30f6d65), .in6(48'h688a1c9fc447), .in7(48'h68882b1bcf55),
    .in8(48'h4ccc6c1b474e), .in9(48'h4ccc069ecc0c), .in10(48'h45dd111ec54a), .in11(48'h17fb760a6e6a),
    .in12(48'h17f3e99a470a), .in13(48'h17f38a1fc84c), .in14(48'h17b6d59fc14e), .in15(48'h17b4f29b4a48),
    .in16(48'h17b4a50b632a), .in17(48'h17b04f8cec6c), .in18(48'h17b0480ca5ae), .in19(48'h17833f184c42),
    .in20(48'h178330886364), .in21(48'h13c7430ce26a), .in22(48'h134f8c88ea2b), .in23(48'h134cb90be525),
    .in24(48'h1348da0f6c21), .in25(48'h13488583793f), .in26(48'h116aa20be022), .in27(48'h103f798dafa4),
    .in28(48'h103f1e09afa9), .in29(48'h103f09096225), .in30(48'h1039609f474c), .in31(48'h1038170bee62),
    .out(multiplexer_1_out), .sel(index[4:0]));
  Multiplexer #(.select(2), .width(13)) multiplexer_2 (
    .in0({2'b11, multiplexer_1_out[39], multiplexer_1_out[35], multiplexer_1_out[31], multiplexer_1_out[27], multiplexer_1_out[23], multiplexer_1_out[19], multiplexer_1_out[15], multiplexer_1_out[12], multiplexer_1_out[8], multiplexer_1_out[4], multiplexer_1_out[0]}),
    .in1({1'b1, multiplexer_1_out[43], multiplexer_1_out[40], multiplexer_1_out[36], multiplexer_1_out[32], multiplexer_1_out[28], multiplexer_1_out[24], multiplexer_1_out[20], multiplexer_1_out[16], multiplexer_1_out[13], multiplexer_1_out[9], multiplexer_1_out[5], multiplexer_1_out[1]}),
    .in2({multiplexer_1_out[46], multiplexer_1_out[44], multiplexer_1_out[41], multiplexer_1_out[37], multiplexer_1_out[33], multiplexer_1_out[29], multiplexer_1_out[25], multiplexer_1_out[21], multiplexer_1_out[17], 1'b1, multiplexer_1_out[10], multiplexer_1_out[6], multiplexer_1_out[2]}),
    .in3({multiplexer_1_out[47], multiplexer_1_out[45], multiplexer_1_out[42], multiplexer_1_out[38], multiplexer_1_out[34], multiplexer_1_out[30], multiplexer_1_out[26], multiplexer_1_out[22], multiplexer_1_out[18], multiplexer_1_out[14], multiplexer_1_out[11], multiplexer_1_out[7], multiplexer_1_out[3]}),
    .out(exp_out), .sel(index[6:5]));
endmodule

module operator_exponent (
  input  [7:0] attenuation,
  input  clk1,
  input  clk2,
  output [9:0] exp_out
);

  wire adder_1_cout, adder_1_out, adder_2_cout, adder_2_out, adder_3_cout, adder_3_out, adder_4_cout,
       adder_4_out, adder_5_cout, adder_5_out, adder_6_cout, adder_6_out, adder_7_cout, adder_7_out,
       adder_8_cout, adder_8_out, adder_9_cout, adder_9_out, adder_10_out, and_1_out, and_2_out, and_3_out,
       d_ff_1_q, d_ff_2_qn, d_ff_3_qn, d_ff_4_qn, d_ff_5_qn, d_ff_6_qn, d_ff_7_qn, d_ff_8_qn, d_ff_9_qn,
       d_ff_10_qn, d_ff_11_qn, d_ff_12_qn, d_ff_13_qn, d_ff_14_qn;
  wire [12:0] exponent_1_exp_out;

  exponent exponent_1 (.index(attenuation[7:1]), .exp_out(exponent_1_exp_out));
  D_Flip_Flop #(.trigger("high")) d_ff_1 (.D(attenuation[0]), .clk(clk1), .Q(d_ff_1_q));  // open: Qn, preset, reset
  D_Flip_Flop #(.trigger("high")) d_ff_2 (
    .D(exponent_1_exp_out[0]), .clk(clk1), .Qn(d_ff_2_qn));  // open: Q, preset, reset
  D_Flip_Flop #(.trigger("high")) d_ff_3 (
    .D(exponent_1_exp_out[1]), .clk(clk1), .Qn(d_ff_3_qn));  // open: Q, preset, reset
  D_Flip_Flop #(.trigger("high")) d_ff_4 (
    .D(exponent_1_exp_out[2]), .clk(clk1), .Qn(d_ff_4_qn));  // open: Q, preset, reset
  D_Flip_Flop #(.trigger("high")) d_ff_5 (
    .D(exponent_1_exp_out[3]), .clk(clk1), .Qn(d_ff_5_qn));  // open: Q, preset, reset
  D_Flip_Flop #(.trigger("high")) d_ff_6 (
    .D(exponent_1_exp_out[4]), .clk(clk1), .Qn(d_ff_6_qn));  // open: Q, preset, reset
  D_Flip_Flop #(.trigger("high")) d_ff_7 (
    .D(exponent_1_exp_out[5]), .clk(clk1), .Qn(d_ff_7_qn));  // open: Q, preset, reset
  D_Flip_Flop #(.trigger("high")) d_ff_8 (
    .D(exponent_1_exp_out[6]), .clk(clk1), .Qn(d_ff_8_qn));  // open: Q, preset, reset
  D_Flip_Flop #(.trigger("high")) d_ff_9 (
    .D(exponent_1_exp_out[7]), .clk(clk1), .Qn(d_ff_9_qn));  // open: Q, preset, reset
  D_Flip_Flop #(.trigger("high")) d_ff_10 (
    .D(exponent_1_exp_out[8]), .clk(clk1), .Qn(d_ff_10_qn));  // open: Q, preset, reset
  D_Flip_Flop #(.trigger("high")) d_ff_11 (
    .D(exponent_1_exp_out[9]), .clk(clk1), .Qn(d_ff_11_qn));  // open: Q, preset, reset
  D_Flip_Flop #(.trigger("high")) d_ff_12 (
    .D(exponent_1_exp_out[10]), .clk(clk1), .Qn(d_ff_12_qn));  // open: Q, preset, reset
  D_Flip_Flop #(.trigger("high")) d_ff_13 (
    .D(exponent_1_exp_out[11]), .clk(clk1), .Qn(d_ff_13_qn));  // open: Q, preset, reset
  D_Flip_Flop #(.trigger("high")) d_ff_14 (
    .D(exponent_1_exp_out[12]), .clk(clk1), .Qn(d_ff_14_qn));  // open: Q, preset, reset
  and and_1 (and_1_out, d_ff_1_q, d_ff_3_qn);
  and and_2 (and_2_out, d_ff_1_q, d_ff_5_qn);
  and and_3 (and_3_out, d_ff_1_q, d_ff_7_qn);
  Adder #(.width(1)) adder_1 (.a(d_ff_2_qn), .b(and_1_out), .out(adder_1_out), .cin(1'b0), .cout(adder_1_cout));
  Adder #(.width(1)) adder_2 (.a(d_ff_4_qn), .b(and_2_out), .out(adder_2_out), .cin(adder_1_cout), .cout(adder_2_cout));
  Adder #(.width(1)) adder_3 (.a(d_ff_6_qn), .b(and_3_out), .out(adder_3_out), .cin(adder_2_cout), .cout(adder_3_cout));
  Adder #(.width(1)) adder_4 (.a(1'b0), .b(d_ff_8_qn), .out(adder_4_out), .cin(adder_3_cout), .cout(adder_4_cout));
  Adder #(.width(1)) adder_5 (.a(1'b0), .b(d_ff_9_qn), .out(adder_5_out), .cin(adder_4_cout), .cout(adder_5_cout));
  Adder #(.width(1)) adder_6 (.a(1'b0), .b(d_ff_10_qn), .out(adder_6_out), .cin(adder_5_cout), .cout(adder_6_cout));
  Adder #(.width(1)) adder_7 (.a(1'b0), .b(d_ff_11_qn), .out(adder_7_out), .cin(adder_6_cout), .cout(adder_7_cout));
  Adder #(.width(1)) adder_8 (.a(1'b0), .b(d_ff_12_qn), .out(adder_8_out), .cin(adder_7_cout), .cout(adder_8_cout));
  Adder #(.width(1)) adder_9 (.a(1'b0), .b(d_ff_13_qn), .out(adder_9_out), .cin(adder_8_cout), .cout(adder_9_cout));
  Adder #(.width(1)) adder_10 (.a(1'b0), .b(d_ff_14_qn), .out(adder_10_out), .cin(adder_9_cout));  // open: cout
  D_Flip_Flop #(.trigger("high")) d_ff_15 (.D(adder_1_out), .clk(clk2), .Q(exp_out[0]));  // open: Qn, preset, reset
  D_Flip_Flop #(.trigger("high")) d_ff_16 (.D(adder_2_out), .clk(clk2), .Q(exp_out[1]));  // open: Qn, preset, reset
  D_Flip_Flop #(.trigger("high")) d_ff_17 (.D(adder_3_out), .clk(clk2), .Q(exp_out[2]));  // open: Qn, preset, reset
  D_Flip_Flop #(.trigger("high")) d_ff_18 (.D(adder_4_out), .clk(clk2), .Q(exp_out[3]));  // open: Qn, preset, reset
  D_Flip_Flop #(.trigger("high")) d_ff_19 (.D(adder_5_out), .clk(clk2), .Q(exp_out[4]));  // open: Qn, preset, reset
  D_Flip_Flop #(.trigger("high")) d_ff_20 (.D(adder_6_out), .clk(clk2), .Q(exp_out[5]));  // open: Qn, preset, reset
  D_Flip_Flop #(.trigger("high")) d_ff_21 (.D(adder_7_out), .clk(clk2), .Q(exp_out[6]));  // open: Qn, preset, reset
  D_Flip_Flop #(.trigger("high")) d_ff_22 (.D(adder_8_out), .clk(clk2), .Q(exp_out[7]));  // open: Qn, preset, reset
  D_Flip_Flop #(.trigger("high")) d_ff_23 (.D(adder_9_out), .clk(clk2), .Q(exp_out[8]));  // open: Qn, preset, reset
  D_Flip_Flop #(.trigger("high")) d_ff_24 (.D(adder_10_out), .clk(clk2), .Q(exp_out[9]));  // open: Qn, preset, reset
endmodule

module operator_shift (
  input  [9:0] exp_value,
  input  [3:0] shift,
  input  mute,
  input  clk1,
  input  clk2,
  output [10:0] out_6
);

  wire nor_1_out, nor_2_out, nor_3_out, nor_4_out, not_1_out, not_2_out, sr_bit_3_valout, sr_bit_4_valout;
  wire [1:0] sr_bit_1_valout;
  wire [10:0] multiplexer_1_out;

  sr_bit sr_bit_1 (.value(shift[0]), .clk1(clk1), .clk2(clk2), .valout(sr_bit_1_valout[0]));
  sr_bit sr_bit_2 (.value(shift[1]), .clk1(clk1), .clk2(clk2), .valout(sr_bit_1_valout[1]));
  sr_bit sr_bit_3 (.value(shift[2]), .clk1(clk1), .clk2(clk2), .valout(sr_bit_3_valout));
  sr_bit sr_bit_4 (.value(shift[3]), .clk1(clk1), .clk2(clk2), .valout(sr_bit_4_valout));
  not not_1 (not_1_out, sr_bit_3_valout);
  not not_2 (not_2_out, sr_bit_4_valout);
  nor nor_1 (nor_1_out, not_1_out, not_2_out, mute);
  nor nor_2 (nor_2_out, sr_bit_3_valout, not_2_out, mute);
  nor nor_3 (nor_3_out, not_1_out, sr_bit_4_valout, mute);
  nor nor_4 (nor_4_out, nor_1_out, nor_2_out, nor_3_out);
  Multiplexer #(.select(2), .width(11)) multiplexer_1 (
    .in0({4'b0001, exp_value[9:3]}), .in1({3'b001, exp_value[9:2]}), .in2({2'b01, exp_value[9:1]}),
    .in3({1'b1, exp_value}), .out(multiplexer_1_out), .sel(sr_bit_1_valout));
  assign out_6 = nor_1_out ? multiplexer_1_out : 11'bz;  // Controlled_Buffer controlled_buffer_1
  assign out_6 = nor_2_out ? {4'b0000, multiplexer_1_out[10:4]} : 11'bz;  // Controlled_Buffer controlled_buffer_2
  assign out_6 = nor_3_out ? {{8{1'b0}}, multiplexer_1_out[10:8]} : 11'bz;  // Controlled_Buffer controlled_buffer_3
  assign out_6 = nor_4_out ? {11{1'b0}} : 11'bz;  // Controlled_Buffer controlled_buffer_4
endmodule

module operator_negate (
  input  [10:0] value,
  input  sign,
  output [11:0] valout
);

  xnor xnor_1 (valout[0], value[0], sign);
  xnor xnor_2 (valout[1], value[1], sign);
  xnor xnor_3 (valout[2], value[2], sign);
  xnor xnor_4 (valout[3], value[3], sign);
  xnor xnor_5 (valout[4], value[4], sign);
  xnor xnor_6 (valout[5], value[5], sign);
  xnor xnor_7 (valout[6], value[6], sign);
  xnor xnor_8 (valout[7], value[7], sign);
  xnor xnor_9 (valout[8], value[8], sign);
  xnor xnor_10 (valout[9], value[9], sign);
  xnor xnor_11 (valout[10], value[10], sign);
  xnor xnor_12 (valout[11], 1'b0, sign);
endmodule

module operator_modvalue (
  input  [11:0] op_value,
  output [8:0] mod_value,
  output [8:0] chan_out
);

  assign mod_value = ~op_value[8:0];  // NOT_Gate not_1, 9 bits wide
  assign chan_out = ~op_value[11:3];  // NOT_Gate not_2, 9 bits wide
endmodule

module sr_12bit (
  input  [11:0] value,
  input  clk1,
  input  clk2,
  output [11:0] outval
);

  sr_bit sr_bit_1 (.value(value[0]), .clk1(clk1), .clk2(clk2), .valout(outval[0]));
  sr_bit sr_bit_2 (.value(value[1]), .clk1(clk1), .clk2(clk2), .valout(outval[1]));
  sr_bit sr_bit_3 (.value(value[2]), .clk1(clk1), .clk2(clk2), .valout(outval[2]));
  sr_bit sr_bit_4 (.value(value[3]), .clk1(clk1), .clk2(clk2), .valout(outval[3]));
  sr_bit sr_bit_5 (.value(value[4]), .clk1(clk1), .clk2(clk2), .valout(outval[4]));
  sr_bit sr_bit_6 (.value(value[5]), .clk1(clk1), .clk2(clk2), .valout(outval[5]));
  sr_bit sr_bit_7 (.value(value[6]), .clk1(clk1), .clk2(clk2), .valout(outval[6]));
  sr_bit sr_bit_8 (.value(value[7]), .clk1(clk1), .clk2(clk2), .valout(outval[7]));
  sr_bit sr_bit_9 (.value(value[8]), .clk1(clk1), .clk2(clk2), .valout(outval[8]));
  sr_bit sr_bit_10 (.value(value[9]), .clk1(clk1), .clk2(clk2), .valout(outval[9]));
  sr_bit sr_bit_11 (.value(value[10]), .clk1(clk1), .clk2(clk2), .valout(outval[10]));
  sr_bit sr_bit_12 (.value(value[11]), .clk1(clk1), .clk2(clk2), .valout(outval[11]));
endmodule

module operator (
  input  [9:0] phase,
  input  [6:0] env,
  input  env_mute,
  input  [2:0] feedback,
  input  fb_enable,
  input  mod_enable,
  input  modcar_sel,
  input  wf_mod,
  input  wf_car,
  input  clk1,
  input  clk2,
  output [8:0] chan_out
);

  wire nand_1_out, nor_1_out, nor_2_out, nor_3_out, nor_4_out, not_1_out, not_2_out, not_4_out,
       sr_bit_1_valout, sr_bit_2_valout;
  wire [3:0] operator_add_env_1_shift;
  wire [7:0] bit_extender_1_out, operator_add_env_1_attenuation, xor_1_out;
  wire [8:0] operator_modvalue_1_mod_value;
  wire [9:0] adder_1_out, not_3_out, operator_exponent_1_exp_out, operator_modmux_1_modulation;
  wire [10:0] operator_shift_1_out_6;
  wire [11:0] controlled_buffer_1_out, controlled_buffer_3_out, operator_logsin_1_logsin_out,
       operator_negate_1_valout, sr_12bit_1_outval, sr_12bit_2_outval, sr_12bit_3_outval, sr_12bit_4_outval,
       sr_12bit_5_outval, sr_12bit_6_outval, sr_12bit_7_outval, sr_12bit_8_outval, sr_12bit_9_outval,
       sr_12bit_10_outval, sr_12bit_11_outval, sr_12bit_12_outval, sr_12bit_13_outval, sr_12bit_14_outval,
       sr_12bit_15_outval, sr_12bit_16_outval, sr_12bit_17_outval, sr_12bit_18_outval;

  not not_1 (not_1_out, modcar_sel);
  not not_2 (not_2_out, not_1_out);
  Adder #(.width(10)) adder_1 (
    .a(phase), .b(operator_modmux_1_modulation), .out(adder_1_out), .cin(1'b0));  // open: cout
  assign controlled_buffer_1_out = not_2_out ? operator_negate_1_valout : 12'bz;  // Controlled_Buffer controlled_buffer_1
  assign controlled_buffer_1_out = not_1_out ? sr_12bit_9_outval : 12'bz;  // Controlled_Buffer controlled_buffer_2
  assign not_3_out = ~adder_1_out;  // NOT_Gate not_3, 10 bits wide
  sr_bit sr_bit_1 (.value(not_3_out[9]), .clk1(clk1), .clk2(clk2), .valout(sr_bit_1_valout));
  sr_bit sr_bit_2 (.value(sr_bit_1_valout), .clk1(clk1), .clk2(clk2), .valout(sr_bit_2_valout));
  assign bit_extender_1_out = {{7{not_3_out[8]}}, not_3_out[8]};  // Bit_Extender bit_extender_1
  sr_12bit sr_12bit_1 (.value(controlled_buffer_1_out), .clk1(clk1), .clk2(clk2), .outval(sr_12bit_1_outval));
  sr_12bit sr_12bit_2 (.value(sr_12bit_1_outval), .clk1(clk1), .clk2(clk2), .outval(sr_12bit_2_outval));
  sr_12bit sr_12bit_3 (.value(sr_12bit_2_outval), .clk1(clk1), .clk2(clk2), .outval(sr_12bit_3_outval));
  sr_12bit sr_12bit_4 (.value(sr_12bit_3_outval), .clk1(clk1), .clk2(clk2), .outval(sr_12bit_4_outval));
  sr_12bit sr_12bit_5 (.value(sr_12bit_4_outval), .clk1(clk1), .clk2(clk2), .outval(sr_12bit_5_outval));
  assign xor_1_out = not_3_out[7:0] ^ bit_extender_1_out;  // XOR_Gate xor_1, 8 bits wide
  nor nor_1 (nor_1_out, sr_bit_2_valout, not_1_out, wf_mod);
  nor nor_2 (nor_2_out, sr_bit_2_valout, not_2_out, wf_car);
  sr_12bit sr_12bit_6 (.value(sr_12bit_5_outval), .clk1(clk1), .clk2(clk2), .outval(sr_12bit_6_outval));
  sr_12bit sr_12bit_7 (.value(sr_12bit_6_outval), .clk1(clk1), .clk2(clk2), .outval(sr_12bit_7_outval));
  sr_12bit sr_12bit_8 (.value(sr_12bit_7_outval), .clk1(clk1), .clk2(clk2), .outval(sr_12bit_8_outval));
  sr_12bit sr_12bit_9 (.value(sr_12bit_8_outval), .clk1(clk1), .clk2(clk2), .outval(sr_12bit_9_outval));
  nor nor_3 (nor_3_out, sr_bit_2_valout, env_mute);
  not not_4 (not_4_out, env_mute);
  nor nor_4 (nor_4_out, nor_1_out, nor_2_out);
  assign controlled_buffer_3_out = not_2_out ? sr_12bit_9_outval : 12'bz;  // Controlled_Buffer controlled_buffer_3
  assign controlled_buffer_3_out = not_1_out ? sr_12bit_18_outval : 12'bz;  // Controlled_Buffer controlled_buffer_4
  nand nand_1 (nand_1_out, not_4_out, nor_4_out);
  operator_logsin operator_logsin_1 (
    .phase(xor_1_out), .clk1(clk1), .clk2(clk2), .logsin_out(operator_logsin_1_logsin_out));
  sr_12bit sr_12bit_10 (.value(controlled_buffer_3_out), .clk1(clk1), .clk2(clk2), .outval(sr_12bit_10_outval));
  sr_12bit sr_12bit_11 (.value(sr_12bit_10_outval), .clk1(clk1), .clk2(clk2), .outval(sr_12bit_11_outval));
  sr_12bit sr_12bit_12 (.value(sr_12bit_11_outval), .clk1(clk1), .clk2(clk2), .outval(sr_12bit_12_outval));
  sr_12bit sr_12bit_13 (.value(sr_12bit_12_outval), .clk1(clk1), .clk2(clk2), .outval(sr_12bit_13_outval));
  sr_12bit sr_12bit_14 (.value(sr_12bit_13_outval), .clk1(clk1), .clk2(clk2), .outval(sr_12bit_14_outval));
  operator_shift operator_shift_1 (
    .exp_value(operator_exponent_1_exp_out), .shift(operator_add_env_1_shift), .mute(nand_1_out),
    .clk1(clk1), .clk2(clk2), .out_6(operator_shift_1_out_6));
  operator_add_env operator_add_env_1 (
    .logsin(operator_logsin_1_logsin_out), .envelope(env), .attenuation(operator_add_env_1_attenuation),
    .shift(operator_add_env_1_shift));
  sr_12bit sr_12bit_15 (.value(sr_12bit_14_outval), .clk1(clk1), .clk2(clk2), .outval(sr_12bit_15_outval));
  sr_12bit sr_12bit_16 (.value(sr_12bit_15_outval), .clk1(clk1), .clk2(clk2), .outval(sr_12bit_16_outval));
  sr_12bit sr_12bit_17 (.value(sr_12bit_16_outval), .clk1(clk1), .clk2(clk2), .outval(sr_12bit_17_outval));
  sr_12bit sr_12bit_18 (.value(sr_12bit_17_outval), .clk1(clk1), .clk2(clk2), .outval(sr_12bit_18_outval));
  operator_negate operator_negate_1 (
    .value(operator_shift_1_out_6), .sign(nor_3_out), .valout(operator_negate_1_valout));
  operator_exponent operator_exponent_1 (
    .attenuation(operator_add_env_1_attenuation), .clk1(clk1), .clk2(clk2),
    .exp_out(operator_exponent_1_exp_out));
  operator_modvalue operator_modvalue_1 (
    .op_value(operator_negate_1_valout), .mod_value(operator_modvalue_1_mod_value), .chan_out(chan_out));
  operator_modmux operator_modmux_1 (
    .mod_value(operator_modvalue_1_mod_value), .old_val1(sr_12bit_6_outval), .old_val2(sr_12bit_15_outval),
    .feedback(feedback), .fb_enable(fb_enable), .mod_enable(mod_enable), .clk1(clk1), .clk2(clk2),
    .modulation(operator_modmux_1_modulation));
endmodule

module operator_modmux (
  input  [8:0] mod_value,
  input  [11:0] old_val1,
  input  [11:0] old_val2,
  input  [2:0] feedback,
  input  fb_enable,
  input  mod_enable,
  input  clk1,
  input  clk2,
  output [9:0] modulation
);

  wire nor_1_out, nor_2_out, nor_3_out, nor_4_out, nor_5_out, nor_6_out, nor_7_out, not_1_out, not_2_out,
       not_3_out, not_4_out;
  wire [0:0] sr_bit_10_valout, sr_bit_11_valout, sr_bit_12_valout, sr_bit_13_valout, sr_bit_14_valout,
       sr_bit_15_valout;
  wire [9:0] and_1_out, and_2_out, and_3_out, and_4_out, and_5_out, and_6_out, and_7_out, and_8_out,
       bit_extender_3_out, bit_extender_4_out, bit_extender_5_out, bit_extender_6_out, bit_extender_7_out,
       bit_extender_8_out, bit_extender_9_out, bit_extender_10_out, sr_bit_21_valout;
  wire [9:1] sr_bit_1_valout;
  wire [12:0] adder_1_out, bit_extender_1_out, bit_extender_2_out, not_5_out;

  not not_1 (not_1_out, feedback[0]);
  not not_2 (not_2_out, feedback[1]);
  not not_3 (not_3_out, feedback[2]);
  not not_4 (not_4_out, fb_enable);
  assign bit_extender_1_out = {{1{old_val1[11]}}, old_val1};  // Bit_Extender bit_extender_1
  assign bit_extender_2_out = {{1{old_val2[11]}}, old_val2};  // Bit_Extender bit_extender_2
  nor nor_1 (nor_1_out, not_4_out, feedback[0], not_2_out, not_3_out);
  nor nor_2 (nor_2_out, not_4_out, not_1_out, feedback[1], not_3_out);
  nor nor_3 (nor_3_out, not_4_out, feedback[0], feedback[1], not_3_out);
  nor nor_4 (nor_4_out, not_4_out, not_1_out, not_2_out, feedback[2]);
  nor nor_5 (nor_5_out, not_4_out, feedback[0], not_2_out, feedback[2]);
  nor nor_6 (nor_6_out, not_4_out, not_1_out, feedback[1], feedback[2]);
  nor nor_7 (nor_7_out, not_4_out, feedback[0], feedback[1], feedback[2]);
  Adder #(.width(13)) adder_1 (.a(bit_extender_1_out), .b(bit_extender_2_out), .out(adder_1_out));  // open: cin, cout
  sr_bit sr_bit_1 (.value(mod_value[0]), .clk1(clk1), .clk2(clk2), .valout(sr_bit_1_valout[1]));
  sr_bit sr_bit_2 (.value(mod_value[1]), .clk1(clk1), .clk2(clk2), .valout(sr_bit_1_valout[2]));
  sr_bit sr_bit_3 (.value(mod_value[2]), .clk1(clk1), .clk2(clk2), .valout(sr_bit_1_valout[3]));
  sr_bit sr_bit_4 (.value(mod_value[3]), .clk1(clk1), .clk2(clk2), .valout(sr_bit_1_valout[4]));
  sr_bit sr_bit_5 (.value(mod_value[4]), .clk1(clk1), .clk2(clk2), .valout(sr_bit_1_valout[5]));
  sr_bit sr_bit_6 (.value(mod_value[5]), .clk1(clk1), .clk2(clk2), .valout(sr_bit_1_valout[6]));
  sr_bit sr_bit_7 (.value(mod_value[6]), .clk1(clk1), .clk2(clk2), .valout(sr_bit_1_valout[7]));
  sr_bit sr_bit_8 (.value(mod_value[7]), .clk1(clk1), .clk2(clk2), .valout(sr_bit_1_valout[8]));
  sr_bit sr_bit_9 (.value(mod_value[8]), .clk1(clk1), .clk2(clk2), .valout(sr_bit_1_valout[9]));
  assign not_5_out = ~adder_1_out;  // NOT_Gate not_5, 13 bits wide
  assign bit_extender_3_out = {{9{mod_enable}}, mod_enable};  // Bit_Extender bit_extender_3
  assign and_1_out = bit_extender_3_out & {sr_bit_1_valout, 1'b0};  // AND_Gate and_1, 10 bits wide
  sr_bit sr_bit_10 (.value(not_5_out[1]), .clk1(clk1), .clk2(clk2), .valout(sr_bit_10_valout[0]));
  sr_bit sr_bit_11 (.value(not_5_out[2]), .clk1(clk1), .clk2(clk2), .valout(sr_bit_11_valout[0]));
  sr_bit sr_bit_12 (.value(not_5_out[3]), .clk1(clk1), .clk2(clk2), .valout(sr_bit_12_valout[0]));
  sr_bit sr_bit_13 (.value(not_5_out[4]), .clk1(clk1), .clk2(clk2), .valout(sr_bit_13_valout[0]));
  sr_bit sr_bit_14 (.value(not_5_out[5]), .clk1(clk1), .clk2(clk2), .valout(sr_bit_14_valout[0]));
  sr_bit sr_bit_15 (.value(not_5_out[6]), .clk1(clk1), .clk2(clk2), .valout(sr_bit_15_valout[0]));
  sr_bit sr_bit_16 (.value(not_5_out[7]), .clk1(clk1), .clk2(clk2), .valout(sr_bit_21_valout[0]));
  sr_bit sr_bit_17 (.value(not_5_out[8]), .clk1(clk1), .clk2(clk2), .valout(sr_bit_21_valout[1]));
  sr_bit sr_bit_18 (.value(not_5_out[9]), .clk1(clk1), .clk2(clk2), .valout(sr_bit_21_valout[2]));
  sr_bit sr_bit_19 (.value(not_5_out[10]), .clk1(clk1), .clk2(clk2), .valout(sr_bit_21_valout[3]));
  sr_bit sr_bit_20 (.value(not_5_out[11]), .clk1(clk1), .clk2(clk2), .valout(sr_bit_21_valout[4]));
  sr_bit sr_bit_21 (.value(not_5_out[12]), .clk1(clk1), .clk2(clk2), .valout(sr_bit_21_valout[9]));
  assign bit_extender_4_out = {{9{nor_1_out}}, nor_1_out};  // Bit_Extender bit_extender_4
  assign and_2_out = bit_extender_4_out & {{5{sr_bit_21_valout[9]}}, sr_bit_21_valout[4:0]};  // AND_Gate and_2, 10 bits wide
  assign bit_extender_5_out = {{9{nor_2_out}}, nor_2_out};  // Bit_Extender bit_extender_5
  assign and_3_out = bit_extender_5_out & {{4{sr_bit_21_valout[9]}}, sr_bit_21_valout[4:0], sr_bit_15_valout[0]};  // AND_Gate and_3, 10 bits wide
  assign bit_extender_6_out = {{9{nor_3_out}}, nor_3_out};  // Bit_Extender bit_extender_6
  assign and_4_out = bit_extender_6_out & {{3{sr_bit_21_valout[9]}}, sr_bit_21_valout[4:0], sr_bit_15_valout[0], sr_bit_14_valout[0]};  // AND_Gate and_4, 10 bits wide
  assign bit_extender_7_out = {{9{nor_4_out}}, nor_4_out};  // Bit_Extender bit_extender_7
  assign and_5_out = bit_extender_7_out & {{2{sr_bit_21_valout[9]}}, sr_bit_21_valout[4:0], sr_bit_15_valout[0], sr_bit_14_valout[0], sr_bit_13_valout[0]};  // AND_Gate and_5, 10 bits wide
  assign bit_extender_8_out = {{9{nor_5_out}}, nor_5_out};  // Bit_Extender bit_extender_8
  assign and_6_out = bit_extender_8_out & {sr_bit_21_valout[9], sr_bit_21_valout[4:0], sr_bit_15_valout[0], sr_bit_14_valout[0], sr_bit_13_valout[0], sr_bit_12_valout[0]};  // AND_Gate and_6, 10 bits wide
  assign bit_extender_9_out = {{9{nor_6_out}}, nor_6_out};  // Bit_Extender bit_extender_9
  assign and_7_out = bit_extender_9_out & {sr_bit_21_valout[4:0], sr_bit_15_valout[0], sr_bit_14_valout[0], sr_bit_13_valout[0], sr_bit_12_valout[0], sr_bit_11_valout[0]};  // AND_Gate and_7, 10 bits wide
  assign bit_extender_10_out = {{9{nor_7_out}}, nor_7_out};  // Bit_Extender bit_extender_10
  assign and_8_out = bit_extender_10_out & {sr_bit_21_valout[3:0], sr_bit_15_valout[0], sr_bit_14_valout[0], sr_bit_13_valout[0], sr_bit_12_valout[0], sr_bit_11_valout[0], sr_bit_10_valout[0]};  // AND_Gate and_8, 10 bits wide
  assign modulation = and_1_out | and_2_out | and_3_out | and_4_out | and_5_out | and_6_out | and_7_out | and_8_out;  // OR_Gate or_1, 10 bits wide
endmodule

module clock_handler (
  input  MCLK,
  input  reset,
  output MCLK1,
  output MCLK2,
  output clk1,
  output clk2,
  output dac_clk
);

  wire buffer_1_out, buffer_2_out, cnt_bit_2_1_c_out, cnt_bit_2_1_val_out, cnt_bit_2_2_val_out,
       controlled_buffer_1_out, controlled_buffer_3_out, controlled_buffer_5_out, controlled_buffer_7_out,
       d_ff_1_q, d_ff_2_q, nor_1_out, nor_2_out, nor_3_out, nor_4_out, nor_5_out, nor_6_out, nor_7_out,
       not_1_out, not_2_out, not_3_out, not_4_out, not_5_out, not_7_out, not_9_out, not_10_out, not_12_out,
       not_13_out, not_14_out, not_15_out, sr_bit_1_valout, sr_bit_2_valout, sr_bit_3_valout,
       sr_bit_4_valout, sr_bit_5_valout;

  not not_1 (not_1_out, MCLK);
  not not_2 (not_2_out, not_1_out);
  sr_bit sr_bit_1 (.value(nor_5_out), .clk1(MCLK1), .clk2(MCLK2), .valout(sr_bit_1_valout));
  nor nor_1 (nor_1_out, not_1_out, not_5_out);
  nor nor_2 (nor_2_out, not_2_out, not_7_out);
  cnt_bit_2 cnt_bit_2_1 (
    .c_in(1'b1), .reset(nor_3_out), .clk1(MCLK1), .clk2(MCLK2), .val_out(cnt_bit_2_1_val_out),
    .c_out(cnt_bit_2_1_c_out));
  not not_3 (not_3_out, nor_1_out);
  not not_4 (not_4_out, nor_2_out);
  not not_5 (not_5_out, not_4_out);
  not not_6 (MCLK1, not_3_out);
  not not_7 (not_7_out, not_3_out);
  not not_8 (MCLK2, not_4_out);
  sr_bit sr_bit_2 (.value(reset), .clk1(MCLK1), .clk2(MCLK2), .valout(sr_bit_2_valout));
  not not_9 (not_9_out, reset);
  cnt_bit_2 cnt_bit_2_2 (
    .c_in(cnt_bit_2_1_c_out), .reset(nor_3_out), .clk1(MCLK1), .clk2(MCLK2), .val_out(cnt_bit_2_2_val_out));  // open: c_out
  sr_bit sr_bit_3 (.value(sr_bit_2_valout), .clk1(MCLK1), .clk2(MCLK2), .valout(sr_bit_3_valout));
  not not_10 (not_10_out, cnt_bit_2_2_val_out);
  nor nor_3 (nor_3_out, sr_bit_3_valout, not_9_out);
  nor nor_4 (nor_4_out, cnt_bit_2_1_val_out, not_10_out);
  nor nor_5 (nor_5_out, cnt_bit_2_1_val_out, cnt_bit_2_2_val_out);
  not not_11 (dac_clk, sr_bit_1_valout);
  sr_bit sr_bit_4 (.value(nor_4_out), .clk1(MCLK1), .clk2(MCLK2), .valout(sr_bit_4_valout));
  sr_bit sr_bit_5 (.value(nor_5_out), .clk1(MCLK1), .clk2(MCLK2), .valout(sr_bit_5_valout));
  D_Flip_Flop #(.trigger("high")) d_ff_1 (.D(sr_bit_4_valout), .clk(MCLK1), .Q(d_ff_1_q));  // open: Qn, preset, reset
  D_Flip_Flop #(.trigger("high")) d_ff_2 (.D(sr_bit_5_valout), .clk(MCLK1), .Q(d_ff_2_q));  // open: Qn, preset, reset
  nor nor_6 (nor_6_out, sr_bit_4_valout, d_ff_1_q);
  nor nor_7 (nor_7_out, sr_bit_5_valout, d_ff_2_q);
  not not_12 (not_12_out, nor_6_out);
  not not_13 (not_13_out, nor_7_out);
  buf buffer_1 (buffer_1_out, not_12_out);
  not not_14 (not_14_out, not_12_out);
  buf buffer_2 (buffer_2_out, not_13_out);
  not not_15 (not_15_out, not_13_out);
  assign controlled_buffer_1_out = buffer_1_out ? 1'b1 : 1'bz;  // Controlled_Buffer controlled_buffer_1
  assign controlled_buffer_1_out = not_14_out ? 1'b0 : 1'bz;  // Controlled_Buffer controlled_buffer_2
  assign controlled_buffer_3_out = not_14_out ? 1'b1 : 1'bz;  // Controlled_Buffer controlled_buffer_3
  assign controlled_buffer_3_out = buffer_1_out ? 1'b0 : 1'bz;  // Controlled_Buffer controlled_buffer_4
  assign controlled_buffer_5_out = buffer_2_out ? 1'b1 : 1'bz;  // Controlled_Buffer controlled_buffer_5
  assign controlled_buffer_5_out = not_15_out ? 1'b0 : 1'bz;  // Controlled_Buffer controlled_buffer_6
  assign controlled_buffer_7_out = not_15_out ? 1'b1 : 1'bz;  // Controlled_Buffer controlled_buffer_7
  assign controlled_buffer_7_out = buffer_2_out ? 1'b0 : 1'bz;  // Controlled_Buffer controlled_buffer_8
  assign clk1 = controlled_buffer_1_out ? 1'b1 : 1'bz;  // Controlled_Buffer controlled_buffer_9
  assign clk1 = controlled_buffer_3_out ? 1'b0 : 1'bz;  // Controlled_Buffer controlled_buffer_10
  assign clk2 = controlled_buffer_5_out ? 1'b1 : 1'bz;  // Controlled_Buffer controlled_buffer_11
  assign clk2 = controlled_buffer_7_out ? 1'b0 : 1'bz;  // Controlled_Buffer controlled_buffer_12
endmodule

module cnt_bit_2 (
  input  c_in,
  input  reset,
  input  clk1,
  input  clk2,
  output val_out,
  output c_out
);

  wire and_1_out, d_ff_1_qn, nor_2_out, not_1_out;

  not not_1 (not_1_out, c_in);
  and and_1 (and_1_out, not_1_out, val_out);
  nor nor_1 (c_out, not_1_out, val_out);
  nor nor_2 (nor_2_out, c_out, and_1_out, reset);
  D_Flip_Flop #(.trigger("high")) d_ff_1 (.D(nor_2_out), .clk(clk1), .Qn(d_ff_1_qn));  // open: Q, preset, reset
  D_Flip_Flop #(.trigger("high")) d_ff_2 (.D(d_ff_1_qn), .clk(clk2), .Q(val_out));  // open: Qn, preset, reset
endmodule

module io_handler (
  input  CS,
  input  WR,
  input  A0,
  input  reset,
  input  mclk1,
  input  mclk2,
  input  clk1,
  input  clk2,
  output write,
  output write0,
  output write1
);

  wire controlled_buffer_1_out, controlled_buffer_2_out, controlled_buffer_5_out, controlled_buffer_6_out,
       d_ff_1_qn, d_ff_2_qn, d_ff_3_qn, d_ff_4_qn, nor_1_out, nor_2_out, nor_3_out, nor_4_out, nor_5_out,
       nor_6_out, nor_7_out, nor_8_out, nor_9_out, not_1_out, not_2_out, not_3_out, not_5_out, not_6_out,
       not_7_out, not_8_out, not_9_out, not_10_out, sr_bit_1_valout, sr_bit_2_valout, sr_bit_3_valout;

  not not_1 (not_1_out, A0);
  not not_2 (not_2_out, not_1_out);
  not not_3 (not_3_out, not_2_out);
  nor nor_1 (nor_1_out, CS, WR, reset);
  nor nor_2 (nor_2_out, CS, WR, CS, not_2_out);
  nor nor_3 (nor_3_out, CS, WR, reset, not_3_out);
  not not_4 (write, nor_1_out);
  not not_5 (not_5_out, nor_2_out);
  not not_6 (not_6_out, nor_3_out);
  nor nor_4 (nor_4_out, not_5_out, sr_bit_3_valout);
  nor nor_5 (nor_5_out, nor_4_out, nor_6_out);
  nor nor_6 (nor_6_out, nor_5_out, sr_bit_3_valout);
  nor nor_7 (nor_7_out, not_6_out, write1);
  nor nor_8 (nor_8_out, nor_7_out, nor_9_out);
  nor nor_9 (nor_9_out, nor_8_out, write1);
  assign controlled_buffer_1_out = mclk2 ? nor_6_out : 1'bz;  // Controlled_Buffer controlled_buffer_1
  assign controlled_buffer_2_out = mclk2 ? nor_9_out : 1'bz;  // Controlled_Buffer controlled_buffer_2
  assign controlled_buffer_1_out = mclk1 ? not_7_out : 1'bz;  // Controlled_Buffer controlled_buffer_3
  assign controlled_buffer_2_out = mclk1 ? not_8_out : 1'bz;  // Controlled_Buffer controlled_buffer_4
  not not_7 (not_7_out, d_ff_1_qn);
  D_Flip_Flop #(.trigger("high")) d_ff_1 (
    .D(controlled_buffer_1_out), .clk(1'b1), .Qn(d_ff_1_qn));  // open: Q, preset, reset
  not not_8 (not_8_out, d_ff_2_qn);
  D_Flip_Flop #(.trigger("high")) d_ff_2 (
    .D(controlled_buffer_2_out), .clk(1'b1), .Qn(d_ff_2_qn));  // open: Q, preset, reset
  sr_bit sr_bit_1 (.value(d_ff_1_qn), .clk1(mclk1), .clk2(mclk2), .valout(sr_bit_1_valout));
  sr_bit sr_bit_2 (.value(d_ff_2_qn), .clk1(mclk1), .clk2(mclk2), .valout(sr_bit_2_valout));
  assign controlled_buffer_5_out = clk2 ? sr_bit_1_valout : 1'bz;  // Controlled_Buffer controlled_buffer_5
  assign controlled_buffer_6_out = clk2 ? sr_bit_2_valout : 1'bz;  // Controlled_Buffer controlled_buffer_6
  assign controlled_buffer_5_out = clk1 ? not_9_out : 1'bz;  // Controlled_Buffer controlled_buffer_7
  assign controlled_buffer_6_out = clk1 ? not_10_out : 1'bz;  // Controlled_Buffer controlled_buffer_8
  not not_9 (not_9_out, d_ff_3_qn);
  D_Flip_Flop #(.trigger("high")) d_ff_3 (
    .D(controlled_buffer_5_out), .clk(1'b1), .Qn(d_ff_3_qn));  // open: Q, preset, reset
  not not_10 (not_10_out, d_ff_4_qn);
  D_Flip_Flop #(.trigger("high")) d_ff_4 (
    .D(controlled_buffer_6_out), .clk(1'b1), .Qn(d_ff_4_qn));  // open: Q, preset, reset
  sr_bit sr_bit_3 (.value(d_ff_3_qn), .clk1(clk1), .clk2(clk2), .valout(sr_bit_3_valout));
  sr_bit sr_bit_4 (.value(d_ff_4_qn), .clk1(clk1), .clk2(clk2), .valout(write1));
  not not_11 (write0, sr_bit_3_valout);
endmodule

module fsm_counters (
  input  reset,
  input  clk1,
  input  clk2,
  output [4:0] fsm_cnt
);

  wire cnt_bit_1_c_out, cnt_bit_2_c_out, cnt_bit_3_c_out, nand_1_out, nand_2_out, nand_3_out, nand_4_out,
       nand_5_out, not_1_out, not_2_out, not_3_out, sr_bit_1_valout, sr_bit_2_valout;

  not not_1 (not_1_out, nand_2_out);
  sr_bit sr_bit_1 (.value(reset), .clk1(clk1), .clk2(clk2), .valout(sr_bit_1_valout));
  sr_bit sr_bit_2 (.value(sr_bit_1_valout), .clk1(clk1), .clk2(clk2), .valout(sr_bit_2_valout));
  not not_2 (not_2_out, sr_bit_2_valout);
  cnt_bit cnt_bit_1 (
    .c_in(1'b1), .reset(nand_3_out), .clk1(clk1), .clk2(clk2), .val_out(fsm_cnt[0]), .c_out(cnt_bit_1_c_out));
  cnt_bit cnt_bit_2 (
    .c_in(not_1_out), .reset(nand_4_out), .clk1(clk1), .clk2(clk2), .val_out(fsm_cnt[3]),
    .c_out(cnt_bit_2_c_out));
  nand nand_1 (nand_1_out, not_2_out, reset);
  not not_3 (not_3_out, nand_2_out);
  cnt_bit cnt_bit_3 (
    .c_in(cnt_bit_1_c_out), .reset(nand_3_out), .clk1(clk1), .clk2(clk2), .val_out(fsm_cnt[1]),
    .c_out(cnt_bit_3_c_out));
  cnt_bit cnt_bit_4 (
    .c_in(cnt_bit_2_c_out), .reset(nand_4_out), .clk1(clk1), .clk2(clk2), .val_out(fsm_cnt[4]));  // open: c_out
  nand nand_2 (nand_2_out, fsm_cnt[0], fsm_cnt[2]);
  nand nand_3 (nand_3_out, nand_2_out, nand_1_out);
  nand nand_4 (nand_4_out, nand_1_out, nand_5_out);
  nand nand_5 (nand_5_out, fsm_cnt[4], not_3_out);
  cnt_bit cnt_bit_5 (
    .c_in(cnt_bit_3_c_out), .reset(nand_3_out), .clk1(clk1), .clk2(clk2), .val_out(fsm_cnt[2]));  // open: c_out
endmodule

module cnt_bit (
  input  c_in,
  input  reset,
  input  clk1,
  input  clk2,
  output val_out,
  output c_out
);

  wire and_1_out, d_ff_1_qn, d_ff_2_q, nor_2_out, not_1_out;

  not not_1 (not_1_out, c_in);
  and and_1 (and_1_out, not_1_out, d_ff_2_q);
  nor nor_1 (c_out, not_1_out, d_ff_2_q);
  nor nor_2 (nor_2_out, c_out, and_1_out, reset);
  D_Flip_Flop #(.trigger("high")) d_ff_1 (.D(nor_2_out), .clk(clk1), .Qn(d_ff_1_qn));  // open: Q, preset, reset
  D_Flip_Flop #(.trigger("high")) d_ff_2 (.D(d_ff_1_qn), .clk(clk2), .Q(d_ff_2_q));  // open: Qn, preset, reset
  not not_2 (val_out, d_ff_2_q);
endmodule

module fsm_table_ds1001 (
  input  [4:0] counter,
  input  rhythm,
  input  clk1,
  input  clk2,
  output out_5,
  output out_6,
  output out_7,
  output out_8,
  output out_9,
  output out_10,
  output out_11,
  output out_12,
  output out_13,
  output out_14,
  output out_15,
  output out_16
);

  wire nor_3_out, nor_5_out, nor_6_out, nor_8_out, nor_9_out, not_1_out, not_3_out, not_4_out,
       sr_bit_1_valout, sr_bit_2_valout, sr_bit_3_valout, sr_bit_4_valout;
  wire [4:0] not_2_out;

  sr_bit sr_bit_1 (.value(counter[4]), .clk1(clk1), .clk2(clk2), .valout(sr_bit_1_valout));
  sr_bit sr_bit_2 (.value(counter[3]), .clk1(clk1), .clk2(clk2), .valout(sr_bit_2_valout));
  sr_bit sr_bit_3 (.value(out_12), .clk1(clk1), .clk2(clk2), .valout(sr_bit_3_valout));
  not not_1 (not_1_out, rhythm);
  sr_bit sr_bit_4 (.value(sr_bit_1_valout), .clk1(clk1), .clk2(clk2), .valout(sr_bit_4_valout));
  sr_bit sr_bit_5 (.value(sr_bit_2_valout), .clk1(clk1), .clk2(clk2), .valout(out_12));
  assign not_2_out = ~counter;  // NOT_Gate not_2, 5 bits wide
  not not_3 (not_3_out, not_1_out);
  sr_bit sr_bit_6 (.value(out_9), .clk1(clk1), .clk2(clk2), .valout(out_15));
  sr_bit sr_bit_7 (.value(out_15), .clk1(clk1), .clk2(clk2), .valout(out_16));
  nor nor_1 (out_5, not_3_out, sr_bit_4_valout, not_4_out);
  nor nor_2 (out_6, not_4_out, nor_3_out);
  nor nor_3 (nor_3_out, not_1_out, not_2_out[4], counter[3], counter[2], counter[1]);
  not not_4 (not_4_out, out_8);
  nor nor_4 (out_7, out_8, nor_5_out, nor_6_out);
  nor nor_5 (nor_5_out, not_1_out, not_2_out[4], counter[3], not_2_out[2], counter[1], counter[0]);
  nor nor_6 (nor_6_out, not_1_out, not_2_out[4], counter[3], counter[2], not_2_out[1], not_2_out[0]);
  nor nor_7 (out_8, nor_8_out, nor_9_out);
  nor nor_8 (nor_8_out, not_2_out[2], counter[0]);
  nor nor_9 (nor_9_out, counter[2], not_2_out[1]);
  nor nor_10 (out_9, not_2_out[4], counter[3], not_2_out[2], counter[1], counter[0]);
  nor nor_11 (out_10, not_2_out[4], counter[3], counter[2], counter[1], not_2_out[0]);
  nor nor_12 (out_11, counter[4], not_2_out[3], not_2_out[2], counter[1], counter[0]);
  nor nor_13 (out_13, out_12, sr_bit_4_valout);
  nor nor_14 (out_14, sr_bit_3_valout, counter[4]);
endmodule

module transparent_latch8 (
  input  [7:0] in_1,
  output [7:0] out_2
);

  D_Flip_Flop #(.trigger("high")) d_ff_1 (.D(in_1[0]), .clk(1'b1), .Qn(out_2[0]));  // open: Q, preset, reset
  D_Flip_Flop #(.trigger("high")) d_ff_2 (.D(in_1[1]), .clk(1'b1), .Qn(out_2[1]));  // open: Q, preset, reset
  D_Flip_Flop #(.trigger("high")) d_ff_3 (.D(in_1[2]), .clk(1'b1), .Qn(out_2[2]));  // open: Q, preset, reset
  D_Flip_Flop #(.trigger("high")) d_ff_4 (.D(in_1[3]), .clk(1'b1), .Qn(out_2[3]));  // open: Q, preset, reset
  D_Flip_Flop #(.trigger("high")) d_ff_5 (.D(in_1[4]), .clk(1'b1), .Qn(out_2[4]));  // open: Q, preset, reset
  D_Flip_Flop #(.trigger("high")) d_ff_6 (.D(in_1[5]), .clk(1'b1), .Qn(out_2[5]));  // open: Q, preset, reset
  D_Flip_Flop #(.trigger("high")) d_ff_7 (.D(in_1[6]), .clk(1'b1), .Qn(out_2[6]));  // open: Q, preset, reset
  D_Flip_Flop #(.trigger("high")) d_ff_8 (.D(in_1[7]), .clk(1'b1), .Qn(out_2[7]));  // open: Q, preset, reset
endmodule

module data_register (
  input  [7:0] data,
  input  write,
  output [7:0] data_reg
);

  wire buffer_1_out, not_1_out;
  wire [7:0] controlled_buffer_1_out, not_2_out, not_3_out;

  not not_1 (not_1_out, write);
  buf buffer_1 (buffer_1_out, write);
  assign controlled_buffer_1_out = buffer_1_out ? not_2_out : 8'bz;  // Controlled_Buffer controlled_buffer_1
  assign controlled_buffer_1_out = not_1_out ? data : 8'bz;  // Controlled_Buffer controlled_buffer_2
  assign not_2_out = ~not_3_out;  // NOT_Gate not_2, 8 bits wide
  assign not_3_out = ~controlled_buffer_1_out;  // NOT_Gate not_3, 8 bits wide
  assign data_reg = ~not_3_out;  // NOT_Gate not_4, 8 bits wide
endmodule

module chan_registers_ctrl (
  input  [7:0] data,
  input  write_addr,
  input  write_data,
  input  reset,
  input  sync,
  input  clk1,
  input  clk2,
  output [7:0] data_out,
  output write20,
  output write30,
  output write10
);

  wire and_1_out, buffer_1_out, buffer_2_out, cnt_bit_2_1_c_out, cnt_bit_2_1_val_out, cnt_bit_2_2_c_out,
       cnt_bit_2_2_val_out, cnt_bit_2_3_c_out, cnt_bit_2_3_val_out, cnt_bit_2_4_c_out, cnt_bit_2_4_val_out,
       cnt_bit_2_5_val_out, controlled_buffer_3_out, d_ff_1_qn, nand_1_out, nand_2_out, nor_1_out, nor_3_out,
       nor_4_out, nor_5_out, nor_6_out, nor_7_out, nor_8_out, nor_9_out, nor_10_out, nor_11_out, nor_12_out,
       not_1_out, not_2_out, not_3_out, not_5_out, not_10_out, sr_bit_1_valout, xor_1_out, xor_2_out,
       xor_3_out, xor_4_out;
  wire [5:0] bit_extender_1_out, controlled_buffer_5_out, not_6_out, transparent_latch6_1_out_2;
  wire [7:0] bit_extender_2_out, controlled_buffer_1_out, nor_2_out, transparent_latch8_1_out_2;

  Bit_Extender #(.out_width(6), .\type ("zero")) bit_extender_1 (.in(data), .out(bit_extender_1_out));
  nor nor_1 (nor_1_out, data[6], data[7]);
  not not_1 (not_1_out, write_addr);
  assign controlled_buffer_1_out = buffer_2_out ? data : 8'bz;  // Controlled_Buffer controlled_buffer_1
  assign controlled_buffer_1_out = not_5_out ? nor_2_out : 8'bz;  // Controlled_Buffer controlled_buffer_2
  not not_2 (not_2_out, not_1_out);
  nand nand_1 (nand_1_out, not_1_out, nor_1_out);
  assign controlled_buffer_3_out = not_2_out ? nor_3_out : 1'bz;  // Controlled_Buffer controlled_buffer_3
  assign controlled_buffer_3_out = not_1_out ? nor_1_out : 1'bz;  // Controlled_Buffer controlled_buffer_4
  assign bit_extender_2_out = {{7{reset}}, reset};  // Bit_Extender bit_extender_2
  not not_3 (not_3_out, nand_1_out);
  buf buffer_1 (buffer_1_out, nand_1_out);
  transparent_latch8 transparent_latch8_1 (.in_1(controlled_buffer_1_out), .out_2(transparent_latch8_1_out_2));
  D_Flip_Flop #(.trigger("high")) d_ff_1 (
    .D(controlled_buffer_3_out), .clk(1'b1), .Qn(d_ff_1_qn));  // open: Q, preset, reset
  assign data_out = ~transparent_latch8_1_out_2;  // NOT_Gate not_4, 8 bits wide
  assign controlled_buffer_5_out = not_3_out ? bit_extender_1_out : 6'bz;  // Controlled_Buffer controlled_buffer_5
  assign controlled_buffer_5_out = buffer_1_out ? not_6_out : 6'bz;  // Controlled_Buffer controlled_buffer_6
  assign nor_2_out = ~(transparent_latch8_1_out_2 | bit_extender_2_out);  // NOR_Gate nor_2, 8 bits wide
  nor nor_3 (nor_3_out, reset, d_ff_1_qn);
  and and_1 (and_1_out, nor_3_out, write_data);
  buf buffer_2 (buffer_2_out, and_1_out);
  not not_5 (not_5_out, and_1_out);
  nor nor_4 (nor_4_out, and_1_out, nor_5_out);
  transparent_latch6 transparent_latch6_1 (.in_1(controlled_buffer_5_out), .out_2(transparent_latch6_1_out_2));
  sr_bit sr_bit_1 (.value(nor_4_out), .clk1(clk1), .clk2(clk2), .valout(sr_bit_1_valout));
  cnt_bit_2 cnt_bit_2_1 (
    .c_in(1'b1), .reset(sync), .clk1(clk1), .clk2(clk2), .val_out(cnt_bit_2_1_val_out),
    .c_out(cnt_bit_2_1_c_out));
  assign not_6_out = ~transparent_latch6_1_out_2;  // NOT_Gate not_6, 6 bits wide
  nor nor_5 (nor_5_out, sr_bit_1_valout, not_1_out, reset);
  nand nand_2 (nand_2_out, nor_12_out, nor_5_out);
  cnt_bit_2 cnt_bit_2_2 (
    .c_in(cnt_bit_2_1_c_out), .reset(sync), .clk1(clk1), .clk2(clk2), .val_out(cnt_bit_2_2_val_out),
    .c_out(cnt_bit_2_2_c_out));
  cnt_bit_2 cnt_bit_2_3 (
    .c_in(cnt_bit_2_4_c_out), .reset(sync), .clk1(clk1), .clk2(clk2), .val_out(cnt_bit_2_3_val_out),
    .c_out(cnt_bit_2_3_c_out));
  nor nor_6 (nor_6_out, not_6_out[4], transparent_latch6_1_out_2[5], nand_2_out);
  nor nor_7 (nor_7_out, transparent_latch6_1_out_2[4], transparent_latch6_1_out_2[5], nand_2_out);
  nor nor_8 (nor_8_out, transparent_latch6_1_out_2[4], not_6_out[5], nand_2_out);
  nor nor_9 (nor_9_out, nor_6_out, reset);
  nor nor_10 (nor_10_out, nor_7_out, reset);
  nor nor_11 (nor_11_out, nor_8_out, reset);
  cnt_bit_2 cnt_bit_2_4 (
    .c_in(cnt_bit_2_2_c_out), .reset(sync), .clk1(clk1), .clk2(clk2), .val_out(cnt_bit_2_4_val_out),
    .c_out(cnt_bit_2_4_c_out));
  cnt_bit_2 cnt_bit_2_5 (
    .c_in(cnt_bit_2_3_c_out), .reset(sync), .clk1(clk1), .clk2(clk2), .val_out(cnt_bit_2_5_val_out));  // open: c_out
  not not_7 (write20, nor_9_out);
  not not_8 (write30, nor_10_out);
  not not_9 (write10, nor_11_out);
  xor xor_1 (xor_1_out, cnt_bit_2_1_val_out, transparent_latch6_1_out_2[0]);
  xor xor_2 (xor_2_out, cnt_bit_2_2_val_out, transparent_latch6_1_out_2[1]);
  xor xor_3 (xor_3_out, cnt_bit_2_4_val_out, transparent_latch6_1_out_2[2]);
  xor xor_4 (xor_4_out, cnt_bit_2_3_val_out, transparent_latch6_1_out_2[3]);
  not not_10 (not_10_out, cnt_bit_2_5_val_out);
  nor nor_12 (nor_12_out, xor_1_out, xor_2_out, xor_3_out, xor_4_out, not_10_out);
endmodule

module transparent_latch6 (
  input  [5:0] in_1,
  output [5:0] out_2
);

  D_Flip_Flop #(.trigger("high")) d_ff_1 (.D(in_1[0]), .clk(1'b1), .Qn(out_2[0]));  // open: Q, preset, reset
  D_Flip_Flop #(.trigger("high")) d_ff_2 (.D(in_1[1]), .clk(1'b1), .Qn(out_2[1]));  // open: Q, preset, reset
  D_Flip_Flop #(.trigger("high")) d_ff_3 (.D(in_1[2]), .clk(1'b1), .Qn(out_2[2]));  // open: Q, preset, reset
  D_Flip_Flop #(.trigger("high")) d_ff_4 (.D(in_1[3]), .clk(1'b1), .Qn(out_2[3]));  // open: Q, preset, reset
  D_Flip_Flop #(.trigger("high")) d_ff_5 (.D(in_1[4]), .clk(1'b1), .Qn(out_2[4]));  // open: Q, preset, reset
  D_Flip_Flop #(.trigger("high")) d_ff_6 (.D(in_1[5]), .clk(1'b1), .Qn(out_2[5]));  // open: Q, preset, reset
endmodule

module chan_registers (
  input  [7:0] data,
  input  write20,
  input  write10,
  input  write30,
  input  sel1,
  input  sel2,
  input  sel3,
  input  volsel1,
  input  volsel2,
  input  clk1,
  input  clk2,
  output [8:0] fnum,
  output [2:0] block_num,
  output key_on,
  output sus_on,
  output [3:0] volume,
  output [3:0] instrument
);

  wire buffer_1_out, buffer_2_out, buffer_3_out, not_1_out, not_2_out, not_3_out;
  wire [3:0] dlatch_4bit_1_out_3, dlatch_4bit_2_out_3, nor_1_out, nor_1_out_2;
  wire [5:0] and_1_out, and_2_out, and_3_out, bit_extender_1_out, bit_extender_2_out, bit_extender_3_out,
       bit_extender_4_out, controlled_buffer_1_out, sr_6bit_1_outval, sr_6bit_2_outval, sr_6bit_3_outval,
       sr_6bit_4_outval, sr_6bit_5_outval, sr_6bit_6_outval, sr_6bit_7_outval, sr_6bit_8_outval,
       sr_6bit_9_outval;
  wire [7:0] and_4_out, and_5_out, and_6_out, and_7_out, and_8_out, and_9_out, bit_extender_5_out,
       bit_extender_6_out, bit_extender_7_out, bit_extender_8_out, bit_extender_9_out, bit_extender_10_out,
       controlled_buffer_3_out, controlled_buffer_5_out, sr_8bit_1_outval, sr_8bit_2_outval,
       sr_8bit_3_outval, sr_8bit_4_outval, sr_8bit_5_outval, sr_8bit_6_outval, sr_8bit_7_outval,
       sr_8bit_8_outval, sr_8bit_9_outval, sr_8bit_10_outval, sr_8bit_11_outval, sr_8bit_12_outval,
       sr_8bit_13_outval, sr_8bit_14_outval, sr_8bit_15_outval, sr_8bit_16_outval, sr_8bit_17_outval,
       sr_8bit_18_outval;

  Bit_Extender #(.out_width(6), .\type ("zero")) bit_extender_1 (.in(data), .out(bit_extender_1_out));
  buf buffer_1 (buffer_1_out, write20);
  not not_1 (not_1_out, write20);
  assign controlled_buffer_1_out = buffer_1_out ? bit_extender_1_out : 6'bz;  // Controlled_Buffer controlled_buffer_1
  assign controlled_buffer_1_out = not_1_out ? sr_6bit_9_outval : 6'bz;  // Controlled_Buffer controlled_buffer_2
  assign bit_extender_2_out = {{5{sel1}}, sel1};  // Bit_Extender bit_extender_2
  assign bit_extender_3_out = {{5{sel2}}, sel2};  // Bit_Extender bit_extender_3
  assign bit_extender_4_out = {{5{sel3}}, sel3};  // Bit_Extender bit_extender_4
  sr_6bit sr_6bit_1 (.value(controlled_buffer_1_out), .clk1(clk1), .clk2(clk2), .outval(sr_6bit_1_outval));
  sr_6bit sr_6bit_2 (.value(sr_6bit_1_outval), .clk1(clk1), .clk2(clk2), .outval(sr_6bit_2_outval));
  sr_6bit sr_6bit_3 (.value(sr_6bit_2_outval), .clk1(clk1), .clk2(clk2), .outval(sr_6bit_3_outval));
  sr_6bit sr_6bit_4 (.value(sr_6bit_3_outval), .clk1(clk1), .clk2(clk2), .outval(sr_6bit_4_outval));
  sr_6bit sr_6bit_5 (.value(sr_6bit_4_outval), .clk1(clk1), .clk2(clk2), .outval(sr_6bit_5_outval));
  assign and_1_out = sr_6bit_2_outval & bit_extender_2_out;  // AND_Gate and_1, 6 bits wide
  assign and_2_out = sr_6bit_5_outval & bit_extender_3_out;  // AND_Gate and_2, 6 bits wide
  assign and_3_out = sr_6bit_8_outval & bit_extender_4_out;  // AND_Gate and_3, 6 bits wide
  assign {sus_on, key_on, block_num, fnum[8]} = and_1_out | and_2_out | and_3_out;  // OR_Gate or_1, 6 bits wide
  sr_6bit sr_6bit_6 (.value(sr_6bit_5_outval), .clk1(clk1), .clk2(clk2), .outval(sr_6bit_6_outval));
  sr_6bit sr_6bit_7 (.value(sr_6bit_6_outval), .clk1(clk1), .clk2(clk2), .outval(sr_6bit_7_outval));
  sr_6bit sr_6bit_8 (.value(sr_6bit_7_outval), .clk1(clk1), .clk2(clk2), .outval(sr_6bit_8_outval));
  sr_6bit sr_6bit_9 (.value(sr_6bit_8_outval), .clk1(clk1), .clk2(clk2), .outval(sr_6bit_9_outval));
  buf buffer_2 (buffer_2_out, write10);
  not not_2 (not_2_out, write10);
  assign controlled_buffer_3_out = buffer_2_out ? data : 8'bz;  // Controlled_Buffer controlled_buffer_3
  assign controlled_buffer_3_out = not_2_out ? sr_8bit_9_outval : 8'bz;  // Controlled_Buffer controlled_buffer_4
  assign bit_extender_5_out = {{7{sel1}}, sel1};  // Bit_Extender bit_extender_5
  assign bit_extender_6_out = {{7{sel2}}, sel2};  // Bit_Extender bit_extender_6
  assign bit_extender_7_out = {{7{sel3}}, sel3};  // Bit_Extender bit_extender_7
  sr_8bit sr_8bit_1 (.value(controlled_buffer_3_out), .clk1(clk1), .clk2(clk2), .outval(sr_8bit_1_outval));
  sr_8bit sr_8bit_2 (.value(sr_8bit_1_outval), .clk1(clk1), .clk2(clk2), .outval(sr_8bit_2_outval));
  sr_8bit sr_8bit_3 (.value(sr_8bit_2_outval), .clk1(clk1), .clk2(clk2), .outval(sr_8bit_3_outval));
  sr_8bit sr_8bit_4 (.value(sr_8bit_3_outval), .clk1(clk1), .clk2(clk2), .outval(sr_8bit_4_outval));
  sr_8bit sr_8bit_5 (.value(sr_8bit_4_outval), .clk1(clk1), .clk2(clk2), .outval(sr_8bit_5_outval));
  assign and_4_out = sr_8bit_2_outval & bit_extender_5_out;  // AND_Gate and_4, 8 bits wide
  assign and_5_out = sr_8bit_5_outval & bit_extender_6_out;  // AND_Gate and_5, 8 bits wide
  assign and_6_out = sr_8bit_8_outval & bit_extender_7_out;  // AND_Gate and_6, 8 bits wide
  assign fnum[7:0] = and_4_out | and_5_out | and_6_out;  // OR_Gate or_2, 8 bits wide
  sr_8bit sr_8bit_6 (.value(sr_8bit_5_outval), .clk1(clk1), .clk2(clk2), .outval(sr_8bit_6_outval));
  sr_8bit sr_8bit_7 (.value(sr_8bit_6_outval), .clk1(clk1), .clk2(clk2), .outval(sr_8bit_7_outval));
  sr_8bit sr_8bit_8 (.value(sr_8bit_7_outval), .clk1(clk1), .clk2(clk2), .outval(sr_8bit_8_outval));
  sr_8bit sr_8bit_9 (.value(sr_8bit_8_outval), .clk1(clk1), .clk2(clk2), .outval(sr_8bit_9_outval));
  buf buffer_3 (buffer_3_out, write30);
  not not_3 (not_3_out, write30);
  assign controlled_buffer_5_out = buffer_3_out ? data : 8'bz;  // Controlled_Buffer controlled_buffer_5
  assign controlled_buffer_5_out = not_3_out ? sr_8bit_18_outval : 8'bz;  // Controlled_Buffer controlled_buffer_6
  assign bit_extender_8_out = {{7{sel1}}, sel1};  // Bit_Extender bit_extender_8
  assign bit_extender_9_out = {{7{sel2}}, sel2};  // Bit_Extender bit_extender_9
  assign bit_extender_10_out = {{7{sel3}}, sel3};  // Bit_Extender bit_extender_10
  sr_8bit sr_8bit_10 (.value(controlled_buffer_5_out), .clk1(clk1), .clk2(clk2), .outval(sr_8bit_10_outval));
  sr_8bit sr_8bit_11 (.value(sr_8bit_10_outval), .clk1(clk1), .clk2(clk2), .outval(sr_8bit_11_outval));
  sr_8bit sr_8bit_12 (.value(sr_8bit_11_outval), .clk1(clk1), .clk2(clk2), .outval(sr_8bit_12_outval));
  sr_8bit sr_8bit_13 (.value(sr_8bit_12_outval), .clk1(clk1), .clk2(clk2), .outval(sr_8bit_13_outval));
  sr_8bit sr_8bit_14 (.value(sr_8bit_13_outval), .clk1(clk1), .clk2(clk2), .outval(sr_8bit_14_outval));
  assign and_7_out = sr_8bit_11_outval & bit_extender_8_out;  // AND_Gate and_7, 8 bits wide
  assign and_8_out = sr_8bit_14_outval & bit_extender_9_out;  // AND_Gate and_8, 8 bits wide
  assign and_9_out = sr_8bit_17_outval & bit_extender_10_out;  // AND_Gate and_9, 8 bits wide
  assign {nor_1_out_2, nor_1_out} = ~(and_7_out | and_8_out | and_9_out);  // NOR_Gate nor_1, 8 bits wide
  sr_8bit sr_8bit_15 (.value(sr_8bit_14_outval), .clk1(clk1), .clk2(clk2), .outval(sr_8bit_15_outval));
  sr_8bit sr_8bit_16 (.value(sr_8bit_15_outval), .clk1(clk1), .clk2(clk2), .outval(sr_8bit_16_outval));
  sr_8bit sr_8bit_17 (.value(sr_8bit_16_outval), .clk1(clk1), .clk2(clk2), .outval(sr_8bit_17_outval));
  sr_8bit sr_8bit_18 (.value(sr_8bit_17_outval), .clk1(clk1), .clk2(clk2), .outval(sr_8bit_18_outval));
  assign volume = volsel1 ? dlatch_4bit_1_out_3 : 4'bz;  // Controlled_Buffer controlled_buffer_7
  dlatch_4bit dlatch_4bit_1 (.in_1(nor_1_out), .in_2(clk1), .out_3(dlatch_4bit_1_out_3));
  dlatch_4bit dlatch_4bit_2 (.in_1(nor_1_out_2), .in_2(clk1), .out_3(dlatch_4bit_2_out_3));
  assign volume = volsel2 ? dlatch_4bit_2_out_3 : 4'bz;  // Controlled_Buffer controlled_buffer_8
  assign instrument = ~nor_1_out_2;  // NOT_Gate not_4, 4 bits wide
endmodule

module sr_8bit (
  input  [7:0] value,
  input  clk1,
  input  clk2,
  output [7:0] outval
);

  sr_bit sr_bit_1 (.value(value[0]), .clk1(clk1), .clk2(clk2), .valout(outval[0]));
  sr_bit sr_bit_2 (.value(value[1]), .clk1(clk1), .clk2(clk2), .valout(outval[1]));
  sr_bit sr_bit_3 (.value(value[2]), .clk1(clk1), .clk2(clk2), .valout(outval[2]));
  sr_bit sr_bit_4 (.value(value[3]), .clk1(clk1), .clk2(clk2), .valout(outval[3]));
  sr_bit sr_bit_5 (.value(value[4]), .clk1(clk1), .clk2(clk2), .valout(outval[4]));
  sr_bit sr_bit_6 (.value(value[5]), .clk1(clk1), .clk2(clk2), .valout(outval[5]));
  sr_bit sr_bit_7 (.value(value[6]), .clk1(clk1), .clk2(clk2), .valout(outval[6]));
  sr_bit sr_bit_8 (.value(value[7]), .clk1(clk1), .clk2(clk2), .valout(outval[7]));
endmodule

module sr_6bit (
  input  [5:0] value,
  input  clk1,
  input  clk2,
  output [5:0] outval
);

  sr_bit sr_bit_1 (.value(value[0]), .clk1(clk1), .clk2(clk2), .valout(outval[0]));
  sr_bit sr_bit_2 (.value(value[1]), .clk1(clk1), .clk2(clk2), .valout(outval[1]));
  sr_bit sr_bit_3 (.value(value[2]), .clk1(clk1), .clk2(clk2), .valout(outval[2]));
  sr_bit sr_bit_4 (.value(value[3]), .clk1(clk1), .clk2(clk2), .valout(outval[3]));
  sr_bit sr_bit_5 (.value(value[4]), .clk1(clk1), .clk2(clk2), .valout(outval[4]));
  sr_bit sr_bit_6 (.value(value[5]), .clk1(clk1), .clk2(clk2), .valout(outval[5]));
endmodule

module dlatch_4bit (
  input  [3:0] in_1,
  input  in_2,
  output [3:0] out_3
);

  D_Flip_Flop #(.trigger("high")) d_ff_1 (.D(in_1[0]), .clk(in_2), .Qn(out_3[0]));  // open: Q, preset, reset
  D_Flip_Flop #(.trigger("high")) d_ff_2 (.D(in_1[1]), .clk(in_2), .Qn(out_3[1]));  // open: Q, preset, reset
  D_Flip_Flop #(.trigger("high")) d_ff_3 (.D(in_1[2]), .clk(in_2), .Qn(out_3[2]));  // open: Q, preset, reset
  D_Flip_Flop #(.trigger("high")) d_ff_4 (.D(in_1[3]), .clk(in_2), .Qn(out_3[3]));  // open: Q, preset, reset
endmodule

module instrument_ctrl (
  input  [3:0] instr,
  input  bd0,
  input  hh,
  input  tom,
  input  bd1,
  input  sd,
  input  tc,
  input  kon,
  input  modcar_sel,
  input  clk1,
  input  clk2,
  output clk2_inv,
  output out_13,
  output force_zerorate,
  output mod_sel_custom,
  output ch_sel_custom,
  output car_sel_custom,
  output modcar_sel_clk1,
  output out_sel1,
  output out_sel2,
  output car_sel,
  output mod_sel,
  output [20:0] inst_sel
);

  wire d_ff_1_q, d_ff_2_qn, d_ff_3_q, nor_1_out, nor_2_out, not_1_out, not_2_out, not_6_out, not_7_out,
       or_1_out;
  wire [3:0] not_3_out;

  not not_1 (not_1_out, clk2);
  not not_2 (not_2_out, not_1_out);
  assign not_3_out = ~instr;  // NOT_Gate not_3, 4 bits wide
  not not_4 (clk2_inv, not_2_out);
  nor nor_1 (nor_1_out, hh, tom);
  or or_1 (or_1_out, bd0, hh, tom, bd1, sd, tc);
  D_Flip_Flop #(.trigger("high")) d_ff_1 (.D(nor_1_out), .clk(clk1), .Q(d_ff_1_q), .Qn(out_13));  // open: preset, reset
  D_Flip_Flop #(.trigger("high")) d_ff_2 (.D(kon), .clk(clk1), .Qn(d_ff_2_qn));  // open: Q, preset, reset
  D_Flip_Flop #(.trigger("high")) d_ff_3 (.D(modcar_sel), .clk(clk1), .Q(d_ff_3_q));  // open: Qn, preset, reset
  nor nor_2 (nor_2_out, or_1_out, instr[0], instr[1], instr[2], instr[3]);
  nor nor_3 (inst_sel[14], or_1_out, not_3_out[0], not_3_out[1], not_3_out[2], not_3_out[3], clk2);
  nor nor_4 (inst_sel[13], or_1_out, instr[0], not_3_out[1], not_3_out[2], not_3_out[3], clk2);
  nor nor_5 (inst_sel[12], or_1_out, not_3_out[0], instr[1], not_3_out[2], not_3_out[3], clk2);
  nor nor_6 (inst_sel[11], or_1_out, instr[0], instr[1], not_3_out[2], not_3_out[3], clk2);
  nor nor_7 (inst_sel[10], or_1_out, not_3_out[0], not_3_out[1], instr[2], not_3_out[3], clk2);
  nor nor_8 (inst_sel[9], or_1_out, instr[0], not_3_out[1], instr[2], not_3_out[3], clk2);
  nor nor_9 (inst_sel[8], or_1_out, not_3_out[0], instr[1], instr[2], not_3_out[3], clk2);
  nor nor_10 (inst_sel[7], or_1_out, instr[0], instr[1], instr[2], not_3_out[3], clk2);
  nor nor_11 (inst_sel[6], or_1_out, not_3_out[0], not_3_out[1], not_3_out[2], instr[3], clk2);
  nor nor_12 (inst_sel[5], or_1_out, instr[0], not_3_out[1], not_3_out[2], instr[3], clk2);
  nor nor_13 (inst_sel[4], or_1_out, not_3_out[0], instr[1], not_3_out[2], instr[3], clk2);
  nor nor_14 (inst_sel[3], or_1_out, instr[0], instr[1], not_3_out[2], instr[3], clk2);
  nor nor_15 (inst_sel[2], or_1_out, not_3_out[0], not_3_out[1], instr[2], instr[3], clk2);
  nor nor_16 (inst_sel[1], or_1_out, instr[0], not_3_out[1], instr[2], instr[3], clk2);
  nor nor_17 (inst_sel[0], or_1_out, not_3_out[0], instr[1], instr[2], instr[3], clk2);
  D_Flip_Flop #(.trigger("high")) d_ff_4 (.D(nor_2_out), .clk(clk1), .Qn(out_sel1));  // open: Q, preset, reset
  and and_1 (force_zerorate, d_ff_1_q, d_ff_2_qn, d_ff_3_q);
  nor nor_18 (mod_sel_custom, d_ff_3_q, out_sel1);
  not not_5 (ch_sel_custom, out_sel1);
  nand nand_1 (inst_sel[15], bd0, clk2_inv);
  nand nand_2 (inst_sel[16], hh, clk2_inv);
  nand nand_3 (inst_sel[17], tom, clk2_inv);
  D_Flip_Flop #(.trigger("high")) d_ff_5 (.D(modcar_sel), .clk(clk1), .Qn(modcar_sel_clk1));  // open: Q, preset, reset
  nand nand_4 (inst_sel[18], bd1, clk2_inv);
  nand nand_5 (inst_sel[19], sd, clk2_inv);
  nand nand_6 (inst_sel[20], tc, clk2_inv);
  not not_6 (not_6_out, clk2);
  nor nor_19 (car_sel_custom, modcar_sel_clk1, out_sel1);
  nor nor_20 (out_sel2, car_sel_custom, modcar_sel_clk1, out_13);
  nand nand_7 (car_sel, not_6_out, modcar_sel);
  nand nand_8 (mod_sel, not_6_out, not_7_out);
  not not_7 (not_7_out, modcar_sel);
endmodule

module rhythm_ctrl1 (
  input  rhythm,
  input  sync,
  input  clk1,
  input  clk2,
  output bd0,
  output hh,
  output tom,
  output bd1,
  output sd,
  output tc
);

  wire sr_bit_1_valout;

  sr_bit sr_bit_1 (.value(sync), .clk1(clk1), .clk2(clk2), .valout(sr_bit_1_valout));
  and and_1 (bd0, rhythm, sr_bit_1_valout);
  sr_bit sr_bit_2 (.value(bd0), .clk1(clk1), .clk2(clk2), .valout(hh));
  sr_bit sr_bit_3 (.value(hh), .clk1(clk1), .clk2(clk2), .valout(tom));
  sr_bit sr_bit_4 (.value(tom), .clk1(clk1), .clk2(clk2), .valout(bd1));
  sr_bit sr_bit_5 (.value(bd1), .clk1(clk1), .clk2(clk2), .valout(sd));
  sr_bit sr_bit_6 (.value(sd), .clk1(clk1), .clk2(clk2), .valout(tc));
endmodule
module instrument_template (
  input  [20:0] instr_sel,
  input  mod_sel,
  input  car_sel,
  input  out_sel1,
  input  out_sel2,
  input  clk1,
  input  clk2,
  input  clk2_inv,
  output [5:0] tl,
  output dc,
  output dm,
  output [2:0] out_12,
  output am,
  output vib,
  output et,
  output ksr,
  output [3:0] multi,
  output [1:0] ksl,
  output [3:0] ar,
  output [3:0] dr,
  output [3:0] sl,
  output [3:0] rr
);

  wire transistor_1_out, transistor_2_out, transistor_3_out, transistor_4_out, transistor_5_out,
       transistor_6_out, transistor_7_out, transistor_8_out, transistor_9_out, transistor_10_out,
       transistor_11_out, transistor_12_out, transistor_13_out, transistor_14_out, transistor_15_out,
       transistor_16_out, transistor_17_out, transistor_18_out, transistor_19_out, transistor_20_out,
       transistor_21_out, transistor_22_out, transistor_23_out, transistor_24_out, transistor_25_out,
       transistor_26_out, transistor_27_out, transistor_28_out, transistor_29_out, transistor_30_out,
       transistor_31_out, transistor_32_out, transistor_33_out, transistor_34_out, transistor_35_out,
       transistor_36_out, transistor_37_out, transistor_38_out, transistor_39_out, transistor_40_out,
       transistor_41_out, transistor_42_out, transistor_43_out, transistor_44_out, transistor_45_out,
       transistor_46_out, transistor_47_out, transistor_48_out, transistor_49_out, transistor_50_out,
       transistor_51_out, transistor_52_out, transistor_53_out, transistor_54_out, transistor_55_out,
       transistor_56_out, transistor_57_out, transistor_58_out, transistor_59_out, transistor_60_out,
       transistor_61_out, transistor_62_out, transistor_63_out, transistor_64_out, transistor_65_out,
       transistor_66_out, transistor_67_out, transistor_68_out, transistor_69_out, transistor_70_out,
       transistor_71_out, transistor_72_out, transistor_73_out, transistor_74_out, transistor_75_out,
       transistor_76_out, transistor_77_out, transistor_78_out, transistor_79_out, transistor_80_out,
       transistor_81_out, transistor_82_out, transistor_83_out, transistor_84_out, transistor_85_out,
       transistor_86_out, transistor_87_out, transistor_88_out, transistor_89_out, transistor_90_out,
       transistor_91_out, transistor_92_out, transistor_93_out, transistor_94_out, transistor_95_out,
       transistor_96_out, transistor_97_out, transistor_98_out, transistor_99_out, transistor_100_out,
       transistor_101_out, transistor_102_out, transistor_103_out, transistor_104_out, transistor_105_out,
       transistor_106_out, transistor_107_out, transistor_108_out, transistor_109_out, transistor_110_out,
       transistor_111_out, transistor_112_out, transistor_113_out, transistor_114_out, transistor_115_out,
       transistor_116_out, transistor_117_out, transistor_118_out, transistor_119_out, transistor_120_out,
       transistor_121_out, transistor_122_out, transistor_123_out, transistor_124_out, transistor_125_out,
       transistor_126_out, transistor_127_out, transistor_128_out, transistor_129_out, transistor_130_out,
       transistor_131_out, transistor_132_out, transistor_133_out, transistor_134_out, transistor_135_out,
       transistor_136_out, transistor_137_out, transistor_138_out, transistor_139_out, transistor_140_out,
       transistor_141_out, transistor_142_out, transistor_143_out, transistor_144_out, transistor_145_out,
       transistor_146_out, transistor_147_out, transistor_148_out, transistor_149_out, transistor_150_out,
       transistor_151_out, transistor_152_out, transistor_153_out, transistor_154_out, transistor_155_out,
       transistor_156_out, transistor_157_out, transistor_158_out, transistor_159_out, transistor_160_out,
       transistor_161_out, transistor_162_out, transistor_163_out, transistor_164_out, transistor_165_out,
       transistor_166_out, transistor_167_out, transistor_168_out, transistor_169_out, transistor_170_out,
       transistor_171_out, transistor_172_out, transistor_173_out, transistor_174_out, transistor_175_out,
       transistor_176_out, transistor_177_out, transistor_178_out, transistor_179_out, transistor_180_out,
       transistor_181_out, transistor_182_out, transistor_183_out, transistor_184_out, transistor_185_out,
       transistor_186_out, transistor_187_out, transistor_188_out, transistor_189_out, transistor_190_out,
       transistor_191_out, transistor_192_out, transistor_193_out, transistor_194_out, transistor_195_out,
       transistor_196_out, transistor_197_out, transistor_198_out, transistor_199_out, transistor_200_out,
       transistor_201_out, transistor_202_out, transistor_203_out, transistor_204_out, transistor_205_out,
       transistor_206_out, transistor_207_out, transistor_208_out, transistor_209_out, transistor_210_out,
       transistor_211_out, transistor_212_out, transistor_213_out, transistor_214_out, transistor_215_out,
       transistor_216_out, transistor_217_out, transistor_218_out, transistor_219_out, transistor_220_out,
       transistor_221_out, transistor_222_out, transistor_223_out, transistor_224_out, transistor_225_out,
       transistor_226_out, transistor_227_out, transistor_228_out, transistor_229_out, transistor_230_out,
       transistor_231_out, transistor_232_out, transistor_233_out, transistor_234_out, transistor_235_out,
       transistor_236_out, transistor_237_out, transistor_238_out, transistor_239_out, transistor_240_out,
       transistor_241_out, transistor_242_out, transistor_243_out, transistor_244_out, transistor_245_out,
       transistor_246_out, transistor_247_out, transistor_248_out, transistor_249_out, transistor_250_out,
       transistor_251_out, transistor_252_out, transistor_253_out, transistor_254_out, transistor_255_out,
       transistor_256_out, transistor_257_out, transistor_258_out, transistor_259_out, transistor_260_out,
       transistor_261_out, transistor_262_out, transistor_263_out, transistor_264_out, transistor_265_out,
       transistor_266_out, transistor_267_out, transistor_268_out, transistor_269_out, transistor_270_out,
       transistor_271_out, transistor_272_out, transistor_273_out, transistor_274_out, transistor_275_out,
       transistor_276_out, transistor_277_out, transistor_278_out, transistor_279_out, transistor_280_out,
       transistor_281_out, transistor_282_out, transistor_283_out, transistor_284_out, transistor_285_out,
       transistor_286_out, transistor_287_out, transistor_288_out, transistor_289_out, transistor_290_out,
       transistor_291_out, transistor_292_out, transistor_293_out, transistor_294_out, transistor_295_out,
       transistor_296_out, transistor_297_out, transistor_298_out, transistor_299_out, transistor_300_out,
       transistor_301_out, transistor_302_out, transistor_303_out, transistor_304_out, transistor_305_out,
       transistor_306_out, transistor_307_out, transistor_308_out, transistor_309_out, transistor_310_out,
       transistor_311_out, transistor_312_out, transistor_313_out, transistor_314_out, transistor_315_out,
       transistor_316_out, transistor_317_out, transistor_318_out, transistor_319_out, transistor_320_out,
       transistor_321_out, transistor_322_out, transistor_323_out, transistor_324_out, transistor_325_out,
       transistor_326_out, transistor_327_out, transistor_328_out, transistor_329_out, transistor_330_out,
       transistor_331_out, transistor_332_out, transistor_333_out, transistor_334_out, transistor_335_out,
       transistor_336_out, transistor_337_out, transistor_338_out, transistor_339_out, transistor_340_out,
       transistor_341_out, transistor_342_out, transistor_343_out, transistor_344_out, transistor_345_out,
       transistor_346_out, transistor_347_out, transistor_348_out, transistor_349_out, transistor_350_out,
       transistor_351_out, transistor_352_out, transistor_353_out, transistor_354_out, transistor_355_out,
       transistor_356_out, transistor_357_out, transistor_358_out, transistor_359_out, transistor_360_out,
       transistor_361_out, transistor_362_out, transistor_363_out, transistor_364_out, transistor_365_out,
       transistor_366_out, transistor_367_out, transistor_368_out, transistor_369_out, transistor_370_out,
       transistor_371_out, transistor_372_out, transistor_373_out, transistor_374_out, transistor_375_out,
       transistor_376_out, transistor_377_out, transistor_378_out, transistor_379_out, transistor_380_out,
       transistor_381_out, transistor_382_out, transistor_383_out, transistor_384_out, transistor_385_out,
       transistor_386_out, transistor_387_out, transistor_388_out, transistor_389_out, transistor_390_out,
       transistor_391_out, transistor_392_out, transistor_393_out, transistor_394_out, transistor_395_out,
       transistor_396_out, transistor_397_out, transistor_398_out, transistor_399_out, transistor_400_out,
       transistor_401_out, transistor_402_out, transistor_403_out, transistor_404_out, transistor_405_out,
       transistor_406_out, transistor_407_out, transistor_408_out, transistor_409_out, transistor_410_out,
       transistor_411_out, transistor_412_out, transistor_413_out, transistor_414_out, transistor_415_out,
       transistor_416_out, transistor_417_out, transistor_418_out, transistor_419_out, transistor_420_out,
       transistor_421_out, transistor_422_out, transistor_423_out, transistor_424_out, transistor_425_out,
       transistor_426_out, transistor_427_out, transistor_428_out, transistor_429_out, transistor_430_out,
       transistor_431_out, transistor_432_out, transistor_433_out, transistor_434_out, transistor_435_out,
       transistor_436_out, transistor_437_out, transistor_438_out, transistor_439_out, transistor_440_out,
       transistor_441_out, transistor_442_out, transistor_443_out, transistor_444_out, transistor_445_out,
       transistor_446_out, transistor_447_out, transistor_448_out, transistor_449_out, transistor_450_out,
       transistor_451_out, transistor_452_out, transistor_453_out, transistor_454_out, transistor_455_out,
       transistor_456_out, transistor_457_out, transistor_458_out, transistor_459_out, transistor_460_out,
       transistor_461_out, transistor_462_out, transistor_463_out, transistor_464_out, transistor_465_out,
       transistor_466_out, transistor_467_out, transistor_468_out, transistor_469_out, transistor_470_out,
       transistor_471_out, transistor_472_out, transistor_473_out, transistor_474_out, transistor_475_out,
       transistor_476_out, transistor_477_out, transistor_478_out, transistor_479_out, transistor_480_out,
       transistor_481_out, transistor_482_out, transistor_483_out, transistor_484_out, transistor_485_out,
       transistor_486_out, transistor_487_out, transistor_488_out, transistor_489_out, transistor_490_out,
       transistor_491_out, transistor_492_out, transistor_493_out, transistor_494_out, transistor_495_out,
       transistor_496_out, transistor_497_out, transistor_498_out, transistor_499_out, transistor_500_out,
       transistor_501_out, transistor_502_out, transistor_503_out, transistor_504_out, transistor_505_out,
       transistor_506_out, transistor_507_out, transistor_508_out, transistor_509_out, transistor_510_out,
       transistor_511_out, transistor_512_out, transistor_513_out, transistor_514_out, transistor_515_out,
       transistor_516_out, transistor_517_out, transistor_518_out, transistor_519_out, transistor_520_out,
       transistor_521_out, transistor_522_out, transistor_523_out, transistor_524_out, transistor_525_out,
       transistor_526_out, transistor_527_out, transistor_528_out, transistor_529_out, transistor_530_out,
       transistor_531_out, transistor_532_out, transistor_533_out, transistor_534_out, transistor_535_out,
       transistor_536_out, transistor_537_out, transistor_538_out, transistor_539_out, transistor_540_out,
       transistor_541_out, transistor_542_out, transistor_543_out, transistor_544_out, transistor_545_out,
       transistor_546_out, transistor_547_out, transistor_548_out, transistor_549_out, transistor_550_out,
       transistor_551_out, transistor_552_out, transistor_553_out, transistor_554_out, transistor_555_out,
       transistor_556_out, transistor_557_out, transistor_558_out, transistor_559_out, transistor_560_out,
       transistor_561_out, transistor_562_out, transistor_563_out, transistor_564_out, transistor_565_out,
       transistor_566_out, transistor_567_out, transistor_568_out, transistor_569_out, transistor_570_out,
       transistor_571_out, transistor_572_out, transistor_573_out, transistor_574_out, transistor_575_out,
       transistor_576_out, transistor_577_out, transistor_578_out, transistor_579_out, transistor_580_out,
       transistor_581_out, transistor_582_out, transistor_583_out, transistor_584_out, transistor_585_out,
       transistor_586_out, transistor_587_out, transistor_588_out, transistor_589_out, transistor_590_out,
       transistor_591_out, transistor_592_out, transistor_593_out, transistor_594_out, transistor_595_out,
       transistor_596_out, transistor_597_out, transistor_598_out, transistor_599_out, transistor_600_out,
       transistor_601_out, transistor_602_out, transistor_603_out, transistor_604_out, transistor_605_out,
       transistor_606_out, transistor_607_out, transistor_608_out, transistor_609_out, transistor_610_out,
       transistor_611_out, transistor_612_out, transistor_613_out, transistor_614_out, transistor_615_out,
       transistor_616_out, transistor_617_out, transistor_618_out, transistor_619_out, transistor_620_out,
       transistor_621_out, transistor_622_out, transistor_623_out, transistor_624_out, transistor_625_out,
       transistor_626_out, transistor_627_out, transistor_628_out, transistor_629_out, transistor_630_out,
       transistor_631_out, transistor_632_out, transistor_633_out, transistor_634_out, transistor_635_out,
       transistor_636_out, transistor_637_out, transistor_638_out, transistor_639_out, transistor_640_out,
       transistor_641_out, transistor_642_out, transistor_643_out, transistor_644_out, transistor_645_out,
       transistor_646_out, transistor_647_out, transistor_648_out, transistor_649_out, transistor_650_out,
       transistor_651_out, transistor_652_out, transistor_653_out, transistor_654_out, transistor_655_out,
       transistor_656_out, transistor_657_out, transistor_658_out, transistor_659_out, transistor_660_out,
       transistor_661_out, transistor_662_out, transistor_663_out, transistor_664_out, transistor_665_out,
       transistor_666_out, transistor_667_out, transistor_668_out, transistor_669_out, transistor_670_out,
       transistor_671_out, transistor_672_out, transistor_673_out, transistor_674_out, transistor_675_out,
       transistor_676_out, transistor_677_out, transistor_678_out, transistor_679_out, transistor_680_out,
       transistor_681_out, transistor_682_out, transistor_683_out, transistor_684_out, transistor_685_out,
       transistor_686_out, transistor_687_out, transistor_688_out, transistor_689_out, transistor_690_out,
       transistor_691_out, transistor_692_out, transistor_693_out, transistor_694_out, transistor_695_out,
       transistor_696_out, transistor_697_out, transistor_698_out, transistor_699_out, transistor_700_out,
       transistor_701_out, transistor_702_out, transistor_703_out, transistor_704_out, transistor_705_out,
       transistor_706_out, transistor_707_out, transistor_708_out, transistor_709_out, transistor_710_out,
       transistor_711_out, transistor_712_out, transistor_713_out, transistor_714_out, transistor_715_out,
       transistor_716_out, transistor_717_out, transistor_718_out, transistor_719_out, transistor_720_out,
       transistor_721_out, transistor_722_out, transistor_723_out, transistor_724_out, transistor_725_out,
       transistor_726_out, transistor_727_out, transistor_728_out, transistor_729_out, transistor_730_out,
       transistor_731_out, transistor_732_out, transistor_733_out, transistor_734_out, transistor_735_out,
       transistor_736_out, transistor_737_out, transistor_738_out, transistor_739_out, transistor_740_out,
       transistor_741_out, transistor_742_out, transistor_743_out, transistor_744_out, transistor_745_out,
       transistor_746_out, transistor_747_out, transistor_748_out, transistor_749_out, transistor_750_out,
       transistor_751_out, transistor_752_out, transistor_753_out, transistor_754_out, transistor_755_out,
       transistor_756_out, transistor_757_out, transistor_758_out, transistor_759_out, transistor_760_out,
       transistor_761_out, transistor_762_out, transistor_763_out, transistor_764_out, transistor_765_out,
       transistor_766_out, transistor_767_out, transistor_768_out, transistor_769_out, transistor_770_out,
       transistor_771_out, transistor_772_out, transistor_773_out, transistor_774_out, transistor_775_out,
       transistor_776_out, transistor_777_out, transistor_778_out, transistor_779_out, transistor_780_out,
       transistor_781_out, transistor_782_out, transistor_783_out, transistor_784_out, transistor_785_out,
       transistor_786_out, transistor_787_out, transistor_788_out, transistor_789_out, transistor_790_out,
       transistor_791_out, transistor_792_out, transistor_793_out, transistor_794_out, transistor_795_out,
       transistor_796_out, transistor_797_out, transistor_798_out, transistor_799_out, transistor_800_out,
       transistor_801_out, transistor_802_out, transistor_803_out, transistor_804_out, transistor_805_out,
       transistor_806_out, transistor_807_out, transistor_808_out, transistor_809_out, transistor_810_out,
       transistor_811_out, transistor_812_out, transistor_813_out, transistor_814_out, transistor_815_out,
       transistor_816_out, transistor_817_out, transistor_818_out, transistor_819_out, transistor_820_out,
       transistor_821_out, transistor_822_out, transistor_823_out, transistor_824_out, transistor_825_out,
       transistor_826_out, transistor_827_out, transistor_828_out, transistor_829_out, transistor_830_out,
       transistor_831_out, transistor_832_out, transistor_833_out, transistor_834_out, transistor_835_out,
       transistor_836_out, transistor_837_out, transistor_838_out, transistor_839_out, transistor_840_out,
       transistor_841_out, transistor_842_out, transistor_843_out, transistor_844_out, transistor_845_out,
       transistor_846_out, transistor_847_out, transistor_848_out, transistor_849_out, transistor_850_out,
       transistor_851_out, transistor_852_out, transistor_853_out, transistor_854_out, transistor_855_out,
       transistor_856_out, transistor_857_out, transistor_858_out, transistor_859_out, transistor_860_out,
       transistor_861_out, transistor_862_out, transistor_863_out, transistor_864_out, transistor_865_out,
       transistor_866_out, transistor_867_out, transistor_868_out, transistor_869_out, transistor_870_out,
       transistor_871_out, transistor_872_out, transistor_873_out, transistor_874_out, transistor_875_out,
       transistor_876_out, transistor_877_out, transistor_878_out, transistor_879_out, transistor_880_out,
       transistor_881_out, transistor_882_out, transistor_883_out, transistor_884_out, transistor_885_out,
       transistor_886_out, transistor_887_out, transistor_888_out, transistor_889_out, transistor_890_out,
       transistor_891_out, transistor_892_out, transistor_893_out, transistor_894_out, transistor_895_out,
       transistor_896_out, transistor_897_out, transistor_898_out, transistor_899_out, transistor_900_out,
       transistor_901_out, transistor_902_out, transistor_903_out, transistor_904_out, transistor_905_out,
       transistor_906_out, transistor_907_out, transistor_908_out, transistor_909_out, transistor_910_out,
       transistor_911_out, transistor_912_out, transistor_913_out, transistor_914_out, transistor_915_out,
       transistor_916_out, transistor_917_out, transistor_918_out, transistor_919_out, transistor_920_out,
       transistor_921_out, transistor_922_out, transistor_923_out, transistor_924_out, transistor_925_out,
       transistor_926_out, transistor_927_out, transistor_928_out, transistor_929_out, transistor_930_out,
       transistor_931_out, transistor_932_out, transistor_933_out, transistor_934_out, transistor_935_out,
       transistor_936_out, transistor_937_out, transistor_938_out, transistor_939_out, transistor_940_out,
       transistor_941_out, transistor_942_out, transistor_943_out, transistor_944_out, transistor_945_out,
       transistor_946_out, transistor_947_out, transistor_948_out, transistor_949_out, transistor_950_out,
       transistor_951_out, transistor_952_out, transistor_953_out, transistor_954_out, transistor_955_out,
       transistor_956_out, transistor_957_out, transistor_958_out, transistor_959_out, transistor_960_out,
       transistor_961_out, transistor_962_out, transistor_963_out, transistor_964_out, transistor_965_out,
       transistor_966_out, transistor_967_out, transistor_968_out, transistor_969_out, transistor_970_out,
       transistor_971_out, transistor_972_out, transistor_973_out, transistor_974_out, transistor_975_out,
       transistor_976_out, transistor_977_out, transistor_978_out, transistor_979_out, transistor_980_out,
       transistor_981_out, transistor_982_out, transistor_983_out, transistor_984_out, transistor_985_out,
       transistor_986_out, transistor_987_out, transistor_988_out, transistor_989_out, transistor_990_out,
       transistor_991_out, transistor_992_out, transistor_993_out, transistor_994_out, transistor_995_out,
       transistor_996_out, transistor_997_out, transistor_998_out, transistor_999_out, transistor_1000_out,
       transistor_1001_out, transistor_1002_out, transistor_1003_out, transistor_1004_out,
       transistor_1005_out, transistor_1006_out, transistor_1007_out, transistor_1008_out,
       transistor_1009_out, transistor_1010_out, transistor_1011_out, transistor_1012_out,
       transistor_1013_out, transistor_1014_out, transistor_1015_out, transistor_1016_out,
       transistor_1017_out, transistor_1018_out, transistor_1019_out, transistor_1020_out,
       transistor_1021_out, transistor_1022_out, transistor_1023_out, transistor_1024_out,
       transistor_1025_out, transistor_1026_out, transistor_1027_out, transistor_1028_out,
       transistor_1029_out, transistor_1030_out, transistor_1031_out, transistor_1032_out,
       transistor_1033_out, transistor_1034_out, transistor_1035_out, transistor_1036_out,
       transistor_1037_out, transistor_1038_out, transistor_1039_out, transistor_1040_out,
       transistor_1041_out, transistor_1042_out, transistor_1043_out, transistor_1044_out,
       transistor_1045_out, transistor_1046_out, transistor_1047_out, transistor_1048_out,
       transistor_1049_out, transistor_1050_out, transistor_1051_out, transistor_1052_out,
       transistor_1053_out, transistor_1054_out, transistor_1055_out, transistor_1056_out,
       transistor_1057_out, transistor_1058_out, transistor_1059_out, transistor_1060_out,
       transistor_1061_out, transistor_1062_out, transistor_1063_out, transistor_1064_out,
       transistor_1065_out, transistor_1066_out, transistor_1067_out, transistor_1068_out,
       transistor_1069_out, transistor_1070_out, transistor_1071_out, transistor_1072_out,
       transistor_1073_out, transistor_1074_out, transistor_1075_out, transistor_1076_out,
       transistor_1077_out, transistor_1078_out, transistor_1079_out, transistor_1080_out,
       transistor_1081_out, transistor_1082_out, transistor_1083_out, transistor_1084_out,
       transistor_1085_out, transistor_1086_out, transistor_1087_out, transistor_1088_out,
       transistor_1089_out, transistor_1090_out, transistor_1091_out, transistor_1092_out,
       transistor_1093_out, transistor_1094_out, transistor_1095_out, transistor_1096_out,
       transistor_1097_out, transistor_1098_out, transistor_1099_out, transistor_1100_out,
       transistor_1101_out, transistor_1102_out, transistor_1103_out, transistor_1104_out,
       transistor_1105_out, transistor_1106_out, transistor_1107_out, transistor_1108_out,
       transistor_1109_out, transistor_1110_out, transistor_1111_out, transistor_1112_out,
       transistor_1113_out, transistor_1114_out, transistor_1115_out, transistor_1116_out,
       transistor_1117_out, transistor_1118_out, transistor_1119_out, transistor_1120_out,
       transistor_1121_out, transistor_1122_out, transistor_1123_out, transistor_1124_out,
       transistor_1125_out, transistor_1126_out, transistor_1127_out, transistor_1128_out,
       transistor_1129_out, transistor_1130_out, transistor_1131_out, transistor_1132_out,
       transistor_1133_out, transistor_1134_out, transistor_1135_out, transistor_1136_out,
       transistor_1137_out, transistor_1138_out, transistor_1139_out, transistor_1140_out,
       transistor_1141_out, transistor_1142_out, transistor_1143_out, transistor_1144_out,
       transistor_1145_out, transistor_1146_out, transistor_1147_out, transistor_1148_out,
       transistor_1149_out, transistor_1150_out, transistor_1151_out, transistor_1152_out,
       transistor_1153_out, transistor_1154_out, transistor_1155_out, transistor_1156_out,
       transistor_1157_out, transistor_1158_out, transistor_1159_out, transistor_1160_out,
       transistor_1161_out, transistor_1162_out, transistor_1163_out, transistor_1164_out,
       transistor_1165_out, transistor_1166_out, transistor_1167_out, transistor_1168_out,
       transistor_1169_out, transistor_1170_out, transistor_1171_out, transistor_1172_out,
       transistor_1173_out, transistor_1174_out, transistor_1175_out, transistor_1176_out,
       transistor_1177_out, transistor_1178_out, transistor_1179_out, transistor_1180_out,
       transistor_1181_out, transistor_1182_out, transistor_1183_out, transistor_1184_out,
       transistor_1185_out, transistor_1186_out, transistor_1187_out, transistor_1188_out,
       transistor_1189_out, transistor_1190_out, transistor_1191_out, transistor_1192_out,
       transistor_1193_out, transistor_1194_out, transistor_1195_out, transistor_1196_out,
       transistor_1197_out, transistor_1198_out, transistor_1199_out, transistor_1200_out,
       transistor_1201_out, transistor_1202_out, transistor_1203_out, transistor_1204_out,
       transistor_1205_out, transistor_1206_out, transistor_1207_out, transistor_1208_out,
       transistor_1209_out, transistor_1210_out, transistor_1211_out, transistor_1212_out,
       transistor_1213_out, transistor_1214_out, transistor_1215_out, transistor_1216_out,
       transistor_1217_out, transistor_1218_out, transistor_1219_out, transistor_1220_out,
       transistor_1221_out, transistor_1222_out, transistor_1223_out, transistor_1224_out,
       transistor_1225_out, transistor_1226_out, transistor_1227_out, transistor_1228_out,
       transistor_1229_out, transistor_1230_out, transistor_1231_out, transistor_1232_out,
       transistor_1233_out, transistor_1234_out, transistor_1235_out, transistor_1236_out,
       transistor_1237_out, transistor_1238_out, transistor_1239_out, transistor_1240_out,
       transistor_1241_out, transistor_1242_out, transistor_1243_out, transistor_1244_out,
       transistor_1245_out, transistor_1246_out, transistor_1247_out, transistor_1248_out,
       transistor_1249_out, transistor_1250_out, transistor_1251_out, transistor_1252_out,
       transistor_1253_out, transistor_1254_out, transistor_1255_out, transistor_1256_out,
       transistor_1257_out, transistor_1258_out, transistor_1259_out, transistor_1260_out,
       transistor_1261_out, transistor_1262_out, transistor_1263_out, transistor_1264_out,
       transistor_1265_out, transistor_1266_out, transistor_1267_out, transistor_1268_out,
       transistor_1269_out, transistor_1270_out, transistor_1271_out, transistor_1272_out,
       transistor_1273_out, transistor_1274_out, transistor_1275_out, transistor_1276_out,
       transistor_1277_out, transistor_1278_out, transistor_1279_out, transistor_1280_out,
       transistor_1281_out, transistor_1282_out, transistor_1283_out, transistor_1284_out,
       transistor_1285_out, transistor_1286_out, transistor_1287_out, transistor_1288_out,
       transistor_1289_out, transistor_1290_out, transistor_1291_out, transistor_1292_out,
       transistor_1293_out, transistor_1294_out, transistor_1295_out, transistor_1296_out,
       transistor_1297_out, transistor_1298_out, transistor_1299_out, transistor_1300_out,
       transistor_1301_out, transistor_1302_out, transistor_1303_out, transistor_1304_out,
       transistor_1305_out, transistor_1306_out, transistor_1307_out, transistor_1308_out,
       transistor_1309_out, transistor_1310_out, transistor_1311_out, transistor_1312_out,
       transistor_1313_out, transistor_1314_out, transistor_1315_out, transistor_1316_out,
       transistor_1317_out, transistor_1318_out, transistor_1319_out, transistor_1320_out,
       transistor_1321_out, transistor_1322_out, transistor_1323_out, transistor_1324_out,
       transistor_1325_out, transistor_1326_out, transistor_1327_out, transistor_1328_out,
       transistor_1329_out, transistor_1330_out, transistor_1331_out, transistor_1332_out,
       transistor_1333_out, transistor_1334_out, transistor_1335_out, transistor_1336_out,
       transistor_1337_out, transistor_1338_out, transistor_1339_out, transistor_1340_out,
       transistor_1341_out, transistor_1342_out, transistor_1343_out, transistor_1344_out,
       transistor_1345_out, transistor_1346_out, transistor_1347_out, transistor_1348_out,
       transistor_1349_out, transistor_1350_out, transistor_1351_out, transistor_1352_out,
       transistor_1353_out, transistor_1354_out, transistor_1355_out, transistor_1356_out,
       transistor_1357_out, transistor_1358_out, transistor_1359_out, transistor_1360_out,
       transistor_1361_out, transistor_1362_out, transistor_1363_out, transistor_1364_out,
       transistor_1365_out, transistor_1366_out, transistor_1367_out, transistor_1368_out,
       transistor_1369_out, transistor_1370_out, transistor_1371_out, transistor_1372_out,
       transistor_1373_out, transistor_1374_out, transistor_1375_out, transistor_1376_out,
       transistor_1377_out, transistor_1378_out, transistor_1379_out, transistor_1380_out,
       transistor_1381_out, transistor_1382_out, transistor_1383_out, transistor_1384_out,
       transistor_1385_out, transistor_1386_out, transistor_1387_out, transistor_1388_out,
       transistor_1389_out, transistor_1390_out, transistor_1391_out, transistor_1392_out,
       transistor_1393_out, transistor_1394_out, transistor_1395_out, transistor_1396_out,
       transistor_1397_out, transistor_1398_out, transistor_1399_out, transistor_1400_out,
       transistor_1401_out, transistor_1402_out, transistor_1403_out, transistor_1404_out,
       transistor_1405_out, transistor_1406_out, transistor_1407_out, transistor_1408_out,
       transistor_1409_out, transistor_1410_out, transistor_1411_out, transistor_1412_out;

  Transistor #(.\type ("n")) transistor_1 (.in(1'b0), .out(transistor_1_out), .gate(clk2_inv));
  Transistor #(.\type ("n")) transistor_2 (.in(1'b0), .out(transistor_2_out), .gate(clk2_inv));
  Transistor #(.\type ("n")) transistor_3 (.in(1'b0), .out(transistor_3_out), .gate(clk2_inv));
  Transistor #(.\type ("n")) transistor_4 (.in(1'b0), .out(transistor_4_out), .gate(clk2_inv));
  Transistor #(.\type ("n")) transistor_5 (.in(1'b0), .out(transistor_5_out), .gate(clk2_inv));
  Transistor #(.\type ("n")) transistor_6 (.in(1'b0), .out(transistor_6_out), .gate(clk2_inv));
  Transistor #(.\type ("n")) transistor_7 (.in(1'b0), .out(transistor_7_out), .gate(clk2_inv));
  Transistor #(.\type ("n")) transistor_8 (.in(1'b0), .out(transistor_8_out), .gate(clk2_inv));
  Transistor #(.\type ("n")) transistor_9 (.in(1'b0), .out(transistor_9_out), .gate(clk2_inv));
  Transistor #(.\type ("n")) transistor_10 (.in(1'b0), .out(transistor_10_out), .gate(clk2_inv));
  Transistor #(.\type ("n")) transistor_11 (.in(1'b0), .out(transistor_11_out), .gate(clk2_inv));
  Transistor #(.\type ("n")) transistor_12 (.in(1'b0), .out(transistor_12_out), .gate(clk2_inv));
  Transistor #(.\type ("n")) transistor_13 (.in(1'b0), .out(transistor_13_out), .gate(clk2_inv));
  Transistor #(.\type ("n")) transistor_14 (.in(1'b0), .out(transistor_14_out), .gate(clk2_inv));
  Transistor #(.\type ("n")) transistor_15 (.in(1'b0), .out(transistor_15_out), .gate(clk2_inv));
  Transistor #(.\type ("n")) transistor_16 (.in(1'b0), .out(transistor_16_out), .gate(clk2_inv));
  Transistor #(.\type ("n")) transistor_17 (.in(1'b0), .out(transistor_17_out), .gate(clk2_inv));
  Transistor #(.\type ("n")) transistor_18 (.in(1'b0), .out(transistor_18_out), .gate(clk2_inv));
  Transistor #(.\type ("n")) transistor_19 (.in(1'b0), .out(transistor_19_out), .gate(clk2_inv));
  Transistor #(.\type ("n")) transistor_20 (.in(1'b0), .out(transistor_20_out), .gate(clk2_inv));
  Transistor #(.\type ("n")) transistor_21 (.in(1'b0), .out(transistor_21_out), .gate(clk2_inv));
  Transistor #(.\type ("n")) transistor_22 (.in(1'b0), .out(transistor_22_out), .gate(clk2_inv));
  Transistor #(.\type ("n")) transistor_23 (.in(1'b0), .out(transistor_23_out), .gate(clk2_inv));
  Transistor #(.\type ("n")) transistor_24 (.in(1'b0), .out(transistor_24_out), .gate(clk2_inv));
  Transistor #(.\type ("n")) transistor_25 (.in(1'b0), .out(transistor_25_out), .gate(clk2_inv));
  Transistor #(.\type ("n")) transistor_26 (.in(1'b0), .out(transistor_26_out), .gate(clk2_inv));
  Transistor #(.\type ("n")) transistor_27 (.in(1'b0), .out(transistor_27_out), .gate(clk2_inv));
  Transistor #(.\type ("n")) transistor_28 (.in(1'b0), .out(transistor_28_out), .gate(clk2_inv));
  Transistor #(.\type ("n")) transistor_29 (.in(1'b0), .out(transistor_29_out), .gate(clk2_inv));
  Transistor #(.\type ("n")) transistor_30 (.in(1'b0), .out(transistor_30_out), .gate(clk2_inv));
  Transistor #(.\type ("n")) transistor_31 (.in(1'b0), .out(transistor_31_out), .gate(clk2_inv));
  Transistor #(.\type ("n")) transistor_32 (.in(1'b0), .out(transistor_32_out), .gate(clk2_inv));
  Transistor #(.\type ("n")) transistor_33 (.in(1'b0), .out(transistor_33_out), .gate(clk2_inv));
  Transistor #(.\type ("n")) transistor_34 (.in(1'b0), .out(transistor_34_out), .gate(clk2_inv));
  Transistor #(.\type ("n")) transistor_35 (.in(1'b0), .out(transistor_35_out), .gate(clk2_inv));
  Transistor #(.\type ("n")) transistor_36 (.in(1'b0), .out(transistor_36_out), .gate(clk2_inv));
  Transistor #(.\type ("n")) transistor_37 (.in(1'b0), .out(transistor_37_out), .gate(clk2_inv));
  Transistor #(.\type ("n")) transistor_38 (.in(1'b0), .out(transistor_38_out), .gate(clk2_inv));
  Transistor #(.\type ("n")) transistor_39 (.in(1'b0), .out(transistor_39_out), .gate(clk2_inv));
  Transistor #(.\type ("n")) transistor_40 (.in(1'b0), .out(transistor_40_out), .gate(clk2_inv));
  Transistor #(.\type ("n")) transistor_41 (.in(1'b0), .out(transistor_41_out), .gate(clk2_inv));
  Transistor #(.\type ("n")) transistor_42 (.in(1'b0), .out(transistor_42_out), .gate(clk2_inv));
  Transistor #(.\type ("n")) transistor_43 (.in(1'b0), .out(transistor_43_out), .gate(clk2_inv));
  Transistor #(.\type ("n")) transistor_44 (.in(1'b0), .out(transistor_44_out), .gate(clk2_inv));
  Transistor #(.\type ("n")) transistor_45 (.in(1'b0), .out(transistor_45_out), .gate(clk2_inv));
  Transistor #(.\type ("n")) transistor_46 (.in(1'b0), .out(transistor_46_out), .gate(clk2_inv));
  Transistor #(.\type ("n")) transistor_47 (.in(1'b0), .out(transistor_47_out), .gate(clk2_inv));
  Transistor #(.\type ("n")) transistor_48 (.in(1'b0), .out(transistor_48_out), .gate(clk2_inv));
  Transistor #(.\type ("n")) transistor_49 (.in(1'b0), .out(transistor_49_out), .gate(clk2_inv));
  Transistor #(.\type ("n")) transistor_50 (.in(1'b0), .out(transistor_50_out), .gate(clk2_inv));
  Transistor #(.\type ("n")) transistor_51 (.in(1'b0), .out(transistor_51_out), .gate(clk2_inv));
  Transistor #(.\type ("n")) transistor_52 (.in(1'b0), .out(transistor_52_out), .gate(clk2_inv));
  Transistor #(.\type ("n")) transistor_53 (.in(1'b0), .out(transistor_53_out), .gate(clk2_inv));
  Transistor #(.\type ("n")) transistor_54 (.in(1'b0), .out(transistor_54_out), .gate(clk2_inv));
  Transistor #(.\type ("n")) transistor_55 (.in(1'b0), .out(transistor_55_out), .gate(clk2_inv));
  Transistor #(.\type ("n")) transistor_56 (.in(1'b0), .out(transistor_56_out), .gate(clk2_inv));
  Transistor #(.\type ("n")) transistor_57 (.in(1'b0), .out(transistor_57_out), .gate(clk2_inv));
  Transistor #(.\type ("n")) transistor_58 (.in(1'b0), .out(transistor_58_out), .gate(clk2_inv));
  Transistor #(.\type ("n")) transistor_59 (.in(1'b0), .out(transistor_59_out), .gate(clk2_inv));
  Transistor #(.\type ("n")) transistor_60 (.in(1'b0), .out(transistor_60_out), .gate(clk2_inv));
  Transistor #(.\type ("n")) transistor_61 (.in(1'b0), .out(transistor_61_out), .gate(clk2_inv));
  Transistor #(.\type ("n")) transistor_62 (.in(1'b0), .out(transistor_62_out), .gate(clk2_inv));
  Transistor #(.\type ("n")) transistor_63 (.in(1'b0), .out(transistor_63_out), .gate(clk2_inv));
  Transistor #(.\type ("n")) transistor_64 (.in(transistor_1_out), .out(transistor_64_out), .gate(instr_sel[20]));
  Transistor #(.\type ("n")) transistor_65 (.in(transistor_2_out), .out(transistor_65_out), .gate(instr_sel[20]));
  Transistor #(.\type ("n")) transistor_66 (.in(transistor_3_out), .out(transistor_66_out), .gate(instr_sel[20]));
  Transistor #(.\type ("n")) transistor_67 (.in(transistor_4_out), .out(transistor_67_out), .gate(instr_sel[20]));
  Transistor #(.\type ("n")) transistor_68 (.in(transistor_5_out), .out(transistor_68_out), .gate(instr_sel[20]));
  Transistor #(.\type ("n")) transistor_69 (.in(transistor_6_out), .out(transistor_69_out), .gate(instr_sel[20]));
  Transistor #(.\type ("n")) transistor_70 (.in(transistor_7_out), .out(transistor_70_out), .gate(instr_sel[20]));
  Transistor #(.\type ("n")) transistor_71 (.in(transistor_8_out), .out(transistor_71_out), .gate(instr_sel[20]));
  Transistor #(.\type ("n")) transistor_72 (.in(transistor_9_out), .out(transistor_72_out), .gate(instr_sel[20]));
  Transistor #(.\type ("n")) transistor_73 (.in(transistor_10_out), .out(transistor_73_out), .gate(instr_sel[20]));
  Transistor #(.\type ("n")) transistor_74 (.in(transistor_11_out), .out(transistor_74_out), .gate(instr_sel[20]));
  Transistor #(.\type ("n")) transistor_75 (.in(transistor_12_out), .out(transistor_75_out), .gate(instr_sel[20]));
  Transistor #(.\type ("n")) transistor_76 (.in(transistor_13_out), .out(transistor_76_out), .gate(instr_sel[20]));
  Transistor #(.\type ("n")) transistor_77 (.in(transistor_14_out), .out(transistor_77_out), .gate(instr_sel[20]));
  Transistor #(.\type ("n")) transistor_78 (.in(transistor_15_out), .out(transistor_78_out), .gate(instr_sel[20]));
  Transistor #(.\type ("n")) transistor_79 (.in(transistor_16_out), .out(transistor_79_out), .gate(instr_sel[20]));
  Transistor #(.\type ("n")) transistor_80 (.in(transistor_17_out), .out(transistor_80_out), .gate(instr_sel[20]));
  Transistor #(.\type ("n")) transistor_81 (.in(transistor_18_out), .out(transistor_81_out), .gate(instr_sel[20]));
  Transistor #(.\type ("n")) transistor_82 (.in(transistor_19_out), .out(transistor_82_out), .gate(instr_sel[20]));
  Transistor #(.\type ("n")) transistor_83 (.in(transistor_20_out), .out(transistor_83_out), .gate(instr_sel[20]));
  Transistor #(.\type ("n")) transistor_84 (.in(transistor_21_out), .out(transistor_84_out), .gate(instr_sel[20]));
  Transistor #(.\type ("n")) transistor_85 (.in(transistor_22_out), .out(transistor_85_out), .gate(instr_sel[20]));
  Transistor #(.\type ("n")) transistor_86 (.in(transistor_23_out), .out(transistor_86_out), .gate(instr_sel[20]));
  Transistor #(.\type ("n")) transistor_87 (.in(transistor_24_out), .out(transistor_87_out), .gate(instr_sel[20]));
  Transistor #(.\type ("n")) transistor_88 (.in(transistor_25_out), .out(transistor_88_out), .gate(instr_sel[20]));
  Transistor #(.\type ("n")) transistor_89 (.in(transistor_26_out), .out(transistor_89_out), .gate(instr_sel[20]));
  Transistor #(.\type ("n")) transistor_90 (.in(transistor_27_out), .out(transistor_90_out), .gate(instr_sel[20]));
  Transistor #(.\type ("n")) transistor_91 (.in(transistor_28_out), .out(transistor_91_out), .gate(instr_sel[20]));
  Transistor #(.\type ("n")) transistor_92 (.in(transistor_29_out), .out(transistor_92_out), .gate(instr_sel[20]));
  Transistor #(.\type ("n")) transistor_93 (.in(transistor_30_out), .out(transistor_93_out), .gate(instr_sel[20]));
  Transistor #(.\type ("n")) transistor_94 (.in(transistor_31_out), .out(transistor_94_out), .gate(instr_sel[20]));
  Transistor #(.\type ("n")) transistor_95 (.in(transistor_32_out), .out(transistor_95_out), .gate(instr_sel[20]));
  Transistor #(.\type ("n")) transistor_96 (.in(transistor_33_out), .out(transistor_96_out), .gate(instr_sel[20]));
  Transistor #(.\type ("n")) transistor_97 (.in(transistor_34_out), .out(transistor_97_out), .gate(instr_sel[20]));
  Transistor #(.\type ("n")) transistor_98 (.in(transistor_35_out), .out(transistor_98_out), .gate(instr_sel[20]));
  Transistor #(.\type ("n")) transistor_99 (.in(transistor_36_out), .out(transistor_99_out), .gate(instr_sel[20]));
  Transistor #(.\type ("n")) transistor_100 (.in(transistor_37_out), .out(transistor_100_out), .gate(instr_sel[20]));
  Transistor #(.\type ("n")) transistor_101 (.in(transistor_38_out), .out(transistor_101_out), .gate(instr_sel[20]));
  Transistor #(.\type ("n")) transistor_102 (.in(transistor_39_out), .out(transistor_102_out), .gate(instr_sel[20]));
  Transistor #(.\type ("n")) transistor_103 (.in(transistor_40_out), .out(transistor_103_out), .gate(instr_sel[20]));
  Transistor #(.\type ("n")) transistor_104 (.in(transistor_41_out), .out(transistor_104_out), .gate(instr_sel[20]));
  Transistor #(.\type ("n")) transistor_105 (.in(transistor_42_out), .out(transistor_105_out), .gate(instr_sel[20]));
  Transistor #(.\type ("n")) transistor_106 (.in(transistor_43_out), .out(transistor_106_out), .gate(instr_sel[20]));
  Transistor #(.\type ("n")) transistor_107 (.in(transistor_44_out), .out(transistor_107_out), .gate(instr_sel[20]));
  Transistor #(.\type ("n")) transistor_108 (.in(transistor_45_out), .out(transistor_108_out), .gate(instr_sel[20]));
  Transistor #(.\type ("n")) transistor_109 (.in(transistor_46_out), .out(transistor_109_out), .gate(instr_sel[20]));
  Transistor #(.\type ("n")) transistor_110 (.in(transistor_47_out), .out(transistor_110_out), .gate(instr_sel[20]));
  Transistor #(.\type ("n")) transistor_111 (.in(transistor_48_out), .out(transistor_111_out), .gate(instr_sel[20]));
  Transistor #(.\type ("n")) transistor_112 (.in(transistor_49_out), .out(transistor_112_out), .gate(instr_sel[20]));
  Transistor #(.\type ("n")) transistor_113 (.in(transistor_50_out), .out(transistor_113_out), .gate(instr_sel[20]));
  Transistor #(.\type ("n")) transistor_114 (.in(transistor_51_out), .out(transistor_114_out), .gate(instr_sel[20]));
  Transistor #(.\type ("n")) transistor_115 (.in(transistor_52_out), .out(transistor_115_out), .gate(instr_sel[20]));
  Transistor #(.\type ("n")) transistor_116 (.in(transistor_53_out), .out(transistor_116_out), .gate(instr_sel[20]));
  Transistor #(.\type ("n")) transistor_117 (.in(transistor_54_out), .out(transistor_117_out), .gate(instr_sel[20]));
  Transistor #(.\type ("n")) transistor_118 (.in(transistor_55_out), .out(transistor_118_out), .gate(instr_sel[20]));
  Transistor #(.\type ("n")) transistor_119 (.in(transistor_56_out), .out(transistor_119_out), .gate(instr_sel[20]));
  Transistor #(.\type ("n")) transistor_120 (.in(transistor_57_out), .out(transistor_120_out), .gate(instr_sel[20]));
  Transistor #(.\type ("n")) transistor_121 (.in(transistor_58_out), .out(transistor_121_out), .gate(instr_sel[20]));
  Transistor #(.\type ("n")) transistor_122 (.in(transistor_59_out), .out(transistor_122_out), .gate(instr_sel[20]));
  Transistor #(.\type ("n")) transistor_123 (.in(transistor_60_out), .out(transistor_123_out), .gate(instr_sel[20]));
  Transistor #(.\type ("n")) transistor_124 (.in(transistor_61_out), .out(transistor_124_out), .gate(instr_sel[20]));
  Transistor #(.\type ("n")) transistor_125 (.in(transistor_62_out), .out(transistor_125_out), .gate(instr_sel[20]));
  Transistor #(.\type ("n")) transistor_126 (.in(transistor_63_out), .out(transistor_126_out), .gate(instr_sel[20]));
  Transistor #(.\type ("n")) transistor_127 (.in(transistor_64_out), .out(transistor_127_out), .gate(instr_sel[19]));
  Transistor #(.\type ("n")) transistor_128 (.in(transistor_65_out), .out(transistor_128_out), .gate(instr_sel[19]));
  Transistor #(.\type ("n")) transistor_129 (.in(transistor_66_out), .out(transistor_129_out), .gate(instr_sel[19]));
  Transistor #(.\type ("n")) transistor_130 (.in(transistor_67_out), .out(transistor_130_out), .gate(instr_sel[19]));
  Transistor #(.\type ("n")) transistor_131 (.in(transistor_68_out), .out(transistor_131_out), .gate(instr_sel[19]));
  Transistor #(.\type ("n")) transistor_132 (.in(transistor_69_out), .out(transistor_132_out), .gate(instr_sel[19]));
  Transistor #(.\type ("n")) transistor_133 (.in(transistor_70_out), .out(transistor_133_out), .gate(instr_sel[19]));
  Transistor #(.\type ("n")) transistor_134 (.in(transistor_71_out), .out(transistor_134_out), .gate(instr_sel[19]));
  Transistor #(.\type ("n")) transistor_135 (.in(transistor_72_out), .out(transistor_135_out), .gate(instr_sel[19]));
  Transistor #(.\type ("n")) transistor_136 (.in(transistor_73_out), .out(transistor_136_out), .gate(instr_sel[19]));
  Transistor #(.\type ("n")) transistor_137 (.in(transistor_74_out), .out(transistor_137_out), .gate(instr_sel[19]));
  Transistor #(.\type ("n")) transistor_138 (.in(transistor_75_out), .out(transistor_138_out), .gate(instr_sel[19]));
  Transistor #(.\type ("n")) transistor_139 (.in(transistor_76_out), .out(transistor_139_out), .gate(instr_sel[19]));
  Transistor #(.\type ("n")) transistor_140 (.in(transistor_77_out), .out(transistor_140_out), .gate(instr_sel[19]));
  Transistor #(.\type ("n")) transistor_141 (.in(transistor_78_out), .out(transistor_141_out), .gate(instr_sel[19]));
  Transistor #(.\type ("n")) transistor_142 (.in(transistor_79_out), .out(transistor_142_out), .gate(instr_sel[19]));
  Transistor #(.\type ("n")) transistor_143 (.in(transistor_80_out), .out(transistor_143_out), .gate(instr_sel[19]));
  Transistor #(.\type ("n")) transistor_144 (.in(transistor_81_out), .out(transistor_144_out), .gate(instr_sel[19]));
  Transistor #(.\type ("n")) transistor_145 (.in(transistor_82_out), .out(transistor_145_out), .gate(instr_sel[19]));
  Transistor #(.\type ("n")) transistor_146 (.in(transistor_83_out), .out(transistor_146_out), .gate(instr_sel[19]));
  Transistor #(.\type ("n")) transistor_147 (.in(transistor_84_out), .out(transistor_147_out), .gate(instr_sel[19]));
  Transistor #(.\type ("n")) transistor_148 (.in(transistor_85_out), .out(transistor_148_out), .gate(instr_sel[19]));
  Transistor #(.\type ("n")) transistor_149 (.in(transistor_86_out), .out(transistor_149_out), .gate(instr_sel[19]));
  Transistor #(.\type ("n")) transistor_150 (.in(transistor_87_out), .out(transistor_150_out), .gate(instr_sel[19]));
  Transistor #(.\type ("n")) transistor_151 (.in(transistor_88_out), .out(transistor_151_out), .gate(instr_sel[19]));
  Transistor #(.\type ("n")) transistor_152 (.in(transistor_89_out), .out(transistor_152_out), .gate(instr_sel[19]));
  Transistor #(.\type ("n")) transistor_153 (.in(transistor_90_out), .out(transistor_153_out), .gate(instr_sel[19]));
  Transistor #(.\type ("n")) transistor_154 (.in(transistor_91_out), .out(transistor_154_out), .gate(instr_sel[19]));
  Transistor #(.\type ("n")) transistor_155 (.in(transistor_92_out), .out(transistor_155_out), .gate(instr_sel[19]));
  Transistor #(.\type ("n")) transistor_156 (.in(transistor_93_out), .out(transistor_156_out), .gate(instr_sel[19]));
  Transistor #(.\type ("n")) transistor_157 (.in(transistor_94_out), .out(transistor_157_out), .gate(instr_sel[19]));
  Transistor #(.\type ("n")) transistor_158 (.in(transistor_95_out), .out(transistor_158_out), .gate(instr_sel[19]));
  Transistor #(.\type ("n")) transistor_159 (.in(transistor_96_out), .out(transistor_159_out), .gate(instr_sel[19]));
  Transistor #(.\type ("n")) transistor_160 (.in(transistor_97_out), .out(transistor_160_out), .gate(instr_sel[19]));
  Transistor #(.\type ("n")) transistor_161 (.in(transistor_98_out), .out(transistor_161_out), .gate(instr_sel[19]));
  Transistor #(.\type ("n")) transistor_162 (.in(transistor_99_out), .out(transistor_162_out), .gate(instr_sel[19]));
  Transistor #(.\type ("n")) transistor_163 (.in(transistor_100_out), .out(transistor_163_out), .gate(instr_sel[19]));
  Transistor #(.\type ("n")) transistor_164 (.in(transistor_101_out), .out(transistor_164_out), .gate(instr_sel[19]));
  Transistor #(.\type ("n")) transistor_165 (.in(transistor_102_out), .out(transistor_165_out), .gate(instr_sel[19]));
  Transistor #(.\type ("n")) transistor_166 (.in(transistor_103_out), .out(transistor_166_out), .gate(instr_sel[19]));
  Transistor #(.\type ("n")) transistor_167 (.in(transistor_104_out), .out(transistor_167_out), .gate(instr_sel[19]));
  Transistor #(.\type ("n")) transistor_168 (.in(transistor_105_out), .out(transistor_168_out), .gate(instr_sel[19]));
  Transistor #(.\type ("n")) transistor_169 (.in(transistor_106_out), .out(transistor_169_out), .gate(instr_sel[19]));
  Transistor #(.\type ("n")) transistor_170 (.in(transistor_107_out), .out(transistor_170_out), .gate(instr_sel[19]));
  Transistor #(.\type ("n")) transistor_171 (.in(transistor_108_out), .out(transistor_171_out), .gate(instr_sel[19]));
  Transistor #(.\type ("n")) transistor_172 (.in(transistor_109_out), .out(transistor_172_out), .gate(instr_sel[19]));
  Transistor #(.\type ("n")) transistor_173 (.in(transistor_110_out), .out(transistor_173_out), .gate(instr_sel[19]));
  Transistor #(.\type ("n")) transistor_174 (.in(transistor_111_out), .out(transistor_174_out), .gate(instr_sel[19]));
  Transistor #(.\type ("n")) transistor_175 (.in(transistor_112_out), .out(transistor_175_out), .gate(instr_sel[19]));
  Transistor #(.\type ("n")) transistor_176 (.in(transistor_113_out), .out(transistor_176_out), .gate(instr_sel[19]));
  Transistor #(.\type ("n")) transistor_177 (.in(transistor_114_out), .out(transistor_177_out), .gate(instr_sel[19]));
  Transistor #(.\type ("n")) transistor_178 (.in(transistor_115_out), .out(transistor_178_out), .gate(instr_sel[19]));
  Transistor #(.\type ("n")) transistor_179 (.in(transistor_116_out), .out(transistor_179_out), .gate(instr_sel[19]));
  Transistor #(.\type ("n")) transistor_180 (.in(transistor_117_out), .out(transistor_180_out), .gate(instr_sel[19]));
  Transistor #(.\type ("n")) transistor_181 (.in(transistor_118_out), .out(transistor_181_out), .gate(instr_sel[19]));
  Transistor #(.\type ("n")) transistor_182 (.in(transistor_119_out), .out(transistor_182_out), .gate(instr_sel[19]));
  Transistor #(.\type ("n")) transistor_183 (.in(transistor_120_out), .out(transistor_183_out), .gate(instr_sel[19]));
  Transistor #(.\type ("n")) transistor_184 (.in(transistor_121_out), .out(transistor_184_out), .gate(instr_sel[19]));
  Transistor #(.\type ("n")) transistor_185 (.in(transistor_122_out), .out(transistor_185_out), .gate(instr_sel[19]));
  Transistor #(.\type ("n")) transistor_186 (.in(transistor_123_out), .out(transistor_186_out), .gate(instr_sel[19]));
  Transistor #(.\type ("n")) transistor_187 (.in(transistor_124_out), .out(transistor_187_out), .gate(instr_sel[19]));
  Transistor #(.\type ("n")) transistor_188 (.in(transistor_125_out), .out(transistor_188_out), .gate(instr_sel[19]));
  Transistor #(.\type ("n")) transistor_189 (.in(transistor_126_out), .out(transistor_189_out), .gate(instr_sel[19]));
  Transistor #(.\type ("n")) transistor_190 (.in(transistor_127_out), .out(transistor_190_out), .gate(instr_sel[18]));
  Transistor #(.\type ("n")) transistor_191 (.in(transistor_190_out), .out(transistor_191_out), .gate(instr_sel[17]));
  Transistor #(.\type ("n")) transistor_192 (.in(transistor_128_out), .out(transistor_192_out), .gate(instr_sel[18]));
  Transistor #(.\type ("n")) transistor_193 (.in(transistor_192_out), .out(transistor_193_out), .gate(instr_sel[17]));
  Transistor #(.\type ("n")) transistor_194 (.in(transistor_129_out), .out(transistor_194_out), .gate(instr_sel[18]));
  Transistor #(.\type ("n")) transistor_195 (.in(transistor_194_out), .out(transistor_195_out), .gate(instr_sel[17]));
  Transistor #(.\type ("n")) transistor_196 (.in(transistor_130_out), .out(transistor_196_out), .gate(instr_sel[18]));
  Transistor #(.\type ("n")) transistor_197 (.in(transistor_196_out), .out(transistor_197_out), .gate(instr_sel[17]));
  Transistor #(.\type ("n")) transistor_198 (.in(transistor_131_out), .out(transistor_198_out), .gate(instr_sel[18]));
  Transistor #(.\type ("n")) transistor_199 (.in(transistor_198_out), .out(transistor_199_out), .gate(instr_sel[17]));
  Transistor #(.\type ("n")) transistor_200 (.in(transistor_132_out), .out(transistor_200_out), .gate(instr_sel[18]));
  Transistor #(.\type ("n")) transistor_201 (.in(transistor_200_out), .out(transistor_201_out), .gate(instr_sel[17]));
  Transistor #(.\type ("n")) transistor_202 (.in(transistor_133_out), .out(transistor_202_out), .gate(instr_sel[18]));
  Transistor #(.\type ("n")) transistor_203 (.in(transistor_202_out), .out(transistor_203_out), .gate(instr_sel[17]));
  Transistor #(.\type ("n")) transistor_204 (.in(transistor_134_out), .out(transistor_204_out), .gate(instr_sel[18]));
  Transistor #(.\type ("n")) transistor_205 (.in(transistor_204_out), .out(transistor_205_out), .gate(instr_sel[17]));
  Transistor #(.\type ("n")) transistor_206 (.in(transistor_135_out), .out(transistor_206_out), .gate(instr_sel[18]));
  Transistor #(.\type ("n")) transistor_207 (.in(transistor_206_out), .out(transistor_207_out), .gate(instr_sel[17]));
  Transistor #(.\type ("n")) transistor_208 (.in(transistor_136_out), .out(transistor_208_out), .gate(instr_sel[18]));
  Transistor #(.\type ("n")) transistor_209 (.in(transistor_208_out), .out(transistor_209_out), .gate(instr_sel[17]));
  Transistor #(.\type ("n")) transistor_210 (.in(transistor_137_out), .out(transistor_210_out), .gate(instr_sel[18]));
  Transistor #(.\type ("n")) transistor_211 (.in(transistor_210_out), .out(transistor_211_out), .gate(instr_sel[17]));
  Transistor #(.\type ("n")) transistor_212 (.in(transistor_138_out), .out(transistor_212_out), .gate(instr_sel[18]));
  Transistor #(.\type ("n")) transistor_213 (.in(transistor_212_out), .out(transistor_213_out), .gate(instr_sel[17]));
  Transistor #(.\type ("n")) transistor_214 (.in(transistor_139_out), .out(transistor_214_out), .gate(instr_sel[18]));
  Transistor #(.\type ("n")) transistor_215 (.in(transistor_214_out), .out(transistor_215_out), .gate(instr_sel[17]));
  Transistor #(.\type ("n")) transistor_216 (.in(transistor_140_out), .out(transistor_216_out), .gate(instr_sel[18]));
  Transistor #(.\type ("n")) transistor_217 (.in(transistor_216_out), .out(transistor_217_out), .gate(instr_sel[17]));
  Transistor #(.\type ("n")) transistor_218 (.in(transistor_141_out), .out(transistor_218_out), .gate(instr_sel[18]));
  Transistor #(.\type ("n")) transistor_219 (.in(transistor_218_out), .out(transistor_219_out), .gate(instr_sel[17]));
  Transistor #(.\type ("n")) transistor_220 (.in(transistor_142_out), .out(transistor_220_out), .gate(instr_sel[18]));
  Transistor #(.\type ("n")) transistor_221 (.in(transistor_220_out), .out(transistor_221_out), .gate(instr_sel[17]));
  Transistor #(.\type ("n")) transistor_222 (.in(transistor_143_out), .out(transistor_222_out), .gate(instr_sel[18]));
  Transistor #(.\type ("n")) transistor_223 (.in(transistor_222_out), .out(transistor_223_out), .gate(instr_sel[17]));
  Transistor #(.\type ("n")) transistor_224 (.in(transistor_144_out), .out(transistor_224_out), .gate(instr_sel[18]));
  Transistor #(.\type ("n")) transistor_225 (.in(transistor_224_out), .out(transistor_225_out), .gate(instr_sel[17]));
  Transistor #(.\type ("n")) transistor_226 (.in(transistor_145_out), .out(transistor_226_out), .gate(instr_sel[18]));
  Transistor #(.\type ("n")) transistor_227 (.in(transistor_226_out), .out(transistor_227_out), .gate(instr_sel[17]));
  Transistor #(.\type ("n")) transistor_228 (.in(transistor_146_out), .out(transistor_228_out), .gate(instr_sel[18]));
  Transistor #(.\type ("n")) transistor_229 (.in(transistor_228_out), .out(transistor_229_out), .gate(instr_sel[17]));
  Transistor #(.\type ("n")) transistor_230 (.in(transistor_147_out), .out(transistor_230_out), .gate(instr_sel[18]));
  Transistor #(.\type ("n")) transistor_231 (.in(transistor_230_out), .out(transistor_231_out), .gate(instr_sel[17]));
  Transistor #(.\type ("n")) transistor_232 (.in(transistor_148_out), .out(transistor_232_out), .gate(instr_sel[18]));
  Transistor #(.\type ("n")) transistor_233 (.in(transistor_232_out), .out(transistor_233_out), .gate(instr_sel[17]));
  Transistor #(.\type ("n")) transistor_234 (.in(transistor_149_out), .out(transistor_234_out), .gate(instr_sel[18]));
  Transistor #(.\type ("n")) transistor_235 (.in(transistor_234_out), .out(transistor_235_out), .gate(instr_sel[17]));
  Transistor #(.\type ("n")) transistor_236 (.in(transistor_150_out), .out(transistor_236_out), .gate(instr_sel[18]));
  Transistor #(.\type ("n")) transistor_237 (.in(transistor_236_out), .out(transistor_237_out), .gate(instr_sel[17]));
  Transistor #(.\type ("n")) transistor_238 (.in(transistor_151_out), .out(transistor_238_out), .gate(instr_sel[18]));
  Transistor #(.\type ("n")) transistor_239 (.in(transistor_238_out), .out(transistor_239_out), .gate(instr_sel[17]));
  Transistor #(.\type ("n")) transistor_240 (.in(transistor_152_out), .out(transistor_240_out), .gate(instr_sel[18]));
  Transistor #(.\type ("n")) transistor_241 (.in(transistor_240_out), .out(transistor_241_out), .gate(instr_sel[17]));
  Transistor #(.\type ("n")) transistor_242 (.in(transistor_153_out), .out(transistor_242_out), .gate(instr_sel[18]));
  Transistor #(.\type ("n")) transistor_243 (.in(transistor_242_out), .out(transistor_243_out), .gate(instr_sel[17]));
  Transistor #(.\type ("n")) transistor_244 (.in(transistor_154_out), .out(transistor_244_out), .gate(instr_sel[18]));
  Transistor #(.\type ("n")) transistor_245 (.in(transistor_244_out), .out(transistor_245_out), .gate(instr_sel[17]));
  Transistor #(.\type ("n")) transistor_246 (.in(transistor_155_out), .out(transistor_246_out), .gate(instr_sel[18]));
  Transistor #(.\type ("n")) transistor_247 (.in(transistor_246_out), .out(transistor_247_out), .gate(instr_sel[17]));
  Transistor #(.\type ("n")) transistor_248 (.in(transistor_156_out), .out(transistor_248_out), .gate(instr_sel[18]));
  Transistor #(.\type ("n")) transistor_249 (.in(transistor_248_out), .out(transistor_249_out), .gate(instr_sel[17]));
  Transistor #(.\type ("n")) transistor_250 (.in(transistor_157_out), .out(transistor_250_out), .gate(instr_sel[18]));
  Transistor #(.\type ("n")) transistor_251 (.in(transistor_250_out), .out(transistor_251_out), .gate(instr_sel[17]));
  Transistor #(.\type ("n")) transistor_252 (.in(transistor_158_out), .out(transistor_252_out), .gate(instr_sel[18]));
  Transistor #(.\type ("n")) transistor_253 (.in(transistor_252_out), .out(transistor_253_out), .gate(instr_sel[17]));
  Transistor #(.\type ("n")) transistor_254 (.in(transistor_159_out), .out(transistor_254_out), .gate(instr_sel[18]));
  Transistor #(.\type ("n")) transistor_255 (.in(transistor_254_out), .out(transistor_255_out), .gate(instr_sel[17]));
  Transistor #(.\type ("n")) transistor_256 (.in(transistor_160_out), .out(transistor_256_out), .gate(instr_sel[18]));
  Transistor #(.\type ("n")) transistor_257 (.in(transistor_256_out), .out(transistor_257_out), .gate(instr_sel[17]));
  Transistor #(.\type ("n")) transistor_258 (.in(transistor_161_out), .out(transistor_258_out), .gate(instr_sel[18]));
  Transistor #(.\type ("n")) transistor_259 (.in(transistor_258_out), .out(transistor_259_out), .gate(instr_sel[17]));
  Transistor #(.\type ("n")) transistor_260 (.in(transistor_162_out), .out(transistor_260_out), .gate(instr_sel[18]));
  Transistor #(.\type ("n")) transistor_261 (.in(transistor_260_out), .out(transistor_261_out), .gate(instr_sel[17]));
  Transistor #(.\type ("n")) transistor_262 (.in(transistor_163_out), .out(transistor_262_out), .gate(instr_sel[18]));
  Transistor #(.\type ("n")) transistor_263 (.in(transistor_262_out), .out(transistor_263_out), .gate(instr_sel[17]));
  Transistor #(.\type ("n")) transistor_264 (.in(transistor_164_out), .out(transistor_264_out), .gate(instr_sel[18]));
  Transistor #(.\type ("n")) transistor_265 (.in(transistor_264_out), .out(transistor_265_out), .gate(instr_sel[17]));
  Transistor #(.\type ("n")) transistor_266 (.in(transistor_165_out), .out(transistor_266_out), .gate(instr_sel[18]));
  Transistor #(.\type ("n")) transistor_267 (.in(transistor_266_out), .out(transistor_267_out), .gate(instr_sel[17]));
  Transistor #(.\type ("n")) transistor_268 (.in(transistor_166_out), .out(transistor_268_out), .gate(instr_sel[18]));
  Transistor #(.\type ("n")) transistor_269 (.in(transistor_268_out), .out(transistor_269_out), .gate(instr_sel[17]));
  Transistor #(.\type ("n")) transistor_270 (.in(transistor_167_out), .out(transistor_270_out), .gate(instr_sel[18]));
  Transistor #(.\type ("n")) transistor_271 (.in(transistor_270_out), .out(transistor_271_out), .gate(instr_sel[17]));
  Transistor #(.\type ("n")) transistor_272 (.in(transistor_168_out), .out(transistor_272_out), .gate(instr_sel[18]));
  Transistor #(.\type ("n")) transistor_273 (.in(transistor_272_out), .out(transistor_273_out), .gate(instr_sel[17]));
  Transistor #(.\type ("n")) transistor_274 (.in(transistor_169_out), .out(transistor_274_out), .gate(instr_sel[18]));
  Transistor #(.\type ("n")) transistor_275 (.in(transistor_274_out), .out(transistor_275_out), .gate(instr_sel[17]));
  Transistor #(.\type ("n")) transistor_276 (.in(transistor_170_out), .out(transistor_276_out), .gate(instr_sel[18]));
  Transistor #(.\type ("n")) transistor_277 (.in(transistor_276_out), .out(transistor_277_out), .gate(instr_sel[17]));
  Transistor #(.\type ("n")) transistor_278 (.in(transistor_171_out), .out(transistor_278_out), .gate(instr_sel[18]));
  Transistor #(.\type ("n")) transistor_279 (.in(transistor_278_out), .out(transistor_279_out), .gate(instr_sel[17]));
  Transistor #(.\type ("n")) transistor_280 (.in(transistor_172_out), .out(transistor_280_out), .gate(instr_sel[18]));
  Transistor #(.\type ("n")) transistor_281 (.in(transistor_280_out), .out(transistor_281_out), .gate(instr_sel[17]));
  Transistor #(.\type ("n")) transistor_282 (.in(transistor_173_out), .out(transistor_282_out), .gate(instr_sel[18]));
  Transistor #(.\type ("n")) transistor_283 (.in(transistor_282_out), .out(transistor_283_out), .gate(instr_sel[17]));
  Transistor #(.\type ("n")) transistor_284 (.in(transistor_174_out), .out(transistor_284_out), .gate(instr_sel[18]));
  Transistor #(.\type ("n")) transistor_285 (.in(transistor_284_out), .out(transistor_285_out), .gate(instr_sel[17]));
  Transistor #(.\type ("n")) transistor_286 (.in(transistor_175_out), .out(transistor_286_out), .gate(instr_sel[18]));
  Transistor #(.\type ("n")) transistor_287 (.in(transistor_286_out), .out(transistor_287_out), .gate(instr_sel[17]));
  Transistor #(.\type ("n")) transistor_288 (.in(transistor_176_out), .out(transistor_288_out), .gate(instr_sel[18]));
  Transistor #(.\type ("n")) transistor_289 (.in(transistor_288_out), .out(transistor_289_out), .gate(instr_sel[17]));
  Transistor #(.\type ("n")) transistor_290 (.in(transistor_177_out), .out(transistor_290_out), .gate(instr_sel[18]));
  Transistor #(.\type ("n")) transistor_291 (.in(transistor_290_out), .out(transistor_291_out), .gate(instr_sel[17]));
  Transistor #(.\type ("n")) transistor_292 (.in(transistor_178_out), .out(transistor_292_out), .gate(instr_sel[18]));
  Transistor #(.\type ("n")) transistor_293 (.in(transistor_292_out), .out(transistor_293_out), .gate(instr_sel[17]));
  Transistor #(.\type ("n")) transistor_294 (.in(transistor_179_out), .out(transistor_294_out), .gate(instr_sel[18]));
  Transistor #(.\type ("n")) transistor_295 (.in(transistor_294_out), .out(transistor_295_out), .gate(instr_sel[17]));
  Transistor #(.\type ("n")) transistor_296 (.in(transistor_180_out), .out(transistor_296_out), .gate(instr_sel[18]));
  Transistor #(.\type ("n")) transistor_297 (.in(transistor_296_out), .out(transistor_297_out), .gate(instr_sel[17]));
  Transistor #(.\type ("n")) transistor_298 (.in(transistor_181_out), .out(transistor_298_out), .gate(instr_sel[18]));
  Transistor #(.\type ("n")) transistor_299 (.in(transistor_298_out), .out(transistor_299_out), .gate(instr_sel[17]));
  Transistor #(.\type ("n")) transistor_300 (.in(transistor_182_out), .out(transistor_300_out), .gate(instr_sel[18]));
  Transistor #(.\type ("n")) transistor_301 (.in(transistor_300_out), .out(transistor_301_out), .gate(instr_sel[17]));
  Transistor #(.\type ("n")) transistor_302 (.in(transistor_183_out), .out(transistor_302_out), .gate(instr_sel[18]));
  Transistor #(.\type ("n")) transistor_303 (.in(transistor_302_out), .out(transistor_303_out), .gate(instr_sel[17]));
  Transistor #(.\type ("n")) transistor_304 (.in(transistor_184_out), .out(transistor_304_out), .gate(instr_sel[18]));
  Transistor #(.\type ("n")) transistor_305 (.in(transistor_304_out), .out(transistor_305_out), .gate(instr_sel[17]));
  Transistor #(.\type ("n")) transistor_306 (.in(transistor_185_out), .out(transistor_306_out), .gate(instr_sel[18]));
  Transistor #(.\type ("n")) transistor_307 (.in(transistor_306_out), .out(transistor_307_out), .gate(instr_sel[17]));
  Transistor #(.\type ("n")) transistor_308 (.in(transistor_186_out), .out(transistor_308_out), .gate(instr_sel[18]));
  Transistor #(.\type ("n")) transistor_309 (.in(transistor_308_out), .out(transistor_309_out), .gate(instr_sel[17]));
  Transistor #(.\type ("n")) transistor_310 (.in(transistor_187_out), .out(transistor_310_out), .gate(instr_sel[18]));
  Transistor #(.\type ("n")) transistor_311 (.in(transistor_310_out), .out(transistor_311_out), .gate(instr_sel[17]));
  Transistor #(.\type ("n")) transistor_312 (.in(transistor_188_out), .out(transistor_312_out), .gate(instr_sel[18]));
  Transistor #(.\type ("n")) transistor_313 (.in(transistor_312_out), .out(transistor_313_out), .gate(instr_sel[17]));
  Transistor #(.\type ("n")) transistor_314 (.in(transistor_189_out), .out(transistor_314_out), .gate(instr_sel[18]));
  Transistor #(.\type ("n")) transistor_315 (.in(transistor_314_out), .out(transistor_315_out), .gate(instr_sel[17]));
  Transistor #(.\type ("n")) transistor_316 (.in(transistor_191_out), .out(transistor_316_out), .gate(instr_sel[16]));
  Transistor #(.\type ("n")) transistor_317 (.in(transistor_193_out), .out(transistor_317_out), .gate(instr_sel[16]));
  Transistor #(.\type ("n")) transistor_318 (.in(transistor_195_out), .out(transistor_318_out), .gate(instr_sel[16]));
  Transistor #(.\type ("n")) transistor_319 (.in(transistor_197_out), .out(transistor_319_out), .gate(instr_sel[16]));
  Transistor #(.\type ("n")) transistor_320 (.in(transistor_199_out), .out(transistor_320_out), .gate(instr_sel[16]));
  Transistor #(.\type ("n")) transistor_321 (.in(transistor_201_out), .out(transistor_321_out), .gate(instr_sel[16]));
  Transistor #(.\type ("n")) transistor_322 (.in(transistor_203_out), .out(transistor_322_out), .gate(instr_sel[16]));
  Transistor #(.\type ("n")) transistor_323 (.in(transistor_205_out), .out(transistor_323_out), .gate(instr_sel[16]));
  Transistor #(.\type ("n")) transistor_324 (.in(transistor_207_out), .out(transistor_324_out), .gate(instr_sel[16]));
  Transistor #(.\type ("n")) transistor_325 (.in(transistor_209_out), .out(transistor_325_out), .gate(instr_sel[16]));
  Transistor #(.\type ("n")) transistor_326 (.in(transistor_211_out), .out(transistor_326_out), .gate(instr_sel[16]));
  Transistor #(.\type ("n")) transistor_327 (.in(transistor_213_out), .out(transistor_327_out), .gate(instr_sel[16]));
  Transistor #(.\type ("n")) transistor_328 (.in(transistor_215_out), .out(transistor_328_out), .gate(instr_sel[16]));
  Transistor #(.\type ("n")) transistor_329 (.in(transistor_217_out), .out(transistor_329_out), .gate(instr_sel[16]));
  Transistor #(.\type ("n")) transistor_330 (.in(transistor_219_out), .out(transistor_330_out), .gate(instr_sel[16]));
  Transistor #(.\type ("n")) transistor_331 (.in(transistor_221_out), .out(transistor_331_out), .gate(instr_sel[16]));
  Transistor #(.\type ("n")) transistor_332 (.in(transistor_223_out), .out(transistor_332_out), .gate(instr_sel[16]));
  Transistor #(.\type ("n")) transistor_333 (.in(transistor_225_out), .out(transistor_333_out), .gate(instr_sel[16]));
  Transistor #(.\type ("n")) transistor_334 (.in(transistor_227_out), .out(transistor_334_out), .gate(instr_sel[16]));
  Transistor #(.\type ("n")) transistor_335 (.in(transistor_229_out), .out(transistor_335_out), .gate(instr_sel[16]));
  Transistor #(.\type ("n")) transistor_336 (.in(transistor_231_out), .out(transistor_336_out), .gate(instr_sel[16]));
  Transistor #(.\type ("n")) transistor_337 (.in(transistor_233_out), .out(transistor_337_out), .gate(instr_sel[16]));
  Transistor #(.\type ("n")) transistor_338 (.in(transistor_235_out), .out(transistor_338_out), .gate(instr_sel[16]));
  Transistor #(.\type ("n")) transistor_339 (.in(transistor_237_out), .out(transistor_339_out), .gate(instr_sel[16]));
  Transistor #(.\type ("n")) transistor_340 (.in(transistor_239_out), .out(transistor_340_out), .gate(instr_sel[16]));
  Transistor #(.\type ("n")) transistor_341 (.in(transistor_241_out), .out(transistor_341_out), .gate(instr_sel[16]));
  Transistor #(.\type ("n")) transistor_342 (.in(transistor_243_out), .out(transistor_342_out), .gate(instr_sel[16]));
  Transistor #(.\type ("n")) transistor_343 (.in(transistor_245_out), .out(transistor_343_out), .gate(instr_sel[16]));
  Transistor #(.\type ("n")) transistor_344 (.in(transistor_247_out), .out(transistor_344_out), .gate(instr_sel[16]));
  Transistor #(.\type ("n")) transistor_345 (.in(transistor_249_out), .out(transistor_345_out), .gate(instr_sel[16]));
  Transistor #(.\type ("n")) transistor_346 (.in(transistor_251_out), .out(transistor_346_out), .gate(instr_sel[16]));
  Transistor #(.\type ("n")) transistor_347 (.in(transistor_253_out), .out(transistor_347_out), .gate(instr_sel[16]));
  Transistor #(.\type ("n")) transistor_348 (.in(transistor_255_out), .out(transistor_348_out), .gate(instr_sel[16]));
  Transistor #(.\type ("n")) transistor_349 (.in(transistor_257_out), .out(transistor_349_out), .gate(instr_sel[16]));
  Transistor #(.\type ("n")) transistor_350 (.in(transistor_259_out), .out(transistor_350_out), .gate(instr_sel[16]));
  Transistor #(.\type ("n")) transistor_351 (.in(transistor_261_out), .out(transistor_351_out), .gate(instr_sel[16]));
  Transistor #(.\type ("n")) transistor_352 (.in(transistor_263_out), .out(transistor_352_out), .gate(instr_sel[16]));
  Transistor #(.\type ("n")) transistor_353 (.in(transistor_265_out), .out(transistor_353_out), .gate(instr_sel[16]));
  Transistor #(.\type ("n")) transistor_354 (.in(transistor_267_out), .out(transistor_354_out), .gate(instr_sel[16]));
  Transistor #(.\type ("n")) transistor_355 (.in(transistor_269_out), .out(transistor_355_out), .gate(instr_sel[16]));
  Transistor #(.\type ("n")) transistor_356 (.in(transistor_271_out), .out(transistor_356_out), .gate(instr_sel[16]));
  Transistor #(.\type ("n")) transistor_357 (.in(transistor_273_out), .out(transistor_357_out), .gate(instr_sel[16]));
  Transistor #(.\type ("n")) transistor_358 (.in(transistor_275_out), .out(transistor_358_out), .gate(instr_sel[16]));
  Transistor #(.\type ("n")) transistor_359 (.in(transistor_277_out), .out(transistor_359_out), .gate(instr_sel[16]));
  Transistor #(.\type ("n")) transistor_360 (.in(transistor_279_out), .out(transistor_360_out), .gate(instr_sel[16]));
  Transistor #(.\type ("n")) transistor_361 (.in(transistor_281_out), .out(transistor_361_out), .gate(instr_sel[16]));
  Transistor #(.\type ("n")) transistor_362 (.in(transistor_283_out), .out(transistor_362_out), .gate(instr_sel[16]));
  Transistor #(.\type ("n")) transistor_363 (.in(transistor_285_out), .out(transistor_363_out), .gate(instr_sel[16]));
  Transistor #(.\type ("n")) transistor_364 (.in(transistor_287_out), .out(transistor_364_out), .gate(instr_sel[16]));
  Transistor #(.\type ("n")) transistor_365 (.in(transistor_289_out), .out(transistor_365_out), .gate(instr_sel[16]));
  Transistor #(.\type ("n")) transistor_366 (.in(transistor_291_out), .out(transistor_366_out), .gate(instr_sel[16]));
  Transistor #(.\type ("n")) transistor_367 (.in(transistor_293_out), .out(transistor_367_out), .gate(instr_sel[16]));
  Transistor #(.\type ("n")) transistor_368 (.in(transistor_295_out), .out(transistor_368_out), .gate(instr_sel[16]));
  Transistor #(.\type ("n")) transistor_369 (.in(transistor_297_out), .out(transistor_369_out), .gate(instr_sel[16]));
  Transistor #(.\type ("n")) transistor_370 (.in(transistor_299_out), .out(transistor_370_out), .gate(instr_sel[16]));
  Transistor #(.\type ("n")) transistor_371 (.in(transistor_301_out), .out(transistor_371_out), .gate(instr_sel[16]));
  Transistor #(.\type ("n")) transistor_372 (.in(transistor_303_out), .out(transistor_372_out), .gate(instr_sel[16]));
  Transistor #(.\type ("n")) transistor_373 (.in(transistor_305_out), .out(transistor_373_out), .gate(instr_sel[16]));
  Transistor #(.\type ("n")) transistor_374 (.in(transistor_307_out), .out(transistor_374_out), .gate(instr_sel[16]));
  Transistor #(.\type ("n")) transistor_375 (.in(transistor_309_out), .out(transistor_375_out), .gate(instr_sel[16]));
  Transistor #(.\type ("n")) transistor_376 (.in(transistor_311_out), .out(transistor_376_out), .gate(instr_sel[16]));
  Transistor #(.\type ("n")) transistor_377 (.in(transistor_313_out), .out(transistor_377_out), .gate(instr_sel[16]));
  Transistor #(.\type ("n")) transistor_378 (.in(transistor_315_out), .out(transistor_378_out), .gate(instr_sel[16]));
  Transistor #(.\type ("n")) transistor_379 (.in(transistor_316_out), .out(transistor_379_out), .gate(instr_sel[15]));
  Transistor #(.\type ("n")) transistor_380 (.in(transistor_317_out), .out(transistor_380_out), .gate(instr_sel[15]));
  Transistor #(.\type ("n")) transistor_381 (.in(transistor_318_out), .out(transistor_381_out), .gate(instr_sel[15]));
  Transistor #(.\type ("n")) transistor_382 (.in(transistor_319_out), .out(transistor_382_out), .gate(instr_sel[15]));
  Transistor #(.\type ("n")) transistor_383 (.in(transistor_320_out), .out(transistor_383_out), .gate(instr_sel[15]));
  Transistor #(.\type ("n")) transistor_384 (.in(transistor_321_out), .out(transistor_384_out), .gate(instr_sel[15]));
  Transistor #(.\type ("n")) transistor_385 (.in(transistor_322_out), .out(transistor_385_out), .gate(instr_sel[15]));
  Transistor #(.\type ("n")) transistor_386 (.in(transistor_323_out), .out(transistor_386_out), .gate(instr_sel[15]));
  Transistor #(.\type ("n")) transistor_387 (.in(transistor_324_out), .out(transistor_387_out), .gate(instr_sel[15]));
  Transistor #(.\type ("n")) transistor_388 (.in(transistor_325_out), .out(transistor_388_out), .gate(instr_sel[15]));
  Transistor #(.\type ("n")) transistor_389 (.in(transistor_326_out), .out(transistor_389_out), .gate(instr_sel[15]));
  Transistor #(.\type ("n")) transistor_390 (.in(transistor_327_out), .out(transistor_390_out), .gate(instr_sel[15]));
  Transistor #(.\type ("n")) transistor_391 (.in(transistor_328_out), .out(transistor_391_out), .gate(instr_sel[15]));
  Transistor #(.\type ("n")) transistor_392 (.in(transistor_329_out), .out(transistor_392_out), .gate(instr_sel[15]));
  Transistor #(.\type ("n")) transistor_393 (.in(transistor_330_out), .out(transistor_393_out), .gate(instr_sel[15]));
  Transistor #(.\type ("n")) transistor_394 (.in(transistor_331_out), .out(transistor_394_out), .gate(instr_sel[15]));
  Transistor #(.\type ("n")) transistor_395 (.in(transistor_332_out), .out(transistor_395_out), .gate(instr_sel[15]));
  Transistor #(.\type ("n")) transistor_396 (.in(transistor_333_out), .out(transistor_396_out), .gate(instr_sel[15]));
  Transistor #(.\type ("n")) transistor_397 (.in(transistor_334_out), .out(transistor_397_out), .gate(instr_sel[15]));
  Transistor #(.\type ("n")) transistor_398 (.in(transistor_335_out), .out(transistor_398_out), .gate(instr_sel[15]));
  Transistor #(.\type ("n")) transistor_399 (.in(transistor_336_out), .out(transistor_399_out), .gate(instr_sel[15]));
  Transistor #(.\type ("n")) transistor_400 (.in(transistor_337_out), .out(transistor_400_out), .gate(instr_sel[15]));
  Transistor #(.\type ("n")) transistor_401 (.in(transistor_338_out), .out(transistor_401_out), .gate(instr_sel[15]));
  Transistor #(.\type ("n")) transistor_402 (.in(transistor_339_out), .out(transistor_402_out), .gate(instr_sel[15]));
  Transistor #(.\type ("n")) transistor_403 (.in(transistor_340_out), .out(transistor_403_out), .gate(instr_sel[15]));
  Transistor #(.\type ("n")) transistor_404 (.in(transistor_341_out), .out(transistor_404_out), .gate(instr_sel[15]));
  Transistor #(.\type ("n")) transistor_405 (.in(transistor_342_out), .out(transistor_405_out), .gate(instr_sel[15]));
  Transistor #(.\type ("n")) transistor_406 (.in(transistor_343_out), .out(transistor_406_out), .gate(instr_sel[15]));
  Transistor #(.\type ("n")) transistor_407 (.in(transistor_344_out), .out(transistor_407_out), .gate(instr_sel[15]));
  Transistor #(.\type ("n")) transistor_408 (.in(transistor_345_out), .out(transistor_408_out), .gate(instr_sel[15]));
  Transistor #(.\type ("n")) transistor_409 (.in(transistor_346_out), .out(transistor_409_out), .gate(instr_sel[15]));
  Transistor #(.\type ("n")) transistor_410 (.in(transistor_347_out), .out(transistor_410_out), .gate(instr_sel[15]));
  Transistor #(.\type ("n")) transistor_411 (.in(transistor_348_out), .out(transistor_411_out), .gate(instr_sel[15]));
  Transistor #(.\type ("n")) transistor_412 (.in(transistor_349_out), .out(transistor_412_out), .gate(instr_sel[15]));
  Transistor #(.\type ("n")) transistor_413 (.in(transistor_350_out), .out(transistor_413_out), .gate(instr_sel[15]));
  Transistor #(.\type ("n")) transistor_414 (.in(transistor_351_out), .out(transistor_414_out), .gate(instr_sel[15]));
  Transistor #(.\type ("n")) transistor_415 (.in(transistor_352_out), .out(transistor_415_out), .gate(instr_sel[15]));
  Transistor #(.\type ("n")) transistor_416 (.in(transistor_353_out), .out(transistor_416_out), .gate(instr_sel[15]));
  Transistor #(.\type ("n")) transistor_417 (.in(transistor_354_out), .out(transistor_417_out), .gate(instr_sel[15]));
  Transistor #(.\type ("n")) transistor_418 (.in(transistor_355_out), .out(transistor_418_out), .gate(instr_sel[15]));
  Transistor #(.\type ("n")) transistor_419 (.in(transistor_356_out), .out(transistor_419_out), .gate(instr_sel[15]));
  Transistor #(.\type ("n")) transistor_420 (.in(transistor_357_out), .out(transistor_420_out), .gate(instr_sel[15]));
  Transistor #(.\type ("n")) transistor_421 (.in(transistor_358_out), .out(transistor_421_out), .gate(instr_sel[15]));
  Transistor #(.\type ("n")) transistor_422 (.in(transistor_359_out), .out(transistor_422_out), .gate(instr_sel[15]));
  Transistor #(.\type ("n")) transistor_423 (.in(transistor_360_out), .out(transistor_423_out), .gate(instr_sel[15]));
  Transistor #(.\type ("n")) transistor_424 (.in(transistor_361_out), .out(transistor_424_out), .gate(instr_sel[15]));
  Transistor #(.\type ("n")) transistor_425 (.in(transistor_362_out), .out(transistor_425_out), .gate(instr_sel[15]));
  Transistor #(.\type ("n")) transistor_426 (.in(transistor_363_out), .out(transistor_426_out), .gate(instr_sel[15]));
  Transistor #(.\type ("n")) transistor_427 (.in(transistor_364_out), .out(transistor_427_out), .gate(instr_sel[15]));
  Transistor #(.\type ("n")) transistor_428 (.in(transistor_365_out), .out(transistor_428_out), .gate(instr_sel[15]));
  Transistor #(.\type ("n")) transistor_429 (.in(transistor_366_out), .out(transistor_429_out), .gate(instr_sel[15]));
  Transistor #(.\type ("n")) transistor_430 (.in(transistor_367_out), .out(transistor_430_out), .gate(instr_sel[15]));
  Transistor #(.\type ("n")) transistor_431 (.in(transistor_368_out), .out(transistor_431_out), .gate(instr_sel[15]));
  Transistor #(.\type ("n")) transistor_432 (.in(transistor_369_out), .out(transistor_432_out), .gate(instr_sel[15]));
  Transistor #(.\type ("n")) transistor_433 (.in(transistor_370_out), .out(transistor_433_out), .gate(instr_sel[15]));
  Transistor #(.\type ("n")) transistor_434 (.in(transistor_371_out), .out(transistor_434_out), .gate(instr_sel[15]));
  Transistor #(.\type ("n")) transistor_435 (.in(transistor_372_out), .out(transistor_435_out), .gate(instr_sel[15]));
  Transistor #(.\type ("n")) transistor_436 (.in(transistor_373_out), .out(transistor_436_out), .gate(instr_sel[15]));
  Transistor #(.\type ("n")) transistor_437 (.in(transistor_374_out), .out(transistor_437_out), .gate(instr_sel[15]));
  Transistor #(.\type ("n")) transistor_438 (.in(transistor_375_out), .out(transistor_438_out), .gate(instr_sel[15]));
  Transistor #(.\type ("n")) transistor_439 (.in(transistor_376_out), .out(transistor_439_out), .gate(instr_sel[15]));
  Transistor #(.\type ("n")) transistor_440 (.in(transistor_377_out), .out(transistor_440_out), .gate(instr_sel[15]));
  Transistor #(.\type ("n")) transistor_441 (.in(transistor_378_out), .out(transistor_441_out), .gate(instr_sel[15]));
  Transistor #(.\type ("n")) transistor_442 (.in(transistor_379_out), .out(transistor_442_out), .gate(instr_sel[14]));
  Transistor #(.\type ("n")) transistor_443 (.in(transistor_442_out), .out(transistor_443_out), .gate(instr_sel[13]));
  Transistor #(.\type ("n")) transistor_444 (.in(transistor_380_out), .out(transistor_444_out), .gate(instr_sel[14]));
  Transistor #(.\type ("n")) transistor_445 (.in(transistor_444_out), .out(transistor_445_out), .gate(instr_sel[13]));
  Transistor #(.\type ("n")) transistor_446 (.in(transistor_381_out), .out(transistor_446_out), .gate(instr_sel[14]));
  Transistor #(.\type ("n")) transistor_447 (.in(transistor_446_out), .out(transistor_447_out), .gate(instr_sel[13]));
  Transistor #(.\type ("n")) transistor_448 (.in(transistor_382_out), .out(transistor_448_out), .gate(instr_sel[14]));
  Transistor #(.\type ("n")) transistor_449 (.in(transistor_448_out), .out(transistor_449_out), .gate(instr_sel[13]));
  Transistor #(.\type ("n")) transistor_450 (.in(transistor_383_out), .out(transistor_450_out), .gate(instr_sel[14]));
  Transistor #(.\type ("n")) transistor_451 (.in(transistor_450_out), .out(transistor_451_out), .gate(instr_sel[13]));
  Transistor #(.\type ("n")) transistor_452 (.in(transistor_384_out), .out(transistor_452_out), .gate(instr_sel[14]));
  Transistor #(.\type ("n")) transistor_453 (.in(transistor_452_out), .out(transistor_453_out), .gate(instr_sel[13]));
  Transistor #(.\type ("n")) transistor_454 (.in(transistor_385_out), .out(transistor_454_out), .gate(instr_sel[14]));
  Transistor #(.\type ("n")) transistor_455 (.in(transistor_454_out), .out(transistor_455_out), .gate(instr_sel[13]));
  Transistor #(.\type ("n")) transistor_456 (.in(transistor_386_out), .out(transistor_456_out), .gate(instr_sel[14]));
  Transistor #(.\type ("n")) transistor_457 (.in(transistor_456_out), .out(transistor_457_out), .gate(instr_sel[13]));
  Transistor #(.\type ("n")) transistor_458 (.in(transistor_387_out), .out(transistor_458_out), .gate(instr_sel[14]));
  Transistor #(.\type ("n")) transistor_459 (.in(transistor_458_out), .out(transistor_459_out), .gate(instr_sel[13]));
  Transistor #(.\type ("n")) transistor_460 (.in(transistor_388_out), .out(transistor_460_out), .gate(instr_sel[14]));
  Transistor #(.\type ("n")) transistor_461 (.in(transistor_460_out), .out(transistor_461_out), .gate(instr_sel[13]));
  Transistor #(.\type ("n")) transistor_462 (.in(transistor_389_out), .out(transistor_462_out), .gate(instr_sel[14]));
  Transistor #(.\type ("n")) transistor_463 (.in(transistor_462_out), .out(transistor_463_out), .gate(instr_sel[13]));
  Transistor #(.\type ("n")) transistor_464 (.in(transistor_390_out), .out(transistor_464_out), .gate(instr_sel[14]));
  Transistor #(.\type ("n")) transistor_465 (.in(transistor_464_out), .out(transistor_465_out), .gate(instr_sel[13]));
  Transistor #(.\type ("n")) transistor_466 (.in(transistor_391_out), .out(transistor_466_out), .gate(instr_sel[14]));
  Transistor #(.\type ("n")) transistor_467 (.in(transistor_466_out), .out(transistor_467_out), .gate(instr_sel[13]));
  Transistor #(.\type ("n")) transistor_468 (.in(transistor_392_out), .out(transistor_468_out), .gate(instr_sel[14]));
  Transistor #(.\type ("n")) transistor_469 (.in(transistor_468_out), .out(transistor_469_out), .gate(instr_sel[13]));
  Transistor #(.\type ("n")) transistor_470 (.in(transistor_393_out), .out(transistor_470_out), .gate(instr_sel[14]));
  Transistor #(.\type ("n")) transistor_471 (.in(transistor_470_out), .out(transistor_471_out), .gate(instr_sel[13]));
  Transistor #(.\type ("n")) transistor_472 (.in(transistor_394_out), .out(transistor_472_out), .gate(instr_sel[14]));
  Transistor #(.\type ("n")) transistor_473 (.in(transistor_472_out), .out(transistor_473_out), .gate(instr_sel[13]));
  Transistor #(.\type ("n")) transistor_474 (.in(transistor_395_out), .out(transistor_474_out), .gate(instr_sel[14]));
  Transistor #(.\type ("n")) transistor_475 (.in(transistor_474_out), .out(transistor_475_out), .gate(instr_sel[13]));
  Transistor #(.\type ("n")) transistor_476 (.in(transistor_396_out), .out(transistor_476_out), .gate(instr_sel[14]));
  Transistor #(.\type ("n")) transistor_477 (.in(transistor_476_out), .out(transistor_477_out), .gate(instr_sel[13]));
  Transistor #(.\type ("n")) transistor_478 (.in(transistor_397_out), .out(transistor_478_out), .gate(instr_sel[14]));
  Transistor #(.\type ("n")) transistor_479 (.in(transistor_478_out), .out(transistor_479_out), .gate(instr_sel[13]));
  Transistor #(.\type ("n")) transistor_480 (.in(transistor_398_out), .out(transistor_480_out), .gate(instr_sel[14]));
  Transistor #(.\type ("n")) transistor_481 (.in(transistor_480_out), .out(transistor_481_out), .gate(instr_sel[13]));
  Transistor #(.\type ("n")) transistor_482 (.in(transistor_399_out), .out(transistor_482_out), .gate(instr_sel[14]));
  Transistor #(.\type ("n")) transistor_483 (.in(transistor_482_out), .out(transistor_483_out), .gate(instr_sel[13]));
  Transistor #(.\type ("n")) transistor_484 (.in(transistor_400_out), .out(transistor_484_out), .gate(instr_sel[14]));
  Transistor #(.\type ("n")) transistor_485 (.in(transistor_484_out), .out(transistor_485_out), .gate(instr_sel[13]));
  Transistor #(.\type ("n")) transistor_486 (.in(transistor_401_out), .out(transistor_486_out), .gate(instr_sel[14]));
  Transistor #(.\type ("n")) transistor_487 (.in(transistor_486_out), .out(transistor_487_out), .gate(instr_sel[13]));
  Transistor #(.\type ("n")) transistor_488 (.in(transistor_402_out), .out(transistor_488_out), .gate(instr_sel[14]));
  Transistor #(.\type ("n")) transistor_489 (.in(transistor_488_out), .out(transistor_489_out), .gate(instr_sel[13]));
  Transistor #(.\type ("n")) transistor_490 (.in(transistor_403_out), .out(transistor_490_out), .gate(instr_sel[14]));
  Transistor #(.\type ("n")) transistor_491 (.in(transistor_490_out), .out(transistor_491_out), .gate(instr_sel[13]));
  Transistor #(.\type ("n")) transistor_492 (.in(transistor_404_out), .out(transistor_492_out), .gate(instr_sel[14]));
  Transistor #(.\type ("n")) transistor_493 (.in(transistor_492_out), .out(transistor_493_out), .gate(instr_sel[13]));
  Transistor #(.\type ("n")) transistor_494 (.in(transistor_405_out), .out(transistor_494_out), .gate(instr_sel[14]));
  Transistor #(.\type ("n")) transistor_495 (.in(transistor_494_out), .out(transistor_495_out), .gate(instr_sel[13]));
  Transistor #(.\type ("n")) transistor_496 (.in(transistor_406_out), .out(transistor_496_out), .gate(instr_sel[14]));
  Transistor #(.\type ("n")) transistor_497 (.in(transistor_496_out), .out(transistor_497_out), .gate(instr_sel[13]));
  Transistor #(.\type ("n")) transistor_498 (.in(transistor_407_out), .out(transistor_498_out), .gate(instr_sel[14]));
  Transistor #(.\type ("n")) transistor_499 (.in(transistor_498_out), .out(transistor_499_out), .gate(instr_sel[13]));
  Transistor #(.\type ("n")) transistor_500 (.in(transistor_408_out), .out(transistor_500_out), .gate(instr_sel[14]));
  Transistor #(.\type ("n")) transistor_501 (.in(transistor_500_out), .out(transistor_501_out), .gate(instr_sel[13]));
  Transistor #(.\type ("n")) transistor_502 (.in(transistor_409_out), .out(transistor_502_out), .gate(instr_sel[14]));
  Transistor #(.\type ("n")) transistor_503 (.in(transistor_502_out), .out(transistor_503_out), .gate(instr_sel[13]));
  Transistor #(.\type ("n")) transistor_504 (.in(transistor_410_out), .out(transistor_504_out), .gate(instr_sel[14]));
  Transistor #(.\type ("n")) transistor_505 (.in(transistor_504_out), .out(transistor_505_out), .gate(instr_sel[13]));
  Transistor #(.\type ("n")) transistor_506 (.in(transistor_411_out), .out(transistor_506_out), .gate(instr_sel[14]));
  Transistor #(.\type ("n")) transistor_507 (.in(transistor_506_out), .out(transistor_507_out), .gate(instr_sel[13]));
  Transistor #(.\type ("n")) transistor_508 (.in(transistor_412_out), .out(transistor_508_out), .gate(instr_sel[14]));
  Transistor #(.\type ("n")) transistor_509 (.in(transistor_508_out), .out(transistor_509_out), .gate(instr_sel[13]));
  Transistor #(.\type ("n")) transistor_510 (.in(transistor_413_out), .out(transistor_510_out), .gate(instr_sel[14]));
  Transistor #(.\type ("n")) transistor_511 (.in(transistor_510_out), .out(transistor_511_out), .gate(instr_sel[13]));
  Transistor #(.\type ("n")) transistor_512 (.in(transistor_414_out), .out(transistor_512_out), .gate(instr_sel[14]));
  Transistor #(.\type ("n")) transistor_513 (.in(transistor_512_out), .out(transistor_513_out), .gate(instr_sel[13]));
  Transistor #(.\type ("n")) transistor_514 (.in(transistor_415_out), .out(transistor_514_out), .gate(instr_sel[14]));
  Transistor #(.\type ("n")) transistor_515 (.in(transistor_514_out), .out(transistor_515_out), .gate(instr_sel[13]));
  Transistor #(.\type ("n")) transistor_516 (.in(transistor_416_out), .out(transistor_516_out), .gate(instr_sel[14]));
  Transistor #(.\type ("n")) transistor_517 (.in(transistor_516_out), .out(transistor_517_out), .gate(instr_sel[13]));
  Transistor #(.\type ("n")) transistor_518 (.in(transistor_417_out), .out(transistor_518_out), .gate(instr_sel[14]));
  Transistor #(.\type ("n")) transistor_519 (.in(transistor_518_out), .out(transistor_519_out), .gate(instr_sel[13]));
  Transistor #(.\type ("n")) transistor_520 (.in(transistor_418_out), .out(transistor_520_out), .gate(instr_sel[14]));
  Transistor #(.\type ("n")) transistor_521 (.in(transistor_520_out), .out(transistor_521_out), .gate(instr_sel[13]));
  Transistor #(.\type ("n")) transistor_522 (.in(transistor_419_out), .out(transistor_522_out), .gate(instr_sel[14]));
  Transistor #(.\type ("n")) transistor_523 (.in(transistor_522_out), .out(transistor_523_out), .gate(instr_sel[13]));
  Transistor #(.\type ("n")) transistor_524 (.in(transistor_420_out), .out(transistor_524_out), .gate(instr_sel[14]));
  Transistor #(.\type ("n")) transistor_525 (.in(transistor_524_out), .out(transistor_525_out), .gate(instr_sel[13]));
  Transistor #(.\type ("n")) transistor_526 (.in(transistor_421_out), .out(transistor_526_out), .gate(instr_sel[14]));
  Transistor #(.\type ("n")) transistor_527 (.in(transistor_526_out), .out(transistor_527_out), .gate(instr_sel[13]));
  Transistor #(.\type ("n")) transistor_528 (.in(transistor_422_out), .out(transistor_528_out), .gate(instr_sel[14]));
  Transistor #(.\type ("n")) transistor_529 (.in(transistor_528_out), .out(transistor_529_out), .gate(instr_sel[13]));
  Transistor #(.\type ("n")) transistor_530 (.in(transistor_423_out), .out(transistor_530_out), .gate(instr_sel[14]));
  Transistor #(.\type ("n")) transistor_531 (.in(transistor_530_out), .out(transistor_531_out), .gate(instr_sel[13]));
  Transistor #(.\type ("n")) transistor_532 (.in(transistor_424_out), .out(transistor_532_out), .gate(instr_sel[14]));
  Transistor #(.\type ("n")) transistor_533 (.in(transistor_532_out), .out(transistor_533_out), .gate(instr_sel[13]));
  Transistor #(.\type ("n")) transistor_534 (.in(transistor_425_out), .out(transistor_534_out), .gate(instr_sel[14]));
  Transistor #(.\type ("n")) transistor_535 (.in(transistor_534_out), .out(transistor_535_out), .gate(instr_sel[13]));
  Transistor #(.\type ("n")) transistor_536 (.in(transistor_426_out), .out(transistor_536_out), .gate(instr_sel[14]));
  Transistor #(.\type ("n")) transistor_537 (.in(transistor_536_out), .out(transistor_537_out), .gate(instr_sel[13]));
  Transistor #(.\type ("n")) transistor_538 (.in(transistor_427_out), .out(transistor_538_out), .gate(instr_sel[14]));
  Transistor #(.\type ("n")) transistor_539 (.in(transistor_538_out), .out(transistor_539_out), .gate(instr_sel[13]));
  Transistor #(.\type ("n")) transistor_540 (.in(transistor_428_out), .out(transistor_540_out), .gate(instr_sel[14]));
  Transistor #(.\type ("n")) transistor_541 (.in(transistor_540_out), .out(transistor_541_out), .gate(instr_sel[13]));
  Transistor #(.\type ("n")) transistor_542 (.in(transistor_429_out), .out(transistor_542_out), .gate(instr_sel[14]));
  Transistor #(.\type ("n")) transistor_543 (.in(transistor_542_out), .out(transistor_543_out), .gate(instr_sel[13]));
  Transistor #(.\type ("n")) transistor_544 (.in(transistor_430_out), .out(transistor_544_out), .gate(instr_sel[14]));
  Transistor #(.\type ("n")) transistor_545 (.in(transistor_544_out), .out(transistor_545_out), .gate(instr_sel[13]));
  Transistor #(.\type ("n")) transistor_546 (.in(transistor_431_out), .out(transistor_546_out), .gate(instr_sel[14]));
  Transistor #(.\type ("n")) transistor_547 (.in(transistor_546_out), .out(transistor_547_out), .gate(instr_sel[13]));
  Transistor #(.\type ("n")) transistor_548 (.in(transistor_432_out), .out(transistor_548_out), .gate(instr_sel[14]));
  Transistor #(.\type ("n")) transistor_549 (.in(transistor_548_out), .out(transistor_549_out), .gate(instr_sel[13]));
  Transistor #(.\type ("n")) transistor_550 (.in(transistor_433_out), .out(transistor_550_out), .gate(instr_sel[14]));
  Transistor #(.\type ("n")) transistor_551 (.in(transistor_550_out), .out(transistor_551_out), .gate(instr_sel[13]));
  Transistor #(.\type ("n")) transistor_552 (.in(transistor_434_out), .out(transistor_552_out), .gate(instr_sel[14]));
  Transistor #(.\type ("n")) transistor_553 (.in(transistor_552_out), .out(transistor_553_out), .gate(instr_sel[13]));
  Transistor #(.\type ("n")) transistor_554 (.in(transistor_435_out), .out(transistor_554_out), .gate(instr_sel[14]));
  Transistor #(.\type ("n")) transistor_555 (.in(transistor_554_out), .out(transistor_555_out), .gate(instr_sel[13]));
  Transistor #(.\type ("n")) transistor_556 (.in(transistor_436_out), .out(transistor_556_out), .gate(instr_sel[14]));
  Transistor #(.\type ("n")) transistor_557 (.in(transistor_556_out), .out(transistor_557_out), .gate(instr_sel[13]));
  Transistor #(.\type ("n")) transistor_558 (.in(transistor_437_out), .out(transistor_558_out), .gate(instr_sel[14]));
  Transistor #(.\type ("n")) transistor_559 (.in(transistor_558_out), .out(transistor_559_out), .gate(instr_sel[13]));
  Transistor #(.\type ("n")) transistor_560 (.in(transistor_438_out), .out(transistor_560_out), .gate(instr_sel[14]));
  Transistor #(.\type ("n")) transistor_561 (.in(transistor_560_out), .out(transistor_561_out), .gate(instr_sel[13]));
  Transistor #(.\type ("n")) transistor_562 (.in(transistor_439_out), .out(transistor_562_out), .gate(instr_sel[14]));
  Transistor #(.\type ("n")) transistor_563 (.in(transistor_562_out), .out(transistor_563_out), .gate(instr_sel[13]));
  Transistor #(.\type ("n")) transistor_564 (.in(transistor_440_out), .out(transistor_564_out), .gate(instr_sel[14]));
  Transistor #(.\type ("n")) transistor_565 (.in(transistor_564_out), .out(transistor_565_out), .gate(instr_sel[13]));
  Transistor #(.\type ("n")) transistor_566 (.in(transistor_441_out), .out(transistor_566_out), .gate(instr_sel[14]));
  Transistor #(.\type ("n")) transistor_567 (.in(transistor_566_out), .out(transistor_567_out), .gate(instr_sel[13]));
  Transistor #(.\type ("n")) transistor_568 (.in(transistor_443_out), .out(transistor_568_out), .gate(instr_sel[12]));
  Transistor #(.\type ("n")) transistor_569 (.in(transistor_445_out), .out(transistor_569_out), .gate(instr_sel[12]));
  Transistor #(.\type ("n")) transistor_570 (.in(transistor_447_out), .out(transistor_570_out), .gate(instr_sel[12]));
  Transistor #(.\type ("n")) transistor_571 (.in(transistor_449_out), .out(transistor_571_out), .gate(instr_sel[12]));
  Transistor #(.\type ("n")) transistor_572 (.in(transistor_451_out), .out(transistor_572_out), .gate(instr_sel[12]));
  Transistor #(.\type ("n")) transistor_573 (.in(transistor_453_out), .out(transistor_573_out), .gate(instr_sel[12]));
  Transistor #(.\type ("n")) transistor_574 (.in(transistor_455_out), .out(transistor_574_out), .gate(instr_sel[12]));
  Transistor #(.\type ("n")) transistor_575 (.in(transistor_457_out), .out(transistor_575_out), .gate(instr_sel[12]));
  Transistor #(.\type ("n")) transistor_576 (.in(transistor_459_out), .out(transistor_576_out), .gate(instr_sel[12]));
  Transistor #(.\type ("n")) transistor_577 (.in(transistor_461_out), .out(transistor_577_out), .gate(instr_sel[12]));
  Transistor #(.\type ("n")) transistor_578 (.in(transistor_463_out), .out(transistor_578_out), .gate(instr_sel[12]));
  Transistor #(.\type ("n")) transistor_579 (.in(transistor_465_out), .out(transistor_579_out), .gate(instr_sel[12]));
  Transistor #(.\type ("n")) transistor_580 (.in(transistor_467_out), .out(transistor_580_out), .gate(instr_sel[12]));
  Transistor #(.\type ("n")) transistor_581 (.in(transistor_469_out), .out(transistor_581_out), .gate(instr_sel[12]));
  Transistor #(.\type ("n")) transistor_582 (.in(transistor_471_out), .out(transistor_582_out), .gate(instr_sel[12]));
  Transistor #(.\type ("n")) transistor_583 (.in(transistor_473_out), .out(transistor_583_out), .gate(instr_sel[12]));
  Transistor #(.\type ("n")) transistor_584 (.in(transistor_475_out), .out(transistor_584_out), .gate(instr_sel[12]));
  Transistor #(.\type ("n")) transistor_585 (.in(transistor_477_out), .out(transistor_585_out), .gate(instr_sel[12]));
  Transistor #(.\type ("n")) transistor_586 (.in(transistor_479_out), .out(transistor_586_out), .gate(instr_sel[12]));
  Transistor #(.\type ("n")) transistor_587 (.in(transistor_481_out), .out(transistor_587_out), .gate(instr_sel[12]));
  Transistor #(.\type ("n")) transistor_588 (.in(transistor_483_out), .out(transistor_588_out), .gate(instr_sel[12]));
  Transistor #(.\type ("n")) transistor_589 (.in(transistor_485_out), .out(transistor_589_out), .gate(instr_sel[12]));
  Transistor #(.\type ("n")) transistor_590 (.in(transistor_487_out), .out(transistor_590_out), .gate(instr_sel[12]));
  Transistor #(.\type ("n")) transistor_591 (.in(transistor_489_out), .out(transistor_591_out), .gate(instr_sel[12]));
  Transistor #(.\type ("n")) transistor_592 (.in(transistor_491_out), .out(transistor_592_out), .gate(instr_sel[12]));
  Transistor #(.\type ("n")) transistor_593 (.in(transistor_493_out), .out(transistor_593_out), .gate(instr_sel[12]));
  Transistor #(.\type ("n")) transistor_594 (.in(transistor_495_out), .out(transistor_594_out), .gate(instr_sel[12]));
  Transistor #(.\type ("n")) transistor_595 (.in(transistor_497_out), .out(transistor_595_out), .gate(instr_sel[12]));
  Transistor #(.\type ("n")) transistor_596 (.in(transistor_499_out), .out(transistor_596_out), .gate(instr_sel[12]));
  Transistor #(.\type ("n")) transistor_597 (.in(transistor_501_out), .out(transistor_597_out), .gate(instr_sel[12]));
  Transistor #(.\type ("n")) transistor_598 (.in(transistor_503_out), .out(transistor_598_out), .gate(instr_sel[12]));
  Transistor #(.\type ("n")) transistor_599 (.in(transistor_505_out), .out(transistor_599_out), .gate(instr_sel[12]));
  Transistor #(.\type ("n")) transistor_600 (.in(transistor_507_out), .out(transistor_600_out), .gate(instr_sel[12]));
  Transistor #(.\type ("n")) transistor_601 (.in(transistor_509_out), .out(transistor_601_out), .gate(instr_sel[12]));
  Transistor #(.\type ("n")) transistor_602 (.in(transistor_511_out), .out(transistor_602_out), .gate(instr_sel[12]));
  Transistor #(.\type ("n")) transistor_603 (.in(transistor_513_out), .out(transistor_603_out), .gate(instr_sel[12]));
  Transistor #(.\type ("n")) transistor_604 (.in(transistor_515_out), .out(transistor_604_out), .gate(instr_sel[12]));
  Transistor #(.\type ("n")) transistor_605 (.in(transistor_517_out), .out(transistor_605_out), .gate(instr_sel[12]));
  Transistor #(.\type ("n")) transistor_606 (.in(transistor_519_out), .out(transistor_606_out), .gate(instr_sel[12]));
  Transistor #(.\type ("n")) transistor_607 (.in(transistor_521_out), .out(transistor_607_out), .gate(instr_sel[12]));
  Transistor #(.\type ("n")) transistor_608 (.in(transistor_523_out), .out(transistor_608_out), .gate(instr_sel[12]));
  Transistor #(.\type ("n")) transistor_609 (.in(transistor_525_out), .out(transistor_609_out), .gate(instr_sel[12]));
  Transistor #(.\type ("n")) transistor_610 (.in(transistor_527_out), .out(transistor_610_out), .gate(instr_sel[12]));
  Transistor #(.\type ("n")) transistor_611 (.in(transistor_529_out), .out(transistor_611_out), .gate(instr_sel[12]));
  Transistor #(.\type ("n")) transistor_612 (.in(transistor_531_out), .out(transistor_612_out), .gate(instr_sel[12]));
  Transistor #(.\type ("n")) transistor_613 (.in(transistor_533_out), .out(transistor_613_out), .gate(instr_sel[12]));
  Transistor #(.\type ("n")) transistor_614 (.in(transistor_535_out), .out(transistor_614_out), .gate(instr_sel[12]));
  Transistor #(.\type ("n")) transistor_615 (.in(transistor_537_out), .out(transistor_615_out), .gate(instr_sel[12]));
  Transistor #(.\type ("n")) transistor_616 (.in(transistor_539_out), .out(transistor_616_out), .gate(instr_sel[12]));
  Transistor #(.\type ("n")) transistor_617 (.in(transistor_541_out), .out(transistor_617_out), .gate(instr_sel[12]));
  Transistor #(.\type ("n")) transistor_618 (.in(transistor_543_out), .out(transistor_618_out), .gate(instr_sel[12]));
  Transistor #(.\type ("n")) transistor_619 (.in(transistor_545_out), .out(transistor_619_out), .gate(instr_sel[12]));
  Transistor #(.\type ("n")) transistor_620 (.in(transistor_547_out), .out(transistor_620_out), .gate(instr_sel[12]));
  Transistor #(.\type ("n")) transistor_621 (.in(transistor_549_out), .out(transistor_621_out), .gate(instr_sel[12]));
  Transistor #(.\type ("n")) transistor_622 (.in(transistor_551_out), .out(transistor_622_out), .gate(instr_sel[12]));
  Transistor #(.\type ("n")) transistor_623 (.in(transistor_553_out), .out(transistor_623_out), .gate(instr_sel[12]));
  Transistor #(.\type ("n")) transistor_624 (.in(transistor_555_out), .out(transistor_624_out), .gate(instr_sel[12]));
  Transistor #(.\type ("n")) transistor_625 (.in(transistor_557_out), .out(transistor_625_out), .gate(instr_sel[12]));
  Transistor #(.\type ("n")) transistor_626 (.in(transistor_559_out), .out(transistor_626_out), .gate(instr_sel[12]));
  Transistor #(.\type ("n")) transistor_627 (.in(transistor_561_out), .out(transistor_627_out), .gate(instr_sel[12]));
  Transistor #(.\type ("n")) transistor_628 (.in(transistor_563_out), .out(transistor_628_out), .gate(instr_sel[12]));
  Transistor #(.\type ("n")) transistor_629 (.in(transistor_565_out), .out(transistor_629_out), .gate(instr_sel[12]));
  Transistor #(.\type ("n")) transistor_630 (.in(transistor_567_out), .out(transistor_630_out), .gate(instr_sel[12]));
  Transistor #(.\type ("n")) transistor_631 (.in(transistor_568_out), .out(transistor_631_out), .gate(instr_sel[11]));
  Transistor #(.\type ("n")) transistor_632 (.in(transistor_569_out), .out(transistor_632_out), .gate(instr_sel[11]));
  Transistor #(.\type ("n")) transistor_633 (.in(transistor_570_out), .out(transistor_633_out), .gate(instr_sel[11]));
  Transistor #(.\type ("n")) transistor_634 (.in(transistor_571_out), .out(transistor_634_out), .gate(instr_sel[11]));
  Transistor #(.\type ("n")) transistor_635 (.in(transistor_572_out), .out(transistor_635_out), .gate(instr_sel[11]));
  Transistor #(.\type ("n")) transistor_636 (.in(transistor_573_out), .out(transistor_636_out), .gate(instr_sel[11]));
  Transistor #(.\type ("n")) transistor_637 (.in(transistor_574_out), .out(transistor_637_out), .gate(instr_sel[11]));
  Transistor #(.\type ("n")) transistor_638 (.in(transistor_575_out), .out(transistor_638_out), .gate(instr_sel[11]));
  Transistor #(.\type ("n")) transistor_639 (.in(transistor_576_out), .out(transistor_639_out), .gate(instr_sel[11]));
  Transistor #(.\type ("n")) transistor_640 (.in(transistor_577_out), .out(transistor_640_out), .gate(instr_sel[11]));
  Transistor #(.\type ("n")) transistor_641 (.in(transistor_578_out), .out(transistor_641_out), .gate(instr_sel[11]));
  Transistor #(.\type ("n")) transistor_642 (.in(transistor_579_out), .out(transistor_642_out), .gate(instr_sel[11]));
  Transistor #(.\type ("n")) transistor_643 (.in(transistor_580_out), .out(transistor_643_out), .gate(instr_sel[11]));
  Transistor #(.\type ("n")) transistor_644 (.in(transistor_581_out), .out(transistor_644_out), .gate(instr_sel[11]));
  Transistor #(.\type ("n")) transistor_645 (.in(transistor_582_out), .out(transistor_645_out), .gate(instr_sel[11]));
  Transistor #(.\type ("n")) transistor_646 (.in(transistor_583_out), .out(transistor_646_out), .gate(instr_sel[11]));
  Transistor #(.\type ("n")) transistor_647 (.in(transistor_584_out), .out(transistor_647_out), .gate(instr_sel[11]));
  Transistor #(.\type ("n")) transistor_648 (.in(transistor_585_out), .out(transistor_648_out), .gate(instr_sel[11]));
  Transistor #(.\type ("n")) transistor_649 (.in(transistor_586_out), .out(transistor_649_out), .gate(instr_sel[11]));
  Transistor #(.\type ("n")) transistor_650 (.in(transistor_587_out), .out(transistor_650_out), .gate(instr_sel[11]));
  Transistor #(.\type ("n")) transistor_651 (.in(transistor_588_out), .out(transistor_651_out), .gate(instr_sel[11]));
  Transistor #(.\type ("n")) transistor_652 (.in(transistor_589_out), .out(transistor_652_out), .gate(instr_sel[11]));
  Transistor #(.\type ("n")) transistor_653 (.in(transistor_590_out), .out(transistor_653_out), .gate(instr_sel[11]));
  Transistor #(.\type ("n")) transistor_654 (.in(transistor_591_out), .out(transistor_654_out), .gate(instr_sel[11]));
  Transistor #(.\type ("n")) transistor_655 (.in(transistor_592_out), .out(transistor_655_out), .gate(instr_sel[11]));
  Transistor #(.\type ("n")) transistor_656 (.in(transistor_593_out), .out(transistor_656_out), .gate(instr_sel[11]));
  Transistor #(.\type ("n")) transistor_657 (.in(transistor_594_out), .out(transistor_657_out), .gate(instr_sel[11]));
  Transistor #(.\type ("n")) transistor_658 (.in(transistor_595_out), .out(transistor_658_out), .gate(instr_sel[11]));
  Transistor #(.\type ("n")) transistor_659 (.in(transistor_596_out), .out(transistor_659_out), .gate(instr_sel[11]));
  Transistor #(.\type ("n")) transistor_660 (.in(transistor_597_out), .out(transistor_660_out), .gate(instr_sel[11]));
  Transistor #(.\type ("n")) transistor_661 (.in(transistor_598_out), .out(transistor_661_out), .gate(instr_sel[11]));
  Transistor #(.\type ("n")) transistor_662 (.in(transistor_599_out), .out(transistor_662_out), .gate(instr_sel[11]));
  Transistor #(.\type ("n")) transistor_663 (.in(transistor_600_out), .out(transistor_663_out), .gate(instr_sel[11]));
  Transistor #(.\type ("n")) transistor_664 (.in(transistor_601_out), .out(transistor_664_out), .gate(instr_sel[11]));
  Transistor #(.\type ("n")) transistor_665 (.in(transistor_602_out), .out(transistor_665_out), .gate(instr_sel[11]));
  Transistor #(.\type ("n")) transistor_666 (.in(transistor_603_out), .out(transistor_666_out), .gate(instr_sel[11]));
  Transistor #(.\type ("n")) transistor_667 (.in(transistor_604_out), .out(transistor_667_out), .gate(instr_sel[11]));
  Transistor #(.\type ("n")) transistor_668 (.in(transistor_605_out), .out(transistor_668_out), .gate(instr_sel[11]));
  Transistor #(.\type ("n")) transistor_669 (.in(transistor_606_out), .out(transistor_669_out), .gate(instr_sel[11]));
  Transistor #(.\type ("n")) transistor_670 (.in(transistor_607_out), .out(transistor_670_out), .gate(instr_sel[11]));
  Transistor #(.\type ("n")) transistor_671 (.in(transistor_608_out), .out(transistor_671_out), .gate(instr_sel[11]));
  Transistor #(.\type ("n")) transistor_672 (.in(transistor_609_out), .out(transistor_672_out), .gate(instr_sel[11]));
  Transistor #(.\type ("n")) transistor_673 (.in(transistor_610_out), .out(transistor_673_out), .gate(instr_sel[11]));
  Transistor #(.\type ("n")) transistor_674 (.in(transistor_611_out), .out(transistor_674_out), .gate(instr_sel[11]));
  Transistor #(.\type ("n")) transistor_675 (.in(transistor_612_out), .out(transistor_675_out), .gate(instr_sel[11]));
  Transistor #(.\type ("n")) transistor_676 (.in(transistor_613_out), .out(transistor_676_out), .gate(instr_sel[11]));
  Transistor #(.\type ("n")) transistor_677 (.in(transistor_614_out), .out(transistor_677_out), .gate(instr_sel[11]));
  Transistor #(.\type ("n")) transistor_678 (.in(transistor_615_out), .out(transistor_678_out), .gate(instr_sel[11]));
  Transistor #(.\type ("n")) transistor_679 (.in(transistor_616_out), .out(transistor_679_out), .gate(instr_sel[11]));
  Transistor #(.\type ("n")) transistor_680 (.in(transistor_617_out), .out(transistor_680_out), .gate(instr_sel[11]));
  Transistor #(.\type ("n")) transistor_681 (.in(transistor_618_out), .out(transistor_681_out), .gate(instr_sel[11]));
  Transistor #(.\type ("n")) transistor_682 (.in(transistor_619_out), .out(transistor_682_out), .gate(instr_sel[11]));
  Transistor #(.\type ("n")) transistor_683 (.in(transistor_620_out), .out(transistor_683_out), .gate(instr_sel[11]));
  Transistor #(.\type ("n")) transistor_684 (.in(transistor_621_out), .out(transistor_684_out), .gate(instr_sel[11]));
  Transistor #(.\type ("n")) transistor_685 (.in(transistor_622_out), .out(transistor_685_out), .gate(instr_sel[11]));
  Transistor #(.\type ("n")) transistor_686 (.in(transistor_623_out), .out(transistor_686_out), .gate(instr_sel[11]));
  Transistor #(.\type ("n")) transistor_687 (.in(transistor_624_out), .out(transistor_687_out), .gate(instr_sel[11]));
  Transistor #(.\type ("n")) transistor_688 (.in(transistor_625_out), .out(transistor_688_out), .gate(instr_sel[11]));
  Transistor #(.\type ("n")) transistor_689 (.in(transistor_626_out), .out(transistor_689_out), .gate(instr_sel[11]));
  Transistor #(.\type ("n")) transistor_690 (.in(transistor_627_out), .out(transistor_690_out), .gate(instr_sel[11]));
  Transistor #(.\type ("n")) transistor_691 (.in(transistor_628_out), .out(transistor_691_out), .gate(instr_sel[11]));
  Transistor #(.\type ("n")) transistor_692 (.in(transistor_629_out), .out(transistor_692_out), .gate(instr_sel[11]));
  Transistor #(.\type ("n")) transistor_693 (.in(transistor_630_out), .out(transistor_693_out), .gate(instr_sel[11]));
  Transistor #(.\type ("n")) transistor_694 (.in(transistor_631_out), .out(transistor_694_out), .gate(instr_sel[10]));
  Transistor #(.\type ("n")) transistor_695 (.in(transistor_694_out), .out(transistor_695_out), .gate(instr_sel[9]));
  Transistor #(.\type ("n")) transistor_696 (.in(transistor_632_out), .out(transistor_696_out), .gate(instr_sel[10]));
  Transistor #(.\type ("n")) transistor_697 (.in(transistor_696_out), .out(transistor_697_out), .gate(instr_sel[9]));
  Transistor #(.\type ("n")) transistor_698 (.in(transistor_633_out), .out(transistor_698_out), .gate(instr_sel[10]));
  Transistor #(.\type ("n")) transistor_699 (.in(transistor_698_out), .out(transistor_699_out), .gate(instr_sel[9]));
  Transistor #(.\type ("n")) transistor_700 (.in(transistor_634_out), .out(transistor_700_out), .gate(instr_sel[10]));
  Transistor #(.\type ("n")) transistor_701 (.in(transistor_700_out), .out(transistor_701_out), .gate(instr_sel[9]));
  Transistor #(.\type ("n")) transistor_702 (.in(transistor_635_out), .out(transistor_702_out), .gate(instr_sel[10]));
  Transistor #(.\type ("n")) transistor_703 (.in(transistor_702_out), .out(transistor_703_out), .gate(instr_sel[9]));
  Transistor #(.\type ("n")) transistor_704 (.in(transistor_636_out), .out(transistor_704_out), .gate(instr_sel[10]));
  Transistor #(.\type ("n")) transistor_705 (.in(transistor_704_out), .out(transistor_705_out), .gate(instr_sel[9]));
  Transistor #(.\type ("n")) transistor_706 (.in(transistor_637_out), .out(transistor_706_out), .gate(instr_sel[10]));
  Transistor #(.\type ("n")) transistor_707 (.in(transistor_706_out), .out(transistor_707_out), .gate(instr_sel[9]));
  Transistor #(.\type ("n")) transistor_708 (.in(transistor_638_out), .out(transistor_708_out), .gate(instr_sel[10]));
  Transistor #(.\type ("n")) transistor_709 (.in(transistor_708_out), .out(transistor_709_out), .gate(instr_sel[9]));
  Transistor #(.\type ("n")) transistor_710 (.in(transistor_639_out), .out(transistor_710_out), .gate(instr_sel[10]));
  Transistor #(.\type ("n")) transistor_711 (.in(transistor_710_out), .out(transistor_711_out), .gate(instr_sel[9]));
  Transistor #(.\type ("n")) transistor_712 (.in(transistor_640_out), .out(transistor_712_out), .gate(instr_sel[10]));
  Transistor #(.\type ("n")) transistor_713 (.in(transistor_712_out), .out(transistor_713_out), .gate(instr_sel[9]));
  Transistor #(.\type ("n")) transistor_714 (.in(transistor_641_out), .out(transistor_714_out), .gate(instr_sel[10]));
  Transistor #(.\type ("n")) transistor_715 (.in(transistor_714_out), .out(transistor_715_out), .gate(instr_sel[9]));
  Transistor #(.\type ("n")) transistor_716 (.in(transistor_642_out), .out(transistor_716_out), .gate(instr_sel[10]));
  Transistor #(.\type ("n")) transistor_717 (.in(transistor_716_out), .out(transistor_717_out), .gate(instr_sel[9]));
  Transistor #(.\type ("n")) transistor_718 (.in(transistor_643_out), .out(transistor_718_out), .gate(instr_sel[10]));
  Transistor #(.\type ("n")) transistor_719 (.in(transistor_718_out), .out(transistor_719_out), .gate(instr_sel[9]));
  Transistor #(.\type ("n")) transistor_720 (.in(transistor_644_out), .out(transistor_720_out), .gate(instr_sel[10]));
  Transistor #(.\type ("n")) transistor_721 (.in(transistor_720_out), .out(transistor_721_out), .gate(instr_sel[9]));
  Transistor #(.\type ("n")) transistor_722 (.in(transistor_645_out), .out(transistor_722_out), .gate(instr_sel[10]));
  Transistor #(.\type ("n")) transistor_723 (.in(transistor_722_out), .out(transistor_723_out), .gate(instr_sel[9]));
  Transistor #(.\type ("n")) transistor_724 (.in(transistor_646_out), .out(transistor_724_out), .gate(instr_sel[10]));
  Transistor #(.\type ("n")) transistor_725 (.in(transistor_724_out), .out(transistor_725_out), .gate(instr_sel[9]));
  Transistor #(.\type ("n")) transistor_726 (.in(transistor_647_out), .out(transistor_726_out), .gate(instr_sel[10]));
  Transistor #(.\type ("n")) transistor_727 (.in(transistor_726_out), .out(transistor_727_out), .gate(instr_sel[9]));
  Transistor #(.\type ("n")) transistor_728 (.in(transistor_648_out), .out(transistor_728_out), .gate(instr_sel[10]));
  Transistor #(.\type ("n")) transistor_729 (.in(transistor_728_out), .out(transistor_729_out), .gate(instr_sel[9]));
  Transistor #(.\type ("n")) transistor_730 (.in(transistor_649_out), .out(transistor_730_out), .gate(instr_sel[10]));
  Transistor #(.\type ("n")) transistor_731 (.in(transistor_730_out), .out(transistor_731_out), .gate(instr_sel[9]));
  Transistor #(.\type ("n")) transistor_732 (.in(transistor_650_out), .out(transistor_732_out), .gate(instr_sel[10]));
  Transistor #(.\type ("n")) transistor_733 (.in(transistor_732_out), .out(transistor_733_out), .gate(instr_sel[9]));
  Transistor #(.\type ("n")) transistor_734 (.in(transistor_651_out), .out(transistor_734_out), .gate(instr_sel[10]));
  Transistor #(.\type ("n")) transistor_735 (.in(transistor_734_out), .out(transistor_735_out), .gate(instr_sel[9]));
  Transistor #(.\type ("n")) transistor_736 (.in(transistor_652_out), .out(transistor_736_out), .gate(instr_sel[10]));
  Transistor #(.\type ("n")) transistor_737 (.in(transistor_736_out), .out(transistor_737_out), .gate(instr_sel[9]));
  Transistor #(.\type ("n")) transistor_738 (.in(transistor_653_out), .out(transistor_738_out), .gate(instr_sel[10]));
  Transistor #(.\type ("n")) transistor_739 (.in(transistor_738_out), .out(transistor_739_out), .gate(instr_sel[9]));
  Transistor #(.\type ("n")) transistor_740 (.in(transistor_654_out), .out(transistor_740_out), .gate(instr_sel[10]));
  Transistor #(.\type ("n")) transistor_741 (.in(transistor_740_out), .out(transistor_741_out), .gate(instr_sel[9]));
  Transistor #(.\type ("n")) transistor_742 (.in(transistor_655_out), .out(transistor_742_out), .gate(instr_sel[10]));
  Transistor #(.\type ("n")) transistor_743 (.in(transistor_742_out), .out(transistor_743_out), .gate(instr_sel[9]));
  Transistor #(.\type ("n")) transistor_744 (.in(transistor_656_out), .out(transistor_744_out), .gate(instr_sel[10]));
  Transistor #(.\type ("n")) transistor_745 (.in(transistor_744_out), .out(transistor_745_out), .gate(instr_sel[9]));
  Transistor #(.\type ("n")) transistor_746 (.in(transistor_657_out), .out(transistor_746_out), .gate(instr_sel[10]));
  Transistor #(.\type ("n")) transistor_747 (.in(transistor_746_out), .out(transistor_747_out), .gate(instr_sel[9]));
  Transistor #(.\type ("n")) transistor_748 (.in(transistor_658_out), .out(transistor_748_out), .gate(instr_sel[10]));
  Transistor #(.\type ("n")) transistor_749 (.in(transistor_748_out), .out(transistor_749_out), .gate(instr_sel[9]));
  Transistor #(.\type ("n")) transistor_750 (.in(transistor_659_out), .out(transistor_750_out), .gate(instr_sel[10]));
  Transistor #(.\type ("n")) transistor_751 (.in(transistor_750_out), .out(transistor_751_out), .gate(instr_sel[9]));
  Transistor #(.\type ("n")) transistor_752 (.in(transistor_660_out), .out(transistor_752_out), .gate(instr_sel[10]));
  Transistor #(.\type ("n")) transistor_753 (.in(transistor_752_out), .out(transistor_753_out), .gate(instr_sel[9]));
  Transistor #(.\type ("n")) transistor_754 (.in(transistor_661_out), .out(transistor_754_out), .gate(instr_sel[10]));
  Transistor #(.\type ("n")) transistor_755 (.in(transistor_754_out), .out(transistor_755_out), .gate(instr_sel[9]));
  Transistor #(.\type ("n")) transistor_756 (.in(transistor_662_out), .out(transistor_756_out), .gate(instr_sel[10]));
  Transistor #(.\type ("n")) transistor_757 (.in(transistor_756_out), .out(transistor_757_out), .gate(instr_sel[9]));
  Transistor #(.\type ("n")) transistor_758 (.in(transistor_663_out), .out(transistor_758_out), .gate(instr_sel[10]));
  Transistor #(.\type ("n")) transistor_759 (.in(transistor_758_out), .out(transistor_759_out), .gate(instr_sel[9]));
  Transistor #(.\type ("n")) transistor_760 (.in(transistor_664_out), .out(transistor_760_out), .gate(instr_sel[10]));
  Transistor #(.\type ("n")) transistor_761 (.in(transistor_760_out), .out(transistor_761_out), .gate(instr_sel[9]));
  Transistor #(.\type ("n")) transistor_762 (.in(transistor_665_out), .out(transistor_762_out), .gate(instr_sel[10]));
  Transistor #(.\type ("n")) transistor_763 (.in(transistor_762_out), .out(transistor_763_out), .gate(instr_sel[9]));
  Transistor #(.\type ("n")) transistor_764 (.in(transistor_666_out), .out(transistor_764_out), .gate(instr_sel[10]));
  Transistor #(.\type ("n")) transistor_765 (.in(transistor_764_out), .out(transistor_765_out), .gate(instr_sel[9]));
  Transistor #(.\type ("n")) transistor_766 (.in(transistor_667_out), .out(transistor_766_out), .gate(instr_sel[10]));
  Transistor #(.\type ("n")) transistor_767 (.in(transistor_766_out), .out(transistor_767_out), .gate(instr_sel[9]));
  Transistor #(.\type ("n")) transistor_768 (.in(transistor_668_out), .out(transistor_768_out), .gate(instr_sel[10]));
  Transistor #(.\type ("n")) transistor_769 (.in(transistor_768_out), .out(transistor_769_out), .gate(instr_sel[9]));
  Transistor #(.\type ("n")) transistor_770 (.in(transistor_669_out), .out(transistor_770_out), .gate(instr_sel[10]));
  Transistor #(.\type ("n")) transistor_771 (.in(transistor_770_out), .out(transistor_771_out), .gate(instr_sel[9]));
  Transistor #(.\type ("n")) transistor_772 (.in(transistor_670_out), .out(transistor_772_out), .gate(instr_sel[10]));
  Transistor #(.\type ("n")) transistor_773 (.in(transistor_772_out), .out(transistor_773_out), .gate(instr_sel[9]));
  Transistor #(.\type ("n")) transistor_774 (.in(transistor_671_out), .out(transistor_774_out), .gate(instr_sel[10]));
  Transistor #(.\type ("n")) transistor_775 (.in(transistor_774_out), .out(transistor_775_out), .gate(instr_sel[9]));
  Transistor #(.\type ("n")) transistor_776 (.in(transistor_672_out), .out(transistor_776_out), .gate(instr_sel[10]));
  Transistor #(.\type ("n")) transistor_777 (.in(transistor_776_out), .out(transistor_777_out), .gate(instr_sel[9]));
  Transistor #(.\type ("n")) transistor_778 (.in(transistor_673_out), .out(transistor_778_out), .gate(instr_sel[10]));
  Transistor #(.\type ("n")) transistor_779 (.in(transistor_778_out), .out(transistor_779_out), .gate(instr_sel[9]));
  Transistor #(.\type ("n")) transistor_780 (.in(transistor_674_out), .out(transistor_780_out), .gate(instr_sel[10]));
  Transistor #(.\type ("n")) transistor_781 (.in(transistor_780_out), .out(transistor_781_out), .gate(instr_sel[9]));
  Transistor #(.\type ("n")) transistor_782 (.in(transistor_675_out), .out(transistor_782_out), .gate(instr_sel[10]));
  Transistor #(.\type ("n")) transistor_783 (.in(transistor_782_out), .out(transistor_783_out), .gate(instr_sel[9]));
  Transistor #(.\type ("n")) transistor_784 (.in(transistor_676_out), .out(transistor_784_out), .gate(instr_sel[10]));
  Transistor #(.\type ("n")) transistor_785 (.in(transistor_784_out), .out(transistor_785_out), .gate(instr_sel[9]));
  Transistor #(.\type ("n")) transistor_786 (.in(transistor_677_out), .out(transistor_786_out), .gate(instr_sel[10]));
  Transistor #(.\type ("n")) transistor_787 (.in(transistor_786_out), .out(transistor_787_out), .gate(instr_sel[9]));
  Transistor #(.\type ("n")) transistor_788 (.in(transistor_678_out), .out(transistor_788_out), .gate(instr_sel[10]));
  Transistor #(.\type ("n")) transistor_789 (.in(transistor_788_out), .out(transistor_789_out), .gate(instr_sel[9]));
  Transistor #(.\type ("n")) transistor_790 (.in(transistor_679_out), .out(transistor_790_out), .gate(instr_sel[10]));
  Transistor #(.\type ("n")) transistor_791 (.in(transistor_790_out), .out(transistor_791_out), .gate(instr_sel[9]));
  Transistor #(.\type ("n")) transistor_792 (.in(transistor_680_out), .out(transistor_792_out), .gate(instr_sel[10]));
  Transistor #(.\type ("n")) transistor_793 (.in(transistor_792_out), .out(transistor_793_out), .gate(instr_sel[9]));
  Transistor #(.\type ("n")) transistor_794 (.in(transistor_681_out), .out(transistor_794_out), .gate(instr_sel[10]));
  Transistor #(.\type ("n")) transistor_795 (.in(transistor_794_out), .out(transistor_795_out), .gate(instr_sel[9]));
  Transistor #(.\type ("n")) transistor_796 (.in(transistor_682_out), .out(transistor_796_out), .gate(instr_sel[10]));
  Transistor #(.\type ("n")) transistor_797 (.in(transistor_796_out), .out(transistor_797_out), .gate(instr_sel[9]));
  Transistor #(.\type ("n")) transistor_798 (.in(transistor_683_out), .out(transistor_798_out), .gate(instr_sel[10]));
  Transistor #(.\type ("n")) transistor_799 (.in(transistor_798_out), .out(transistor_799_out), .gate(instr_sel[9]));
  Transistor #(.\type ("n")) transistor_800 (.in(transistor_684_out), .out(transistor_800_out), .gate(instr_sel[10]));
  Transistor #(.\type ("n")) transistor_801 (.in(transistor_800_out), .out(transistor_801_out), .gate(instr_sel[9]));
  Transistor #(.\type ("n")) transistor_802 (.in(transistor_685_out), .out(transistor_802_out), .gate(instr_sel[10]));
  Transistor #(.\type ("n")) transistor_803 (.in(transistor_802_out), .out(transistor_803_out), .gate(instr_sel[9]));
  Transistor #(.\type ("n")) transistor_804 (.in(transistor_686_out), .out(transistor_804_out), .gate(instr_sel[10]));
  Transistor #(.\type ("n")) transistor_805 (.in(transistor_804_out), .out(transistor_805_out), .gate(instr_sel[9]));
  Transistor #(.\type ("n")) transistor_806 (.in(transistor_687_out), .out(transistor_806_out), .gate(instr_sel[10]));
  Transistor #(.\type ("n")) transistor_807 (.in(transistor_806_out), .out(transistor_807_out), .gate(instr_sel[9]));
  Transistor #(.\type ("n")) transistor_808 (.in(transistor_688_out), .out(transistor_808_out), .gate(instr_sel[10]));
  Transistor #(.\type ("n")) transistor_809 (.in(transistor_808_out), .out(transistor_809_out), .gate(instr_sel[9]));
  Transistor #(.\type ("n")) transistor_810 (.in(transistor_689_out), .out(transistor_810_out), .gate(instr_sel[10]));
  Transistor #(.\type ("n")) transistor_811 (.in(transistor_810_out), .out(transistor_811_out), .gate(instr_sel[9]));
  Transistor #(.\type ("n")) transistor_812 (.in(transistor_690_out), .out(transistor_812_out), .gate(instr_sel[10]));
  Transistor #(.\type ("n")) transistor_813 (.in(transistor_812_out), .out(transistor_813_out), .gate(instr_sel[9]));
  Transistor #(.\type ("n")) transistor_814 (.in(transistor_691_out), .out(transistor_814_out), .gate(instr_sel[10]));
  Transistor #(.\type ("n")) transistor_815 (.in(transistor_814_out), .out(transistor_815_out), .gate(instr_sel[9]));
  Transistor #(.\type ("n")) transistor_816 (.in(transistor_692_out), .out(transistor_816_out), .gate(instr_sel[10]));
  Transistor #(.\type ("n")) transistor_817 (.in(transistor_816_out), .out(transistor_817_out), .gate(instr_sel[9]));
  Transistor #(.\type ("n")) transistor_818 (.in(transistor_693_out), .out(transistor_818_out), .gate(instr_sel[10]));
  Transistor #(.\type ("n")) transistor_819 (.in(transistor_818_out), .out(transistor_819_out), .gate(instr_sel[9]));
  Transistor #(.\type ("n")) transistor_820 (.in(transistor_695_out), .out(transistor_820_out), .gate(instr_sel[8]));
  Transistor #(.\type ("n")) transistor_821 (.in(transistor_697_out), .out(transistor_821_out), .gate(instr_sel[8]));
  Transistor #(.\type ("n")) transistor_822 (.in(transistor_699_out), .out(transistor_822_out), .gate(instr_sel[8]));
  Transistor #(.\type ("n")) transistor_823 (.in(transistor_701_out), .out(transistor_823_out), .gate(instr_sel[8]));
  Transistor #(.\type ("n")) transistor_824 (.in(transistor_703_out), .out(transistor_824_out), .gate(instr_sel[8]));
  Transistor #(.\type ("n")) transistor_825 (.in(transistor_705_out), .out(transistor_825_out), .gate(instr_sel[8]));
  Transistor #(.\type ("n")) transistor_826 (.in(transistor_707_out), .out(transistor_826_out), .gate(instr_sel[8]));
  Transistor #(.\type ("n")) transistor_827 (.in(transistor_709_out), .out(transistor_827_out), .gate(instr_sel[8]));
  Transistor #(.\type ("n")) transistor_828 (.in(transistor_711_out), .out(transistor_828_out), .gate(instr_sel[8]));
  Transistor #(.\type ("n")) transistor_829 (.in(transistor_713_out), .out(transistor_829_out), .gate(instr_sel[8]));
  Transistor #(.\type ("n")) transistor_830 (.in(transistor_715_out), .out(transistor_830_out), .gate(instr_sel[8]));
  Transistor #(.\type ("n")) transistor_831 (.in(transistor_717_out), .out(transistor_831_out), .gate(instr_sel[8]));
  Transistor #(.\type ("n")) transistor_832 (.in(transistor_719_out), .out(transistor_832_out), .gate(instr_sel[8]));
  Transistor #(.\type ("n")) transistor_833 (.in(transistor_721_out), .out(transistor_833_out), .gate(instr_sel[8]));
  Transistor #(.\type ("n")) transistor_834 (.in(transistor_723_out), .out(transistor_834_out), .gate(instr_sel[8]));
  Transistor #(.\type ("n")) transistor_835 (.in(transistor_725_out), .out(transistor_835_out), .gate(instr_sel[8]));
  Transistor #(.\type ("n")) transistor_836 (.in(transistor_727_out), .out(transistor_836_out), .gate(instr_sel[8]));
  Transistor #(.\type ("n")) transistor_837 (.in(transistor_729_out), .out(transistor_837_out), .gate(instr_sel[8]));
  Transistor #(.\type ("n")) transistor_838 (.in(transistor_731_out), .out(transistor_838_out), .gate(instr_sel[8]));
  Transistor #(.\type ("n")) transistor_839 (.in(transistor_733_out), .out(transistor_839_out), .gate(instr_sel[8]));
  Transistor #(.\type ("n")) transistor_840 (.in(transistor_735_out), .out(transistor_840_out), .gate(instr_sel[8]));
  Transistor #(.\type ("n")) transistor_841 (.in(transistor_737_out), .out(transistor_841_out), .gate(instr_sel[8]));
  Transistor #(.\type ("n")) transistor_842 (.in(transistor_739_out), .out(transistor_842_out), .gate(instr_sel[8]));
  Transistor #(.\type ("n")) transistor_843 (.in(transistor_741_out), .out(transistor_843_out), .gate(instr_sel[8]));
  Transistor #(.\type ("n")) transistor_844 (.in(transistor_743_out), .out(transistor_844_out), .gate(instr_sel[8]));
  Transistor #(.\type ("n")) transistor_845 (.in(transistor_745_out), .out(transistor_845_out), .gate(instr_sel[8]));
  Transistor #(.\type ("n")) transistor_846 (.in(transistor_747_out), .out(transistor_846_out), .gate(instr_sel[8]));
  Transistor #(.\type ("n")) transistor_847 (.in(transistor_749_out), .out(transistor_847_out), .gate(instr_sel[8]));
  Transistor #(.\type ("n")) transistor_848 (.in(transistor_751_out), .out(transistor_848_out), .gate(instr_sel[8]));
  Transistor #(.\type ("n")) transistor_849 (.in(transistor_753_out), .out(transistor_849_out), .gate(instr_sel[8]));
  Transistor #(.\type ("n")) transistor_850 (.in(transistor_755_out), .out(transistor_850_out), .gate(instr_sel[8]));
  Transistor #(.\type ("n")) transistor_851 (.in(transistor_757_out), .out(transistor_851_out), .gate(instr_sel[8]));
  Transistor #(.\type ("n")) transistor_852 (.in(transistor_759_out), .out(transistor_852_out), .gate(instr_sel[8]));
  Transistor #(.\type ("n")) transistor_853 (.in(transistor_761_out), .out(transistor_853_out), .gate(instr_sel[8]));
  Transistor #(.\type ("n")) transistor_854 (.in(transistor_763_out), .out(transistor_854_out), .gate(instr_sel[8]));
  Transistor #(.\type ("n")) transistor_855 (.in(transistor_765_out), .out(transistor_855_out), .gate(instr_sel[8]));
  Transistor #(.\type ("n")) transistor_856 (.in(transistor_767_out), .out(transistor_856_out), .gate(instr_sel[8]));
  Transistor #(.\type ("n")) transistor_857 (.in(transistor_769_out), .out(transistor_857_out), .gate(instr_sel[8]));
  Transistor #(.\type ("n")) transistor_858 (.in(transistor_771_out), .out(transistor_858_out), .gate(instr_sel[8]));
  Transistor #(.\type ("n")) transistor_859 (.in(transistor_773_out), .out(transistor_859_out), .gate(instr_sel[8]));
  Transistor #(.\type ("n")) transistor_860 (.in(transistor_775_out), .out(transistor_860_out), .gate(instr_sel[8]));
  Transistor #(.\type ("n")) transistor_861 (.in(transistor_777_out), .out(transistor_861_out), .gate(instr_sel[8]));
  Transistor #(.\type ("n")) transistor_862 (.in(transistor_779_out), .out(transistor_862_out), .gate(instr_sel[8]));
  Transistor #(.\type ("n")) transistor_863 (.in(transistor_781_out), .out(transistor_863_out), .gate(instr_sel[8]));
  Transistor #(.\type ("n")) transistor_864 (.in(transistor_783_out), .out(transistor_864_out), .gate(instr_sel[8]));
  Transistor #(.\type ("n")) transistor_865 (.in(transistor_785_out), .out(transistor_865_out), .gate(instr_sel[8]));
  Transistor #(.\type ("n")) transistor_866 (.in(transistor_787_out), .out(transistor_866_out), .gate(instr_sel[8]));
  Transistor #(.\type ("n")) transistor_867 (.in(transistor_789_out), .out(transistor_867_out), .gate(instr_sel[8]));
  Transistor #(.\type ("n")) transistor_868 (.in(transistor_791_out), .out(transistor_868_out), .gate(instr_sel[8]));
  Transistor #(.\type ("n")) transistor_869 (.in(transistor_793_out), .out(transistor_869_out), .gate(instr_sel[8]));
  Transistor #(.\type ("n")) transistor_870 (.in(transistor_795_out), .out(transistor_870_out), .gate(instr_sel[8]));
  Transistor #(.\type ("n")) transistor_871 (.in(transistor_797_out), .out(transistor_871_out), .gate(instr_sel[8]));
  Transistor #(.\type ("n")) transistor_872 (.in(transistor_799_out), .out(transistor_872_out), .gate(instr_sel[8]));
  Transistor #(.\type ("n")) transistor_873 (.in(transistor_801_out), .out(transistor_873_out), .gate(instr_sel[8]));
  Transistor #(.\type ("n")) transistor_874 (.in(transistor_803_out), .out(transistor_874_out), .gate(instr_sel[8]));
  Transistor #(.\type ("n")) transistor_875 (.in(transistor_805_out), .out(transistor_875_out), .gate(instr_sel[8]));
  Transistor #(.\type ("n")) transistor_876 (.in(transistor_807_out), .out(transistor_876_out), .gate(instr_sel[8]));
  Transistor #(.\type ("n")) transistor_877 (.in(transistor_809_out), .out(transistor_877_out), .gate(instr_sel[8]));
  Transistor #(.\type ("n")) transistor_878 (.in(transistor_811_out), .out(transistor_878_out), .gate(instr_sel[8]));
  Transistor #(.\type ("n")) transistor_879 (.in(transistor_813_out), .out(transistor_879_out), .gate(instr_sel[8]));
  Transistor #(.\type ("n")) transistor_880 (.in(transistor_815_out), .out(transistor_880_out), .gate(instr_sel[8]));
  Transistor #(.\type ("n")) transistor_881 (.in(transistor_817_out), .out(transistor_881_out), .gate(instr_sel[8]));
  Transistor #(.\type ("n")) transistor_882 (.in(transistor_819_out), .out(transistor_882_out), .gate(instr_sel[8]));
  Transistor #(.\type ("n")) transistor_883 (.in(transistor_820_out), .out(transistor_883_out), .gate(instr_sel[7]));
  Transistor #(.\type ("n")) transistor_884 (.in(transistor_821_out), .out(transistor_884_out), .gate(instr_sel[7]));
  Transistor #(.\type ("n")) transistor_885 (.in(transistor_822_out), .out(transistor_885_out), .gate(instr_sel[7]));
  Transistor #(.\type ("n")) transistor_886 (.in(transistor_823_out), .out(transistor_886_out), .gate(instr_sel[7]));
  Transistor #(.\type ("n")) transistor_887 (.in(transistor_824_out), .out(transistor_887_out), .gate(instr_sel[7]));
  Transistor #(.\type ("n")) transistor_888 (.in(transistor_825_out), .out(transistor_888_out), .gate(instr_sel[7]));
  Transistor #(.\type ("n")) transistor_889 (.in(transistor_826_out), .out(transistor_889_out), .gate(instr_sel[7]));
  Transistor #(.\type ("n")) transistor_890 (.in(transistor_827_out), .out(transistor_890_out), .gate(instr_sel[7]));
  Transistor #(.\type ("n")) transistor_891 (.in(transistor_828_out), .out(transistor_891_out), .gate(instr_sel[7]));
  Transistor #(.\type ("n")) transistor_892 (.in(transistor_829_out), .out(transistor_892_out), .gate(instr_sel[7]));
  Transistor #(.\type ("n")) transistor_893 (.in(transistor_830_out), .out(transistor_893_out), .gate(instr_sel[7]));
  Transistor #(.\type ("n")) transistor_894 (.in(transistor_831_out), .out(transistor_894_out), .gate(instr_sel[7]));
  Transistor #(.\type ("n")) transistor_895 (.in(transistor_832_out), .out(transistor_895_out), .gate(instr_sel[7]));
  Transistor #(.\type ("n")) transistor_896 (.in(transistor_833_out), .out(transistor_896_out), .gate(instr_sel[7]));
  Transistor #(.\type ("n")) transistor_897 (.in(transistor_834_out), .out(transistor_897_out), .gate(instr_sel[7]));
  Transistor #(.\type ("n")) transistor_898 (.in(transistor_835_out), .out(transistor_898_out), .gate(instr_sel[7]));
  Transistor #(.\type ("n")) transistor_899 (.in(transistor_836_out), .out(transistor_899_out), .gate(instr_sel[7]));
  Transistor #(.\type ("n")) transistor_900 (.in(transistor_837_out), .out(transistor_900_out), .gate(instr_sel[7]));
  Transistor #(.\type ("n")) transistor_901 (.in(transistor_838_out), .out(transistor_901_out), .gate(instr_sel[7]));
  Transistor #(.\type ("n")) transistor_902 (.in(transistor_839_out), .out(transistor_902_out), .gate(instr_sel[7]));
  Transistor #(.\type ("n")) transistor_903 (.in(transistor_840_out), .out(transistor_903_out), .gate(instr_sel[7]));
  Transistor #(.\type ("n")) transistor_904 (.in(transistor_841_out), .out(transistor_904_out), .gate(instr_sel[7]));
  Transistor #(.\type ("n")) transistor_905 (.in(transistor_842_out), .out(transistor_905_out), .gate(instr_sel[7]));
  Transistor #(.\type ("n")) transistor_906 (.in(transistor_843_out), .out(transistor_906_out), .gate(instr_sel[7]));
  Transistor #(.\type ("n")) transistor_907 (.in(transistor_844_out), .out(transistor_907_out), .gate(instr_sel[7]));
  Transistor #(.\type ("n")) transistor_908 (.in(transistor_845_out), .out(transistor_908_out), .gate(instr_sel[7]));
  Transistor #(.\type ("n")) transistor_909 (.in(transistor_846_out), .out(transistor_909_out), .gate(instr_sel[7]));
  Transistor #(.\type ("n")) transistor_910 (.in(transistor_847_out), .out(transistor_910_out), .gate(instr_sel[7]));
  Transistor #(.\type ("n")) transistor_911 (.in(transistor_848_out), .out(transistor_911_out), .gate(instr_sel[7]));
  Transistor #(.\type ("n")) transistor_912 (.in(transistor_849_out), .out(transistor_912_out), .gate(instr_sel[7]));
  Transistor #(.\type ("n")) transistor_913 (.in(transistor_850_out), .out(transistor_913_out), .gate(instr_sel[7]));
  Transistor #(.\type ("n")) transistor_914 (.in(transistor_851_out), .out(transistor_914_out), .gate(instr_sel[7]));
  Transistor #(.\type ("n")) transistor_915 (.in(transistor_852_out), .out(transistor_915_out), .gate(instr_sel[7]));
  Transistor #(.\type ("n")) transistor_916 (.in(transistor_853_out), .out(transistor_916_out), .gate(instr_sel[7]));
  Transistor #(.\type ("n")) transistor_917 (.in(transistor_854_out), .out(transistor_917_out), .gate(instr_sel[7]));
  Transistor #(.\type ("n")) transistor_918 (.in(transistor_855_out), .out(transistor_918_out), .gate(instr_sel[7]));
  Transistor #(.\type ("n")) transistor_919 (.in(transistor_856_out), .out(transistor_919_out), .gate(instr_sel[7]));
  Transistor #(.\type ("n")) transistor_920 (.in(transistor_857_out), .out(transistor_920_out), .gate(instr_sel[7]));
  Transistor #(.\type ("n")) transistor_921 (.in(transistor_858_out), .out(transistor_921_out), .gate(instr_sel[7]));
  Transistor #(.\type ("n")) transistor_922 (.in(transistor_859_out), .out(transistor_922_out), .gate(instr_sel[7]));
  Transistor #(.\type ("n")) transistor_923 (.in(transistor_860_out), .out(transistor_923_out), .gate(instr_sel[7]));
  Transistor #(.\type ("n")) transistor_924 (.in(transistor_861_out), .out(transistor_924_out), .gate(instr_sel[7]));
  Transistor #(.\type ("n")) transistor_925 (.in(transistor_862_out), .out(transistor_925_out), .gate(instr_sel[7]));
  Transistor #(.\type ("n")) transistor_926 (.in(transistor_863_out), .out(transistor_926_out), .gate(instr_sel[7]));
  Transistor #(.\type ("n")) transistor_927 (.in(transistor_864_out), .out(transistor_927_out), .gate(instr_sel[7]));
  Transistor #(.\type ("n")) transistor_928 (.in(transistor_865_out), .out(transistor_928_out), .gate(instr_sel[7]));
  Transistor #(.\type ("n")) transistor_929 (.in(transistor_866_out), .out(transistor_929_out), .gate(instr_sel[7]));
  Transistor #(.\type ("n")) transistor_930 (.in(transistor_867_out), .out(transistor_930_out), .gate(instr_sel[7]));
  Transistor #(.\type ("n")) transistor_931 (.in(transistor_868_out), .out(transistor_931_out), .gate(instr_sel[7]));
  Transistor #(.\type ("n")) transistor_932 (.in(transistor_869_out), .out(transistor_932_out), .gate(instr_sel[7]));
  Transistor #(.\type ("n")) transistor_933 (.in(transistor_870_out), .out(transistor_933_out), .gate(instr_sel[7]));
  Transistor #(.\type ("n")) transistor_934 (.in(transistor_871_out), .out(transistor_934_out), .gate(instr_sel[7]));
  Transistor #(.\type ("n")) transistor_935 (.in(transistor_872_out), .out(transistor_935_out), .gate(instr_sel[7]));
  Transistor #(.\type ("n")) transistor_936 (.in(transistor_873_out), .out(transistor_936_out), .gate(instr_sel[7]));
  Transistor #(.\type ("n")) transistor_937 (.in(transistor_874_out), .out(transistor_937_out), .gate(instr_sel[7]));
  Transistor #(.\type ("n")) transistor_938 (.in(transistor_875_out), .out(transistor_938_out), .gate(instr_sel[7]));
  Transistor #(.\type ("n")) transistor_939 (.in(transistor_876_out), .out(transistor_939_out), .gate(instr_sel[7]));
  Transistor #(.\type ("n")) transistor_940 (.in(transistor_877_out), .out(transistor_940_out), .gate(instr_sel[7]));
  Transistor #(.\type ("n")) transistor_941 (.in(transistor_878_out), .out(transistor_941_out), .gate(instr_sel[7]));
  Transistor #(.\type ("n")) transistor_942 (.in(transistor_879_out), .out(transistor_942_out), .gate(instr_sel[7]));
  Transistor #(.\type ("n")) transistor_943 (.in(transistor_880_out), .out(transistor_943_out), .gate(instr_sel[7]));
  Transistor #(.\type ("n")) transistor_944 (.in(transistor_881_out), .out(transistor_944_out), .gate(instr_sel[7]));
  Transistor #(.\type ("n")) transistor_945 (.in(transistor_882_out), .out(transistor_945_out), .gate(instr_sel[7]));
  Transistor #(.\type ("n")) transistor_946 (.in(transistor_883_out), .out(transistor_946_out), .gate(instr_sel[6]));
  Transistor #(.\type ("n")) transistor_947 (.in(transistor_946_out), .out(transistor_947_out), .gate(instr_sel[5]));
  Transistor #(.\type ("n")) transistor_948 (.in(transistor_884_out), .out(transistor_948_out), .gate(instr_sel[6]));
  Transistor #(.\type ("n")) transistor_949 (.in(transistor_948_out), .out(transistor_949_out), .gate(instr_sel[5]));
  Transistor #(.\type ("n")) transistor_950 (.in(transistor_885_out), .out(transistor_950_out), .gate(instr_sel[6]));
  Transistor #(.\type ("n")) transistor_951 (.in(transistor_950_out), .out(transistor_951_out), .gate(instr_sel[5]));
  Transistor #(.\type ("n")) transistor_952 (.in(transistor_886_out), .out(transistor_952_out), .gate(instr_sel[6]));
  Transistor #(.\type ("n")) transistor_953 (.in(transistor_952_out), .out(transistor_953_out), .gate(instr_sel[5]));
  Transistor #(.\type ("n")) transistor_954 (.in(transistor_887_out), .out(transistor_954_out), .gate(instr_sel[6]));
  Transistor #(.\type ("n")) transistor_955 (.in(transistor_954_out), .out(transistor_955_out), .gate(instr_sel[5]));
  Transistor #(.\type ("n")) transistor_956 (.in(transistor_888_out), .out(transistor_956_out), .gate(instr_sel[6]));
  Transistor #(.\type ("n")) transistor_957 (.in(transistor_956_out), .out(transistor_957_out), .gate(instr_sel[5]));
  Transistor #(.\type ("n")) transistor_958 (.in(transistor_889_out), .out(transistor_958_out), .gate(instr_sel[6]));
  Transistor #(.\type ("n")) transistor_959 (.in(transistor_958_out), .out(transistor_959_out), .gate(instr_sel[5]));
  Transistor #(.\type ("n")) transistor_960 (.in(transistor_890_out), .out(transistor_960_out), .gate(instr_sel[6]));
  Transistor #(.\type ("n")) transistor_961 (.in(transistor_960_out), .out(transistor_961_out), .gate(instr_sel[5]));
  Transistor #(.\type ("n")) transistor_962 (.in(transistor_891_out), .out(transistor_962_out), .gate(instr_sel[6]));
  Transistor #(.\type ("n")) transistor_963 (.in(transistor_962_out), .out(transistor_963_out), .gate(instr_sel[5]));
  Transistor #(.\type ("n")) transistor_964 (.in(transistor_892_out), .out(transistor_964_out), .gate(instr_sel[6]));
  Transistor #(.\type ("n")) transistor_965 (.in(transistor_964_out), .out(transistor_965_out), .gate(instr_sel[5]));
  Transistor #(.\type ("n")) transistor_966 (.in(transistor_893_out), .out(transistor_966_out), .gate(instr_sel[6]));
  Transistor #(.\type ("n")) transistor_967 (.in(transistor_966_out), .out(transistor_967_out), .gate(instr_sel[5]));
  Transistor #(.\type ("n")) transistor_968 (.in(transistor_894_out), .out(transistor_968_out), .gate(instr_sel[6]));
  Transistor #(.\type ("n")) transistor_969 (.in(transistor_968_out), .out(transistor_969_out), .gate(instr_sel[5]));
  Transistor #(.\type ("n")) transistor_970 (.in(transistor_895_out), .out(transistor_970_out), .gate(instr_sel[6]));
  Transistor #(.\type ("n")) transistor_971 (.in(transistor_970_out), .out(transistor_971_out), .gate(instr_sel[5]));
  Transistor #(.\type ("n")) transistor_972 (.in(transistor_896_out), .out(transistor_972_out), .gate(instr_sel[6]));
  Transistor #(.\type ("n")) transistor_973 (.in(transistor_972_out), .out(transistor_973_out), .gate(instr_sel[5]));
  Transistor #(.\type ("n")) transistor_974 (.in(transistor_897_out), .out(transistor_974_out), .gate(instr_sel[6]));
  Transistor #(.\type ("n")) transistor_975 (.in(transistor_974_out), .out(transistor_975_out), .gate(instr_sel[5]));
  Transistor #(.\type ("n")) transistor_976 (.in(transistor_898_out), .out(transistor_976_out), .gate(instr_sel[6]));
  Transistor #(.\type ("n")) transistor_977 (.in(transistor_976_out), .out(transistor_977_out), .gate(instr_sel[5]));
  Transistor #(.\type ("n")) transistor_978 (.in(transistor_899_out), .out(transistor_978_out), .gate(instr_sel[6]));
  Transistor #(.\type ("n")) transistor_979 (.in(transistor_978_out), .out(transistor_979_out), .gate(instr_sel[5]));
  Transistor #(.\type ("n")) transistor_980 (.in(transistor_900_out), .out(transistor_980_out), .gate(instr_sel[6]));
  Transistor #(.\type ("n")) transistor_981 (.in(transistor_980_out), .out(transistor_981_out), .gate(instr_sel[5]));
  Transistor #(.\type ("n")) transistor_982 (.in(transistor_901_out), .out(transistor_982_out), .gate(instr_sel[6]));
  Transistor #(.\type ("n")) transistor_983 (.in(transistor_982_out), .out(transistor_983_out), .gate(instr_sel[5]));
  Transistor #(.\type ("n")) transistor_984 (.in(transistor_902_out), .out(transistor_984_out), .gate(instr_sel[6]));
  Transistor #(.\type ("n")) transistor_985 (.in(transistor_984_out), .out(transistor_985_out), .gate(instr_sel[5]));
  Transistor #(.\type ("n")) transistor_986 (.in(transistor_903_out), .out(transistor_986_out), .gate(instr_sel[6]));
  Transistor #(.\type ("n")) transistor_987 (.in(transistor_986_out), .out(transistor_987_out), .gate(instr_sel[5]));
  Transistor #(.\type ("n")) transistor_988 (.in(transistor_904_out), .out(transistor_988_out), .gate(instr_sel[6]));
  Transistor #(.\type ("n")) transistor_989 (.in(transistor_988_out), .out(transistor_989_out), .gate(instr_sel[5]));
  Transistor #(.\type ("n")) transistor_990 (.in(transistor_905_out), .out(transistor_990_out), .gate(instr_sel[6]));
  Transistor #(.\type ("n")) transistor_991 (.in(transistor_990_out), .out(transistor_991_out), .gate(instr_sel[5]));
  Transistor #(.\type ("n")) transistor_992 (.in(transistor_906_out), .out(transistor_992_out), .gate(instr_sel[6]));
  Transistor #(.\type ("n")) transistor_993 (.in(transistor_992_out), .out(transistor_993_out), .gate(instr_sel[5]));
  Transistor #(.\type ("n")) transistor_994 (.in(transistor_907_out), .out(transistor_994_out), .gate(instr_sel[6]));
  Transistor #(.\type ("n")) transistor_995 (.in(transistor_994_out), .out(transistor_995_out), .gate(instr_sel[5]));
  Transistor #(.\type ("n")) transistor_996 (.in(transistor_908_out), .out(transistor_996_out), .gate(instr_sel[6]));
  Transistor #(.\type ("n")) transistor_997 (.in(transistor_996_out), .out(transistor_997_out), .gate(instr_sel[5]));
  Transistor #(.\type ("n")) transistor_998 (.in(transistor_909_out), .out(transistor_998_out), .gate(instr_sel[6]));
  Transistor #(.\type ("n")) transistor_999 (.in(transistor_998_out), .out(transistor_999_out), .gate(instr_sel[5]));
  Transistor #(.\type ("n")) transistor_1000 (.in(transistor_910_out), .out(transistor_1000_out), .gate(instr_sel[6]));
  Transistor #(.\type ("n")) transistor_1001 (.in(transistor_1000_out), .out(transistor_1001_out), .gate(instr_sel[5]));
  Transistor #(.\type ("n")) transistor_1002 (.in(transistor_911_out), .out(transistor_1002_out), .gate(instr_sel[6]));
  Transistor #(.\type ("n")) transistor_1003 (.in(transistor_1002_out), .out(transistor_1003_out), .gate(instr_sel[5]));
  Transistor #(.\type ("n")) transistor_1004 (.in(transistor_912_out), .out(transistor_1004_out), .gate(instr_sel[6]));
  Transistor #(.\type ("n")) transistor_1005 (.in(transistor_1004_out), .out(transistor_1005_out), .gate(instr_sel[5]));
  Transistor #(.\type ("n")) transistor_1006 (.in(transistor_913_out), .out(transistor_1006_out), .gate(instr_sel[6]));
  Transistor #(.\type ("n")) transistor_1007 (.in(transistor_1006_out), .out(transistor_1007_out), .gate(instr_sel[5]));
  Transistor #(.\type ("n")) transistor_1008 (.in(transistor_914_out), .out(transistor_1008_out), .gate(instr_sel[6]));
  Transistor #(.\type ("n")) transistor_1009 (.in(transistor_1008_out), .out(transistor_1009_out), .gate(instr_sel[5]));
  Transistor #(.\type ("n")) transistor_1010 (.in(transistor_915_out), .out(transistor_1010_out), .gate(instr_sel[6]));
  Transistor #(.\type ("n")) transistor_1011 (.in(transistor_1010_out), .out(transistor_1011_out), .gate(instr_sel[5]));
  Transistor #(.\type ("n")) transistor_1012 (.in(transistor_916_out), .out(transistor_1012_out), .gate(instr_sel[6]));
  Transistor #(.\type ("n")) transistor_1013 (.in(transistor_1012_out), .out(transistor_1013_out), .gate(instr_sel[5]));
  Transistor #(.\type ("n")) transistor_1014 (.in(transistor_917_out), .out(transistor_1014_out), .gate(instr_sel[6]));
  Transistor #(.\type ("n")) transistor_1015 (.in(transistor_1014_out), .out(transistor_1015_out), .gate(instr_sel[5]));
  Transistor #(.\type ("n")) transistor_1016 (.in(transistor_918_out), .out(transistor_1016_out), .gate(instr_sel[6]));
  Transistor #(.\type ("n")) transistor_1017 (.in(transistor_1016_out), .out(transistor_1017_out), .gate(instr_sel[5]));
  Transistor #(.\type ("n")) transistor_1018 (.in(transistor_919_out), .out(transistor_1018_out), .gate(instr_sel[6]));
  Transistor #(.\type ("n")) transistor_1019 (.in(transistor_1018_out), .out(transistor_1019_out), .gate(instr_sel[5]));
  Transistor #(.\type ("n")) transistor_1020 (.in(transistor_920_out), .out(transistor_1020_out), .gate(instr_sel[6]));
  Transistor #(.\type ("n")) transistor_1021 (.in(transistor_1020_out), .out(transistor_1021_out), .gate(instr_sel[5]));
  Transistor #(.\type ("n")) transistor_1022 (.in(transistor_921_out), .out(transistor_1022_out), .gate(instr_sel[6]));
  Transistor #(.\type ("n")) transistor_1023 (.in(transistor_1022_out), .out(transistor_1023_out), .gate(instr_sel[5]));
  Transistor #(.\type ("n")) transistor_1024 (.in(transistor_922_out), .out(transistor_1024_out), .gate(instr_sel[6]));
  Transistor #(.\type ("n")) transistor_1025 (.in(transistor_1024_out), .out(transistor_1025_out), .gate(instr_sel[5]));
  Transistor #(.\type ("n")) transistor_1026 (.in(transistor_923_out), .out(transistor_1026_out), .gate(instr_sel[6]));
  Transistor #(.\type ("n")) transistor_1027 (.in(transistor_1026_out), .out(transistor_1027_out), .gate(instr_sel[5]));
  Transistor #(.\type ("n")) transistor_1028 (.in(transistor_924_out), .out(transistor_1028_out), .gate(instr_sel[6]));
  Transistor #(.\type ("n")) transistor_1029 (.in(transistor_1028_out), .out(transistor_1029_out), .gate(instr_sel[5]));
  Transistor #(.\type ("n")) transistor_1030 (.in(transistor_925_out), .out(transistor_1030_out), .gate(instr_sel[6]));
  Transistor #(.\type ("n")) transistor_1031 (.in(transistor_1030_out), .out(transistor_1031_out), .gate(instr_sel[5]));
  Transistor #(.\type ("n")) transistor_1032 (.in(transistor_926_out), .out(transistor_1032_out), .gate(instr_sel[6]));
  Transistor #(.\type ("n")) transistor_1033 (.in(transistor_1032_out), .out(transistor_1033_out), .gate(instr_sel[5]));
  Transistor #(.\type ("n")) transistor_1034 (.in(transistor_927_out), .out(transistor_1034_out), .gate(instr_sel[6]));
  Transistor #(.\type ("n")) transistor_1035 (.in(transistor_1034_out), .out(transistor_1035_out), .gate(instr_sel[5]));
  Transistor #(.\type ("n")) transistor_1036 (.in(transistor_928_out), .out(transistor_1036_out), .gate(instr_sel[6]));
  Transistor #(.\type ("n")) transistor_1037 (.in(transistor_1036_out), .out(transistor_1037_out), .gate(instr_sel[5]));
  Transistor #(.\type ("n")) transistor_1038 (.in(transistor_929_out), .out(transistor_1038_out), .gate(instr_sel[6]));
  Transistor #(.\type ("n")) transistor_1039 (.in(transistor_1038_out), .out(transistor_1039_out), .gate(instr_sel[5]));
  Transistor #(.\type ("n")) transistor_1040 (.in(transistor_930_out), .out(transistor_1040_out), .gate(instr_sel[6]));
  Transistor #(.\type ("n")) transistor_1041 (.in(transistor_1040_out), .out(transistor_1041_out), .gate(instr_sel[5]));
  Transistor #(.\type ("n")) transistor_1042 (.in(transistor_931_out), .out(transistor_1042_out), .gate(instr_sel[6]));
  Transistor #(.\type ("n")) transistor_1043 (.in(transistor_1042_out), .out(transistor_1043_out), .gate(instr_sel[5]));
  Transistor #(.\type ("n")) transistor_1044 (.in(transistor_932_out), .out(transistor_1044_out), .gate(instr_sel[6]));
  Transistor #(.\type ("n")) transistor_1045 (.in(transistor_1044_out), .out(transistor_1045_out), .gate(instr_sel[5]));
  Transistor #(.\type ("n")) transistor_1046 (.in(transistor_933_out), .out(transistor_1046_out), .gate(instr_sel[6]));
  Transistor #(.\type ("n")) transistor_1047 (.in(transistor_1046_out), .out(transistor_1047_out), .gate(instr_sel[5]));
  Transistor #(.\type ("n")) transistor_1048 (.in(transistor_934_out), .out(transistor_1048_out), .gate(instr_sel[6]));
  Transistor #(.\type ("n")) transistor_1049 (.in(transistor_1048_out), .out(transistor_1049_out), .gate(instr_sel[5]));
  Transistor #(.\type ("n")) transistor_1050 (.in(transistor_935_out), .out(transistor_1050_out), .gate(instr_sel[6]));
  Transistor #(.\type ("n")) transistor_1051 (.in(transistor_1050_out), .out(transistor_1051_out), .gate(instr_sel[5]));
  Transistor #(.\type ("n")) transistor_1052 (.in(transistor_936_out), .out(transistor_1052_out), .gate(instr_sel[6]));
  Transistor #(.\type ("n")) transistor_1053 (.in(transistor_1052_out), .out(transistor_1053_out), .gate(instr_sel[5]));
  Transistor #(.\type ("n")) transistor_1054 (.in(transistor_937_out), .out(transistor_1054_out), .gate(instr_sel[6]));
  Transistor #(.\type ("n")) transistor_1055 (.in(transistor_1054_out), .out(transistor_1055_out), .gate(instr_sel[5]));
  Transistor #(.\type ("n")) transistor_1056 (.in(transistor_938_out), .out(transistor_1056_out), .gate(instr_sel[6]));
  Transistor #(.\type ("n")) transistor_1057 (.in(transistor_1056_out), .out(transistor_1057_out), .gate(instr_sel[5]));
  Transistor #(.\type ("n")) transistor_1058 (.in(transistor_939_out), .out(transistor_1058_out), .gate(instr_sel[6]));
  Transistor #(.\type ("n")) transistor_1059 (.in(transistor_1058_out), .out(transistor_1059_out), .gate(instr_sel[5]));
  Transistor #(.\type ("n")) transistor_1060 (.in(transistor_940_out), .out(transistor_1060_out), .gate(instr_sel[6]));
  Transistor #(.\type ("n")) transistor_1061 (.in(transistor_1060_out), .out(transistor_1061_out), .gate(instr_sel[5]));
  Transistor #(.\type ("n")) transistor_1062 (.in(transistor_941_out), .out(transistor_1062_out), .gate(instr_sel[6]));
  Transistor #(.\type ("n")) transistor_1063 (.in(transistor_1062_out), .out(transistor_1063_out), .gate(instr_sel[5]));
  Transistor #(.\type ("n")) transistor_1064 (.in(transistor_942_out), .out(transistor_1064_out), .gate(instr_sel[6]));
  Transistor #(.\type ("n")) transistor_1065 (.in(transistor_1064_out), .out(transistor_1065_out), .gate(instr_sel[5]));
  Transistor #(.\type ("n")) transistor_1066 (.in(transistor_943_out), .out(transistor_1066_out), .gate(instr_sel[6]));
  Transistor #(.\type ("n")) transistor_1067 (.in(transistor_1066_out), .out(transistor_1067_out), .gate(instr_sel[5]));
  Transistor #(.\type ("n")) transistor_1068 (.in(transistor_944_out), .out(transistor_1068_out), .gate(instr_sel[6]));
  Transistor #(.\type ("n")) transistor_1069 (.in(transistor_1068_out), .out(transistor_1069_out), .gate(instr_sel[5]));
  Transistor #(.\type ("n")) transistor_1070 (.in(transistor_945_out), .out(transistor_1070_out), .gate(instr_sel[6]));
  Transistor #(.\type ("n")) transistor_1071 (.in(transistor_1070_out), .out(transistor_1071_out), .gate(instr_sel[5]));
  Transistor #(.\type ("n")) transistor_1072 (.in(transistor_947_out), .out(transistor_1072_out), .gate(instr_sel[4]));
  Transistor #(.\type ("n")) transistor_1073 (.in(transistor_949_out), .out(transistor_1073_out), .gate(instr_sel[4]));
  Transistor #(.\type ("n")) transistor_1074 (.in(transistor_951_out), .out(transistor_1074_out), .gate(instr_sel[4]));
  Transistor #(.\type ("n")) transistor_1075 (.in(transistor_953_out), .out(transistor_1075_out), .gate(instr_sel[4]));
  Transistor #(.\type ("n")) transistor_1076 (.in(transistor_955_out), .out(transistor_1076_out), .gate(instr_sel[4]));
  Transistor #(.\type ("n")) transistor_1077 (.in(transistor_957_out), .out(transistor_1077_out), .gate(instr_sel[4]));
  Transistor #(.\type ("n")) transistor_1078 (.in(transistor_959_out), .out(transistor_1078_out), .gate(instr_sel[4]));
  Transistor #(.\type ("n")) transistor_1079 (.in(transistor_961_out), .out(transistor_1079_out), .gate(instr_sel[4]));
  Transistor #(.\type ("n")) transistor_1080 (.in(transistor_963_out), .out(transistor_1080_out), .gate(instr_sel[4]));
  Transistor #(.\type ("n")) transistor_1081 (.in(transistor_965_out), .out(transistor_1081_out), .gate(instr_sel[4]));
  Transistor #(.\type ("n")) transistor_1082 (.in(transistor_967_out), .out(transistor_1082_out), .gate(instr_sel[4]));
  Transistor #(.\type ("n")) transistor_1083 (.in(transistor_969_out), .out(transistor_1083_out), .gate(instr_sel[4]));
  Transistor #(.\type ("n")) transistor_1084 (.in(transistor_971_out), .out(transistor_1084_out), .gate(instr_sel[4]));
  Transistor #(.\type ("n")) transistor_1085 (.in(transistor_973_out), .out(transistor_1085_out), .gate(instr_sel[4]));
  Transistor #(.\type ("n")) transistor_1086 (.in(transistor_975_out), .out(transistor_1086_out), .gate(instr_sel[4]));
  Transistor #(.\type ("n")) transistor_1087 (.in(transistor_977_out), .out(transistor_1087_out), .gate(instr_sel[4]));
  Transistor #(.\type ("n")) transistor_1088 (.in(transistor_979_out), .out(transistor_1088_out), .gate(instr_sel[4]));
  Transistor #(.\type ("n")) transistor_1089 (.in(transistor_981_out), .out(transistor_1089_out), .gate(instr_sel[4]));
  Transistor #(.\type ("n")) transistor_1090 (.in(transistor_983_out), .out(transistor_1090_out), .gate(instr_sel[4]));
  Transistor #(.\type ("n")) transistor_1091 (.in(transistor_985_out), .out(transistor_1091_out), .gate(instr_sel[4]));
  Transistor #(.\type ("n")) transistor_1092 (.in(transistor_987_out), .out(transistor_1092_out), .gate(instr_sel[4]));
  Transistor #(.\type ("n")) transistor_1093 (.in(transistor_989_out), .out(transistor_1093_out), .gate(instr_sel[4]));
  Transistor #(.\type ("n")) transistor_1094 (.in(transistor_991_out), .out(transistor_1094_out), .gate(instr_sel[4]));
  Transistor #(.\type ("n")) transistor_1095 (.in(transistor_993_out), .out(transistor_1095_out), .gate(instr_sel[4]));
  Transistor #(.\type ("n")) transistor_1096 (.in(transistor_995_out), .out(transistor_1096_out), .gate(instr_sel[4]));
  Transistor #(.\type ("n")) transistor_1097 (.in(transistor_997_out), .out(transistor_1097_out), .gate(instr_sel[4]));
  Transistor #(.\type ("n")) transistor_1098 (.in(transistor_999_out), .out(transistor_1098_out), .gate(instr_sel[4]));
  Transistor #(.\type ("n")) transistor_1099 (.in(transistor_1001_out), .out(transistor_1099_out), .gate(instr_sel[4]));
  Transistor #(.\type ("n")) transistor_1100 (.in(transistor_1003_out), .out(transistor_1100_out), .gate(instr_sel[4]));
  Transistor #(.\type ("n")) transistor_1101 (.in(transistor_1005_out), .out(transistor_1101_out), .gate(instr_sel[4]));
  Transistor #(.\type ("n")) transistor_1102 (.in(transistor_1007_out), .out(transistor_1102_out), .gate(instr_sel[4]));
  Transistor #(.\type ("n")) transistor_1103 (.in(transistor_1009_out), .out(transistor_1103_out), .gate(instr_sel[4]));
  Transistor #(.\type ("n")) transistor_1104 (.in(transistor_1011_out), .out(transistor_1104_out), .gate(instr_sel[4]));
  Transistor #(.\type ("n")) transistor_1105 (.in(transistor_1013_out), .out(transistor_1105_out), .gate(instr_sel[4]));
  Transistor #(.\type ("n")) transistor_1106 (.in(transistor_1015_out), .out(transistor_1106_out), .gate(instr_sel[4]));
  Transistor #(.\type ("n")) transistor_1107 (.in(transistor_1017_out), .out(transistor_1107_out), .gate(instr_sel[4]));
  Transistor #(.\type ("n")) transistor_1108 (.in(transistor_1019_out), .out(transistor_1108_out), .gate(instr_sel[4]));
  Transistor #(.\type ("n")) transistor_1109 (.in(transistor_1021_out), .out(transistor_1109_out), .gate(instr_sel[4]));
  Transistor #(.\type ("n")) transistor_1110 (.in(transistor_1023_out), .out(transistor_1110_out), .gate(instr_sel[4]));
  Transistor #(.\type ("n")) transistor_1111 (.in(transistor_1025_out), .out(transistor_1111_out), .gate(instr_sel[4]));
  Transistor #(.\type ("n")) transistor_1112 (.in(transistor_1027_out), .out(transistor_1112_out), .gate(instr_sel[4]));
  Transistor #(.\type ("n")) transistor_1113 (.in(transistor_1029_out), .out(transistor_1113_out), .gate(instr_sel[4]));
  Transistor #(.\type ("n")) transistor_1114 (.in(transistor_1031_out), .out(transistor_1114_out), .gate(instr_sel[4]));
  Transistor #(.\type ("n")) transistor_1115 (.in(transistor_1033_out), .out(transistor_1115_out), .gate(instr_sel[4]));
  Transistor #(.\type ("n")) transistor_1116 (.in(transistor_1035_out), .out(transistor_1116_out), .gate(instr_sel[4]));
  Transistor #(.\type ("n")) transistor_1117 (.in(transistor_1037_out), .out(transistor_1117_out), .gate(instr_sel[4]));
  Transistor #(.\type ("n")) transistor_1118 (.in(transistor_1039_out), .out(transistor_1118_out), .gate(instr_sel[4]));
  Transistor #(.\type ("n")) transistor_1119 (.in(transistor_1041_out), .out(transistor_1119_out), .gate(instr_sel[4]));
  Transistor #(.\type ("n")) transistor_1120 (.in(transistor_1043_out), .out(transistor_1120_out), .gate(instr_sel[4]));
  Transistor #(.\type ("n")) transistor_1121 (.in(transistor_1045_out), .out(transistor_1121_out), .gate(instr_sel[4]));
  Transistor #(.\type ("n")) transistor_1122 (.in(transistor_1047_out), .out(transistor_1122_out), .gate(instr_sel[4]));
  Transistor #(.\type ("n")) transistor_1123 (.in(transistor_1049_out), .out(transistor_1123_out), .gate(instr_sel[4]));
  Transistor #(.\type ("n")) transistor_1124 (.in(transistor_1051_out), .out(transistor_1124_out), .gate(instr_sel[4]));
  Transistor #(.\type ("n")) transistor_1125 (.in(transistor_1053_out), .out(transistor_1125_out), .gate(instr_sel[4]));
  Transistor #(.\type ("n")) transistor_1126 (.in(transistor_1055_out), .out(transistor_1126_out), .gate(instr_sel[4]));
  Transistor #(.\type ("n")) transistor_1127 (.in(transistor_1057_out), .out(transistor_1127_out), .gate(instr_sel[4]));
  Transistor #(.\type ("n")) transistor_1128 (.in(transistor_1059_out), .out(transistor_1128_out), .gate(instr_sel[4]));
  Transistor #(.\type ("n")) transistor_1129 (.in(transistor_1061_out), .out(transistor_1129_out), .gate(instr_sel[4]));
  Transistor #(.\type ("n")) transistor_1130 (.in(transistor_1063_out), .out(transistor_1130_out), .gate(instr_sel[4]));
  Transistor #(.\type ("n")) transistor_1131 (.in(transistor_1065_out), .out(transistor_1131_out), .gate(instr_sel[4]));
  Transistor #(.\type ("n")) transistor_1132 (.in(transistor_1067_out), .out(transistor_1132_out), .gate(instr_sel[4]));
  Transistor #(.\type ("n")) transistor_1133 (.in(transistor_1069_out), .out(transistor_1133_out), .gate(instr_sel[4]));
  Transistor #(.\type ("n")) transistor_1134 (.in(transistor_1071_out), .out(transistor_1134_out), .gate(instr_sel[4]));
  Transistor #(.\type ("n")) transistor_1135 (.in(transistor_1072_out), .out(transistor_1135_out), .gate(instr_sel[3]));
  Transistor #(.\type ("n")) transistor_1136 (.in(transistor_1073_out), .out(transistor_1136_out), .gate(instr_sel[3]));
  Transistor #(.\type ("n")) transistor_1137 (.in(transistor_1074_out), .out(transistor_1137_out), .gate(instr_sel[3]));
  Transistor #(.\type ("n")) transistor_1138 (.in(transistor_1075_out), .out(transistor_1138_out), .gate(instr_sel[3]));
  Transistor #(.\type ("n")) transistor_1139 (.in(transistor_1076_out), .out(transistor_1139_out), .gate(instr_sel[3]));
  Transistor #(.\type ("n")) transistor_1140 (.in(transistor_1077_out), .out(transistor_1140_out), .gate(instr_sel[3]));
  Transistor #(.\type ("n")) transistor_1141 (.in(transistor_1078_out), .out(transistor_1141_out), .gate(instr_sel[3]));
  Transistor #(.\type ("n")) transistor_1142 (.in(transistor_1079_out), .out(transistor_1142_out), .gate(instr_sel[3]));
  Transistor #(.\type ("n")) transistor_1143 (.in(transistor_1080_out), .out(transistor_1143_out), .gate(instr_sel[3]));
  Transistor #(.\type ("n")) transistor_1144 (.in(transistor_1081_out), .out(transistor_1144_out), .gate(instr_sel[3]));
  Transistor #(.\type ("n")) transistor_1145 (.in(transistor_1082_out), .out(transistor_1145_out), .gate(instr_sel[3]));
  Transistor #(.\type ("n")) transistor_1146 (.in(transistor_1083_out), .out(transistor_1146_out), .gate(instr_sel[3]));
  Transistor #(.\type ("n")) transistor_1147 (.in(transistor_1084_out), .out(transistor_1147_out), .gate(instr_sel[3]));
  Transistor #(.\type ("n")) transistor_1148 (.in(transistor_1085_out), .out(transistor_1148_out), .gate(instr_sel[3]));
  Transistor #(.\type ("n")) transistor_1149 (.in(transistor_1086_out), .out(transistor_1149_out), .gate(instr_sel[3]));
  Transistor #(.\type ("n")) transistor_1150 (.in(transistor_1087_out), .out(transistor_1150_out), .gate(instr_sel[3]));
  Transistor #(.\type ("n")) transistor_1151 (.in(transistor_1088_out), .out(transistor_1151_out), .gate(instr_sel[3]));
  Transistor #(.\type ("n")) transistor_1152 (.in(transistor_1089_out), .out(transistor_1152_out), .gate(instr_sel[3]));
  Transistor #(.\type ("n")) transistor_1153 (.in(transistor_1090_out), .out(transistor_1153_out), .gate(instr_sel[3]));
  Transistor #(.\type ("n")) transistor_1154 (.in(transistor_1091_out), .out(transistor_1154_out), .gate(instr_sel[3]));
  Transistor #(.\type ("n")) transistor_1155 (.in(transistor_1092_out), .out(transistor_1155_out), .gate(instr_sel[3]));
  Transistor #(.\type ("n")) transistor_1156 (.in(transistor_1093_out), .out(transistor_1156_out), .gate(instr_sel[3]));
  Transistor #(.\type ("n")) transistor_1157 (.in(transistor_1094_out), .out(transistor_1157_out), .gate(instr_sel[3]));
  Transistor #(.\type ("n")) transistor_1158 (.in(transistor_1095_out), .out(transistor_1158_out), .gate(instr_sel[3]));
  Transistor #(.\type ("n")) transistor_1159 (.in(transistor_1096_out), .out(transistor_1159_out), .gate(instr_sel[3]));
  Transistor #(.\type ("n")) transistor_1160 (.in(transistor_1097_out), .out(transistor_1160_out), .gate(instr_sel[3]));
  Transistor #(.\type ("n")) transistor_1161 (.in(transistor_1098_out), .out(transistor_1161_out), .gate(instr_sel[3]));
  Transistor #(.\type ("n")) transistor_1162 (.in(transistor_1099_out), .out(transistor_1162_out), .gate(instr_sel[3]));
  Transistor #(.\type ("n")) transistor_1163 (.in(transistor_1100_out), .out(transistor_1163_out), .gate(instr_sel[3]));
  Transistor #(.\type ("n")) transistor_1164 (.in(transistor_1101_out), .out(transistor_1164_out), .gate(instr_sel[3]));
  Transistor #(.\type ("n")) transistor_1165 (.in(transistor_1102_out), .out(transistor_1165_out), .gate(instr_sel[3]));
  Transistor #(.\type ("n")) transistor_1166 (.in(transistor_1103_out), .out(transistor_1166_out), .gate(instr_sel[3]));
  Transistor #(.\type ("n")) transistor_1167 (.in(transistor_1104_out), .out(transistor_1167_out), .gate(instr_sel[3]));
  Transistor #(.\type ("n")) transistor_1168 (.in(transistor_1105_out), .out(transistor_1168_out), .gate(instr_sel[3]));
  Transistor #(.\type ("n")) transistor_1169 (.in(transistor_1106_out), .out(transistor_1169_out), .gate(instr_sel[3]));
  Transistor #(.\type ("n")) transistor_1170 (.in(transistor_1107_out), .out(transistor_1170_out), .gate(instr_sel[3]));
  Transistor #(.\type ("n")) transistor_1171 (.in(transistor_1108_out), .out(transistor_1171_out), .gate(instr_sel[3]));
  Transistor #(.\type ("n")) transistor_1172 (.in(transistor_1109_out), .out(transistor_1172_out), .gate(instr_sel[3]));
  Transistor #(.\type ("n")) transistor_1173 (.in(transistor_1110_out), .out(transistor_1173_out), .gate(instr_sel[3]));
  Transistor #(.\type ("n")) transistor_1174 (.in(transistor_1111_out), .out(transistor_1174_out), .gate(instr_sel[3]));
  Transistor #(.\type ("n")) transistor_1175 (.in(transistor_1112_out), .out(transistor_1175_out), .gate(instr_sel[3]));
  Transistor #(.\type ("n")) transistor_1176 (.in(transistor_1113_out), .out(transistor_1176_out), .gate(instr_sel[3]));
  Transistor #(.\type ("n")) transistor_1177 (.in(transistor_1114_out), .out(transistor_1177_out), .gate(instr_sel[3]));
  Transistor #(.\type ("n")) transistor_1178 (.in(transistor_1115_out), .out(transistor_1178_out), .gate(instr_sel[3]));
  Transistor #(.\type ("n")) transistor_1179 (.in(transistor_1116_out), .out(transistor_1179_out), .gate(instr_sel[3]));
  Transistor #(.\type ("n")) transistor_1180 (.in(transistor_1117_out), .out(transistor_1180_out), .gate(instr_sel[3]));
  Transistor #(.\type ("n")) transistor_1181 (.in(transistor_1118_out), .out(transistor_1181_out), .gate(instr_sel[3]));
  Transistor #(.\type ("n")) transistor_1182 (.in(transistor_1119_out), .out(transistor_1182_out), .gate(instr_sel[3]));
  Transistor #(.\type ("n")) transistor_1183 (.in(transistor_1120_out), .out(transistor_1183_out), .gate(instr_sel[3]));
  Transistor #(.\type ("n")) transistor_1184 (.in(transistor_1121_out), .out(transistor_1184_out), .gate(instr_sel[3]));
  Transistor #(.\type ("n")) transistor_1185 (.in(transistor_1122_out), .out(transistor_1185_out), .gate(instr_sel[3]));
  Transistor #(.\type ("n")) transistor_1186 (.in(transistor_1123_out), .out(transistor_1186_out), .gate(instr_sel[3]));
  Transistor #(.\type ("n")) transistor_1187 (.in(transistor_1124_out), .out(transistor_1187_out), .gate(instr_sel[3]));
  Transistor #(.\type ("n")) transistor_1188 (.in(transistor_1125_out), .out(transistor_1188_out), .gate(instr_sel[3]));
  Transistor #(.\type ("n")) transistor_1189 (.in(transistor_1126_out), .out(transistor_1189_out), .gate(instr_sel[3]));
  Transistor #(.\type ("n")) transistor_1190 (.in(transistor_1127_out), .out(transistor_1190_out), .gate(instr_sel[3]));
  Transistor #(.\type ("n")) transistor_1191 (.in(transistor_1128_out), .out(transistor_1191_out), .gate(instr_sel[3]));
  Transistor #(.\type ("n")) transistor_1192 (.in(transistor_1129_out), .out(transistor_1192_out), .gate(instr_sel[3]));
  Transistor #(.\type ("n")) transistor_1193 (.in(transistor_1130_out), .out(transistor_1193_out), .gate(instr_sel[3]));
  Transistor #(.\type ("n")) transistor_1194 (.in(transistor_1131_out), .out(transistor_1194_out), .gate(instr_sel[3]));
  Transistor #(.\type ("n")) transistor_1195 (.in(transistor_1132_out), .out(transistor_1195_out), .gate(instr_sel[3]));
  Transistor #(.\type ("n")) transistor_1196 (.in(transistor_1133_out), .out(transistor_1196_out), .gate(instr_sel[3]));
  Transistor #(.\type ("n")) transistor_1197 (.in(transistor_1134_out), .out(transistor_1197_out), .gate(instr_sel[3]));
  Transistor #(.\type ("n")) transistor_1198 (.in(transistor_1135_out), .out(transistor_1198_out), .gate(instr_sel[2]));
  Transistor #(.\type ("n")) transistor_1199 (.in(transistor_1198_out), .out(transistor_1199_out), .gate(instr_sel[1]));
  Transistor #(.\type ("n")) transistor_1200 (.in(transistor_1136_out), .out(transistor_1200_out), .gate(instr_sel[2]));
  Transistor #(.\type ("n")) transistor_1201 (.in(transistor_1200_out), .out(transistor_1201_out), .gate(instr_sel[1]));
  Transistor #(.\type ("n")) transistor_1202 (.in(transistor_1137_out), .out(transistor_1202_out), .gate(instr_sel[2]));
  Transistor #(.\type ("n")) transistor_1203 (.in(transistor_1202_out), .out(transistor_1203_out), .gate(instr_sel[1]));
  Transistor #(.\type ("n")) transistor_1204 (.in(transistor_1138_out), .out(transistor_1204_out), .gate(instr_sel[2]));
  Transistor #(.\type ("n")) transistor_1205 (.in(transistor_1204_out), .out(transistor_1205_out), .gate(instr_sel[1]));
  Transistor #(.\type ("n")) transistor_1206 (.in(transistor_1139_out), .out(transistor_1206_out), .gate(instr_sel[2]));
  Transistor #(.\type ("n")) transistor_1207 (.in(transistor_1206_out), .out(transistor_1207_out), .gate(instr_sel[1]));
  Transistor #(.\type ("n")) transistor_1208 (.in(transistor_1140_out), .out(transistor_1208_out), .gate(instr_sel[2]));
  Transistor #(.\type ("n")) transistor_1209 (.in(transistor_1208_out), .out(transistor_1209_out), .gate(instr_sel[1]));
  Transistor #(.\type ("n")) transistor_1210 (.in(transistor_1141_out), .out(transistor_1210_out), .gate(instr_sel[2]));
  Transistor #(.\type ("n")) transistor_1211 (.in(transistor_1210_out), .out(transistor_1211_out), .gate(instr_sel[1]));
  Transistor #(.\type ("n")) transistor_1212 (.in(transistor_1142_out), .out(transistor_1212_out), .gate(instr_sel[2]));
  Transistor #(.\type ("n")) transistor_1213 (.in(transistor_1212_out), .out(transistor_1213_out), .gate(instr_sel[1]));
  Transistor #(.\type ("n")) transistor_1214 (.in(transistor_1143_out), .out(transistor_1214_out), .gate(instr_sel[2]));
  Transistor #(.\type ("n")) transistor_1215 (.in(transistor_1214_out), .out(transistor_1215_out), .gate(instr_sel[1]));
  Transistor #(.\type ("n")) transistor_1216 (.in(transistor_1144_out), .out(transistor_1216_out), .gate(instr_sel[2]));
  Transistor #(.\type ("n")) transistor_1217 (.in(transistor_1216_out), .out(transistor_1217_out), .gate(instr_sel[1]));
  Transistor #(.\type ("n")) transistor_1218 (.in(transistor_1145_out), .out(transistor_1218_out), .gate(instr_sel[2]));
  Transistor #(.\type ("n")) transistor_1219 (.in(transistor_1218_out), .out(transistor_1219_out), .gate(instr_sel[1]));
  Transistor #(.\type ("n")) transistor_1220 (.in(transistor_1146_out), .out(transistor_1220_out), .gate(instr_sel[2]));
  Transistor #(.\type ("n")) transistor_1221 (.in(transistor_1220_out), .out(transistor_1221_out), .gate(instr_sel[1]));
  Transistor #(.\type ("n")) transistor_1222 (.in(transistor_1147_out), .out(transistor_1222_out), .gate(instr_sel[2]));
  Transistor #(.\type ("n")) transistor_1223 (.in(transistor_1222_out), .out(transistor_1223_out), .gate(instr_sel[1]));
  Transistor #(.\type ("n")) transistor_1224 (.in(transistor_1148_out), .out(transistor_1224_out), .gate(instr_sel[2]));
  Transistor #(.\type ("n")) transistor_1225 (.in(transistor_1224_out), .out(transistor_1225_out), .gate(instr_sel[1]));
  Transistor #(.\type ("n")) transistor_1226 (.in(transistor_1149_out), .out(transistor_1226_out), .gate(instr_sel[2]));
  Transistor #(.\type ("n")) transistor_1227 (.in(transistor_1226_out), .out(transistor_1227_out), .gate(instr_sel[1]));
  Transistor #(.\type ("n")) transistor_1228 (.in(transistor_1150_out), .out(transistor_1228_out), .gate(instr_sel[2]));
  Transistor #(.\type ("n")) transistor_1229 (.in(transistor_1228_out), .out(transistor_1229_out), .gate(instr_sel[1]));
  Transistor #(.\type ("n")) transistor_1230 (.in(transistor_1151_out), .out(transistor_1230_out), .gate(instr_sel[2]));
  Transistor #(.\type ("n")) transistor_1231 (.in(transistor_1230_out), .out(transistor_1231_out), .gate(instr_sel[1]));
  Transistor #(.\type ("n")) transistor_1232 (.in(transistor_1152_out), .out(transistor_1232_out), .gate(instr_sel[2]));
  Transistor #(.\type ("n")) transistor_1233 (.in(transistor_1232_out), .out(transistor_1233_out), .gate(instr_sel[1]));
  Transistor #(.\type ("n")) transistor_1234 (.in(transistor_1153_out), .out(transistor_1234_out), .gate(instr_sel[2]));
  Transistor #(.\type ("n")) transistor_1235 (.in(transistor_1234_out), .out(transistor_1235_out), .gate(instr_sel[1]));
  Transistor #(.\type ("n")) transistor_1236 (.in(transistor_1154_out), .out(transistor_1236_out), .gate(instr_sel[2]));
  Transistor #(.\type ("n")) transistor_1237 (.in(transistor_1236_out), .out(transistor_1237_out), .gate(instr_sel[1]));
  Transistor #(.\type ("n")) transistor_1238 (.in(transistor_1155_out), .out(transistor_1238_out), .gate(instr_sel[2]));
  Transistor #(.\type ("n")) transistor_1239 (.in(transistor_1238_out), .out(transistor_1239_out), .gate(instr_sel[1]));
  Transistor #(.\type ("n")) transistor_1240 (.in(transistor_1156_out), .out(transistor_1240_out), .gate(instr_sel[2]));
  Transistor #(.\type ("n")) transistor_1241 (.in(transistor_1240_out), .out(transistor_1241_out), .gate(instr_sel[1]));
  Transistor #(.\type ("n")) transistor_1242 (.in(transistor_1157_out), .out(transistor_1242_out), .gate(instr_sel[2]));
  Transistor #(.\type ("n")) transistor_1243 (.in(transistor_1242_out), .out(transistor_1243_out), .gate(instr_sel[1]));
  Transistor #(.\type ("n")) transistor_1244 (.in(transistor_1158_out), .out(transistor_1244_out), .gate(instr_sel[2]));
  Transistor #(.\type ("n")) transistor_1245 (.in(transistor_1244_out), .out(transistor_1245_out), .gate(instr_sel[1]));
  Transistor #(.\type ("n")) transistor_1246 (.in(transistor_1159_out), .out(transistor_1246_out), .gate(instr_sel[2]));
  Transistor #(.\type ("n")) transistor_1247 (.in(transistor_1246_out), .out(transistor_1247_out), .gate(instr_sel[1]));
  Transistor #(.\type ("n")) transistor_1248 (.in(transistor_1160_out), .out(transistor_1248_out), .gate(instr_sel[2]));
  Transistor #(.\type ("n")) transistor_1249 (.in(transistor_1248_out), .out(transistor_1249_out), .gate(instr_sel[1]));
  Transistor #(.\type ("n")) transistor_1250 (.in(transistor_1161_out), .out(transistor_1250_out), .gate(instr_sel[2]));
  Transistor #(.\type ("n")) transistor_1251 (.in(transistor_1250_out), .out(transistor_1251_out), .gate(instr_sel[1]));
  Transistor #(.\type ("n")) transistor_1252 (.in(transistor_1162_out), .out(transistor_1252_out), .gate(instr_sel[2]));
  Transistor #(.\type ("n")) transistor_1253 (.in(transistor_1252_out), .out(transistor_1253_out), .gate(instr_sel[1]));
  Transistor #(.\type ("n")) transistor_1254 (.in(transistor_1163_out), .out(transistor_1254_out), .gate(instr_sel[2]));
  Transistor #(.\type ("n")) transistor_1255 (.in(transistor_1254_out), .out(transistor_1255_out), .gate(instr_sel[1]));
  Transistor #(.\type ("n")) transistor_1256 (.in(transistor_1164_out), .out(transistor_1256_out), .gate(instr_sel[2]));
  Transistor #(.\type ("n")) transistor_1257 (.in(transistor_1256_out), .out(transistor_1257_out), .gate(instr_sel[1]));
  Transistor #(.\type ("n")) transistor_1258 (.in(transistor_1165_out), .out(transistor_1258_out), .gate(instr_sel[2]));
  Transistor #(.\type ("n")) transistor_1259 (.in(transistor_1258_out), .out(transistor_1259_out), .gate(instr_sel[1]));
  Transistor #(.\type ("n")) transistor_1260 (.in(transistor_1166_out), .out(transistor_1260_out), .gate(instr_sel[2]));
  Transistor #(.\type ("n")) transistor_1261 (.in(transistor_1260_out), .out(transistor_1261_out), .gate(instr_sel[1]));
  Transistor #(.\type ("n")) transistor_1262 (.in(transistor_1167_out), .out(transistor_1262_out), .gate(instr_sel[2]));
  Transistor #(.\type ("n")) transistor_1263 (.in(transistor_1262_out), .out(transistor_1263_out), .gate(instr_sel[1]));
  Transistor #(.\type ("n")) transistor_1264 (.in(transistor_1168_out), .out(transistor_1264_out), .gate(instr_sel[2]));
  Transistor #(.\type ("n")) transistor_1265 (.in(transistor_1264_out), .out(transistor_1265_out), .gate(instr_sel[1]));
  Transistor #(.\type ("n")) transistor_1266 (.in(transistor_1169_out), .out(transistor_1266_out), .gate(instr_sel[2]));
  Transistor #(.\type ("n")) transistor_1267 (.in(transistor_1266_out), .out(transistor_1267_out), .gate(instr_sel[1]));
  Transistor #(.\type ("n")) transistor_1268 (.in(transistor_1170_out), .out(transistor_1268_out), .gate(instr_sel[2]));
  Transistor #(.\type ("n")) transistor_1269 (.in(transistor_1268_out), .out(transistor_1269_out), .gate(instr_sel[1]));
  Transistor #(.\type ("n")) transistor_1270 (.in(transistor_1171_out), .out(transistor_1270_out), .gate(instr_sel[2]));
  Transistor #(.\type ("n")) transistor_1271 (.in(transistor_1270_out), .out(transistor_1271_out), .gate(instr_sel[1]));
  Transistor #(.\type ("n")) transistor_1272 (.in(transistor_1172_out), .out(transistor_1272_out), .gate(instr_sel[2]));
  Transistor #(.\type ("n")) transistor_1273 (.in(transistor_1272_out), .out(transistor_1273_out), .gate(instr_sel[1]));
  Transistor #(.\type ("n")) transistor_1274 (.in(transistor_1173_out), .out(transistor_1274_out), .gate(instr_sel[2]));
  Transistor #(.\type ("n")) transistor_1275 (.in(transistor_1274_out), .out(transistor_1275_out), .gate(instr_sel[1]));
  Transistor #(.\type ("n")) transistor_1276 (.in(transistor_1174_out), .out(transistor_1276_out), .gate(instr_sel[2]));
  Transistor #(.\type ("n")) transistor_1277 (.in(transistor_1276_out), .out(transistor_1277_out), .gate(instr_sel[1]));
  Transistor #(.\type ("n")) transistor_1278 (.in(transistor_1175_out), .out(transistor_1278_out), .gate(instr_sel[2]));
  Transistor #(.\type ("n")) transistor_1279 (.in(transistor_1278_out), .out(transistor_1279_out), .gate(instr_sel[1]));
  Transistor #(.\type ("n")) transistor_1280 (.in(transistor_1176_out), .out(transistor_1280_out), .gate(instr_sel[2]));
  Transistor #(.\type ("n")) transistor_1281 (.in(transistor_1280_out), .out(transistor_1281_out), .gate(instr_sel[1]));
  Transistor #(.\type ("n")) transistor_1282 (.in(transistor_1177_out), .out(transistor_1282_out), .gate(instr_sel[2]));
  Transistor #(.\type ("n")) transistor_1283 (.in(transistor_1282_out), .out(transistor_1283_out), .gate(instr_sel[1]));
  Transistor #(.\type ("n")) transistor_1284 (.in(transistor_1178_out), .out(transistor_1284_out), .gate(instr_sel[2]));
  Transistor #(.\type ("n")) transistor_1285 (.in(transistor_1284_out), .out(transistor_1285_out), .gate(instr_sel[1]));
  Transistor #(.\type ("n")) transistor_1286 (.in(transistor_1179_out), .out(transistor_1286_out), .gate(instr_sel[2]));
  Transistor #(.\type ("n")) transistor_1287 (.in(transistor_1286_out), .out(transistor_1287_out), .gate(instr_sel[1]));
  Transistor #(.\type ("n")) transistor_1288 (.in(transistor_1180_out), .out(transistor_1288_out), .gate(instr_sel[2]));
  Transistor #(.\type ("n")) transistor_1289 (.in(transistor_1288_out), .out(transistor_1289_out), .gate(instr_sel[1]));
  Transistor #(.\type ("n")) transistor_1290 (.in(transistor_1181_out), .out(transistor_1290_out), .gate(instr_sel[2]));
  Transistor #(.\type ("n")) transistor_1291 (.in(transistor_1290_out), .out(transistor_1291_out), .gate(instr_sel[1]));
  Transistor #(.\type ("n")) transistor_1292 (.in(transistor_1182_out), .out(transistor_1292_out), .gate(instr_sel[2]));
  Transistor #(.\type ("n")) transistor_1293 (.in(transistor_1292_out), .out(transistor_1293_out), .gate(instr_sel[1]));
  Transistor #(.\type ("n")) transistor_1294 (.in(transistor_1183_out), .out(transistor_1294_out), .gate(instr_sel[2]));
  Transistor #(.\type ("n")) transistor_1295 (.in(transistor_1294_out), .out(transistor_1295_out), .gate(instr_sel[1]));
  Transistor #(.\type ("n")) transistor_1296 (.in(transistor_1184_out), .out(transistor_1296_out), .gate(instr_sel[2]));
  Transistor #(.\type ("n")) transistor_1297 (.in(transistor_1296_out), .out(transistor_1297_out), .gate(instr_sel[1]));
  Transistor #(.\type ("n")) transistor_1298 (.in(transistor_1185_out), .out(transistor_1298_out), .gate(instr_sel[2]));
  Transistor #(.\type ("n")) transistor_1299 (.in(transistor_1298_out), .out(transistor_1299_out), .gate(instr_sel[1]));
  Transistor #(.\type ("n")) transistor_1300 (.in(transistor_1186_out), .out(transistor_1300_out), .gate(instr_sel[2]));
  Transistor #(.\type ("n")) transistor_1301 (.in(transistor_1300_out), .out(transistor_1301_out), .gate(instr_sel[1]));
  Transistor #(.\type ("n")) transistor_1302 (.in(transistor_1187_out), .out(transistor_1302_out), .gate(instr_sel[2]));
  Transistor #(.\type ("n")) transistor_1303 (.in(transistor_1302_out), .out(transistor_1303_out), .gate(instr_sel[1]));
  Transistor #(.\type ("n")) transistor_1304 (.in(transistor_1188_out), .out(transistor_1304_out), .gate(instr_sel[2]));
  Transistor #(.\type ("n")) transistor_1305 (.in(transistor_1304_out), .out(transistor_1305_out), .gate(instr_sel[1]));
  Transistor #(.\type ("n")) transistor_1306 (.in(transistor_1189_out), .out(transistor_1306_out), .gate(instr_sel[2]));
  Transistor #(.\type ("n")) transistor_1307 (.in(transistor_1306_out), .out(transistor_1307_out), .gate(instr_sel[1]));
  Transistor #(.\type ("n")) transistor_1308 (.in(transistor_1190_out), .out(transistor_1308_out), .gate(instr_sel[2]));
  Transistor #(.\type ("n")) transistor_1309 (.in(transistor_1308_out), .out(transistor_1309_out), .gate(instr_sel[1]));
  Transistor #(.\type ("n")) transistor_1310 (.in(transistor_1191_out), .out(transistor_1310_out), .gate(instr_sel[2]));
  Transistor #(.\type ("n")) transistor_1311 (.in(transistor_1310_out), .out(transistor_1311_out), .gate(instr_sel[1]));
  Transistor #(.\type ("n")) transistor_1312 (.in(transistor_1192_out), .out(transistor_1312_out), .gate(instr_sel[2]));
  Transistor #(.\type ("n")) transistor_1313 (.in(transistor_1312_out), .out(transistor_1313_out), .gate(instr_sel[1]));
  Transistor #(.\type ("n")) transistor_1314 (.in(transistor_1193_out), .out(transistor_1314_out), .gate(instr_sel[2]));
  Transistor #(.\type ("n")) transistor_1315 (.in(transistor_1314_out), .out(transistor_1315_out), .gate(instr_sel[1]));
  Transistor #(.\type ("n")) transistor_1316 (.in(transistor_1194_out), .out(transistor_1316_out), .gate(instr_sel[2]));
  Transistor #(.\type ("n")) transistor_1317 (.in(transistor_1316_out), .out(transistor_1317_out), .gate(instr_sel[1]));
  Transistor #(.\type ("n")) transistor_1318 (.in(transistor_1195_out), .out(transistor_1318_out), .gate(instr_sel[2]));
  Transistor #(.\type ("n")) transistor_1319 (.in(transistor_1318_out), .out(transistor_1319_out), .gate(instr_sel[1]));
  Transistor #(.\type ("n")) transistor_1320 (.in(transistor_1196_out), .out(transistor_1320_out), .gate(instr_sel[2]));
  Transistor #(.\type ("n")) transistor_1321 (.in(transistor_1320_out), .out(transistor_1321_out), .gate(instr_sel[1]));
  Transistor #(.\type ("n")) transistor_1322 (.in(transistor_1197_out), .out(transistor_1322_out), .gate(instr_sel[2]));
  Transistor #(.\type ("n")) transistor_1323 (.in(transistor_1322_out), .out(transistor_1323_out), .gate(instr_sel[1]));
  Transistor #(.\type ("n")) transistor_1324 (.in(transistor_1199_out), .out(transistor_1324_out), .gate(instr_sel[0]));
  Transistor #(.\type ("n")) transistor_1325 (.in(transistor_1201_out), .out(transistor_1325_out), .gate(instr_sel[0]));
  Transistor #(.\type ("n")) transistor_1326 (.in(transistor_1203_out), .out(transistor_1326_out), .gate(instr_sel[0]));
  Transistor #(.\type ("n")) transistor_1327 (.in(transistor_1205_out), .out(transistor_1327_out), .gate(instr_sel[0]));
  Transistor #(.\type ("n")) transistor_1328 (.in(transistor_1207_out), .out(transistor_1328_out), .gate(instr_sel[0]));
  Transistor #(.\type ("n")) transistor_1329 (.in(transistor_1209_out), .out(transistor_1329_out), .gate(instr_sel[0]));
  Transistor #(.\type ("n")) transistor_1330 (.in(transistor_1211_out), .out(transistor_1330_out), .gate(instr_sel[0]));
  Transistor #(.\type ("n")) transistor_1331 (.in(transistor_1213_out), .out(transistor_1331_out), .gate(instr_sel[0]));
  Transistor #(.\type ("n")) transistor_1332 (.in(transistor_1215_out), .out(transistor_1332_out), .gate(instr_sel[0]));
  Transistor #(.\type ("n")) transistor_1333 (.in(transistor_1217_out), .out(transistor_1333_out), .gate(instr_sel[0]));
  Transistor #(.\type ("n")) transistor_1334 (.in(transistor_1219_out), .out(transistor_1334_out), .gate(instr_sel[0]));
  Transistor #(.\type ("n")) transistor_1335 (.in(transistor_1221_out), .out(transistor_1335_out), .gate(instr_sel[0]));
  Transistor #(.\type ("n")) transistor_1336 (.in(transistor_1223_out), .out(transistor_1336_out), .gate(instr_sel[0]));
  Transistor #(.\type ("n")) transistor_1337 (.in(transistor_1225_out), .out(transistor_1337_out), .gate(instr_sel[0]));
  Transistor #(.\type ("n")) transistor_1338 (.in(transistor_1227_out), .out(transistor_1338_out), .gate(instr_sel[0]));
  Transistor #(.\type ("n")) transistor_1339 (.in(transistor_1229_out), .out(transistor_1339_out), .gate(instr_sel[0]));
  Transistor #(.\type ("n")) transistor_1340 (.in(transistor_1231_out), .out(transistor_1340_out), .gate(instr_sel[0]));
  Transistor #(.\type ("n")) transistor_1341 (.in(transistor_1233_out), .out(transistor_1341_out), .gate(instr_sel[0]));
  Transistor #(.\type ("n")) transistor_1342 (.in(transistor_1235_out), .out(transistor_1342_out), .gate(instr_sel[0]));
  Transistor #(.\type ("n")) transistor_1343 (.in(transistor_1237_out), .out(transistor_1343_out), .gate(instr_sel[0]));
  Transistor #(.\type ("n")) transistor_1344 (.in(transistor_1239_out), .out(transistor_1344_out), .gate(instr_sel[0]));
  Transistor #(.\type ("n")) transistor_1345 (.in(transistor_1241_out), .out(transistor_1345_out), .gate(instr_sel[0]));
  Transistor #(.\type ("n")) transistor_1346 (.in(transistor_1243_out), .out(transistor_1346_out), .gate(instr_sel[0]));
  Transistor #(.\type ("n")) transistor_1347 (.in(transistor_1245_out), .out(transistor_1347_out), .gate(instr_sel[0]));
  Transistor #(.\type ("n")) transistor_1348 (.in(transistor_1247_out), .out(transistor_1348_out), .gate(instr_sel[0]));
  Transistor #(.\type ("n")) transistor_1349 (.in(transistor_1249_out), .out(transistor_1349_out), .gate(instr_sel[0]));
  Transistor #(.\type ("n")) transistor_1350 (.in(transistor_1251_out), .out(transistor_1350_out), .gate(instr_sel[0]));
  Transistor #(.\type ("n")) transistor_1351 (.in(transistor_1253_out), .out(transistor_1351_out), .gate(instr_sel[0]));
  Transistor #(.\type ("n")) transistor_1352 (.in(transistor_1255_out), .out(transistor_1352_out), .gate(instr_sel[0]));
  Transistor #(.\type ("n")) transistor_1353 (.in(transistor_1257_out), .out(transistor_1353_out), .gate(instr_sel[0]));
  Transistor #(.\type ("n")) transistor_1354 (.in(transistor_1259_out), .out(transistor_1354_out), .gate(instr_sel[0]));
  Transistor #(.\type ("n")) transistor_1355 (.in(transistor_1261_out), .out(transistor_1355_out), .gate(instr_sel[0]));
  Transistor #(.\type ("n")) transistor_1356 (.in(transistor_1263_out), .out(transistor_1356_out), .gate(instr_sel[0]));
  Transistor #(.\type ("n")) transistor_1357 (.in(transistor_1265_out), .out(transistor_1357_out), .gate(instr_sel[0]));
  Transistor #(.\type ("n")) transistor_1358 (.in(transistor_1267_out), .out(transistor_1358_out), .gate(instr_sel[0]));
  Transistor #(.\type ("n")) transistor_1359 (.in(transistor_1269_out), .out(transistor_1359_out), .gate(instr_sel[0]));
  Transistor #(.\type ("n")) transistor_1360 (.in(transistor_1271_out), .out(transistor_1360_out), .gate(instr_sel[0]));
  Transistor #(.\type ("n")) transistor_1361 (.in(transistor_1273_out), .out(transistor_1361_out), .gate(instr_sel[0]));
  Transistor #(.\type ("n")) transistor_1362 (.in(transistor_1275_out), .out(transistor_1362_out), .gate(instr_sel[0]));
  Transistor #(.\type ("n")) transistor_1363 (.in(transistor_1277_out), .out(transistor_1363_out), .gate(instr_sel[0]));
  Transistor #(.\type ("n")) transistor_1364 (.in(transistor_1279_out), .out(transistor_1364_out), .gate(instr_sel[0]));
  Transistor #(.\type ("n")) transistor_1365 (.in(transistor_1281_out), .out(transistor_1365_out), .gate(instr_sel[0]));
  Transistor #(.\type ("n")) transistor_1366 (.in(transistor_1283_out), .out(transistor_1366_out), .gate(instr_sel[0]));
  Transistor #(.\type ("n")) transistor_1367 (.in(transistor_1285_out), .out(transistor_1367_out), .gate(instr_sel[0]));
  Transistor #(.\type ("n")) transistor_1368 (.in(transistor_1287_out), .out(transistor_1368_out), .gate(instr_sel[0]));
  Transistor #(.\type ("n")) transistor_1369 (.in(transistor_1289_out), .out(transistor_1369_out), .gate(instr_sel[0]));
  Transistor #(.\type ("n")) transistor_1370 (.in(transistor_1291_out), .out(transistor_1370_out), .gate(instr_sel[0]));
  Transistor #(.\type ("n")) transistor_1371 (.in(transistor_1293_out), .out(transistor_1371_out), .gate(instr_sel[0]));
  Transistor #(.\type ("n")) transistor_1372 (.in(transistor_1295_out), .out(transistor_1372_out), .gate(instr_sel[0]));
  Transistor #(.\type ("n")) transistor_1373 (.in(transistor_1297_out), .out(transistor_1373_out), .gate(instr_sel[0]));
  Transistor #(.\type ("n")) transistor_1374 (.in(transistor_1299_out), .out(transistor_1374_out), .gate(instr_sel[0]));
  Transistor #(.\type ("n")) transistor_1375 (.in(transistor_1301_out), .out(transistor_1375_out), .gate(instr_sel[0]));
  Transistor #(.\type ("n")) transistor_1376 (.in(transistor_1303_out), .out(transistor_1376_out), .gate(instr_sel[0]));
  Transistor #(.\type ("n")) transistor_1377 (.in(transistor_1305_out), .out(transistor_1377_out), .gate(instr_sel[0]));
  Transistor #(.\type ("n")) transistor_1378 (.in(transistor_1307_out), .out(transistor_1378_out), .gate(instr_sel[0]));
  Transistor #(.\type ("n")) transistor_1379 (.in(transistor_1309_out), .out(transistor_1379_out), .gate(instr_sel[0]));
  Transistor #(.\type ("n")) transistor_1380 (.in(transistor_1311_out), .out(transistor_1380_out), .gate(instr_sel[0]));
  Transistor #(.\type ("n")) transistor_1381 (.in(transistor_1313_out), .out(transistor_1381_out), .gate(instr_sel[0]));
  Transistor #(.\type ("n")) transistor_1382 (.in(transistor_1315_out), .out(transistor_1382_out), .gate(instr_sel[0]));
  Transistor #(.\type ("n")) transistor_1383 (.in(transistor_1317_out), .out(transistor_1383_out), .gate(instr_sel[0]));
  Transistor #(.\type ("n")) transistor_1384 (.in(transistor_1319_out), .out(transistor_1384_out), .gate(instr_sel[0]));
  Transistor #(.\type ("n")) transistor_1385 (.in(transistor_1321_out), .out(transistor_1385_out), .gate(instr_sel[0]));
  Transistor #(.\type ("n")) transistor_1386 (.in(transistor_1323_out), .out(transistor_1386_out), .gate(instr_sel[0]));
  assign transistor_1324_out = clk2 ? 1'b1 : 1'bz;  // Controlled_Buffer controlled_buffer_1
  assign transistor_1325_out = clk2 ? 1'b1 : 1'bz;  // Controlled_Buffer controlled_buffer_2
  assign transistor_1326_out = clk2 ? 1'b1 : 1'bz;  // Controlled_Buffer controlled_buffer_3
  assign transistor_1327_out = clk2 ? 1'b1 : 1'bz;  // Controlled_Buffer controlled_buffer_4
  assign transistor_1328_out = clk2 ? 1'b1 : 1'bz;  // Controlled_Buffer controlled_buffer_5
  assign transistor_1329_out = clk2 ? 1'b1 : 1'bz;  // Controlled_Buffer controlled_buffer_6
  assign transistor_1330_out = clk2 ? 1'b1 : 1'bz;  // Controlled_Buffer controlled_buffer_7
  assign transistor_1331_out = clk2 ? 1'b1 : 1'bz;  // Controlled_Buffer controlled_buffer_8
  assign transistor_1332_out = clk2 ? 1'b1 : 1'bz;  // Controlled_Buffer controlled_buffer_9
  assign transistor_1333_out = clk2 ? 1'b1 : 1'bz;  // Controlled_Buffer controlled_buffer_10
  assign transistor_1334_out = clk2 ? 1'b1 : 1'bz;  // Controlled_Buffer controlled_buffer_11
  Transistor #(.\type ("n")) transistor_1387 (.in(transistor_1335_out), .out(transistor_1387_out), .gate(mod_sel));
  Transistor #(.\type ("n")) transistor_1388 (.in(transistor_1337_out), .out(transistor_1388_out), .gate(mod_sel));
  Transistor #(.\type ("n")) transistor_1389 (.in(transistor_1339_out), .out(transistor_1389_out), .gate(mod_sel));
  Transistor #(.\type ("n")) transistor_1390 (.in(transistor_1341_out), .out(transistor_1390_out), .gate(mod_sel));
  Transistor #(.\type ("n")) transistor_1391 (.in(transistor_1343_out), .out(transistor_1391_out), .gate(mod_sel));
  Transistor #(.\type ("n")) transistor_1392 (.in(transistor_1345_out), .out(transistor_1392_out), .gate(mod_sel));
  Transistor #(.\type ("n")) transistor_1393 (.in(transistor_1347_out), .out(transistor_1393_out), .gate(mod_sel));
  Transistor #(.\type ("n")) transistor_1394 (.in(transistor_1349_out), .out(transistor_1394_out), .gate(mod_sel));
  Transistor #(.\type ("n")) transistor_1395 (.in(transistor_1351_out), .out(transistor_1395_out), .gate(mod_sel));
  Transistor #(.\type ("n")) transistor_1396 (.in(transistor_1353_out), .out(transistor_1396_out), .gate(mod_sel));
  Transistor #(.\type ("n")) transistor_1397 (.in(transistor_1355_out), .out(transistor_1397_out), .gate(mod_sel));
  Transistor #(.\type ("n")) transistor_1398 (.in(transistor_1357_out), .out(transistor_1398_out), .gate(mod_sel));
  Transistor #(.\type ("n")) transistor_1399 (.in(transistor_1359_out), .out(transistor_1399_out), .gate(mod_sel));
  Transistor #(.\type ("n")) transistor_1400 (.in(transistor_1361_out), .out(transistor_1400_out), .gate(mod_sel));
  Transistor #(.\type ("n")) transistor_1401 (.in(transistor_1363_out), .out(transistor_1401_out), .gate(mod_sel));
  Transistor #(.\type ("n")) transistor_1402 (.in(transistor_1365_out), .out(transistor_1402_out), .gate(mod_sel));
  Transistor #(.\type ("n")) transistor_1403 (.in(transistor_1367_out), .out(transistor_1403_out), .gate(mod_sel));
  Transistor #(.\type ("n")) transistor_1404 (.in(transistor_1369_out), .out(transistor_1404_out), .gate(mod_sel));
  Transistor #(.\type ("n")) transistor_1405 (.in(transistor_1371_out), .out(transistor_1405_out), .gate(mod_sel));
  Transistor #(.\type ("n")) transistor_1406 (.in(transistor_1373_out), .out(transistor_1406_out), .gate(mod_sel));
  Transistor #(.\type ("n")) transistor_1407 (.in(transistor_1375_out), .out(transistor_1407_out), .gate(mod_sel));
  Transistor #(.\type ("n")) transistor_1408 (.in(transistor_1377_out), .out(transistor_1408_out), .gate(mod_sel));
  Transistor #(.\type ("n")) transistor_1409 (.in(transistor_1379_out), .out(transistor_1409_out), .gate(mod_sel));
  Transistor #(.\type ("n")) transistor_1410 (.in(transistor_1381_out), .out(transistor_1410_out), .gate(mod_sel));
  Transistor #(.\type ("n")) transistor_1411 (.in(transistor_1383_out), .out(transistor_1411_out), .gate(mod_sel));
  Transistor #(.\type ("n")) transistor_1412 (.in(transistor_1385_out), .out(transistor_1412_out), .gate(mod_sel));
  assign transistor_1387_out = clk2 ? 1'b1 : 1'bz;  // Controlled_Buffer controlled_buffer_12
  Transistor #(.\type ("n")) transistor_1413 (.in(transistor_1336_out), .out(transistor_1387_out), .gate(car_sel));
  assign transistor_1388_out = clk2 ? 1'b1 : 1'bz;  // Controlled_Buffer controlled_buffer_13
  Transistor #(.\type ("n")) transistor_1414 (.in(transistor_1338_out), .out(transistor_1388_out), .gate(car_sel));
  assign transistor_1389_out = clk2 ? 1'b1 : 1'bz;  // Controlled_Buffer controlled_buffer_14
  Transistor #(.\type ("n")) transistor_1415 (.in(transistor_1340_out), .out(transistor_1389_out), .gate(car_sel));
  assign transistor_1390_out = clk2 ? 1'b1 : 1'bz;  // Controlled_Buffer controlled_buffer_15
  Transistor #(.\type ("n")) transistor_1416 (.in(transistor_1342_out), .out(transistor_1390_out), .gate(car_sel));
  assign transistor_1391_out = clk2 ? 1'b1 : 1'bz;  // Controlled_Buffer controlled_buffer_16
  Transistor #(.\type ("n")) transistor_1417 (.in(transistor_1344_out), .out(transistor_1391_out), .gate(car_sel));
  assign transistor_1392_out = clk2 ? 1'b1 : 1'bz;  // Controlled_Buffer controlled_buffer_17
  Transistor #(.\type ("n")) transistor_1418 (.in(transistor_1346_out), .out(transistor_1392_out), .gate(car_sel));
  assign transistor_1393_out = clk2 ? 1'b1 : 1'bz;  // Controlled_Buffer controlled_buffer_18
  Transistor #(.\type ("n")) transistor_1419 (.in(transistor_1348_out), .out(transistor_1393_out), .gate(car_sel));
  assign transistor_1394_out = clk2 ? 1'b1 : 1'bz;  // Controlled_Buffer controlled_buffer_19
  Transistor #(.\type ("n")) transistor_1420 (.in(transistor_1350_out), .out(transistor_1394_out), .gate(car_sel));
  assign transistor_1395_out = clk2 ? 1'b1 : 1'bz;  // Controlled_Buffer controlled_buffer_20
  Transistor #(.\type ("n")) transistor_1421 (.in(transistor_1352_out), .out(transistor_1395_out), .gate(car_sel));
  assign transistor_1396_out = clk2 ? 1'b1 : 1'bz;  // Controlled_Buffer controlled_buffer_21
  Transistor #(.\type ("n")) transistor_1422 (.in(transistor_1354_out), .out(transistor_1396_out), .gate(car_sel));
  assign transistor_1397_out = clk2 ? 1'b1 : 1'bz;  // Controlled_Buffer controlled_buffer_22
  Transistor #(.\type ("n")) transistor_1423 (.in(transistor_1356_out), .out(transistor_1397_out), .gate(car_sel));
  assign transistor_1398_out = clk2 ? 1'b1 : 1'bz;  // Controlled_Buffer controlled_buffer_23
  Transistor #(.\type ("n")) transistor_1424 (.in(transistor_1358_out), .out(transistor_1398_out), .gate(car_sel));
  assign transistor_1399_out = clk2 ? 1'b1 : 1'bz;  // Controlled_Buffer controlled_buffer_24
  Transistor #(.\type ("n")) transistor_1425 (.in(transistor_1360_out), .out(transistor_1399_out), .gate(car_sel));
  assign transistor_1400_out = clk2 ? 1'b1 : 1'bz;  // Controlled_Buffer controlled_buffer_25
  Transistor #(.\type ("n")) transistor_1426 (.in(transistor_1362_out), .out(transistor_1400_out), .gate(car_sel));
  assign transistor_1401_out = clk2 ? 1'b1 : 1'bz;  // Controlled_Buffer controlled_buffer_26
  Transistor #(.\type ("n")) transistor_1427 (.in(transistor_1364_out), .out(transistor_1401_out), .gate(car_sel));
  assign transistor_1402_out = clk2 ? 1'b1 : 1'bz;  // Controlled_Buffer controlled_buffer_27
  Transistor #(.\type ("n")) transistor_1428 (.in(transistor_1366_out), .out(transistor_1402_out), .gate(car_sel));
  assign transistor_1403_out = clk2 ? 1'b1 : 1'bz;  // Controlled_Buffer controlled_buffer_28
  Transistor #(.\type ("n")) transistor_1429 (.in(transistor_1368_out), .out(transistor_1403_out), .gate(car_sel));
  assign transistor_1404_out = clk2 ? 1'b1 : 1'bz;  // Controlled_Buffer controlled_buffer_29
  Transistor #(.\type ("n")) transistor_1430 (.in(transistor_1370_out), .out(transistor_1404_out), .gate(car_sel));
  assign transistor_1405_out = clk2 ? 1'b1 : 1'bz;  // Controlled_Buffer controlled_buffer_30
  Transistor #(.\type ("n")) transistor_1431 (.in(transistor_1372_out), .out(transistor_1405_out), .gate(car_sel));
  assign transistor_1406_out = clk2 ? 1'b1 : 1'bz;  // Controlled_Buffer controlled_buffer_31
  Transistor #(.\type ("n")) transistor_1432 (.in(transistor_1374_out), .out(transistor_1406_out), .gate(car_sel));
  assign transistor_1407_out = clk2 ? 1'b1 : 1'bz;  // Controlled_Buffer controlled_buffer_32
  Transistor #(.\type ("n")) transistor_1433 (.in(transistor_1376_out), .out(transistor_1407_out), .gate(car_sel));
  assign transistor_1408_out = clk2 ? 1'b1 : 1'bz;  // Controlled_Buffer controlled_buffer_33
  Transistor #(.\type ("n")) transistor_1434 (.in(transistor_1378_out), .out(transistor_1408_out), .gate(car_sel));
  assign transistor_1409_out = clk2 ? 1'b1 : 1'bz;  // Controlled_Buffer controlled_buffer_34
  Transistor #(.\type ("n")) transistor_1435 (.in(transistor_1380_out), .out(transistor_1409_out), .gate(car_sel));
  assign transistor_1410_out = clk2 ? 1'b1 : 1'bz;  // Controlled_Buffer controlled_buffer_35
  Transistor #(.\type ("n")) transistor_1436 (.in(transistor_1382_out), .out(transistor_1410_out), .gate(car_sel));
  assign transistor_1411_out = clk2 ? 1'b1 : 1'bz;  // Controlled_Buffer controlled_buffer_36
  Transistor #(.\type ("n")) transistor_1437 (.in(transistor_1384_out), .out(transistor_1411_out), .gate(car_sel));
  assign transistor_1412_out = clk2 ? 1'b1 : 1'bz;  // Controlled_Buffer controlled_buffer_37
  Transistor #(.\type ("n")) transistor_1438 (.in(transistor_1386_out), .out(transistor_1412_out), .gate(car_sel));
  instrument_out instrument_out_1 (.value(transistor_1324_out), .clk1(clk1), .oe(out_sel2), .out_4(tl[0]));
  instrument_out instrument_out_2 (.value(transistor_1325_out), .clk1(clk1), .oe(out_sel2), .out_4(tl[1]));
  instrument_out instrument_out_3 (.value(transistor_1326_out), .clk1(clk1), .oe(out_sel2), .out_4(tl[2]));
  instrument_out instrument_out_4 (.value(transistor_1327_out), .clk1(clk1), .oe(out_sel2), .out_4(tl[3]));
  instrument_out instrument_out_5 (.value(transistor_1328_out), .clk1(clk1), .oe(out_sel2), .out_4(tl[4]));
  instrument_out instrument_out_6 (.value(transistor_1329_out), .clk1(clk1), .oe(out_sel2), .out_4(tl[5]));
  instrument_out instrument_out_7 (.value(transistor_1330_out), .clk1(clk1), .oe(out_sel1), .out_4(dc));
  instrument_out instrument_out_8 (.value(transistor_1331_out), .clk1(clk1), .oe(out_sel1), .out_4(dm));
  instrument_out instrument_out_9 (.value(transistor_1332_out), .clk1(clk1), .oe(out_sel1), .out_4(out_12[2]));
  instrument_out instrument_out_10 (.value(transistor_1333_out), .clk1(clk1), .oe(out_sel1), .out_4(out_12[1]));
  instrument_out instrument_out_11 (.value(transistor_1334_out), .clk1(clk1), .oe(out_sel1), .out_4(out_12[0]));
  instrument_out instrument_out_12 (.value(transistor_1387_out), .clk1(clk1), .oe(out_sel1), .out_4(am));
  instrument_out instrument_out_13 (.value(transistor_1388_out), .clk1(clk1), .oe(out_sel1), .out_4(vib));
  instrument_out instrument_out_14 (.value(transistor_1389_out), .clk1(clk1), .oe(out_sel1), .out_4(et));
  instrument_out instrument_out_15 (.value(transistor_1390_out), .clk1(clk1), .oe(out_sel1), .out_4(ksr));
  instrument_out instrument_out_16 (.value(transistor_1391_out), .clk1(clk1), .oe(out_sel1), .out_4(multi[3]));
  instrument_out instrument_out_17 (.value(transistor_1392_out), .clk1(clk1), .oe(out_sel1), .out_4(multi[2]));
  instrument_out instrument_out_18 (.value(transistor_1393_out), .clk1(clk1), .oe(out_sel1), .out_4(multi[1]));
  instrument_out instrument_out_19 (.value(transistor_1394_out), .clk1(clk1), .oe(out_sel1), .out_4(multi[0]));
  instrument_out instrument_out_20 (.value(transistor_1395_out), .clk1(clk1), .oe(out_sel1), .out_4(ksl[1]));
  instrument_out instrument_out_21 (.value(transistor_1396_out), .clk1(clk1), .oe(out_sel1), .out_4(ksl[0]));
  instrument_out instrument_out_22 (.value(transistor_1397_out), .clk1(clk1), .oe(out_sel1), .out_4(ar[3]));
  instrument_out instrument_out_23 (.value(transistor_1398_out), .clk1(clk1), .oe(out_sel1), .out_4(ar[2]));
  instrument_out instrument_out_24 (.value(transistor_1399_out), .clk1(clk1), .oe(out_sel1), .out_4(ar[1]));
  instrument_out instrument_out_25 (.value(transistor_1400_out), .clk1(clk1), .oe(out_sel1), .out_4(ar[0]));
  instrument_out instrument_out_26 (.value(transistor_1401_out), .clk1(clk1), .oe(out_sel1), .out_4(dr[3]));
  instrument_out instrument_out_27 (.value(transistor_1402_out), .clk1(clk1), .oe(out_sel1), .out_4(dr[2]));
  instrument_out instrument_out_28 (.value(transistor_1403_out), .clk1(clk1), .oe(out_sel1), .out_4(dr[1]));
  instrument_out instrument_out_29 (.value(transistor_1404_out), .clk1(clk1), .oe(out_sel1), .out_4(dr[0]));
  instrument_out instrument_out_30 (.value(transistor_1405_out), .clk1(clk1), .oe(out_sel1), .out_4(sl[3]));
  instrument_out instrument_out_31 (.value(transistor_1406_out), .clk1(clk1), .oe(out_sel1), .out_4(sl[2]));
  instrument_out instrument_out_32 (.value(transistor_1407_out), .clk1(clk1), .oe(out_sel1), .out_4(sl[1]));
  instrument_out instrument_out_33 (.value(transistor_1408_out), .clk1(clk1), .oe(out_sel1), .out_4(sl[0]));
  instrument_out instrument_out_34 (.value(transistor_1409_out), .clk1(clk1), .oe(out_sel1), .out_4(rr[3]));
  instrument_out instrument_out_35 (.value(transistor_1410_out), .clk1(clk1), .oe(out_sel1), .out_4(rr[2]));
  instrument_out instrument_out_36 (.value(transistor_1411_out), .clk1(clk1), .oe(out_sel1), .out_4(rr[1]));
  instrument_out instrument_out_37 (.value(transistor_1412_out), .clk1(clk1), .oe(out_sel1), .out_4(rr[0]));
endmodule

module instrument_out (
  input  value,
  input  clk1,
  input  oe,
  output out_4
);

  wire d_ff_1_qn, d_ff_2_q, d_ff_3_qn;

  D_Flip_Flop #(.trigger("high")) d_ff_1 (.D(value), .clk(1'b1), .Qn(d_ff_1_qn));  // open: Q, preset, reset
  D_Flip_Flop #(.trigger("high")) d_ff_2 (.D(d_ff_1_qn), .clk(1'b1), .Q(d_ff_2_q));  // open: Qn, preset, reset
  D_Flip_Flop #(.trigger("high")) d_ff_3 (.D(d_ff_2_q), .clk(clk1), .Qn(d_ff_3_qn));  // open: Q, preset, reset
  assign out_4 = oe ? d_ff_3_qn : 1'bz;  // Controlled_Buffer controlled_buffer_1
endmodule

module instrument_ds1001 (
  input  [20:0] instr_sel,
  input  mod_sel,
  input  car_sel,
  input  out_sel1,
  input  out_sel2,
  input  clk1,
  input  clk2,
  input  clk2_inv,
  output [5:0] tl,
  output dc,
  output dm,
  output [2:0] fb,
  output am,
  output vib,
  output et,
  output ksr,
  output [3:0] multi,
  output [1:0] ksl,
  output [3:0] ar,
  output [3:0] dr,
  output [3:0] sl,
  output [3:0] rr
);

  wire transistor_1_out, transistor_2_out, transistor_3_out, transistor_4_out, transistor_5_out,
       transistor_6_out, transistor_7_out, transistor_8_out, transistor_9_out, transistor_10_out,
       transistor_11_out, transistor_12_out, transistor_13_out, transistor_14_out, transistor_15_out,
       transistor_16_out, transistor_17_out, transistor_18_out, transistor_19_out, transistor_20_out,
       transistor_21_out, transistor_22_out, transistor_23_out, transistor_24_out, transistor_25_out,
       transistor_26_out, transistor_27_out, transistor_28_out, transistor_29_out, transistor_30_out,
       transistor_31_out, transistor_32_out, transistor_33_out, transistor_34_out, transistor_35_out,
       transistor_36_out, transistor_37_out, transistor_38_out, transistor_39_out, transistor_40_out,
       transistor_41_out, transistor_42_out, transistor_43_out, transistor_44_out, transistor_45_out,
       transistor_46_out, transistor_47_out, transistor_48_out, transistor_49_out, transistor_50_out,
       transistor_51_out, transistor_52_out, transistor_53_out, transistor_54_out, transistor_55_out,
       transistor_56_out, transistor_57_out, transistor_58_out, transistor_59_out, transistor_60_out,
       transistor_61_out, transistor_62_out, transistor_63_out, transistor_64_out, transistor_65_out,
       transistor_66_out, transistor_67_out, transistor_68_out, transistor_69_out, transistor_70_out,
       transistor_71_out, transistor_72_out, transistor_73_out, transistor_74_out, transistor_75_out,
       transistor_76_out, transistor_77_out, transistor_78_out, transistor_79_out, transistor_80_out,
       transistor_81_out, transistor_82_out, transistor_83_out, transistor_84_out, transistor_85_out,
       transistor_86_out, transistor_87_out, transistor_88_out, transistor_89_out, transistor_90_out,
       transistor_91_out, transistor_92_out, transistor_93_out, transistor_94_out, transistor_95_out,
       transistor_96_out, transistor_97_out, transistor_98_out, transistor_99_out, transistor_100_out,
       transistor_101_out, transistor_102_out, transistor_103_out, transistor_104_out, transistor_105_out,
       transistor_106_out, transistor_107_out, transistor_108_out, transistor_109_out, transistor_110_out,
       transistor_111_out, transistor_112_out, transistor_113_out, transistor_114_out, transistor_115_out,
       transistor_116_out, transistor_117_out, transistor_118_out, transistor_119_out, transistor_120_out,
       transistor_121_out, transistor_122_out, transistor_123_out, transistor_124_out, transistor_125_out,
       transistor_126_out, transistor_127_out, transistor_128_out, transistor_129_out, transistor_130_out,
       transistor_131_out, transistor_132_out, transistor_133_out, transistor_134_out, transistor_135_out,
       transistor_136_out, transistor_137_out, transistor_138_out, transistor_139_out, transistor_140_out,
       transistor_141_out, transistor_142_out, transistor_143_out, transistor_144_out, transistor_145_out,
       transistor_146_out, transistor_147_out, transistor_148_out, transistor_149_out, transistor_150_out,
       transistor_151_out, transistor_152_out, transistor_153_out, transistor_154_out, transistor_155_out,
       transistor_156_out, transistor_157_out, transistor_158_out, transistor_159_out, transistor_160_out,
       transistor_161_out, transistor_162_out, transistor_163_out, transistor_164_out, transistor_165_out,
       transistor_166_out, transistor_167_out, transistor_168_out, transistor_169_out, transistor_170_out,
       transistor_171_out, transistor_172_out, transistor_173_out, transistor_174_out, transistor_175_out,
       transistor_176_out, transistor_177_out, transistor_178_out, transistor_179_out, transistor_180_out,
       transistor_181_out, transistor_182_out, transistor_183_out, transistor_184_out, transistor_185_out,
       transistor_186_out, transistor_187_out, transistor_188_out, transistor_189_out, transistor_190_out,
       transistor_191_out, transistor_192_out, transistor_193_out, transistor_194_out, transistor_195_out,
       transistor_196_out, transistor_197_out, transistor_198_out, transistor_199_out, transistor_200_out,
       transistor_201_out, transistor_202_out, transistor_203_out, transistor_204_out, transistor_205_out,
       transistor_206_out, transistor_207_out, transistor_208_out, transistor_209_out, transistor_210_out,
       transistor_211_out, transistor_212_out, transistor_213_out, transistor_214_out, transistor_215_out,
       transistor_216_out, transistor_217_out, transistor_218_out, transistor_219_out, transistor_220_out,
       transistor_221_out, transistor_222_out, transistor_223_out, transistor_224_out, transistor_225_out,
       transistor_226_out, transistor_227_out, transistor_228_out, transistor_229_out, transistor_230_out,
       transistor_231_out, transistor_232_out, transistor_233_out, transistor_234_out, transistor_235_out,
       transistor_236_out, transistor_237_out, transistor_238_out, transistor_239_out, transistor_240_out,
       transistor_241_out, transistor_242_out, transistor_243_out, transistor_244_out, transistor_245_out,
       transistor_246_out, transistor_247_out, transistor_248_out, transistor_249_out, transistor_250_out,
       transistor_251_out, transistor_252_out, transistor_253_out, transistor_254_out, transistor_255_out,
       transistor_256_out, transistor_257_out, transistor_258_out, transistor_259_out, transistor_260_out,
       transistor_261_out, transistor_262_out, transistor_263_out, transistor_264_out, transistor_265_out,
       transistor_266_out, transistor_267_out, transistor_268_out, transistor_269_out, transistor_270_out,
       transistor_271_out, transistor_272_out, transistor_273_out, transistor_274_out, transistor_275_out,
       transistor_276_out, transistor_277_out, transistor_278_out, transistor_279_out, transistor_280_out,
       transistor_281_out, transistor_282_out, transistor_283_out, transistor_284_out, transistor_285_out,
       transistor_286_out, transistor_287_out, transistor_288_out, transistor_289_out, transistor_290_out,
       transistor_291_out, transistor_292_out, transistor_293_out, transistor_294_out, transistor_295_out,
       transistor_296_out, transistor_297_out, transistor_298_out, transistor_299_out, transistor_300_out,
       transistor_301_out, transistor_302_out, transistor_303_out, transistor_304_out, transistor_305_out,
       transistor_306_out, transistor_307_out, transistor_308_out, transistor_309_out, transistor_310_out,
       transistor_311_out, transistor_312_out, transistor_313_out, transistor_314_out, transistor_315_out,
       transistor_316_out, transistor_317_out, transistor_318_out, transistor_319_out, transistor_320_out,
       transistor_321_out, transistor_322_out, transistor_323_out, transistor_324_out, transistor_325_out,
       transistor_326_out, transistor_327_out, transistor_328_out, transistor_329_out, transistor_330_out,
       transistor_331_out, transistor_332_out, transistor_333_out, transistor_334_out, transistor_335_out,
       transistor_336_out, transistor_337_out, transistor_338_out, transistor_339_out, transistor_340_out,
       transistor_341_out, transistor_342_out, transistor_343_out, transistor_344_out, transistor_345_out,
       transistor_346_out, transistor_347_out, transistor_348_out, transistor_349_out, transistor_350_out,
       transistor_351_out, transistor_352_out, transistor_353_out, transistor_354_out, transistor_355_out,
       transistor_356_out, transistor_357_out, transistor_358_out, transistor_359_out, transistor_360_out,
       transistor_361_out, transistor_362_out, transistor_363_out, transistor_364_out, transistor_365_out,
       transistor_366_out, transistor_367_out, transistor_368_out, transistor_369_out, transistor_370_out,
       transistor_371_out, transistor_372_out, transistor_373_out, transistor_374_out, transistor_375_out,
       transistor_376_out, transistor_377_out, transistor_378_out, transistor_379_out, transistor_380_out,
       transistor_381_out, transistor_382_out, transistor_383_out, transistor_384_out, transistor_385_out,
       transistor_386_out, transistor_387_out, transistor_388_out, transistor_389_out, transistor_390_out,
       transistor_391_out, transistor_392_out, transistor_393_out, transistor_394_out, transistor_395_out,
       transistor_396_out, transistor_397_out, transistor_398_out, transistor_399_out, transistor_400_out,
       transistor_401_out, transistor_402_out, transistor_403_out, transistor_404_out, transistor_405_out,
       transistor_406_out, transistor_407_out, transistor_408_out, transistor_409_out, transistor_410_out,
       transistor_411_out, transistor_412_out, transistor_413_out, transistor_414_out, transistor_415_out,
       transistor_416_out, transistor_417_out, transistor_418_out, transistor_419_out, transistor_420_out,
       transistor_421_out, transistor_422_out, transistor_423_out, transistor_424_out, transistor_425_out,
       transistor_426_out, transistor_427_out, transistor_428_out, transistor_429_out, transistor_430_out,
       transistor_431_out, transistor_432_out, transistor_433_out, transistor_434_out, transistor_435_out,
       transistor_436_out, transistor_437_out, transistor_438_out, transistor_439_out, transistor_440_out,
       transistor_441_out, transistor_442_out, transistor_443_out, transistor_444_out, transistor_445_out,
       transistor_446_out, transistor_447_out, transistor_448_out, transistor_449_out, transistor_450_out,
       transistor_451_out, transistor_452_out, transistor_453_out, transistor_454_out, transistor_455_out,
       transistor_456_out, transistor_457_out, transistor_458_out, transistor_459_out, transistor_460_out,
       transistor_461_out, transistor_462_out, transistor_463_out, transistor_464_out, transistor_465_out,
       transistor_466_out, transistor_467_out, transistor_468_out, transistor_469_out, transistor_470_out,
       transistor_471_out, transistor_472_out, transistor_473_out, transistor_474_out, transistor_475_out,
       transistor_476_out, transistor_477_out, transistor_478_out, transistor_479_out, transistor_480_out,
       transistor_481_out, transistor_482_out, transistor_483_out, transistor_484_out, transistor_485_out,
       transistor_486_out, transistor_487_out, transistor_488_out, transistor_489_out, transistor_490_out,
       transistor_491_out, transistor_492_out, transistor_493_out;

  Transistor #(.\type ("n")) transistor_1 (.in(1'b0), .out(transistor_1_out), .gate(clk2_inv));
  Transistor #(.\type ("n")) transistor_2 (.in(1'b0), .out(transistor_2_out), .gate(clk2_inv));
  Transistor #(.\type ("n")) transistor_3 (.in(1'b0), .out(transistor_3_out), .gate(clk2_inv));
  Transistor #(.\type ("n")) transistor_4 (.in(1'b0), .out(transistor_4_out), .gate(clk2_inv));
  Transistor #(.\type ("n")) transistor_5 (.in(1'b0), .out(transistor_5_out), .gate(clk2_inv));
  Transistor #(.\type ("n")) transistor_6 (.in(1'b0), .out(transistor_6_out), .gate(clk2_inv));
  Transistor #(.\type ("n")) transistor_7 (.in(1'b0), .out(transistor_7_out), .gate(clk2_inv));
  Transistor #(.\type ("n")) transistor_8 (.in(1'b0), .out(transistor_8_out), .gate(clk2_inv));
  Transistor #(.\type ("n")) transistor_9 (.in(1'b0), .out(transistor_9_out), .gate(clk2_inv));
  Transistor #(.\type ("n")) transistor_10 (.in(1'b0), .out(transistor_10_out), .gate(clk2_inv));
  Transistor #(.\type ("n")) transistor_11 (.in(1'b0), .out(transistor_11_out), .gate(clk2_inv));
  Transistor #(.\type ("n")) transistor_12 (.in(1'b0), .out(transistor_12_out), .gate(clk2_inv));
  Transistor #(.\type ("n")) transistor_13 (.in(1'b0), .out(transistor_13_out), .gate(clk2_inv));
  Transistor #(.\type ("n")) transistor_14 (.in(1'b0), .out(transistor_14_out), .gate(clk2_inv));
  Transistor #(.\type ("n")) transistor_15 (.in(1'b0), .out(transistor_15_out), .gate(clk2_inv));
  Transistor #(.\type ("n")) transistor_16 (.in(1'b0), .out(transistor_16_out), .gate(clk2_inv));
  Transistor #(.\type ("n")) transistor_17 (.in(1'b0), .out(transistor_17_out), .gate(clk2_inv));
  Transistor #(.\type ("n")) transistor_18 (.in(1'b0), .out(transistor_18_out), .gate(clk2_inv));
  Transistor #(.\type ("n")) transistor_19 (.in(1'b0), .out(transistor_19_out), .gate(clk2_inv));
  Transistor #(.\type ("n")) transistor_20 (.in(1'b0), .out(transistor_20_out), .gate(clk2_inv));
  Transistor #(.\type ("n")) transistor_21 (.in(1'b0), .out(transistor_21_out), .gate(clk2_inv));
  Transistor #(.\type ("n")) transistor_22 (.in(1'b0), .out(transistor_22_out), .gate(clk2_inv));
  Transistor #(.\type ("n")) transistor_23 (.in(1'b0), .out(transistor_23_out), .gate(clk2_inv));
  Transistor #(.\type ("n")) transistor_24 (.in(1'b0), .out(transistor_24_out), .gate(clk2_inv));
  Transistor #(.\type ("n")) transistor_25 (.in(1'b0), .out(transistor_25_out), .gate(clk2_inv));
  Transistor #(.\type ("n")) transistor_26 (.in(1'b0), .out(transistor_26_out), .gate(clk2_inv));
  Transistor #(.\type ("n")) transistor_27 (.in(1'b0), .out(transistor_27_out), .gate(clk2_inv));
  Transistor #(.\type ("n")) transistor_28 (.in(1'b0), .out(transistor_28_out), .gate(clk2_inv));
  Transistor #(.\type ("n")) transistor_29 (.in(1'b0), .out(transistor_29_out), .gate(clk2_inv));
  Transistor #(.\type ("n")) transistor_30 (.in(1'b0), .out(transistor_30_out), .gate(clk2_inv));
  Transistor #(.\type ("n")) transistor_31 (.in(1'b0), .out(transistor_31_out), .gate(clk2_inv));
  Transistor #(.\type ("n")) transistor_32 (.in(1'b0), .out(transistor_32_out), .gate(clk2_inv));
  Transistor #(.\type ("n")) transistor_33 (.in(1'b0), .out(transistor_33_out), .gate(clk2_inv));
  Transistor #(.\type ("n")) transistor_34 (.in(1'b0), .out(transistor_34_out), .gate(clk2_inv));
  Transistor #(.\type ("n")) transistor_35 (.in(1'b0), .out(transistor_35_out), .gate(clk2_inv));
  Transistor #(.\type ("n")) transistor_36 (.in(1'b0), .out(transistor_36_out), .gate(clk2_inv));
  Transistor #(.\type ("n")) transistor_37 (.in(1'b0), .out(transistor_37_out), .gate(clk2_inv));
  Transistor #(.\type ("n")) transistor_38 (.in(1'b0), .out(transistor_38_out), .gate(clk2_inv));
  Transistor #(.\type ("n")) transistor_39 (.in(1'b0), .out(transistor_39_out), .gate(clk2_inv));
  Transistor #(.\type ("n")) transistor_40 (.in(1'b0), .out(transistor_40_out), .gate(clk2_inv));
  Transistor #(.\type ("n")) transistor_41 (.in(1'b0), .out(transistor_41_out), .gate(clk2_inv));
  Transistor #(.\type ("n")) transistor_42 (.in(1'b0), .out(transistor_42_out), .gate(clk2_inv));
  Transistor #(.\type ("n")) transistor_43 (.in(1'b0), .out(transistor_43_out), .gate(clk2_inv));
  Transistor #(.\type ("n")) transistor_44 (.in(1'b0), .out(transistor_44_out), .gate(clk2_inv));
  Transistor #(.\type ("n")) transistor_45 (.in(1'b0), .out(transistor_45_out), .gate(clk2_inv));
  Transistor #(.\type ("n")) transistor_46 (.in(1'b0), .out(transistor_46_out), .gate(clk2_inv));
  Transistor #(.\type ("n")) transistor_47 (.in(1'b0), .out(transistor_47_out), .gate(clk2_inv));
  Transistor #(.\type ("n")) transistor_48 (.in(1'b0), .out(transistor_48_out), .gate(clk2_inv));
  Transistor #(.\type ("n")) transistor_49 (.in(1'b0), .out(transistor_49_out), .gate(clk2_inv));
  Transistor #(.\type ("n")) transistor_50 (.in(1'b0), .out(transistor_50_out), .gate(clk2_inv));
  Transistor #(.\type ("n")) transistor_51 (.in(1'b0), .out(transistor_51_out), .gate(clk2_inv));
  Transistor #(.\type ("n")) transistor_52 (.in(1'b0), .out(transistor_52_out), .gate(clk2_inv));
  Transistor #(.\type ("n")) transistor_53 (.in(1'b0), .out(transistor_53_out), .gate(clk2_inv));
  Transistor #(.\type ("n")) transistor_54 (.in(1'b0), .out(transistor_54_out), .gate(clk2_inv));
  Transistor #(.\type ("n")) transistor_55 (.in(1'b0), .out(transistor_55_out), .gate(clk2_inv));
  Transistor #(.\type ("n")) transistor_56 (.in(1'b0), .out(transistor_56_out), .gate(clk2_inv));
  Transistor #(.\type ("n")) transistor_57 (.in(1'b0), .out(transistor_57_out), .gate(clk2_inv));
  Transistor #(.\type ("n")) transistor_58 (.in(1'b0), .out(transistor_58_out), .gate(clk2_inv));
  Transistor #(.\type ("n")) transistor_59 (.in(1'b0), .out(transistor_59_out), .gate(clk2_inv));
  Transistor #(.\type ("n")) transistor_60 (.in(1'b0), .out(transistor_60_out), .gate(clk2_inv));
  Transistor #(.\type ("n")) transistor_61 (.in(1'b0), .out(transistor_61_out), .gate(clk2_inv));
  Transistor #(.\type ("n")) transistor_62 (.in(1'b0), .out(transistor_62_out), .gate(clk2_inv));
  Transistor #(.\type ("n")) transistor_63 (.in(1'b0), .out(transistor_63_out), .gate(clk2_inv));
  Transistor #(.\type ("n")) transistor_64 (.in(transistor_27_out), .out(transistor_64_out), .gate(instr_sel[20]));
  Transistor #(.\type ("n")) transistor_65 (.in(transistor_33_out), .out(transistor_65_out), .gate(instr_sel[20]));
  Transistor #(.\type ("n")) transistor_66 (.in(transistor_37_out), .out(transistor_66_out), .gate(instr_sel[20]));
  Transistor #(.\type ("n")) transistor_67 (.in(transistor_41_out), .out(transistor_67_out), .gate(instr_sel[20]));
  Transistor #(.\type ("n")) transistor_68 (.in(transistor_45_out), .out(transistor_68_out), .gate(instr_sel[20]));
  Transistor #(.\type ("n")) transistor_69 (.in(transistor_51_out), .out(transistor_69_out), .gate(instr_sel[20]));
  Transistor #(.\type ("n")) transistor_70 (.in(transistor_55_out), .out(transistor_70_out), .gate(instr_sel[20]));
  Transistor #(.\type ("n")) transistor_71 (.in(transistor_59_out), .out(transistor_71_out), .gate(instr_sel[20]));
  Transistor #(.\type ("n")) transistor_72 (.in(transistor_63_out), .out(transistor_72_out), .gate(instr_sel[20]));
  Transistor #(.\type ("n")) transistor_73 (.in(transistor_64_out), .out(transistor_73_out), .gate(instr_sel[19]));
  Transistor #(.\type ("n")) transistor_74 (.in(transistor_65_out), .out(transistor_74_out), .gate(instr_sel[19]));
  Transistor #(.\type ("n")) transistor_75 (.in(transistor_35_out), .out(transistor_75_out), .gate(instr_sel[19]));
  Transistor #(.\type ("n")) transistor_76 (.in(transistor_39_out), .out(transistor_76_out), .gate(instr_sel[19]));
  Transistor #(.\type ("n")) transistor_77 (.in(transistor_67_out), .out(transistor_77_out), .gate(instr_sel[19]));
  Transistor #(.\type ("n")) transistor_78 (.in(transistor_69_out), .out(transistor_78_out), .gate(instr_sel[19]));
  Transistor #(.\type ("n")) transistor_79 (.in(transistor_57_out), .out(transistor_79_out), .gate(instr_sel[19]));
  Transistor #(.\type ("n")) transistor_80 (.in(transistor_22_out), .out(transistor_80_out), .gate(instr_sel[17]));
  Transistor #(.\type ("n")) transistor_81 (.in(transistor_26_out), .out(transistor_81_out), .gate(instr_sel[17]));
  Transistor #(.\type ("n")) transistor_82 (.in(transistor_73_out), .out(transistor_82_out), .gate(instr_sel[18]));
  Transistor #(.\type ("n")) transistor_83 (.in(transistor_32_out), .out(transistor_83_out), .gate(instr_sel[17]));
  Transistor #(.\type ("n")) transistor_84 (.in(transistor_74_out), .out(transistor_84_out), .gate(instr_sel[18]));
  Transistor #(.\type ("n")) transistor_85 (.in(transistor_34_out), .out(transistor_85_out), .gate(instr_sel[17]));
  Transistor #(.\type ("n")) transistor_86 (.in(transistor_75_out), .out(transistor_86_out), .gate(instr_sel[18]));
  Transistor #(.\type ("n")) transistor_87 (.in(transistor_36_out), .out(transistor_87_out), .gate(instr_sel[17]));
  Transistor #(.\type ("n")) transistor_88 (.in(transistor_66_out), .out(transistor_88_out), .gate(instr_sel[18]));
  Transistor #(.\type ("n")) transistor_89 (.in(transistor_38_out), .out(transistor_89_out), .gate(instr_sel[17]));
  Transistor #(.\type ("n")) transistor_90 (.in(transistor_76_out), .out(transistor_90_out), .gate(instr_sel[18]));
  Transistor #(.\type ("n")) transistor_91 (.in(transistor_40_out), .out(transistor_91_out), .gate(instr_sel[17]));
  Transistor #(.\type ("n")) transistor_92 (.in(transistor_77_out), .out(transistor_92_out), .gate(instr_sel[18]));
  Transistor #(.\type ("n")) transistor_93 (.in(transistor_50_out), .out(transistor_93_out), .gate(instr_sel[17]));
  Transistor #(.\type ("n")) transistor_94 (.in(transistor_78_out), .out(transistor_94_out), .gate(instr_sel[18]));
  Transistor #(.\type ("n")) transistor_95 (.in(transistor_53_out), .out(transistor_95_out), .gate(instr_sel[18]));
  Transistor #(.\type ("n")) transistor_96 (.in(transistor_54_out), .out(transistor_96_out), .gate(instr_sel[17]));
  Transistor #(.\type ("n")) transistor_97 (.in(transistor_56_out), .out(transistor_97_out), .gate(instr_sel[17]));
  Transistor #(.\type ("n")) transistor_98 (.in(transistor_79_out), .out(transistor_98_out), .gate(instr_sel[18]));
  Transistor #(.\type ("n")) transistor_99 (.in(transistor_71_out), .out(transistor_99_out), .gate(instr_sel[18]));
  Transistor #(.\type ("n")) transistor_100 (.in(transistor_62_out), .out(transistor_100_out), .gate(instr_sel[17]));
  Transistor #(.\type ("n")) transistor_101 (.in(transistor_72_out), .out(transistor_101_out), .gate(instr_sel[18]));
  Transistor #(.\type ("n")) transistor_102 (.in(transistor_81_out), .out(transistor_102_out), .gate(instr_sel[16]));
  Transistor #(.\type ("n")) transistor_103 (.in(transistor_83_out), .out(transistor_103_out), .gate(instr_sel[16]));
  Transistor #(.\type ("n")) transistor_104 (.in(transistor_85_out), .out(transistor_104_out), .gate(instr_sel[16]));
  Transistor #(.\type ("n")) transistor_105 (.in(transistor_91_out), .out(transistor_105_out), .gate(instr_sel[16]));
  Transistor #(.\type ("n")) transistor_106 (.in(transistor_48_out), .out(transistor_106_out), .gate(instr_sel[16]));
  Transistor #(.\type ("n")) transistor_107 (.in(transistor_52_out), .out(transistor_107_out), .gate(instr_sel[16]));
  Transistor #(.\type ("n")) transistor_108 (.in(transistor_58_out), .out(transistor_108_out), .gate(instr_sel[16]));
  Transistor #(.\type ("n")) transistor_109 (.in(transistor_60_out), .out(transistor_109_out), .gate(instr_sel[16]));
  Transistor #(.\type ("n")) transistor_110 (.in(transistor_100_out), .out(transistor_110_out), .gate(instr_sel[16]));
  Transistor #(.\type ("n")) transistor_111 (.in(transistor_2_out), .out(transistor_111_out), .gate(instr_sel[15]));
  Transistor #(.\type ("n")) transistor_112 (.in(transistor_3_out), .out(transistor_112_out), .gate(instr_sel[15]));
  Transistor #(.\type ("n")) transistor_113 (.in(transistor_8_out), .out(transistor_113_out), .gate(instr_sel[15]));
  Transistor #(.\type ("n")) transistor_114 (.in(transistor_9_out), .out(transistor_114_out), .gate(instr_sel[15]));
  Transistor #(.\type ("n")) transistor_115 (.in(transistor_10_out), .out(transistor_115_out), .gate(instr_sel[15]));
  Transistor #(.\type ("n")) transistor_116 (.in(transistor_11_out), .out(transistor_116_out), .gate(instr_sel[15]));
  Transistor #(.\type ("n")) transistor_117 (.in(transistor_102_out), .out(transistor_117_out), .gate(instr_sel[15]));
  Transistor #(.\type ("n")) transistor_118 (.in(transistor_103_out), .out(transistor_118_out), .gate(instr_sel[15]));
  Transistor #(.\type ("n")) transistor_119 (.in(transistor_104_out), .out(transistor_119_out), .gate(instr_sel[15]));
  Transistor #(.\type ("n")) transistor_120 (.in(transistor_89_out), .out(transistor_120_out), .gate(instr_sel[15]));
  Transistor #(.\type ("n")) transistor_121 (.in(transistor_105_out), .out(transistor_121_out), .gate(instr_sel[15]));
  Transistor #(.\type ("n")) transistor_122 (.in(transistor_42_out), .out(transistor_122_out), .gate(instr_sel[15]));
  Transistor #(.\type ("n")) transistor_123 (.in(transistor_44_out), .out(transistor_123_out), .gate(instr_sel[15]));
  Transistor #(.\type ("n")) transistor_124 (.in(transistor_46_out), .out(transistor_124_out), .gate(instr_sel[15]));
  Transistor #(.\type ("n")) transistor_125 (.in(transistor_93_out), .out(transistor_125_out), .gate(instr_sel[15]));
  Transistor #(.\type ("n")) transistor_126 (.in(transistor_107_out), .out(transistor_126_out), .gate(instr_sel[15]));
  Transistor #(.\type ("n")) transistor_127 (.in(transistor_97_out), .out(transistor_127_out), .gate(instr_sel[15]));
  Transistor #(.\type ("n")) transistor_128 (.in(transistor_109_out), .out(transistor_128_out), .gate(instr_sel[15]));
  Transistor #(.\type ("n")) transistor_129 (.in(transistor_112_out), .out(transistor_129_out), .gate(instr_sel[14]));
  Transistor #(.\type ("n")) transistor_130 (.in(transistor_129_out), .out(transistor_130_out), .gate(instr_sel[13]));
  Transistor #(.\type ("n")) transistor_131 (.in(transistor_4_out), .out(transistor_131_out), .gate(instr_sel[14]));
  Transistor #(.\type ("n")) transistor_132 (.in(transistor_131_out), .out(transistor_132_out), .gate(instr_sel[13]));
  Transistor #(.\type ("n")) transistor_133 (.in(transistor_6_out), .out(transistor_133_out), .gate(instr_sel[14]));
  Transistor #(.\type ("n")) transistor_134 (.in(transistor_14_out), .out(transistor_134_out), .gate(instr_sel[13]));
  Transistor #(.\type ("n")) transistor_135 (.in(transistor_15_out), .out(transistor_135_out), .gate(instr_sel[14]));
  Transistor #(.\type ("n")) transistor_136 (.in(transistor_135_out), .out(transistor_136_out), .gate(instr_sel[13]));
  Transistor #(.\type ("n")) transistor_137 (.in(transistor_16_out), .out(transistor_137_out), .gate(instr_sel[14]));
  Transistor #(.\type ("n")) transistor_138 (.in(transistor_137_out), .out(transistor_138_out), .gate(instr_sel[13]));
  Transistor #(.\type ("n")) transistor_139 (.in(transistor_17_out), .out(transistor_139_out), .gate(instr_sel[14]));
  Transistor #(.\type ("n")) transistor_140 (.in(transistor_139_out), .out(transistor_140_out), .gate(instr_sel[13]));
  Transistor #(.\type ("n")) transistor_141 (.in(transistor_19_out), .out(transistor_141_out), .gate(instr_sel[14]));
  Transistor #(.\type ("n")) transistor_142 (.in(transistor_25_out), .out(transistor_142_out), .gate(instr_sel[14]));
  Transistor #(.\type ("n")) transistor_143 (.in(transistor_142_out), .out(transistor_143_out), .gate(instr_sel[13]));
  Transistor #(.\type ("n")) transistor_144 (.in(transistor_117_out), .out(transistor_144_out), .gate(instr_sel[14]));
  Transistor #(.\type ("n")) transistor_145 (.in(transistor_144_out), .out(transistor_145_out), .gate(instr_sel[13]));
  Transistor #(.\type ("n")) transistor_146 (.in(transistor_82_out), .out(transistor_146_out), .gate(instr_sel[13]));
  Transistor #(.\type ("n")) transistor_147 (.in(transistor_118_out), .out(transistor_147_out), .gate(instr_sel[14]));
  Transistor #(.\type ("n")) transistor_148 (.in(transistor_147_out), .out(transistor_148_out), .gate(instr_sel[13]));
  Transistor #(.\type ("n")) transistor_149 (.in(transistor_84_out), .out(transistor_149_out), .gate(instr_sel[14]));
  Transistor #(.\type ("n")) transistor_150 (.in(transistor_149_out), .out(transistor_150_out), .gate(instr_sel[13]));
  Transistor #(.\type ("n")) transistor_151 (.in(transistor_119_out), .out(transistor_151_out), .gate(instr_sel[14]));
  Transistor #(.\type ("n")) transistor_152 (.in(transistor_86_out), .out(transistor_152_out), .gate(instr_sel[14]));
  Transistor #(.\type ("n")) transistor_153 (.in(transistor_152_out), .out(transistor_153_out), .gate(instr_sel[13]));
  Transistor #(.\type ("n")) transistor_154 (.in(transistor_120_out), .out(transistor_154_out), .gate(instr_sel[13]));
  Transistor #(.\type ("n")) transistor_155 (.in(transistor_90_out), .out(transistor_155_out), .gate(instr_sel[14]));
  Transistor #(.\type ("n")) transistor_156 (.in(transistor_122_out), .out(transistor_156_out), .gate(instr_sel[13]));
  Transistor #(.\type ("n")) transistor_157 (.in(transistor_43_out), .out(transistor_157_out), .gate(instr_sel[14]));
  Transistor #(.\type ("n")) transistor_158 (.in(transistor_124_out), .out(transistor_158_out), .gate(instr_sel[14]));
  Transistor #(.\type ("n")) transistor_159 (.in(transistor_47_out), .out(transistor_159_out), .gate(instr_sel[14]));
  Transistor #(.\type ("n")) transistor_160 (.in(transistor_49_out), .out(transistor_160_out), .gate(instr_sel[13]));
  Transistor #(.\type ("n")) transistor_161 (.in(transistor_125_out), .out(transistor_161_out), .gate(instr_sel[14]));
  Transistor #(.\type ("n")) transistor_162 (.in(transistor_94_out), .out(transistor_162_out), .gate(instr_sel[13]));
  Transistor #(.\type ("n")) transistor_163 (.in(transistor_126_out), .out(transistor_163_out), .gate(instr_sel[13]));
  Transistor #(.\type ("n")) transistor_164 (.in(transistor_95_out), .out(transistor_164_out), .gate(instr_sel[13]));
  Transistor #(.\type ("n")) transistor_165 (.in(transistor_96_out), .out(transistor_165_out), .gate(instr_sel[14]));
  Transistor #(.\type ("n")) transistor_166 (.in(transistor_165_out), .out(transistor_166_out), .gate(instr_sel[13]));
  Transistor #(.\type ("n")) transistor_167 (.in(transistor_70_out), .out(transistor_167_out), .gate(instr_sel[13]));
  Transistor #(.\type ("n")) transistor_168 (.in(transistor_108_out), .out(transistor_168_out), .gate(instr_sel[14]));
  Transistor #(.\type ("n")) transistor_169 (.in(transistor_99_out), .out(transistor_169_out), .gate(instr_sel[14]));
  Transistor #(.\type ("n")) transistor_170 (.in(transistor_169_out), .out(transistor_170_out), .gate(instr_sel[13]));
  Transistor #(.\type ("n")) transistor_171 (.in(transistor_128_out), .out(transistor_171_out), .gate(instr_sel[14]));
  Transistor #(.\type ("n")) transistor_172 (.in(transistor_171_out), .out(transistor_172_out), .gate(instr_sel[13]));
  Transistor #(.\type ("n")) transistor_173 (.in(transistor_61_out), .out(transistor_173_out), .gate(instr_sel[14]));
  Transistor #(.\type ("n")) transistor_174 (.in(transistor_173_out), .out(transistor_174_out), .gate(instr_sel[13]));
  Transistor #(.\type ("n")) transistor_175 (.in(transistor_110_out), .out(transistor_175_out), .gate(instr_sel[13]));
  Transistor #(.\type ("n")) transistor_176 (.in(transistor_111_out), .out(transistor_176_out), .gate(instr_sel[12]));
  Transistor #(.\type ("n")) transistor_177 (.in(transistor_5_out), .out(transistor_177_out), .gate(instr_sel[12]));
  Transistor #(.\type ("n")) transistor_178 (.in(transistor_133_out), .out(transistor_178_out), .gate(instr_sel[12]));
  Transistor #(.\type ("n")) transistor_179 (.in(transistor_114_out), .out(transistor_179_out), .gate(instr_sel[12]));
  Transistor #(.\type ("n")) transistor_180 (.in(transistor_116_out), .out(transistor_180_out), .gate(instr_sel[12]));
  Transistor #(.\type ("n")) transistor_181 (.in(transistor_143_out), .out(transistor_181_out), .gate(instr_sel[12]));
  Transistor #(.\type ("n")) transistor_182 (.in(transistor_145_out), .out(transistor_182_out), .gate(instr_sel[12]));
  Transistor #(.\type ("n")) transistor_183 (.in(transistor_28_out), .out(transistor_183_out), .gate(instr_sel[12]));
  Transistor #(.\type ("n")) transistor_184 (.in(transistor_30_out), .out(transistor_184_out), .gate(instr_sel[12]));
  Transistor #(.\type ("n")) transistor_185 (.in(transistor_148_out), .out(transistor_185_out), .gate(instr_sel[12]));
  Transistor #(.\type ("n")) transistor_186 (.in(transistor_150_out), .out(transistor_186_out), .gate(instr_sel[12]));
  Transistor #(.\type ("n")) transistor_187 (.in(transistor_151_out), .out(transistor_187_out), .gate(instr_sel[12]));
  Transistor #(.\type ("n")) transistor_188 (.in(transistor_155_out), .out(transistor_188_out), .gate(instr_sel[12]));
  Transistor #(.\type ("n")) transistor_189 (.in(transistor_121_out), .out(transistor_189_out), .gate(instr_sel[12]));
  Transistor #(.\type ("n")) transistor_190 (.in(transistor_157_out), .out(transistor_190_out), .gate(instr_sel[12]));
  Transistor #(.\type ("n")) transistor_191 (.in(transistor_158_out), .out(transistor_191_out), .gate(instr_sel[12]));
  Transistor #(.\type ("n")) transistor_192 (.in(transistor_159_out), .out(transistor_192_out), .gate(instr_sel[12]));
  Transistor #(.\type ("n")) transistor_193 (.in(transistor_172_out), .out(transistor_193_out), .gate(instr_sel[12]));
  Transistor #(.\type ("n")) transistor_194 (.in(transistor_174_out), .out(transistor_194_out), .gate(instr_sel[12]));
  Transistor #(.\type ("n")) transistor_195 (.in(transistor_175_out), .out(transistor_195_out), .gate(instr_sel[12]));
  Transistor #(.\type ("n")) transistor_196 (.in(transistor_176_out), .out(transistor_196_out), .gate(instr_sel[11]));
  Transistor #(.\type ("n")) transistor_197 (.in(transistor_178_out), .out(transistor_197_out), .gate(instr_sel[11]));
  Transistor #(.\type ("n")) transistor_198 (.in(transistor_179_out), .out(transistor_198_out), .gate(instr_sel[11]));
  Transistor #(.\type ("n")) transistor_199 (.in(transistor_115_out), .out(transistor_199_out), .gate(instr_sel[11]));
  Transistor #(.\type ("n")) transistor_200 (.in(transistor_134_out), .out(transistor_200_out), .gate(instr_sel[11]));
  Transistor #(.\type ("n")) transistor_201 (.in(transistor_138_out), .out(transistor_201_out), .gate(instr_sel[11]));
  Transistor #(.\type ("n")) transistor_202 (.in(transistor_140_out), .out(transistor_202_out), .gate(instr_sel[11]));
  Transistor #(.\type ("n")) transistor_203 (.in(transistor_18_out), .out(transistor_203_out), .gate(instr_sel[11]));
  Transistor #(.\type ("n")) transistor_204 (.in(transistor_181_out), .out(transistor_204_out), .gate(instr_sel[11]));
  Transistor #(.\type ("n")) transistor_205 (.in(transistor_182_out), .out(transistor_205_out), .gate(instr_sel[11]));
  Transistor #(.\type ("n")) transistor_206 (.in(transistor_146_out), .out(transistor_206_out), .gate(instr_sel[11]));
  Transistor #(.\type ("n")) transistor_207 (.in(transistor_187_out), .out(transistor_207_out), .gate(instr_sel[11]));
  Transistor #(.\type ("n")) transistor_208 (.in(transistor_153_out), .out(transistor_208_out), .gate(instr_sel[11]));
  Transistor #(.\type ("n")) transistor_209 (.in(transistor_87_out), .out(transistor_209_out), .gate(instr_sel[11]));
  Transistor #(.\type ("n")) transistor_210 (.in(transistor_88_out), .out(transistor_210_out), .gate(instr_sel[11]));
  Transistor #(.\type ("n")) transistor_211 (.in(transistor_188_out), .out(transistor_211_out), .gate(instr_sel[11]));
  Transistor #(.\type ("n")) transistor_212 (.in(transistor_156_out), .out(transistor_212_out), .gate(instr_sel[11]));
  Transistor #(.\type ("n")) transistor_213 (.in(transistor_190_out), .out(transistor_213_out), .gate(instr_sel[11]));
  Transistor #(.\type ("n")) transistor_214 (.in(transistor_191_out), .out(transistor_214_out), .gate(instr_sel[11]));
  Transistor #(.\type ("n")) transistor_215 (.in(transistor_166_out), .out(transistor_215_out), .gate(instr_sel[11]));
  Transistor #(.\type ("n")) transistor_216 (.in(transistor_167_out), .out(transistor_216_out), .gate(instr_sel[11]));
  Transistor #(.\type ("n")) transistor_217 (.in(transistor_127_out), .out(transistor_217_out), .gate(instr_sel[11]));
  Transistor #(.\type ("n")) transistor_218 (.in(transistor_170_out), .out(transistor_218_out), .gate(instr_sel[11]));
  Transistor #(.\type ("n")) transistor_219 (.in(transistor_194_out), .out(transistor_219_out), .gate(instr_sel[11]));
  Transistor #(.\type ("n")) transistor_220 (.in(transistor_1_out), .out(transistor_220_out), .gate(instr_sel[10]));
  Transistor #(.\type ("n")) transistor_221 (.in(transistor_130_out), .out(transistor_221_out), .gate(instr_sel[9]));
  Transistor #(.\type ("n")) transistor_222 (.in(transistor_132_out), .out(transistor_222_out), .gate(instr_sel[10]));
  Transistor #(.\type ("n")) transistor_223 (.in(transistor_222_out), .out(transistor_223_out), .gate(instr_sel[9]));
  Transistor #(.\type ("n")) transistor_224 (.in(transistor_177_out), .out(transistor_224_out), .gate(instr_sel[9]));
  Transistor #(.\type ("n")) transistor_225 (.in(transistor_197_out), .out(transistor_225_out), .gate(instr_sel[9]));
  Transistor #(.\type ("n")) transistor_226 (.in(transistor_113_out), .out(transistor_226_out), .gate(instr_sel[9]));
  Transistor #(.\type ("n")) transistor_227 (.in(transistor_198_out), .out(transistor_227_out), .gate(instr_sel[10]));
  Transistor #(.\type ("n")) transistor_228 (.in(transistor_227_out), .out(transistor_228_out), .gate(instr_sel[9]));
  Transistor #(.\type ("n")) transistor_229 (.in(transistor_199_out), .out(transistor_229_out), .gate(instr_sel[10]));
  Transistor #(.\type ("n")) transistor_230 (.in(transistor_229_out), .out(transistor_230_out), .gate(instr_sel[9]));
  Transistor #(.\type ("n")) transistor_231 (.in(transistor_180_out), .out(transistor_231_out), .gate(instr_sel[10]));
  Transistor #(.\type ("n")) transistor_232 (.in(transistor_231_out), .out(transistor_232_out), .gate(instr_sel[9]));
  Transistor #(.\type ("n")) transistor_233 (.in(transistor_12_out), .out(transistor_233_out), .gate(instr_sel[9]));
  Transistor #(.\type ("n")) transistor_234 (.in(transistor_13_out), .out(transistor_234_out), .gate(instr_sel[10]));
  Transistor #(.\type ("n")) transistor_235 (.in(transistor_136_out), .out(transistor_235_out), .gate(instr_sel[10]));
  Transistor #(.\type ("n")) transistor_236 (.in(transistor_201_out), .out(transistor_236_out), .gate(instr_sel[9]));
  Transistor #(.\type ("n")) transistor_237 (.in(transistor_203_out), .out(transistor_237_out), .gate(instr_sel[10]));
  Transistor #(.\type ("n")) transistor_238 (.in(transistor_237_out), .out(transistor_238_out), .gate(instr_sel[9]));
  Transistor #(.\type ("n")) transistor_239 (.in(transistor_80_out), .out(transistor_239_out), .gate(instr_sel[10]));
  Transistor #(.\type ("n")) transistor_240 (.in(transistor_239_out), .out(transistor_240_out), .gate(instr_sel[9]));
  Transistor #(.\type ("n")) transistor_241 (.in(transistor_24_out), .out(transistor_241_out), .gate(instr_sel[10]));
  Transistor #(.\type ("n")) transistor_242 (.in(transistor_205_out), .out(transistor_242_out), .gate(instr_sel[10]));
  Transistor #(.\type ("n")) transistor_243 (.in(transistor_242_out), .out(transistor_243_out), .gate(instr_sel[9]));
  Transistor #(.\type ("n")) transistor_244 (.in(transistor_206_out), .out(transistor_244_out), .gate(instr_sel[10]));
  Transistor #(.\type ("n")) transistor_245 (.in(transistor_244_out), .out(transistor_245_out), .gate(instr_sel[9]));
  Transistor #(.\type ("n")) transistor_246 (.in(transistor_185_out), .out(transistor_246_out), .gate(instr_sel[10]));
  Transistor #(.\type ("n")) transistor_247 (.in(transistor_246_out), .out(transistor_247_out), .gate(instr_sel[9]));
  Transistor #(.\type ("n")) transistor_248 (.in(transistor_186_out), .out(transistor_248_out), .gate(instr_sel[10]));
  Transistor #(.\type ("n")) transistor_249 (.in(transistor_248_out), .out(transistor_249_out), .gate(instr_sel[9]));
  Transistor #(.\type ("n")) transistor_250 (.in(transistor_207_out), .out(transistor_250_out), .gate(instr_sel[10]));
  Transistor #(.\type ("n")) transistor_251 (.in(transistor_208_out), .out(transistor_251_out), .gate(instr_sel[10]));
  Transistor #(.\type ("n")) transistor_252 (.in(transistor_209_out), .out(transistor_252_out), .gate(instr_sel[10]));
  Transistor #(.\type ("n")) transistor_253 (.in(transistor_252_out), .out(transistor_253_out), .gate(instr_sel[9]));
  Transistor #(.\type ("n")) transistor_254 (.in(transistor_210_out), .out(transistor_254_out), .gate(instr_sel[10]));
  Transistor #(.\type ("n")) transistor_255 (.in(transistor_254_out), .out(transistor_255_out), .gate(instr_sel[9]));
  Transistor #(.\type ("n")) transistor_256 (.in(transistor_154_out), .out(transistor_256_out), .gate(instr_sel[10]));
  Transistor #(.\type ("n")) transistor_257 (.in(transistor_211_out), .out(transistor_257_out), .gate(instr_sel[10]));
  Transistor #(.\type ("n")) transistor_258 (.in(transistor_189_out), .out(transistor_258_out), .gate(instr_sel[10]));
  Transistor #(.\type ("n")) transistor_259 (.in(transistor_258_out), .out(transistor_259_out), .gate(instr_sel[9]));
  Transistor #(.\type ("n")) transistor_260 (.in(transistor_92_out), .out(transistor_260_out), .gate(instr_sel[10]));
  Transistor #(.\type ("n")) transistor_261 (.in(transistor_213_out), .out(transistor_261_out), .gate(instr_sel[9]));
  Transistor #(.\type ("n")) transistor_262 (.in(transistor_192_out), .out(transistor_262_out), .gate(instr_sel[9]));
  Transistor #(.\type ("n")) transistor_263 (.in(transistor_161_out), .out(transistor_263_out), .gate(instr_sel[9]));
  Transistor #(.\type ("n")) transistor_264 (.in(transistor_163_out), .out(transistor_264_out), .gate(instr_sel[10]));
  Transistor #(.\type ("n")) transistor_265 (.in(transistor_215_out), .out(transistor_265_out), .gate(instr_sel[9]));
  Transistor #(.\type ("n")) transistor_266 (.in(transistor_216_out), .out(transistor_266_out), .gate(instr_sel[10]));
  Transistor #(.\type ("n")) transistor_267 (.in(transistor_193_out), .out(transistor_267_out), .gate(instr_sel[10]));
  Transistor #(.\type ("n")) transistor_268 (.in(transistor_219_out), .out(transistor_268_out), .gate(instr_sel[10]));
  Transistor #(.\type ("n")) transistor_269 (.in(transistor_268_out), .out(transistor_269_out), .gate(instr_sel[9]));
  Transistor #(.\type ("n")) transistor_270 (.in(transistor_195_out), .out(transistor_270_out), .gate(instr_sel[9]));
  Transistor #(.\type ("n")) transistor_271 (.in(transistor_220_out), .out(transistor_271_out), .gate(instr_sel[8]));
  Transistor #(.\type ("n")) transistor_272 (.in(transistor_223_out), .out(transistor_272_out), .gate(instr_sel[8]));
  Transistor #(.\type ("n")) transistor_273 (.in(transistor_225_out), .out(transistor_273_out), .gate(instr_sel[8]));
  Transistor #(.\type ("n")) transistor_274 (.in(transistor_236_out), .out(transistor_274_out), .gate(instr_sel[8]));
  Transistor #(.\type ("n")) transistor_275 (.in(transistor_238_out), .out(transistor_275_out), .gate(instr_sel[8]));
  Transistor #(.\type ("n")) transistor_276 (.in(transistor_141_out), .out(transistor_276_out), .gate(instr_sel[8]));
  Transistor #(.\type ("n")) transistor_277 (.in(transistor_240_out), .out(transistor_277_out), .gate(instr_sel[8]));
  Transistor #(.\type ("n")) transistor_278 (.in(transistor_243_out), .out(transistor_278_out), .gate(instr_sel[8]));
  Transistor #(.\type ("n")) transistor_279 (.in(transistor_245_out), .out(transistor_279_out), .gate(instr_sel[8]));
  Transistor #(.\type ("n")) transistor_280 (.in(transistor_250_out), .out(transistor_280_out), .gate(instr_sel[8]));
  Transistor #(.\type ("n")) transistor_281 (.in(transistor_251_out), .out(transistor_281_out), .gate(instr_sel[8]));
  Transistor #(.\type ("n")) transistor_282 (.in(transistor_255_out), .out(transistor_282_out), .gate(instr_sel[8]));
  Transistor #(.\type ("n")) transistor_283 (.in(transistor_257_out), .out(transistor_283_out), .gate(instr_sel[8]));
  Transistor #(.\type ("n")) transistor_284 (.in(transistor_68_out), .out(transistor_284_out), .gate(instr_sel[8]));
  Transistor #(.\type ("n")) transistor_285 (.in(transistor_262_out), .out(transistor_285_out), .gate(instr_sel[8]));
  Transistor #(.\type ("n")) transistor_286 (.in(transistor_263_out), .out(transistor_286_out), .gate(instr_sel[8]));
  Transistor #(.\type ("n")) transistor_287 (.in(transistor_264_out), .out(transistor_287_out), .gate(instr_sel[8]));
  Transistor #(.\type ("n")) transistor_288 (.in(transistor_265_out), .out(transistor_288_out), .gate(instr_sel[8]));
  Transistor #(.\type ("n")) transistor_289 (.in(transistor_267_out), .out(transistor_289_out), .gate(instr_sel[8]));
  Transistor #(.\type ("n")) transistor_290 (.in(transistor_101_out), .out(transistor_290_out), .gate(instr_sel[8]));
  Transistor #(.\type ("n")) transistor_291 (.in(transistor_271_out), .out(transistor_291_out), .gate(instr_sel[7]));
  Transistor #(.\type ("n")) transistor_292 (.in(transistor_224_out), .out(transistor_292_out), .gate(instr_sel[7]));
  Transistor #(.\type ("n")) transistor_293 (.in(transistor_7_out), .out(transistor_293_out), .gate(instr_sel[7]));
  Transistor #(.\type ("n")) transistor_294 (.in(transistor_228_out), .out(transistor_294_out), .gate(instr_sel[7]));
  Transistor #(.\type ("n")) transistor_295 (.in(transistor_230_out), .out(transistor_295_out), .gate(instr_sel[7]));
  Transistor #(.\type ("n")) transistor_296 (.in(transistor_232_out), .out(transistor_296_out), .gate(instr_sel[7]));
  Transistor #(.\type ("n")) transistor_297 (.in(transistor_274_out), .out(transistor_297_out), .gate(instr_sel[7]));
  Transistor #(.\type ("n")) transistor_298 (.in(transistor_202_out), .out(transistor_298_out), .gate(instr_sel[7]));
  Transistor #(.\type ("n")) transistor_299 (.in(transistor_241_out), .out(transistor_299_out), .gate(instr_sel[7]));
  Transistor #(.\type ("n")) transistor_300 (.in(transistor_278_out), .out(transistor_300_out), .gate(instr_sel[7]));
  Transistor #(.\type ("n")) transistor_301 (.in(transistor_279_out), .out(transistor_301_out), .gate(instr_sel[7]));
  Transistor #(.\type ("n")) transistor_302 (.in(transistor_247_out), .out(transistor_302_out), .gate(instr_sel[7]));
  Transistor #(.\type ("n")) transistor_303 (.in(transistor_281_out), .out(transistor_303_out), .gate(instr_sel[7]));
  Transistor #(.\type ("n")) transistor_304 (.in(transistor_253_out), .out(transistor_304_out), .gate(instr_sel[7]));
  Transistor #(.\type ("n")) transistor_305 (.in(transistor_282_out), .out(transistor_305_out), .gate(instr_sel[7]));
  Transistor #(.\type ("n")) transistor_306 (.in(transistor_283_out), .out(transistor_306_out), .gate(instr_sel[7]));
  Transistor #(.\type ("n")) transistor_307 (.in(transistor_123_out), .out(transistor_307_out), .gate(instr_sel[7]));
  Transistor #(.\type ("n")) transistor_308 (.in(transistor_284_out), .out(transistor_308_out), .gate(instr_sel[7]));
  Transistor #(.\type ("n")) transistor_309 (.in(transistor_266_out), .out(transistor_309_out), .gate(instr_sel[7]));
  Transistor #(.\type ("n")) transistor_310 (.in(transistor_218_out), .out(transistor_310_out), .gate(instr_sel[7]));
  Transistor #(.\type ("n")) transistor_311 (.in(transistor_269_out), .out(transistor_311_out), .gate(instr_sel[7]));
  Transistor #(.\type ("n")) transistor_312 (.in(transistor_270_out), .out(transistor_312_out), .gate(instr_sel[7]));
  Transistor #(.\type ("n")) transistor_313 (.in(transistor_290_out), .out(transistor_313_out), .gate(instr_sel[7]));
  Transistor #(.\type ("n")) transistor_314 (.in(transistor_196_out), .out(transistor_314_out), .gate(instr_sel[6]));
  Transistor #(.\type ("n")) transistor_315 (.in(transistor_221_out), .out(transistor_315_out), .gate(instr_sel[6]));
  Transistor #(.\type ("n")) transistor_316 (.in(transistor_272_out), .out(transistor_316_out), .gate(instr_sel[6]));
  Transistor #(.\type ("n")) transistor_317 (.in(transistor_316_out), .out(transistor_317_out), .gate(instr_sel[5]));
  Transistor #(.\type ("n")) transistor_318 (.in(transistor_292_out), .out(transistor_318_out), .gate(instr_sel[5]));
  Transistor #(.\type ("n")) transistor_319 (.in(transistor_273_out), .out(transistor_319_out), .gate(instr_sel[6]));
  Transistor #(.\type ("n")) transistor_320 (.in(transistor_294_out), .out(transistor_320_out), .gate(instr_sel[6]));
  Transistor #(.\type ("n")) transistor_321 (.in(transistor_295_out), .out(transistor_321_out), .gate(instr_sel[6]));
  Transistor #(.\type ("n")) transistor_322 (.in(transistor_296_out), .out(transistor_322_out), .gate(instr_sel[6]));
  Transistor #(.\type ("n")) transistor_323 (.in(transistor_235_out), .out(transistor_323_out), .gate(instr_sel[6]));
  Transistor #(.\type ("n")) transistor_324 (.in(transistor_297_out), .out(transistor_324_out), .gate(instr_sel[6]));
  Transistor #(.\type ("n")) transistor_325 (.in(transistor_298_out), .out(transistor_325_out), .gate(instr_sel[6]));
  Transistor #(.\type ("n")) transistor_326 (.in(transistor_299_out), .out(transistor_326_out), .gate(instr_sel[5]));
  Transistor #(.\type ("n")) transistor_327 (.in(transistor_300_out), .out(transistor_327_out), .gate(instr_sel[6]));
  Transistor #(.\type ("n")) transistor_328 (.in(transistor_301_out), .out(transistor_328_out), .gate(instr_sel[6]));
  Transistor #(.\type ("n")) transistor_329 (.in(transistor_328_out), .out(transistor_329_out), .gate(instr_sel[5]));
  Transistor #(.\type ("n")) transistor_330 (.in(transistor_302_out), .out(transistor_330_out), .gate(instr_sel[6]));
  Transistor #(.\type ("n")) transistor_331 (.in(transistor_330_out), .out(transistor_331_out), .gate(instr_sel[5]));
  Transistor #(.\type ("n")) transistor_332 (.in(transistor_249_out), .out(transistor_332_out), .gate(instr_sel[6]));
  Transistor #(.\type ("n")) transistor_333 (.in(transistor_332_out), .out(transistor_333_out), .gate(instr_sel[5]));
  Transistor #(.\type ("n")) transistor_334 (.in(transistor_303_out), .out(transistor_334_out), .gate(instr_sel[5]));
  Transistor #(.\type ("n")) transistor_335 (.in(transistor_304_out), .out(transistor_335_out), .gate(instr_sel[5]));
  Transistor #(.\type ("n")) transistor_336 (.in(transistor_305_out), .out(transistor_336_out), .gate(instr_sel[5]));
  Transistor #(.\type ("n")) transistor_337 (.in(transistor_307_out), .out(transistor_337_out), .gate(instr_sel[6]));
  Transistor #(.\type ("n")) transistor_338 (.in(transistor_337_out), .out(transistor_338_out), .gate(instr_sel[5]));
  Transistor #(.\type ("n")) transistor_339 (.in(transistor_308_out), .out(transistor_339_out), .gate(instr_sel[5]));
  Transistor #(.\type ("n")) transistor_340 (.in(transistor_214_out), .out(transistor_340_out), .gate(instr_sel[5]));
  Transistor #(.\type ("n")) transistor_341 (.in(transistor_285_out), .out(transistor_341_out), .gate(instr_sel[6]));
  Transistor #(.\type ("n")) transistor_342 (.in(transistor_106_out), .out(transistor_342_out), .gate(instr_sel[5]));
  Transistor #(.\type ("n")) transistor_343 (.in(transistor_160_out), .out(transistor_343_out), .gate(instr_sel[5]));
  Transistor #(.\type ("n")) transistor_344 (.in(transistor_286_out), .out(transistor_344_out), .gate(instr_sel[5]));
  Transistor #(.\type ("n")) transistor_345 (.in(transistor_162_out), .out(transistor_345_out), .gate(instr_sel[5]));
  Transistor #(.\type ("n")) transistor_346 (.in(transistor_287_out), .out(transistor_346_out), .gate(instr_sel[5]));
  Transistor #(.\type ("n")) transistor_347 (.in(transistor_164_out), .out(transistor_347_out), .gate(instr_sel[5]));
  Transistor #(.\type ("n")) transistor_348 (.in(transistor_288_out), .out(transistor_348_out), .gate(instr_sel[6]));
  Transistor #(.\type ("n")) transistor_349 (.in(transistor_348_out), .out(transistor_349_out), .gate(instr_sel[5]));
  Transistor #(.\type ("n")) transistor_350 (.in(transistor_309_out), .out(transistor_350_out), .gate(instr_sel[5]));
  Transistor #(.\type ("n")) transistor_351 (.in(transistor_168_out), .out(transistor_351_out), .gate(instr_sel[5]));
  Transistor #(.\type ("n")) transistor_352 (.in(transistor_310_out), .out(transistor_352_out), .gate(instr_sel[6]));
  Transistor #(.\type ("n")) transistor_353 (.in(transistor_352_out), .out(transistor_353_out), .gate(instr_sel[5]));
  Transistor #(.\type ("n")) transistor_354 (.in(transistor_311_out), .out(transistor_354_out), .gate(instr_sel[6]));
  Transistor #(.\type ("n")) transistor_355 (.in(transistor_312_out), .out(transistor_355_out), .gate(instr_sel[6]));
  Transistor #(.\type ("n")) transistor_356 (.in(transistor_313_out), .out(transistor_356_out), .gate(instr_sel[6]));
  Transistor #(.\type ("n")) transistor_357 (.in(transistor_314_out), .out(transistor_357_out), .gate(instr_sel[4]));
  Transistor #(.\type ("n")) transistor_358 (.in(transistor_315_out), .out(transistor_358_out), .gate(instr_sel[4]));
  Transistor #(.\type ("n")) transistor_359 (.in(transistor_317_out), .out(transistor_359_out), .gate(instr_sel[4]));
  Transistor #(.\type ("n")) transistor_360 (.in(transistor_318_out), .out(transistor_360_out), .gate(instr_sel[4]));
  Transistor #(.\type ("n")) transistor_361 (.in(transistor_320_out), .out(transistor_361_out), .gate(instr_sel[4]));
  Transistor #(.\type ("n")) transistor_362 (.in(transistor_321_out), .out(transistor_362_out), .gate(instr_sel[4]));
  Transistor #(.\type ("n")) transistor_363 (.in(transistor_324_out), .out(transistor_363_out), .gate(instr_sel[4]));
  Transistor #(.\type ("n")) transistor_364 (.in(transistor_325_out), .out(transistor_364_out), .gate(instr_sel[4]));
  Transistor #(.\type ("n")) transistor_365 (.in(transistor_275_out), .out(transistor_365_out), .gate(instr_sel[4]));
  Transistor #(.\type ("n")) transistor_366 (.in(transistor_326_out), .out(transistor_366_out), .gate(instr_sel[4]));
  Transistor #(.\type ("n")) transistor_367 (.in(transistor_329_out), .out(transistor_367_out), .gate(instr_sel[4]));
  Transistor #(.\type ("n")) transistor_368 (.in(transistor_331_out), .out(transistor_368_out), .gate(instr_sel[4]));
  Transistor #(.\type ("n")) transistor_369 (.in(transistor_280_out), .out(transistor_369_out), .gate(instr_sel[4]));
  Transistor #(.\type ("n")) transistor_370 (.in(transistor_334_out), .out(transistor_370_out), .gate(instr_sel[4]));
  Transistor #(.\type ("n")) transistor_371 (.in(transistor_335_out), .out(transistor_371_out), .gate(instr_sel[4]));
  Transistor #(.\type ("n")) transistor_372 (.in(transistor_336_out), .out(transistor_372_out), .gate(instr_sel[4]));
  Transistor #(.\type ("n")) transistor_373 (.in(transistor_306_out), .out(transistor_373_out), .gate(instr_sel[4]));
  Transistor #(.\type ("n")) transistor_374 (.in(transistor_261_out), .out(transistor_374_out), .gate(instr_sel[4]));
  Transistor #(.\type ("n")) transistor_375 (.in(transistor_339_out), .out(transistor_375_out), .gate(instr_sel[4]));
  Transistor #(.\type ("n")) transistor_376 (.in(transistor_340_out), .out(transistor_376_out), .gate(instr_sel[4]));
  Transistor #(.\type ("n")) transistor_377 (.in(transistor_347_out), .out(transistor_377_out), .gate(instr_sel[4]));
  Transistor #(.\type ("n")) transistor_378 (.in(transistor_98_out), .out(transistor_378_out), .gate(instr_sel[4]));
  Transistor #(.\type ("n")) transistor_379 (.in(transistor_355_out), .out(transistor_379_out), .gate(instr_sel[4]));
  Transistor #(.\type ("n")) transistor_380 (.in(transistor_358_out), .out(transistor_380_out), .gate(instr_sel[3]));
  Transistor #(.\type ("n")) transistor_381 (.in(transistor_359_out), .out(transistor_381_out), .gate(instr_sel[3]));
  Transistor #(.\type ("n")) transistor_382 (.in(transistor_361_out), .out(transistor_382_out), .gate(instr_sel[3]));
  Transistor #(.\type ("n")) transistor_383 (.in(transistor_362_out), .out(transistor_383_out), .gate(instr_sel[3]));
  Transistor #(.\type ("n")) transistor_384 (.in(transistor_322_out), .out(transistor_384_out), .gate(instr_sel[3]));
  Transistor #(.\type ("n")) transistor_385 (.in(transistor_323_out), .out(transistor_385_out), .gate(instr_sel[3]));
  Transistor #(.\type ("n")) transistor_386 (.in(transistor_363_out), .out(transistor_386_out), .gate(instr_sel[3]));
  Transistor #(.\type ("n")) transistor_387 (.in(transistor_364_out), .out(transistor_387_out), .gate(instr_sel[3]));
  Transistor #(.\type ("n")) transistor_388 (.in(transistor_365_out), .out(transistor_388_out), .gate(instr_sel[3]));
  Transistor #(.\type ("n")) transistor_389 (.in(transistor_327_out), .out(transistor_389_out), .gate(instr_sel[3]));
  Transistor #(.\type ("n")) transistor_390 (.in(transistor_367_out), .out(transistor_390_out), .gate(instr_sel[3]));
  Transistor #(.\type ("n")) transistor_391 (.in(transistor_368_out), .out(transistor_391_out), .gate(instr_sel[3]));
  Transistor #(.\type ("n")) transistor_392 (.in(transistor_370_out), .out(transistor_392_out), .gate(instr_sel[3]));
  Transistor #(.\type ("n")) transistor_393 (.in(transistor_371_out), .out(transistor_393_out), .gate(instr_sel[3]));
  Transistor #(.\type ("n")) transistor_394 (.in(transistor_372_out), .out(transistor_394_out), .gate(instr_sel[3]));
  Transistor #(.\type ("n")) transistor_395 (.in(transistor_259_out), .out(transistor_395_out), .gate(instr_sel[3]));
  Transistor #(.\type ("n")) transistor_396 (.in(transistor_374_out), .out(transistor_396_out), .gate(instr_sel[3]));
  Transistor #(.\type ("n")) transistor_397 (.in(transistor_344_out), .out(transistor_397_out), .gate(instr_sel[3]));
  Transistor #(.\type ("n")) transistor_398 (.in(transistor_346_out), .out(transistor_398_out), .gate(instr_sel[3]));
  Transistor #(.\type ("n")) transistor_399 (.in(transistor_377_out), .out(transistor_399_out), .gate(instr_sel[3]));
  Transistor #(.\type ("n")) transistor_400 (.in(transistor_353_out), .out(transistor_400_out), .gate(instr_sel[3]));
  Transistor #(.\type ("n")) transistor_401 (.in(transistor_354_out), .out(transistor_401_out), .gate(instr_sel[3]));
  Transistor #(.\type ("n")) transistor_402 (.in(transistor_379_out), .out(transistor_402_out), .gate(instr_sel[3]));
  Transistor #(.\type ("n")) transistor_403 (.in(transistor_356_out), .out(transistor_403_out), .gate(instr_sel[3]));
  Transistor #(.\type ("n")) transistor_404 (.in(transistor_357_out), .out(transistor_404_out), .gate(instr_sel[1]));
  Transistor #(.\type ("n")) transistor_405 (.in(transistor_380_out), .out(transistor_405_out), .gate(instr_sel[2]));
  Transistor #(.\type ("n")) transistor_406 (.in(transistor_381_out), .out(transistor_406_out), .gate(instr_sel[1]));
  Transistor #(.\type ("n")) transistor_407 (.in(transistor_226_out), .out(transistor_407_out), .gate(instr_sel[2]));
  Transistor #(.\type ("n")) transistor_408 (.in(transistor_407_out), .out(transistor_408_out), .gate(instr_sel[1]));
  Transistor #(.\type ("n")) transistor_409 (.in(transistor_382_out), .out(transistor_409_out), .gate(instr_sel[1]));
  Transistor #(.\type ("n")) transistor_410 (.in(transistor_384_out), .out(transistor_410_out), .gate(instr_sel[1]));
  Transistor #(.\type ("n")) transistor_411 (.in(transistor_385_out), .out(transistor_411_out), .gate(instr_sel[1]));
  Transistor #(.\type ("n")) transistor_412 (.in(transistor_388_out), .out(transistor_412_out), .gate(instr_sel[2]));
  Transistor #(.\type ("n")) transistor_413 (.in(transistor_412_out), .out(transistor_413_out), .gate(instr_sel[1]));
  Transistor #(.\type ("n")) transistor_414 (.in(transistor_276_out), .out(transistor_414_out), .gate(instr_sel[2]));
  Transistor #(.\type ("n")) transistor_415 (.in(transistor_366_out), .out(transistor_415_out), .gate(instr_sel[1]));
  Transistor #(.\type ("n")) transistor_416 (.in(transistor_389_out), .out(transistor_416_out), .gate(instr_sel[2]));
  Transistor #(.\type ("n")) transistor_417 (.in(transistor_416_out), .out(transistor_417_out), .gate(instr_sel[1]));
  Transistor #(.\type ("n")) transistor_418 (.in(transistor_390_out), .out(transistor_418_out), .gate(instr_sel[2]));
  Transistor #(.\type ("n")) transistor_419 (.in(transistor_418_out), .out(transistor_419_out), .gate(instr_sel[1]));
  Transistor #(.\type ("n")) transistor_420 (.in(transistor_391_out), .out(transistor_420_out), .gate(instr_sel[2]));
  Transistor #(.\type ("n")) transistor_421 (.in(transistor_420_out), .out(transistor_421_out), .gate(instr_sel[1]));
  Transistor #(.\type ("n")) transistor_422 (.in(transistor_333_out), .out(transistor_422_out), .gate(instr_sel[2]));
  Transistor #(.\type ("n")) transistor_423 (.in(transistor_422_out), .out(transistor_423_out), .gate(instr_sel[1]));
  Transistor #(.\type ("n")) transistor_424 (.in(transistor_369_out), .out(transistor_424_out), .gate(instr_sel[2]));
  Transistor #(.\type ("n")) transistor_425 (.in(transistor_424_out), .out(transistor_425_out), .gate(instr_sel[1]));
  Transistor #(.\type ("n")) transistor_426 (.in(transistor_392_out), .out(transistor_426_out), .gate(instr_sel[1]));
  Transistor #(.\type ("n")) transistor_427 (.in(transistor_393_out), .out(transistor_427_out), .gate(instr_sel[2]));
  Transistor #(.\type ("n")) transistor_428 (.in(transistor_394_out), .out(transistor_428_out), .gate(instr_sel[2]));
  Transistor #(.\type ("n")) transistor_429 (.in(transistor_428_out), .out(transistor_429_out), .gate(instr_sel[1]));
  Transistor #(.\type ("n")) transistor_430 (.in(transistor_256_out), .out(transistor_430_out), .gate(instr_sel[2]));
  Transistor #(.\type ("n")) transistor_431 (.in(transistor_430_out), .out(transistor_431_out), .gate(instr_sel[1]));
  Transistor #(.\type ("n")) transistor_432 (.in(transistor_373_out), .out(transistor_432_out), .gate(instr_sel[2]));
  Transistor #(.\type ("n")) transistor_433 (.in(transistor_432_out), .out(transistor_433_out), .gate(instr_sel[1]));
  Transistor #(.\type ("n")) transistor_434 (.in(transistor_395_out), .out(transistor_434_out), .gate(instr_sel[2]));
  Transistor #(.\type ("n")) transistor_435 (.in(transistor_434_out), .out(transistor_435_out), .gate(instr_sel[1]));
  Transistor #(.\type ("n")) transistor_436 (.in(transistor_396_out), .out(transistor_436_out), .gate(instr_sel[1]));
  Transistor #(.\type ("n")) transistor_437 (.in(transistor_338_out), .out(transistor_437_out), .gate(instr_sel[2]));
  Transistor #(.\type ("n")) transistor_438 (.in(transistor_375_out), .out(transistor_438_out), .gate(instr_sel[2]));
  Transistor #(.\type ("n")) transistor_439 (.in(transistor_438_out), .out(transistor_439_out), .gate(instr_sel[1]));
  Transistor #(.\type ("n")) transistor_440 (.in(transistor_398_out), .out(transistor_440_out), .gate(instr_sel[2]));
  Transistor #(.\type ("n")) transistor_441 (.in(transistor_440_out), .out(transistor_441_out), .gate(instr_sel[1]));
  Transistor #(.\type ("n")) transistor_442 (.in(transistor_350_out), .out(transistor_442_out), .gate(instr_sel[2]));
  Transistor #(.\type ("n")) transistor_443 (.in(transistor_442_out), .out(transistor_443_out), .gate(instr_sel[1]));
  Transistor #(.\type ("n")) transistor_444 (.in(transistor_289_out), .out(transistor_444_out), .gate(instr_sel[1]));
  Transistor #(.\type ("n")) transistor_445 (.in(transistor_401_out), .out(transistor_445_out), .gate(instr_sel[2]));
  Transistor #(.\type ("n")) transistor_446 (.in(transistor_445_out), .out(transistor_446_out), .gate(instr_sel[1]));
  Transistor #(.\type ("n")) transistor_447 (.in(transistor_402_out), .out(transistor_447_out), .gate(instr_sel[1]));
  Transistor #(.\type ("n")) transistor_448 (.in(transistor_406_out), .out(transistor_448_out), .gate(instr_sel[0]));
  Transistor #(.\type ("n")) transistor_449 (.in(transistor_319_out), .out(transistor_449_out), .gate(instr_sel[0]));
  Transistor #(.\type ("n")) transistor_450 (.in(transistor_409_out), .out(transistor_450_out), .gate(instr_sel[0]));
  Transistor #(.\type ("n")) transistor_451 (.in(transistor_383_out), .out(transistor_451_out), .gate(instr_sel[0]));
  Transistor #(.\type ("n")) transistor_452 (.in(transistor_387_out), .out(transistor_452_out), .gate(instr_sel[0]));
  Transistor #(.\type ("n")) transistor_453 (.in(transistor_415_out), .out(transistor_453_out), .gate(instr_sel[0]));
  Transistor #(.\type ("n")) transistor_454 (.in(transistor_417_out), .out(transistor_454_out), .gate(instr_sel[0]));
  Transistor #(.\type ("n")) transistor_455 (.in(transistor_419_out), .out(transistor_455_out), .gate(instr_sel[0]));
  Transistor #(.\type ("n")) transistor_456 (.in(transistor_421_out), .out(transistor_456_out), .gate(instr_sel[0]));
  Transistor #(.\type ("n")) transistor_457 (.in(transistor_423_out), .out(transistor_457_out), .gate(instr_sel[0]));
  Transistor #(.\type ("n")) transistor_458 (.in(transistor_425_out), .out(transistor_458_out), .gate(instr_sel[0]));
  Transistor #(.\type ("n")) transistor_459 (.in(transistor_427_out), .out(transistor_459_out), .gate(instr_sel[0]));
  Transistor #(.\type ("n")) transistor_460 (.in(transistor_435_out), .out(transistor_460_out), .gate(instr_sel[0]));
  Transistor #(.\type ("n")) transistor_461 (.in(transistor_341_out), .out(transistor_461_out), .gate(instr_sel[0]));
  Transistor #(.\type ("n")) transistor_462 (.in(transistor_397_out), .out(transistor_462_out), .gate(instr_sel[0]));
  Transistor #(.\type ("n")) transistor_463 (.in(transistor_399_out), .out(transistor_463_out), .gate(instr_sel[0]));
  Transistor #(.\type ("n")) transistor_464 (.in(transistor_400_out), .out(transistor_464_out), .gate(instr_sel[0]));
  Transistor #(.\type ("n")) transistor_465 (.in(transistor_444_out), .out(transistor_465_out), .gate(instr_sel[0]));
  Transistor #(.\type ("n")) transistor_466 (.in(transistor_446_out), .out(transistor_466_out), .gate(instr_sel[0]));
  Transistor #(.\type ("n")) transistor_467 (.in(transistor_403_out), .out(transistor_467_out), .gate(instr_sel[0]));
  assign transistor_291_out = clk2 ? 1'b1 : 1'bz;  // Controlled_Buffer controlled_buffer_1
  assign transistor_404_out = clk2 ? 1'b1 : 1'bz;  // Controlled_Buffer controlled_buffer_2
  assign transistor_405_out = clk2 ? 1'b1 : 1'bz;  // Controlled_Buffer controlled_buffer_3
  assign transistor_448_out = clk2 ? 1'b1 : 1'bz;  // Controlled_Buffer controlled_buffer_4
  assign transistor_360_out = clk2 ? 1'b1 : 1'bz;  // Controlled_Buffer controlled_buffer_5
  assign transistor_449_out = clk2 ? 1'b1 : 1'bz;  // Controlled_Buffer controlled_buffer_6
  assign transistor_293_out = clk2 ? 1'b1 : 1'bz;  // Controlled_Buffer controlled_buffer_7
  assign transistor_408_out = clk2 ? 1'b1 : 1'bz;  // Controlled_Buffer controlled_buffer_8
  assign transistor_450_out = clk2 ? 1'b1 : 1'bz;  // Controlled_Buffer controlled_buffer_9
  assign transistor_451_out = clk2 ? 1'b1 : 1'bz;  // Controlled_Buffer controlled_buffer_10
  assign transistor_410_out = clk2 ? 1'b1 : 1'bz;  // Controlled_Buffer controlled_buffer_11
  Transistor #(.\type ("n")) transistor_468 (.in(transistor_233_out), .out(transistor_468_out), .gate(mod_sel));
  Transistor #(.\type ("n")) transistor_469 (.in(transistor_200_out), .out(transistor_469_out), .gate(mod_sel));
  Transistor #(.\type ("n")) transistor_470 (.in(transistor_386_out), .out(transistor_470_out), .gate(mod_sel));
  Transistor #(.\type ("n")) transistor_471 (.in(transistor_413_out), .out(transistor_471_out), .gate(mod_sel));
  Transistor #(.\type ("n")) transistor_472 (.in(transistor_20_out), .out(transistor_472_out), .gate(mod_sel));
  Transistor #(.\type ("n")) transistor_473 (.in(transistor_277_out), .out(transistor_473_out), .gate(mod_sel));
  Transistor #(.\type ("n")) transistor_474 (.in(transistor_453_out), .out(transistor_474_out), .gate(mod_sel));
  Transistor #(.\type ("n")) transistor_475 (.in(transistor_454_out), .out(transistor_475_out), .gate(mod_sel));
  Transistor #(.\type ("n")) transistor_476 (.in(transistor_183_out), .out(transistor_476_out), .gate(mod_sel));
  Transistor #(.\type ("n")) transistor_477 (.in(transistor_184_out), .out(transistor_477_out), .gate(mod_sel));
  Transistor #(.\type ("n")) transistor_478 (.in(transistor_456_out), .out(transistor_478_out), .gate(mod_sel));
  Transistor #(.\type ("n")) transistor_479 (.in(transistor_458_out), .out(transistor_479_out), .gate(mod_sel));
  Transistor #(.\type ("n")) transistor_480 (.in(transistor_459_out), .out(transistor_480_out), .gate(mod_sel));
  Transistor #(.\type ("n")) transistor_481 (.in(transistor_431_out), .out(transistor_481_out), .gate(mod_sel));
  Transistor #(.\type ("n")) transistor_482 (.in(transistor_460_out), .out(transistor_482_out), .gate(mod_sel));
  Transistor #(.\type ("n")) transistor_483 (.in(transistor_212_out), .out(transistor_483_out), .gate(mod_sel));
  Transistor #(.\type ("n")) transistor_484 (.in(transistor_437_out), .out(transistor_484_out), .gate(mod_sel));
  Transistor #(.\type ("n")) transistor_485 (.in(transistor_376_out), .out(transistor_485_out), .gate(mod_sel));
  Transistor #(.\type ("n")) transistor_486 (.in(transistor_342_out), .out(transistor_486_out), .gate(mod_sel));
  Transistor #(.\type ("n")) transistor_487 (.in(transistor_462_out), .out(transistor_487_out), .gate(mod_sel));
  Transistor #(.\type ("n")) transistor_488 (.in(transistor_441_out), .out(transistor_488_out), .gate(mod_sel));
  Transistor #(.\type ("n")) transistor_489 (.in(transistor_349_out), .out(transistor_489_out), .gate(mod_sel));
  Transistor #(.\type ("n")) transistor_490 (.in(transistor_217_out), .out(transistor_490_out), .gate(mod_sel));
  Transistor #(.\type ("n")) transistor_491 (.in(transistor_351_out), .out(transistor_491_out), .gate(mod_sel));
  Transistor #(.\type ("n")) transistor_492 (.in(transistor_465_out), .out(transistor_492_out), .gate(mod_sel));
  Transistor #(.\type ("n")) transistor_493 (.in(transistor_447_out), .out(transistor_493_out), .gate(mod_sel));
  assign transistor_468_out = clk2 ? 1'b1 : 1'bz;  // Controlled_Buffer controlled_buffer_12
  Transistor #(.\type ("n")) transistor_494 (.in(transistor_234_out), .out(transistor_468_out), .gate(car_sel));
  assign transistor_469_out = clk2 ? 1'b1 : 1'bz;  // Controlled_Buffer controlled_buffer_13
  Transistor #(.\type ("n")) transistor_495 (.in(transistor_411_out), .out(transistor_469_out), .gate(car_sel));
  assign transistor_470_out = clk2 ? 1'b1 : 1'bz;  // Controlled_Buffer controlled_buffer_14
  Transistor #(.\type ("n")) transistor_496 (.in(transistor_452_out), .out(transistor_470_out), .gate(car_sel));
  assign transistor_471_out = clk2 ? 1'b1 : 1'bz;  // Controlled_Buffer controlled_buffer_15
  Transistor #(.\type ("n")) transistor_497 (.in(transistor_414_out), .out(transistor_471_out), .gate(car_sel));
  assign transistor_472_out = clk2 ? 1'b1 : 1'bz;  // Controlled_Buffer controlled_buffer_16
  Transistor #(.\type ("n")) transistor_498 (.in(transistor_21_out), .out(transistor_472_out), .gate(car_sel));
  assign transistor_473_out = clk2 ? 1'b1 : 1'bz;  // Controlled_Buffer controlled_buffer_17
  Transistor #(.\type ("n")) transistor_499 (.in(transistor_23_out), .out(transistor_473_out), .gate(car_sel));
  assign transistor_474_out = clk2 ? 1'b1 : 1'bz;  // Controlled_Buffer controlled_buffer_18
  Transistor #(.\type ("n")) transistor_500 (.in(transistor_204_out), .out(transistor_474_out), .gate(car_sel));
  assign transistor_475_out = clk2 ? 1'b1 : 1'bz;  // Controlled_Buffer controlled_buffer_19
  Transistor #(.\type ("n")) transistor_501 (.in(transistor_455_out), .out(transistor_475_out), .gate(car_sel));
  assign transistor_476_out = clk2 ? 1'b1 : 1'bz;  // Controlled_Buffer controlled_buffer_20
  Transistor #(.\type ("n")) transistor_502 (.in(transistor_29_out), .out(transistor_476_out), .gate(car_sel));
  assign transistor_477_out = clk2 ? 1'b1 : 1'bz;  // Controlled_Buffer controlled_buffer_21
  Transistor #(.\type ("n")) transistor_503 (.in(transistor_31_out), .out(transistor_477_out), .gate(car_sel));
  assign transistor_478_out = clk2 ? 1'b1 : 1'bz;  // Controlled_Buffer controlled_buffer_22
  Transistor #(.\type ("n")) transistor_504 (.in(transistor_457_out), .out(transistor_478_out), .gate(car_sel));
  assign transistor_479_out = clk2 ? 1'b1 : 1'bz;  // Controlled_Buffer controlled_buffer_23
  Transistor #(.\type ("n")) transistor_505 (.in(transistor_426_out), .out(transistor_479_out), .gate(car_sel));
  assign transistor_480_out = clk2 ? 1'b1 : 1'bz;  // Controlled_Buffer controlled_buffer_24
  Transistor #(.\type ("n")) transistor_506 (.in(transistor_429_out), .out(transistor_480_out), .gate(car_sel));
  assign transistor_481_out = clk2 ? 1'b1 : 1'bz;  // Controlled_Buffer controlled_buffer_25
  Transistor #(.\type ("n")) transistor_507 (.in(transistor_433_out), .out(transistor_481_out), .gate(car_sel));
  assign transistor_482_out = clk2 ? 1'b1 : 1'bz;  // Controlled_Buffer controlled_buffer_26
  Transistor #(.\type ("n")) transistor_508 (.in(transistor_260_out), .out(transistor_482_out), .gate(car_sel));
  assign transistor_483_out = clk2 ? 1'b1 : 1'bz;  // Controlled_Buffer controlled_buffer_27
  Transistor #(.\type ("n")) transistor_509 (.in(transistor_436_out), .out(transistor_483_out), .gate(car_sel));
  assign transistor_484_out = clk2 ? 1'b1 : 1'bz;  // Controlled_Buffer controlled_buffer_28
  Transistor #(.\type ("n")) transistor_510 (.in(transistor_439_out), .out(transistor_484_out), .gate(car_sel));
  assign transistor_485_out = clk2 ? 1'b1 : 1'bz;  // Controlled_Buffer controlled_buffer_29
  Transistor #(.\type ("n")) transistor_511 (.in(transistor_461_out), .out(transistor_485_out), .gate(car_sel));
  assign transistor_486_out = clk2 ? 1'b1 : 1'bz;  // Controlled_Buffer controlled_buffer_30
  Transistor #(.\type ("n")) transistor_512 (.in(transistor_343_out), .out(transistor_486_out), .gate(car_sel));
  assign transistor_487_out = clk2 ? 1'b1 : 1'bz;  // Controlled_Buffer controlled_buffer_31
  Transistor #(.\type ("n")) transistor_513 (.in(transistor_345_out), .out(transistor_487_out), .gate(car_sel));
  assign transistor_488_out = clk2 ? 1'b1 : 1'bz;  // Controlled_Buffer controlled_buffer_32
  Transistor #(.\type ("n")) transistor_514 (.in(transistor_463_out), .out(transistor_488_out), .gate(car_sel));
  assign transistor_489_out = clk2 ? 1'b1 : 1'bz;  // Controlled_Buffer controlled_buffer_33
  Transistor #(.\type ("n")) transistor_515 (.in(transistor_443_out), .out(transistor_489_out), .gate(car_sel));
  assign transistor_490_out = clk2 ? 1'b1 : 1'bz;  // Controlled_Buffer controlled_buffer_34
  Transistor #(.\type ("n")) transistor_516 (.in(transistor_378_out), .out(transistor_490_out), .gate(car_sel));
  assign transistor_491_out = clk2 ? 1'b1 : 1'bz;  // Controlled_Buffer controlled_buffer_35
  Transistor #(.\type ("n")) transistor_517 (.in(transistor_464_out), .out(transistor_491_out), .gate(car_sel));
  assign transistor_492_out = clk2 ? 1'b1 : 1'bz;  // Controlled_Buffer controlled_buffer_36
  Transistor #(.\type ("n")) transistor_518 (.in(transistor_466_out), .out(transistor_492_out), .gate(car_sel));
  assign transistor_493_out = clk2 ? 1'b1 : 1'bz;  // Controlled_Buffer controlled_buffer_37
  Transistor #(.\type ("n")) transistor_519 (.in(transistor_467_out), .out(transistor_493_out), .gate(car_sel));
  instrument_out instrument_out_1 (.value(transistor_291_out), .clk1(clk1), .oe(out_sel2), .out_4(tl[0]));
  instrument_out instrument_out_2 (.value(transistor_404_out), .clk1(clk1), .oe(out_sel2), .out_4(tl[1]));
  instrument_out instrument_out_3 (.value(transistor_405_out), .clk1(clk1), .oe(out_sel2), .out_4(tl[2]));
  instrument_out instrument_out_4 (.value(transistor_448_out), .clk1(clk1), .oe(out_sel2), .out_4(tl[3]));
  instrument_out instrument_out_5 (.value(transistor_360_out), .clk1(clk1), .oe(out_sel2), .out_4(tl[4]));
  instrument_out instrument_out_6 (.value(transistor_449_out), .clk1(clk1), .oe(out_sel2), .out_4(tl[5]));
  instrument_out instrument_out_7 (.value(transistor_293_out), .clk1(clk1), .oe(out_sel1), .out_4(dc));
  instrument_out instrument_out_8 (.value(transistor_408_out), .clk1(clk1), .oe(out_sel1), .out_4(dm));
  instrument_out instrument_out_9 (.value(transistor_450_out), .clk1(clk1), .oe(out_sel1), .out_4(fb[2]));
  instrument_out instrument_out_10 (.value(transistor_451_out), .clk1(clk1), .oe(out_sel1), .out_4(fb[1]));
  instrument_out instrument_out_11 (.value(transistor_410_out), .clk1(clk1), .oe(out_sel1), .out_4(fb[0]));
  instrument_out instrument_out_12 (.value(transistor_468_out), .clk1(clk1), .oe(out_sel1), .out_4(am));
  instrument_out instrument_out_13 (.value(transistor_469_out), .clk1(clk1), .oe(out_sel1), .out_4(vib));
  instrument_out instrument_out_14 (.value(transistor_470_out), .clk1(clk1), .oe(out_sel1), .out_4(et));
  instrument_out instrument_out_15 (.value(transistor_471_out), .clk1(clk1), .oe(out_sel1), .out_4(ksr));
  instrument_out instrument_out_16 (.value(transistor_472_out), .clk1(clk1), .oe(out_sel1), .out_4(multi[3]));
  instrument_out instrument_out_17 (.value(transistor_473_out), .clk1(clk1), .oe(out_sel1), .out_4(multi[2]));
  instrument_out instrument_out_18 (.value(transistor_474_out), .clk1(clk1), .oe(out_sel1), .out_4(multi[1]));
  instrument_out instrument_out_19 (.value(transistor_475_out), .clk1(clk1), .oe(out_sel1), .out_4(multi[0]));
  instrument_out instrument_out_20 (.value(transistor_476_out), .clk1(clk1), .oe(out_sel1), .out_4(ksl[1]));
  instrument_out instrument_out_21 (.value(transistor_477_out), .clk1(clk1), .oe(out_sel1), .out_4(ksl[0]));
  instrument_out instrument_out_22 (.value(transistor_478_out), .clk1(clk1), .oe(out_sel1), .out_4(ar[3]));
  instrument_out instrument_out_23 (.value(transistor_479_out), .clk1(clk1), .oe(out_sel1), .out_4(ar[2]));
  instrument_out instrument_out_24 (.value(transistor_480_out), .clk1(clk1), .oe(out_sel1), .out_4(ar[1]));
  instrument_out instrument_out_25 (.value(transistor_481_out), .clk1(clk1), .oe(out_sel1), .out_4(ar[0]));
  instrument_out instrument_out_26 (.value(transistor_482_out), .clk1(clk1), .oe(out_sel1), .out_4(dr[3]));
  instrument_out instrument_out_27 (.value(transistor_483_out), .clk1(clk1), .oe(out_sel1), .out_4(dr[2]));
  instrument_out instrument_out_28 (.value(transistor_484_out), .clk1(clk1), .oe(out_sel1), .out_4(dr[1]));
  instrument_out instrument_out_29 (.value(transistor_485_out), .clk1(clk1), .oe(out_sel1), .out_4(dr[0]));
  instrument_out instrument_out_30 (.value(transistor_486_out), .clk1(clk1), .oe(out_sel1), .out_4(sl[3]));
  instrument_out instrument_out_31 (.value(transistor_487_out), .clk1(clk1), .oe(out_sel1), .out_4(sl[2]));
  instrument_out instrument_out_32 (.value(transistor_488_out), .clk1(clk1), .oe(out_sel1), .out_4(sl[1]));
  instrument_out instrument_out_33 (.value(transistor_489_out), .clk1(clk1), .oe(out_sel1), .out_4(sl[0]));
  instrument_out instrument_out_34 (.value(transistor_490_out), .clk1(clk1), .oe(out_sel1), .out_4(rr[3]));
  instrument_out instrument_out_35 (.value(transistor_491_out), .clk1(clk1), .oe(out_sel1), .out_4(rr[2]));
  instrument_out instrument_out_36 (.value(transistor_492_out), .clk1(clk1), .oe(out_sel1), .out_4(rr[1]));
  instrument_out instrument_out_37 (.value(transistor_493_out), .clk1(clk1), .oe(out_sel1), .out_4(rr[0]));
endmodule

module kon_ctrl (
  input  keyon,
  input  hh,
  input  tc,
  input  tomtom,
  input  sd,
  input  bd0,
  input  bd1,
  input  hh_kon,
  input  tc_kon,
  input  tom_kon,
  input  sd_kon,
  input  bd_kon,
  output keyon_comb
);

  wire and_1_out, and_2_out, and_3_out, and_4_out, and_5_out, and_6_out;

  and and_1 (and_1_out, hh, hh_kon);
  and and_2 (and_2_out, tc, tc_kon);
  and and_3 (and_3_out, tomtom, tom_kon);
  and and_4 (and_4_out, sd, sd_kon);
  and and_5 (and_5_out, bd0, bd_kon);
  and and_6 (and_6_out, bd1, bd_kon);
  or or_1 (keyon_comb, keyon, and_1_out, and_2_out, and_3_out, and_4_out, and_5_out, and_6_out);
endmodule

module rate_calc (
  input  [3:0] ar,
  input  [3:0] dr,
  input  [3:0] rr,
  input  [1:0] eg_state,
  input  egtype,
  input  sustain,
  input  zero_rate,
  input  clk1,
  output [3:0] rate
);

  wire d_ff_1_qn, d_ff_2_qn, d_ff_3_qn, d_ff_4_q, d_ff_4_qn, d_ff_5_q, nand_1_out, nand_2_out, nand_3_out,
       nor_2_out, nor_3_out;
  wire [2:2] nor_1_out;
  wire [3:0] and_1_out, and_2_out, and_3_out, bit_extender_1_out, bit_extender_2_out, bit_extender_3_out,
       bit_extender_4_out, nor_4_out;

  D_Flip_Flop #(.trigger("high")) d_ff_1 (.D(eg_state[0]), .clk(clk1), .Qn(d_ff_1_qn));  // open: Q, preset, reset
  D_Flip_Flop #(.trigger("high")) d_ff_2 (.D(eg_state[1]), .clk(clk1), .Qn(d_ff_2_qn));  // open: Q, preset, reset
  D_Flip_Flop #(.trigger("high")) d_ff_3 (.D(sustain), .clk(clk1), .Qn(d_ff_3_qn));  // open: Q, preset, reset
  D_Flip_Flop #(.trigger("high")) d_ff_4 (
    .D(eg_state[0]), .clk(clk1), .Q(d_ff_4_q), .Qn(d_ff_4_qn));  // open: preset, reset
  D_Flip_Flop #(.trigger("high")) d_ff_5 (.D(eg_state[1]), .clk(clk1), .Q(d_ff_5_q));  // open: Qn, preset, reset
  assign and_1_out = ar & bit_extender_2_out;  // AND_Gate and_1, 4 bits wide
  assign and_2_out = dr & bit_extender_3_out;  // AND_Gate and_2, 4 bits wide
  assign and_3_out = rr & bit_extender_4_out;  // AND_Gate and_3, 4 bits wide
  nor nor_1 (nor_1_out[2], d_ff_1_qn, d_ff_2_qn, d_ff_3_qn);
  assign bit_extender_1_out = {{3{zero_rate}}, zero_rate};  // Bit_Extender bit_extender_1
  assign bit_extender_2_out = {{3{nor_2_out}}, nor_2_out};  // Bit_Extender bit_extender_2
  nor nor_2 (nor_2_out, d_ff_4_q, d_ff_5_q);
  assign bit_extender_3_out = {{3{nor_3_out}}, nor_3_out};  // Bit_Extender bit_extender_3
  nor nor_3 (nor_3_out, d_ff_4_qn, d_ff_5_q);
  assign bit_extender_4_out = {{3{nand_1_out}}, nand_1_out};  // Bit_Extender bit_extender_4
  nand nand_1 (nand_1_out, nand_2_out, nand_3_out);
  nand nand_2 (nand_2_out, d_ff_4_qn, d_ff_5_q, egtype);
  nand nand_3 (nand_3_out, d_ff_4_q, d_ff_5_q, d_ff_3_qn);
  assign nor_4_out = ~(and_1_out | and_2_out | and_3_out | {1'b0, nor_1_out[2], 1'b0, nor_1_out[2]});  // NOR_Gate nor_4, 4 bits wide
  assign rate = ~(nor_4_out | bit_extender_1_out);  // NOR_Gate nor_5, 4 bits wide
endmodule

module phase_gen (
  input  [8:0] fnum,
  input  [2:0] blockval,
  input  [3:0] multi,
  input  phase_reset,
  input  modcar_sel,
  input  rhythm,
  input  sd,
  input  tc,
  input  hh,
  input  debug_load,
  input  clock_lfo,
  input  test1,
  input  test2,
  input  test3,
  input  vib,
  input  clk1,
  input  clk2,
  output [9:0] phase_out,
  output phasegen_dbg,
  output clock_tremolo
);

  wire controlled_buffer_1_out, noise_lfsr_1_out_4, nor_1_out, not_1_out, not_2_out, sr_bit_1_valout,
       sr_bit_2_valout, sr_bit_3_valout, sr_bit_4_valout, sr_bit_5_valout, sr_bit_6_valout, sr_bit_7_valout,
       sr_bit_8_valout, sr_bit_9_valout, sr_bit_10_valout, sr_bit_11_valout, sr_bit_12_valout,
       sr_bit_13_valout, sr_bit_14_valout, sr_bit_15_valout;
  wire [2:0] sr_3bit_1_outval;
  wire [8:0] phase_gen_mem_1_valout_2, sr_9bit_1_outval;
  wire [9:0] multi_decode_1_multi_ctrl, phase_gen_mem_1_valout;
  wire [10:0] vibrato_1_fnum_vibrato;
  wire [16:0] fnum_block_1_freq;
  wire [18:0] adder_1_out, bit_extender_1_out, freq_multiply_1_freq_multi, nand_1_out, not_3_out,
       sr_19bit_1_outval, sr_19bit_2_outval;

  sr_bit sr_bit_1 (.value(phase_reset), .clk1(clk1), .clk2(clk2), .valout(sr_bit_1_valout));
  sr_bit sr_bit_2 (.value(sr_bit_1_valout), .clk1(clk1), .clk2(clk2), .valout(sr_bit_2_valout));
  sr_bit sr_bit_3 (.value(sr_bit_2_valout), .clk1(clk1), .clk2(clk2), .valout(sr_bit_3_valout));
  sr_bit sr_bit_4 (.value(sr_bit_3_valout), .clk1(clk1), .clk2(clk2), .valout(sr_bit_4_valout));
  not not_1 (not_1_out, modcar_sel);
  sr_9bit sr_9bit_1 (.value(fnum), .clk1(clk1), .clk2(clk2), .outval(sr_9bit_1_outval));
  sr_3bit sr_3bit_1 (.value(blockval), .clk1(clk1), .clk2(clk2), .outval(sr_3bit_1_outval));
  sr_19bit sr_19bit_1 (.value(freq_multiply_1_freq_multi), .clk1(clk1), .clk2(clk2), .outval(sr_19bit_1_outval));
  sr_19bit sr_19bit_2 (.value(nand_1_out), .clk1(clk1), .clk2(clk2), .outval(sr_19bit_2_outval));
  sr_bit sr_bit_5 (.value(sr_bit_4_valout), .clk1(clk1), .clk2(clk2), .valout(sr_bit_5_valout));
  assign controlled_buffer_1_out = not_1_out ? phase_reset : 1'bz;  // Controlled_Buffer controlled_buffer_1
  sr_bit sr_bit_6 (.value(sr_bit_5_valout), .clk1(clk1), .clk2(clk2), .valout(sr_bit_6_valout));
  assign controlled_buffer_1_out = modcar_sel ? sr_bit_15_valout : 1'bz;  // Controlled_Buffer controlled_buffer_2
  sr_bit sr_bit_7 (.value(sr_bit_6_valout), .clk1(clk1), .clk2(clk2), .valout(sr_bit_7_valout));
  Adder #(.width(19)) adder_1 (
    .a(sr_19bit_1_outval), .b(sr_19bit_2_outval), .out(adder_1_out), .cin(1'b1));  // open: cout
  nor nor_1 (nor_1_out, test2, not_2_out);
  assign nand_1_out = ~({phase_gen_mem_1_valout, phase_gen_mem_1_valout_2} & bit_extender_1_out);  // NAND_Gate nand_1, 19 bits wide
  sr_bit sr_bit_8 (.value(sr_bit_7_valout), .clk1(clk1), .clk2(clk2), .valout(sr_bit_8_valout));
  not not_2 (not_2_out, controlled_buffer_1_out);
  assign not_3_out = ~adder_1_out;  // NOT_Gate not_3, 19 bits wide
  assign bit_extender_1_out = {{18{nor_1_out}}, nor_1_out};  // Bit_Extender bit_extender_1
  sr_bit sr_bit_9 (.value(sr_bit_8_valout), .clk1(clk1), .clk2(clk2), .valout(sr_bit_9_valout));
  sr_bit sr_bit_10 (.value(sr_bit_9_valout), .clk1(clk1), .clk2(clk2), .valout(sr_bit_10_valout));
  vibrato vibrato_1 (
    .clock_lfo(clock_lfo), .test1(test1), .test3(test3), .vib(vib), .fnum(sr_9bit_1_outval), .clk1(clk1),
    .clk2(clk2), .clock_tremolo(clock_tremolo), .fnum_vibrato(vibrato_1_fnum_vibrato));
  fnum_block fnum_block_1 (.fnum(vibrato_1_fnum_vibrato), .blockval(sr_3bit_1_outval), .freq(fnum_block_1_freq));
  sr_bit sr_bit_11 (.value(sr_bit_10_valout), .clk1(clk1), .clk2(clk2), .valout(sr_bit_11_valout));
  sr_bit sr_bit_12 (.value(sr_bit_11_valout), .clk1(clk1), .clk2(clk2), .valout(sr_bit_12_valout));
  phase_gen_mem phase_gen_mem_1 (
    .value(not_3_out), .clk1(clk1), .clk2(clk2), .valout({phase_gen_mem_1_valout, phase_gen_mem_1_valout_2}));
  sr_bit sr_bit_13 (.value(sr_bit_12_valout), .clk1(clk1), .clk2(clk2), .valout(sr_bit_13_valout));
  freq_multiply freq_multiply_1 (
    .multi_ctrl(multi_decode_1_multi_ctrl), .freq(fnum_block_1_freq), .freq_multi(freq_multiply_1_freq_multi));
  sr_bit sr_bit_14 (.value(sr_bit_13_valout), .clk1(clk1), .clk2(clk2), .valout(sr_bit_14_valout));
  multi_decode multi_decode_1 (.multi(multi), .multi_ctrl(multi_decode_1_multi_ctrl));
  noise_lfsr noise_lfsr_1 (.test(test1), .clk1(clk1), .clk2(clk2), .out_4(noise_lfsr_1_out_4));
  sr_bit sr_bit_15 (.value(sr_bit_14_valout), .clk1(clk1), .clk2(clk2), .valout(sr_bit_15_valout));
  rhythm_phasegen rhythm_phasegen_1 (
    .phase(phase_gen_mem_1_valout), .noise(noise_lfsr_1_out_4), .rhythm(rhythm), .sd(sd), .tc(tc), .hh(hh),
    .clk1(clk1), .phaseout(phase_out));
  phasegen_debug phasegen_debug_1 (
    .phase(phase_gen_mem_1_valout_2), .load(debug_load), .clk1(clk1), .clk2(clk2), .valout(phasegen_dbg));
endmodule

module multi_decode (
  input  [3:0] multi,
  output [9:0] multi_ctrl
);

  wire nor_1_out, nor_2_out, nor_3_out, nor_4_out, nor_5_out, nor_6_out, nor_7_out, nor_8_out, nor_9_out,
       nor_10_out, nor_11_out, nor_12_out, nor_13_out;
  wire [3:0] not_1_out;

  assign not_1_out = ~multi;  // NOT_Gate not_1, 4 bits wide
  nor nor_1 (nor_1_out, multi[3], multi[2], multi[1]);
  nor nor_2 (nor_2_out, multi[3], multi[2], not_1_out[1]);
  nor nor_3 (nor_3_out, multi[3], not_1_out[2], multi[1]);
  nor nor_4 (nor_4_out, multi[3], not_1_out[2], not_1_out[1], multi[0]);
  nor nor_5 (nor_5_out, multi[3], not_1_out[2], not_1_out[1], not_1_out[0]);
  nor nor_6 (nor_6_out, not_1_out[3], multi[2], multi[1], multi[0]);
  nor nor_7 (nor_7_out, not_1_out[3], multi[2], multi[1], not_1_out[0]);
  nor nor_8 (nor_8_out, not_1_out[3], multi[2], not_1_out[1], multi[0]);
  nor nor_9 (nor_9_out, not_1_out[3], multi[2], not_1_out[1], not_1_out[0]);
  nor nor_10 (nor_10_out, not_1_out[3], not_1_out[2], multi[1], multi[0]);
  nor nor_11 (nor_11_out, not_1_out[3], not_1_out[2], multi[1], not_1_out[0]);
  nor nor_12 (nor_12_out, not_1_out[3], not_1_out[2], not_1_out[1], multi[0]);
  nor nor_13 (nor_13_out, not_1_out[3], not_1_out[2], not_1_out[1], not_1_out[0]);
  or or_1 (multi_ctrl[9], nor_10_out, nor_9_out, nor_8_out, nor_7_out);
  or or_2 (multi_ctrl[8], nor_6_out, nor_5_out, nor_4_out, nor_3_out, nor_2_out);
  buf buffer_1 (multi_ctrl[7], nor_1_out);
  or or_3 (multi_ctrl[6], nor_13_out, nor_12_out, nor_11_out);
  buf buffer_2 (multi_ctrl[5], nor_13_out);
  or or_4 (multi_ctrl[4], nor_10_out, nor_6_out, nor_1_out);
  or or_5 (multi_ctrl[3], nor_11_out, nor_7_out, nor_3_out);
  or or_6 (multi_ctrl[2], nor_12_out, nor_8_out, nor_4_out);
  buf buffer_3 (multi_ctrl[1], nor_2_out);
  or or_7 (multi_ctrl[0], nor_9_out, nor_5_out);
endmodule

module freq_multiply (
  input  [9:0] multi_ctrl,
  input  [16:0] freq,
  output [18:0] freq_multi
);

  wire [16:0] controlled_buffer_1_out;
  wire [17:0] not_1_out;
  wire [18:0] adder_1_out, controlled_buffer_5_out;

  assign controlled_buffer_1_out = multi_ctrl[9] ? freq : 17'bz;  // Controlled_Buffer controlled_buffer_1
  assign controlled_buffer_1_out = multi_ctrl[8] ? {freq[15:0], 1'b0} : 17'bz;  // Controlled_Buffer controlled_buffer_2
  assign controlled_buffer_1_out = multi_ctrl[7] ? {freq[14:0], 2'b00} : 17'bz;  // Controlled_Buffer controlled_buffer_3
  assign controlled_buffer_1_out = multi_ctrl[6] ? {17{1'b0}} : 17'bz;  // Controlled_Buffer controlled_buffer_4
  assign not_1_out = ~{1'b0, freq};  // NOT_Gate not_1, 18 bits wide
  assign controlled_buffer_5_out = multi_ctrl[5] ? {3'b000, freq[16:1]} : 19'bz;  // Controlled_Buffer controlled_buffer_5
  assign controlled_buffer_5_out = multi_ctrl[4] ? {{2{not_1_out[17]}}, not_1_out[16:0]} : 19'bz;  // Controlled_Buffer controlled_buffer_6
  assign controlled_buffer_5_out = multi_ctrl[3] ? {1'b0, freq, 1'b0} : 19'bz;  // Controlled_Buffer controlled_buffer_7
  assign controlled_buffer_5_out = multi_ctrl[2] ? {2'b00, freq} : 19'bz;  // Controlled_Buffer controlled_buffer_8
  assign controlled_buffer_5_out = multi_ctrl[1] ? {freq, 2'b00} : 19'bz;  // Controlled_Buffer controlled_buffer_9
  assign controlled_buffer_5_out = multi_ctrl[0] ? {19{1'b0}} : 19'bz;  // Controlled_Buffer controlled_buffer_10
  Adder #(.width(19)) adder_1 (
    .a(controlled_buffer_5_out), .b({controlled_buffer_1_out, 2'b00}), .out(adder_1_out), .cin(multi_ctrl[4]));  // open: cout
  assign freq_multi = ~adder_1_out;  // NOT_Gate not_2, 19 bits wide
endmodule
module sr_9bit (
  input  [8:0] value,
  input  clk1,
  input  clk2,
  output [8:0] outval
);

  sr_bit sr_bit_1 (.value(value[0]), .clk1(clk1), .clk2(clk2), .valout(outval[0]));
  sr_bit sr_bit_2 (.value(value[1]), .clk1(clk1), .clk2(clk2), .valout(outval[1]));
  sr_bit sr_bit_3 (.value(value[2]), .clk1(clk1), .clk2(clk2), .valout(outval[2]));
  sr_bit sr_bit_4 (.value(value[3]), .clk1(clk1), .clk2(clk2), .valout(outval[3]));
  sr_bit sr_bit_5 (.value(value[4]), .clk1(clk1), .clk2(clk2), .valout(outval[4]));
  sr_bit sr_bit_6 (.value(value[5]), .clk1(clk1), .clk2(clk2), .valout(outval[5]));
  sr_bit sr_bit_7 (.value(value[6]), .clk1(clk1), .clk2(clk2), .valout(outval[6]));
  sr_bit sr_bit_8 (.value(value[7]), .clk1(clk1), .clk2(clk2), .valout(outval[7]));
  sr_bit sr_bit_9 (.value(value[8]), .clk1(clk1), .clk2(clk2), .valout(outval[8]));
endmodule

module vibrato (
  input  clock_lfo,
  input  test1,
  input  test3,
  input  vib,
  input  [8:0] fnum,
  input  clk1,
  input  clk2,
  output clock_tremolo,
  output [10:0] fnum_vibrato
);

  wire adder_1_cout, and_1_out, and_2_out, and_3_out, and_4_out, cnt_bit_2_1_c_out, cnt_bit_2_2_c_out,
       cnt_bit_2_3_c_out, cnt_bit_2_3_val_out, cnt_bit_2_4_c_out, cnt_bit_2_5_c_out, cnt_bit_2_6_c_out,
       cnt_bit_2_6_val_out, cnt_bit_2_7_c_out, cnt_bit_2_8_c_out, cnt_bit_2_9_val_out, cnt_bit_2_10_c_out,
       cnt_bit_2_11_c_out, cnt_bit_2_12_c_out, cnt_bit_2_13_c_out, nand_1_out, nand_2_out, nand_3_out,
       nand_4_out, nor_1_out, nor_2_out, nor_4_out, nor_5_out, not_1_out, not_2_out, not_3_out, not_4_out,
       not_5_out, not_6_out;
  wire [9:0] xor_3_out;

  nand nand_1 (nand_1_out, clock_lfo, test3);
  nand nand_2 (nand_2_out, nand_1_out, not_1_out);
  not not_1 (not_1_out, cnt_bit_2_13_c_out);
  cnt_bit_2 cnt_bit_2_1 (
    .c_in(clock_lfo), .reset(test1), .clk1(clk1), .clk2(clk2), .c_out(cnt_bit_2_1_c_out));  // open: val_out
  cnt_bit_2 cnt_bit_2_2 (
    .c_in(cnt_bit_2_12_c_out), .reset(test1), .clk1(clk1), .clk2(clk2), .c_out(cnt_bit_2_2_c_out));  // open: val_out
  cnt_bit_2 cnt_bit_2_3 (
    .c_in(nand_2_out), .reset(test1), .clk1(clk1), .clk2(clk2), .val_out(cnt_bit_2_3_val_out),
    .c_out(cnt_bit_2_3_c_out));
  nand nand_3 (nand_3_out, nor_5_out, fnum[8]);
  and and_1 (and_1_out, fnum[8], nor_4_out);
  and and_2 (and_2_out, fnum[7], nor_5_out);
  and and_3 (and_3_out, fnum[7], nor_4_out);
  and and_4 (and_4_out, fnum[6], nor_5_out);
  nor nor_1 (nor_1_out, and_1_out, and_2_out);
  nor nor_2 (nor_2_out, and_3_out, and_4_out);
  cnt_bit_2 cnt_bit_2_4 (
    .c_in(cnt_bit_2_1_c_out), .reset(test1), .clk1(clk1), .clk2(clk2), .c_out(cnt_bit_2_4_c_out));  // open: val_out
  cnt_bit_2 cnt_bit_2_5 (
    .c_in(cnt_bit_2_2_c_out), .reset(test1), .clk1(clk1), .clk2(clk2), .c_out(cnt_bit_2_5_c_out));  // open: val_out
  cnt_bit_2 cnt_bit_2_6 (
    .c_in(cnt_bit_2_3_c_out), .reset(test1), .clk1(clk1), .clk2(clk2), .val_out(cnt_bit_2_6_val_out),
    .c_out(cnt_bit_2_6_c_out));
  xor xor_1 (xor_3_out[2], nand_3_out, xor_3_out[9]);
  xor xor_2 (xor_3_out[1], nor_1_out, xor_3_out[9]);
  xor xor_3 (xor_3_out[0], nor_2_out, xor_3_out[9]);
  cnt_bit_2 cnt_bit_2_7 (
    .c_in(cnt_bit_2_4_c_out), .reset(test1), .clk1(clk1), .clk2(clk2), .c_out(cnt_bit_2_7_c_out));  // open: val_out
  cnt_bit_2 cnt_bit_2_8 (
    .c_in(cnt_bit_2_5_c_out), .reset(test1), .clk1(clk1), .clk2(clk2), .c_out(cnt_bit_2_8_c_out));  // open: val_out
  cnt_bit_2 cnt_bit_2_9 (
    .c_in(cnt_bit_2_6_c_out), .reset(test1), .clk1(clk1), .clk2(clk2), .val_out(cnt_bit_2_9_val_out));  // open: c_out
  Adder #(.width(10)) adder_1 (
    .a({fnum, 1'b0}), .b({{7{xor_3_out[9]}}, xor_3_out[2:0]}), .out(fnum_vibrato[9:0]), .cin(xor_3_out[9]),
    .cout(adder_1_cout));
  not not_2 (not_2_out, cnt_bit_2_3_val_out);
  not not_3 (not_3_out, cnt_bit_2_6_val_out);
  not not_4 (not_4_out, adder_1_cout);
  nor nor_3 (fnum_vibrato[10], xor_3_out[9], not_4_out);
  cnt_bit_2 cnt_bit_2_10 (
    .c_in(cnt_bit_2_7_c_out), .reset(test1), .clk1(clk1), .clk2(clk2), .c_out(cnt_bit_2_10_c_out));  // open: val_out
  cnt_bit_2 cnt_bit_2_11 (
    .c_in(cnt_bit_2_8_c_out), .reset(test1), .clk1(clk1), .clk2(clk2), .c_out(cnt_bit_2_11_c_out));  // open: val_out
  not not_5 (not_5_out, not_2_out);
  nand nand_4 (nand_4_out, not_5_out, not_3_out);
  nor nor_4 (nor_4_out, not_5_out, vib);
  nor nor_5 (nor_5_out, nand_4_out, vib);
  cnt_bit_2 cnt_bit_2_12 (
    .c_in(cnt_bit_2_10_c_out), .reset(test1), .clk1(clk1), .clk2(clk2), .c_out(cnt_bit_2_12_c_out));  // open: val_out
  cnt_bit_2 cnt_bit_2_13 (
    .c_in(cnt_bit_2_11_c_out), .reset(test1), .clk1(clk1), .clk2(clk2), .c_out(cnt_bit_2_13_c_out));  // open: val_out
  nor nor_6 (xor_3_out[9], cnt_bit_2_9_val_out, vib);
  not not_6 (not_6_out, cnt_bit_2_2_c_out);
  not not_7 (clock_tremolo, not_6_out);
endmodule

module sr_3bit (
  input  [2:0] value,
  input  clk1,
  input  clk2,
  output [2:0] outval
);

  sr_bit sr_bit_1 (.value(value[0]), .clk1(clk1), .clk2(clk2), .valout(outval[0]));
  sr_bit sr_bit_2 (.value(value[1]), .clk1(clk1), .clk2(clk2), .valout(outval[1]));
  sr_bit sr_bit_3 (.value(value[2]), .clk1(clk1), .clk2(clk2), .valout(outval[2]));
endmodule

module fnum_block (
  input  [10:0] fnum,
  input  [2:0] blockval,
  output [16:0] freq
);

  wire [13:0] multiplexer_1_out;

  Multiplexer #(.select(2), .width(14)) multiplexer_1 (
    .in0({3'b000, fnum}), .in1({2'b00, fnum, 1'b0}), .in2({1'b0, fnum, 2'b00}), .in3({fnum, 3'b000}),
    .out(multiplexer_1_out), .sel(blockval[1:0]));
  Multiplexer #(.width(17)) multiplexer_2 (
    .in0({4'b0000, multiplexer_1_out[13:1]}), .in1({multiplexer_1_out, 3'b000}), .out(freq), .sel(blockval[2]));
endmodule

module sr_19bit (
  input  [18:0] value,
  input  clk1,
  input  clk2,
  output [18:0] outval
);

  sr_bit sr_bit_1 (.value(value[0]), .clk1(clk1), .clk2(clk2), .valout(outval[0]));
  sr_bit sr_bit_2 (.value(value[1]), .clk1(clk1), .clk2(clk2), .valout(outval[1]));
  sr_bit sr_bit_3 (.value(value[2]), .clk1(clk1), .clk2(clk2), .valout(outval[2]));
  sr_bit sr_bit_4 (.value(value[3]), .clk1(clk1), .clk2(clk2), .valout(outval[3]));
  sr_bit sr_bit_5 (.value(value[4]), .clk1(clk1), .clk2(clk2), .valout(outval[4]));
  sr_bit sr_bit_6 (.value(value[5]), .clk1(clk1), .clk2(clk2), .valout(outval[5]));
  sr_bit sr_bit_7 (.value(value[6]), .clk1(clk1), .clk2(clk2), .valout(outval[6]));
  sr_bit sr_bit_8 (.value(value[7]), .clk1(clk1), .clk2(clk2), .valout(outval[7]));
  sr_bit sr_bit_9 (.value(value[8]), .clk1(clk1), .clk2(clk2), .valout(outval[8]));
  sr_bit sr_bit_10 (.value(value[9]), .clk1(clk1), .clk2(clk2), .valout(outval[9]));
  sr_bit sr_bit_11 (.value(value[10]), .clk1(clk1), .clk2(clk2), .valout(outval[10]));
  sr_bit sr_bit_12 (.value(value[11]), .clk1(clk1), .clk2(clk2), .valout(outval[11]));
  sr_bit sr_bit_13 (.value(value[12]), .clk1(clk1), .clk2(clk2), .valout(outval[12]));
  sr_bit sr_bit_14 (.value(value[13]), .clk1(clk1), .clk2(clk2), .valout(outval[13]));
  sr_bit sr_bit_15 (.value(value[14]), .clk1(clk1), .clk2(clk2), .valout(outval[14]));
  sr_bit sr_bit_16 (.value(value[15]), .clk1(clk1), .clk2(clk2), .valout(outval[15]));
  sr_bit sr_bit_17 (.value(value[16]), .clk1(clk1), .clk2(clk2), .valout(outval[16]));
  sr_bit sr_bit_18 (.value(value[17]), .clk1(clk1), .clk2(clk2), .valout(outval[17]));
  sr_bit sr_bit_19 (.value(value[18]), .clk1(clk1), .clk2(clk2), .valout(outval[18]));
endmodule

module phase_gen_mem (
  input  [18:0] value,
  input  clk1,
  input  clk2,
  output [18:0] valout
);

  wire [18:0] sr_19bit_1_outval, sr_19bit_2_outval, sr_19bit_3_outval, sr_19bit_4_outval, sr_19bit_5_outval,
       sr_19bit_6_outval, sr_19bit_7_outval, sr_19bit_8_outval, sr_19bit_9_outval, sr_19bit_10_outval,
       sr_19bit_11_outval, sr_19bit_12_outval, sr_19bit_13_outval, sr_19bit_14_outval, sr_19bit_15_outval,
       sr_19bit_16_outval;

  sr_19bit sr_19bit_1 (.value(value), .clk1(clk1), .clk2(clk2), .outval(sr_19bit_1_outval));
  sr_19bit sr_19bit_2 (.value(sr_19bit_1_outval), .clk1(clk1), .clk2(clk2), .outval(sr_19bit_2_outval));
  sr_19bit sr_19bit_3 (.value(sr_19bit_2_outval), .clk1(clk1), .clk2(clk2), .outval(sr_19bit_3_outval));
  sr_19bit sr_19bit_4 (.value(sr_19bit_3_outval), .clk1(clk1), .clk2(clk2), .outval(sr_19bit_4_outval));
  sr_19bit sr_19bit_5 (.value(sr_19bit_4_outval), .clk1(clk1), .clk2(clk2), .outval(sr_19bit_5_outval));
  sr_19bit sr_19bit_6 (.value(sr_19bit_5_outval), .clk1(clk1), .clk2(clk2), .outval(sr_19bit_6_outval));
  sr_19bit sr_19bit_7 (.value(sr_19bit_6_outval), .clk1(clk1), .clk2(clk2), .outval(sr_19bit_7_outval));
  sr_19bit sr_19bit_8 (.value(sr_19bit_7_outval), .clk1(clk1), .clk2(clk2), .outval(sr_19bit_8_outval));
  sr_19bit sr_19bit_9 (.value(sr_19bit_8_outval), .clk1(clk1), .clk2(clk2), .outval(sr_19bit_9_outval));
  sr_19bit sr_19bit_10 (.value(sr_19bit_9_outval), .clk1(clk1), .clk2(clk2), .outval(sr_19bit_10_outval));
  sr_19bit sr_19bit_11 (.value(sr_19bit_10_outval), .clk1(clk1), .clk2(clk2), .outval(sr_19bit_11_outval));
  sr_19bit sr_19bit_12 (.value(sr_19bit_11_outval), .clk1(clk1), .clk2(clk2), .outval(sr_19bit_12_outval));
  sr_19bit sr_19bit_13 (.value(sr_19bit_12_outval), .clk1(clk1), .clk2(clk2), .outval(sr_19bit_13_outval));
  sr_19bit sr_19bit_14 (.value(sr_19bit_13_outval), .clk1(clk1), .clk2(clk2), .outval(sr_19bit_14_outval));
  sr_19bit sr_19bit_15 (.value(sr_19bit_14_outval), .clk1(clk1), .clk2(clk2), .outval(sr_19bit_15_outval));
  sr_19bit sr_19bit_16 (.value(sr_19bit_15_outval), .clk1(clk1), .clk2(clk2), .outval(sr_19bit_16_outval));
  sr_19bit sr_19bit_17 (.value(sr_19bit_16_outval), .clk1(clk1), .clk2(clk2), .outval(valout));
endmodule

module rhythm_phasegen (
  input  [9:0] phase,
  input  noise,
  input  rhythm,
  input  sd,
  input  tc,
  input  hh,
  input  clk1,
  output [9:0] phaseout
);
endmodule

module phasegen_debug (
  input  [8:0] phase,
  input  load,
  input  clk1,
  input  clk2,
  output valout
);
endmodule
