// Logisim project mmc1.circ as structural Verilog: 1 circuit, main circuit main
module main (
  input  clk,
  input  d,
  output q
);

  wire multiplexer_1_out, multiplexer_2_out, not_1_out, not_2_out, not_3_out, not_4_out;

  Multiplexer multiplexer_1 (.in0(d), .in1(not_2_out), .out(multiplexer_1_out), .sel(clk));
  not not_1 (not_1_out, multiplexer_1_out);
  not not_2 (not_2_out, not_1_out);
  Multiplexer multiplexer_2 (.in0(not_3_out), .in1(not_1_out), .out(multiplexer_2_out), .sel(clk));
  not not_3 (not_3_out, not_4_out);
  not not_4 (not_4_out, multiplexer_2_out);
  not not_5 (q, multiplexer_2_out);

  // Notes on the sheet:
  //   master
  //   slave
endmodule
